// Digital circuit 74573.dig as structural Verilog
// OCTAL D􏰳-TYPE TRANSPARENT LATCHES WITH 3􏰳STATE OUTPUTS
module _74573 (
  input  _0D,
  input  _1D,
  input  _2D,
  input  _3D,
  input  _4D,
  input  _5D,
  input  _6D,
  input  _7D,
  input  LE,
  input  nOE,
  input  VCC,
  input  GND,
  output _0Q,
  output _1Q,
  output _2Q,
  output _3Q,
  output _4Q,
  output _5Q,
  output _6Q,
  output _7Q
);

  wire and_1_out, and_2_out, and_3_out, and_4_out, and_5_out, and_6_out, and_7_out, and_8_out, and_9_out,
       and_10_out, and_11_out, and_12_out, and_13_out, and_14_out, and_15_out, and_16_out, rs_ff_as_1_q,
       rs_ff_as_2_q, rs_ff_as_3_q, rs_ff_as_4_q, rs_ff_as_5_q, rs_ff_as_6_q, rs_ff_as_7_q, rs_ff_as_8_q;

  PowerSupply powersupply_1 (.VDD(VCC), .GND(GND));
  and and_1 (and_1_out, LE, _0D);
  and and_2 (and_2_out, LE, ~_0D);  // And
  and and_3 (and_3_out, LE, _1D);
  and and_4 (and_4_out, LE, ~_1D);  // And
  and and_5 (and_5_out, LE, _2D);
  and and_6 (and_6_out, LE, ~_2D);  // And
  and and_7 (and_7_out, LE, _3D);
  and and_8 (and_8_out, LE, ~_3D);  // And
  and and_9 (and_9_out, LE, _4D);
  and and_10 (and_10_out, LE, ~_4D);  // And
  and and_11 (and_11_out, LE, _5D);
  and and_12 (and_12_out, LE, ~_5D);  // And
  and and_13 (and_13_out, LE, _6D);
  and and_14 (and_14_out, LE, ~_6D);  // And
  and and_15 (and_15_out, LE, _7D);
  and and_16 (and_16_out, LE, ~_7D);  // And
  RS_FF_AS rs_ff_as_1 (.S(and_1_out), .R(and_2_out), .Q(rs_ff_as_1_q));  // open: nQ
  RS_FF_AS rs_ff_as_2 (.S(and_3_out), .R(and_4_out), .Q(rs_ff_as_2_q));  // open: nQ
  RS_FF_AS rs_ff_as_3 (.S(and_5_out), .R(and_6_out), .Q(rs_ff_as_3_q));  // open: nQ
  RS_FF_AS rs_ff_as_4 (.S(and_7_out), .R(and_8_out), .Q(rs_ff_as_4_q));  // open: nQ
  RS_FF_AS rs_ff_as_5 (.S(and_9_out), .R(and_10_out), .Q(rs_ff_as_5_q));  // open: nQ
  RS_FF_AS rs_ff_as_6 (.S(and_11_out), .R(and_12_out), .Q(rs_ff_as_6_q));  // open: nQ
  RS_FF_AS rs_ff_as_7 (.S(and_13_out), .R(and_14_out), .Q(rs_ff_as_7_q));  // open: nQ
  RS_FF_AS rs_ff_as_8 (.S(and_15_out), .R(and_16_out), .Q(rs_ff_as_8_q));  // open: nQ
  assign _0Q = ~nOE ? rs_ff_as_1_q : 1'bz;  // DriverInvSel driverinvsel_1
  assign _1Q = ~nOE ? rs_ff_as_2_q : 1'bz;  // DriverInvSel driverinvsel_2
  assign _2Q = ~nOE ? rs_ff_as_3_q : 1'bz;  // DriverInvSel driverinvsel_3
  assign _3Q = ~nOE ? rs_ff_as_4_q : 1'bz;  // DriverInvSel driverinvsel_4
  assign _4Q = ~nOE ? rs_ff_as_5_q : 1'bz;  // DriverInvSel driverinvsel_5
  assign _5Q = ~nOE ? rs_ff_as_6_q : 1'bz;  // DriverInvSel driverinvsel_6
  assign _6Q = ~nOE ? rs_ff_as_7_q : 1'bz;  // DriverInvSel driverinvsel_7
  assign _7Q = ~nOE ? rs_ff_as_8_q : 1'bz;  // DriverInvSel driverinvsel_8

  // Notes on the sheet:
  //   _0D: pin 2
  //   _1D: pin 3
  //   _2D: pin 4
  //   _3D: pin 5
  //   _4D: pin 6
  //   _5D: pin 7
  //   _6D: pin 8
  //   _7D: pin 9
  //   LE: pin 11
  //   nOE: pin 1
  //   VCC: pin 20, default 1
  //   _0Q: pin 19
  //   _1Q: pin 18
  //   _2Q: pin 17
  //   _3Q: pin 16
  //   _4Q: pin 15
  //   _5Q: pin 14
  //   _6Q: pin 13
  //   _7Q: pin 12
  //   GND: pin 10
endmodule
