// Digital circuit AC.dig as structural Verilog
module AC (
  input  CLR,
  input  [11:0] IN,
  input  LATCH,
  input  CLR_2,
  output [11:0] OUT
);

  wire not_1_out;

  not not_1 (not_1_out, CLR_2);
  // _74173 _74173_1: pin names not known; wires that end beside it: 1'b1, 1'b0, IN[0], IN[1], IN[2], IN[3], 1'b0, 1'b0, LATCH, CLR, not_1_out, not_1_out, OUT[0], OUT[1], OUT[2], OUT[3]
  // _74173 _74173_2: pin names not known; wires that end beside it: 1'b1, 1'b0, IN[4], IN[5], IN[6], IN[7], 1'b0, 1'b0, LATCH, CLR, not_1_out, not_1_out, OUT[4], OUT[5], OUT[6], OUT[7]
  // _74173 _74173_3: pin names not known; wires that end beside it: 1'b1, 1'b0, IN[8], IN[9], IN[10], IN[11], 1'b0, 1'b0, LATCH, CLR, not_1_out, not_1_out, OUT[8], OUT[9], OUT[10], OUT[11]

  // Notes on the sheet:
  //   3 pcs 74173 Quad D-type FF with asynch CLR
endmodule
