// Digital circuit AOC.dig as structural Verilog
module AOC (
);

  wire OPR_CMA;
  wire [11:0] and_1_out, bitextender_1_out, bitextender_2_out, or_1_out, pulldown_1_out, undriven, xor_1_out;

  // Probe AC on undriven
  BitExtender #(.inputBits(1), .outputBits(12)) bitextender_1 (.out(bitextender_1_out));  // open: in
  assign and_1_out = undriven & ~bitextender_1_out;  // And and_1, 12 bits wide
  // Probe on and_1_out
  PullDown #(.Bits(12)) pulldown_1 (.out(pulldown_1_out));
  assign or_1_out = pulldown_1_out | and_1_out;  // Or or_1, 12 bits wide
  // Probe on pulldown_1_out
  // Probe on or_1_out
  BitExtender #(.inputBits(1), .outputBits(12)) bitextender_2 (.in(OPR_CMA), .out(bitextender_2_out));
  LED led_1 (.in(OPR_CMA));
  assign xor_1_out = or_1_out ^ bitextender_2_out;  // XOr xor_1, 12 bits wide
  // Probe on xor_1_out

  // Notes on the sheet:
  //   CLA
  //   OSR
  //   CMA
endmodule
