// Digital circuit AUTOSPY.dig as structural Verilog
module AUTOSPY (
  input  [24:0] DAW,
  output [11:0] _10,
  output [11:0] _11,
  output [11:0] _12,
  output [11:0] _13,
  output [11:0] _14,
  output [11:0] _15,
  output [11:0] _16,
  output [11:0] _17
);

  wire and_1_out, and_2_out, and_3_out, and_4_out, and_5_out, and_6_out, and_7_out, and_8_out,
       comparator_1_eq, comparator_2_eq, comparator_3_eq, comparator_4_eq, comparator_5_eq, comparator_6_eq,
       comparator_7_eq, comparator_8_eq;

  Comparator #(.Bits(12)) comparator_1 (.a(DAW[23:12]), .b(12'h8), .eq(comparator_1_eq));  // open: gt, lt
  Comparator #(.Bits(12)) comparator_2 (.a(DAW[23:12]), .b(12'h9), .eq(comparator_2_eq));  // open: gt, lt
  Comparator #(.Bits(12)) comparator_3 (.a(DAW[23:12]), .b(12'ha), .eq(comparator_3_eq));  // open: gt, lt
  Comparator #(.Bits(12)) comparator_4 (.a(DAW[23:12]), .b(12'hb), .eq(comparator_4_eq));  // open: gt, lt
  Comparator #(.Bits(12)) comparator_5 (.a(DAW[23:12]), .b(12'hc), .eq(comparator_5_eq));  // open: gt, lt
  Comparator #(.Bits(12)) comparator_6 (.a(DAW[23:12]), .b(12'hd), .eq(comparator_6_eq));  // open: gt, lt
  Comparator #(.Bits(12)) comparator_7 (.a(DAW[23:12]), .b(12'he), .eq(comparator_7_eq));  // open: gt, lt
  Comparator #(.Bits(12)) comparator_8 (.a(DAW[23:12]), .b(12'hf), .eq(comparator_8_eq));  // open: gt, lt
  and and_1 (and_1_out, comparator_1_eq, DAW[24]);
  and and_2 (and_2_out, comparator_2_eq, DAW[24]);
  and and_3 (and_3_out, comparator_3_eq, DAW[24]);
  and and_4 (and_4_out, comparator_4_eq, DAW[24]);
  and and_5 (and_5_out, comparator_5_eq, DAW[24]);
  and and_6 (and_6_out, comparator_6_eq, DAW[24]);
  and and_7 (and_7_out, comparator_7_eq, DAW[24]);
  and and_8 (and_8_out, comparator_8_eq, DAW[24]);
  Register #(.Bits(12)) register_1 (.D(DAW[11:0]), .C(and_1_out), .en(1'b1), .Q(_10));
  Register #(.Bits(12)) register_2 (.D(DAW[11:0]), .C(and_2_out), .en(1'b1), .Q(_11));
  Register #(.Bits(12)) register_3 (.D(DAW[11:0]), .C(and_3_out), .en(1'b1), .Q(_12));
  Register #(.Bits(12)) register_4 (.D(DAW[11:0]), .C(and_4_out), .en(1'b1), .Q(_13));
  Register #(.Bits(12)) register_5 (.D(DAW[11:0]), .C(and_5_out), .en(1'b1), .Q(_14));
  Register #(.Bits(12)) register_6 (.D(DAW[11:0]), .C(and_6_out), .en(1'b1), .Q(_15));
  Register #(.Bits(12)) register_7 (.D(DAW[11:0]), .C(and_7_out), .en(1'b1), .Q(_16));
  Register #(.Bits(12)) register_8 (.D(DAW[11:0]), .C(and_8_out), .en(1'b1), .Q(_17));

  // Notes on the sheet:
  //   RAM-DATA(12)
  //   RAM-ADDRESS(12)
  //   RAM_WE
endmodule
