// Digital circuit COUNTER.dig as structural Verilog
module COUNTER (
  input  i1,
  input  i2,
  input  i3,
  input  i4,
  input  i5,
  input  i6,
  input  i7,
  input  i8,
  input  i9,
  input  i10,
  input  i11,
  input  i12,
  input  i13,
  input  i14,
  input  i15,
  input  i16,
  input  i17,
  input  i18,
  input  i19,
  input  i20,
  input  i21,
  input  i22,
  input  i23,
  input  i24,
  input  i25,
  input  i26,
  input  i27,
  input  i28,
  input  i29,
  input  i30,
  input  i31,
  input  i32,
  input  C,
  input  E,
  output [31:0] o1,
  output [31:0] o2,
  output [31:0] o3,
  output [31:0] o4,
  output [31:0] o5,
  output [31:0] o6,
  output [31:0] o7,
  output [31:0] o8,
  output [31:0] o9,
  output [31:0] o10,
  output [31:0] o11,
  output [31:0] o12,
  output [31:0] o13,
  output [31:0] o14,
  output [31:0] o15,
  output [31:0] o16,
  output [31:0] o17,
  output [31:0] o18,
  output [31:0] o19,
  output [31:0] o20,
  output [31:0] o21,
  output [31:0] o22,
  output [31:0] o23,
  output [31:0] o24,
  output [31:0] o25,
  output [31:0] o26,
  output [31:0] o27,
  output [31:0] o28,
  output [31:0] o29,
  output [31:0] o30,
  output [31:0] o31,
  output [31:0] o32
);

  Counter #(.Bits(32)) CNT1 (.en(E), .C(i1), .clr(C), .out(o1));  // open: ovf
  Counter #(.Bits(32)) CNT2 (.en(E), .C(i2), .clr(C), .out(o2));  // open: ovf
  Counter #(.Bits(32)) CNT3 (.en(E), .C(i3), .clr(C), .out(o3));  // open: ovf
  Counter #(.Bits(32)) CNT4 (.en(E), .C(i4), .clr(C), .out(o4));  // open: ovf
  Counter #(.Bits(32)) CNT5 (.en(E), .C(i5), .clr(C), .out(o5));  // open: ovf
  Counter #(.Bits(32)) CNT6 (.en(E), .C(i6), .clr(C), .out(o6));  // open: ovf
  Counter #(.Bits(32)) CNT7 (.en(E), .C(i7), .clr(C), .out(o7));  // open: ovf
  Counter #(.Bits(32)) CNT8 (.en(E), .C(i8), .clr(C), .out(o8));  // open: ovf
  Counter #(.Bits(32)) CNT9 (.en(E), .C(i9), .clr(C), .out(o9));  // open: ovf
  Counter #(.Bits(32)) CNT10 (.en(E), .C(i10), .clr(C), .out(o10));  // open: ovf
  Counter #(.Bits(32)) CNT11 (.en(E), .C(i11), .clr(C), .out(o11));  // open: ovf
  Counter #(.Bits(32)) CNT12 (.en(E), .C(i12), .clr(C), .out(o12));  // open: ovf
  Counter #(.Bits(32)) CNT13 (.en(E), .C(i13), .clr(C), .out(o13));  // open: ovf
  Counter #(.Bits(32)) CNT14 (.en(E), .C(i14), .clr(C), .out(o14));  // open: ovf
  Counter #(.Bits(32)) CNT15 (.en(E), .C(i15), .clr(C), .out(o15));  // open: ovf
  Counter #(.Bits(32)) CNT16 (.en(E), .C(i16), .clr(C), .out(o16));  // open: ovf
  Counter #(.Bits(32)) CNT17 (.en(E), .C(i17), .clr(C), .out(o17));  // open: ovf
  Counter #(.Bits(32)) CNT18 (.en(E), .C(i18), .clr(C), .out(o18));  // open: ovf
  Counter #(.Bits(32)) CNT19 (.en(E), .C(i19), .clr(C), .out(o19));  // open: ovf
  Counter #(.Bits(32)) CNT20 (.en(E), .C(i20), .clr(C), .out(o20));  // open: ovf
  Counter #(.Bits(32)) CNT21 (.en(E), .C(i21), .clr(C), .out(o21));  // open: ovf
  Counter #(.Bits(32)) CNT22 (.en(E), .C(i22), .clr(C), .out(o22));  // open: ovf
  Counter #(.Bits(32)) CNT23 (.en(E), .C(i23), .clr(C), .out(o23));  // open: ovf
  Counter #(.Bits(32)) CNT24 (.en(E), .C(i24), .clr(C), .out(o24));  // open: ovf
  Counter #(.Bits(32)) CNT25 (.en(E), .C(i25), .clr(C), .out(o25));  // open: ovf
  Counter #(.Bits(32)) CNT26 (.en(E), .C(i26), .clr(C), .out(o26));  // open: ovf
  Counter #(.Bits(32)) CNT27 (.en(E), .C(i27), .clr(C), .out(o27));  // open: ovf
  Counter #(.Bits(32)) CNT28 (.en(E), .C(i28), .clr(C), .out(o28));  // open: ovf
  Counter #(.Bits(32)) CNT29 (.en(E), .C(i29), .clr(C), .out(o29));  // open: ovf
  Counter #(.Bits(32)) CNT30 (.en(E), .C(i30), .clr(C), .out(o30));  // open: ovf
  Counter #(.Bits(32)) CNT31 (.en(E), .C(i31), .clr(C), .out(o31));  // open: ovf
  Counter #(.Bits(32)) CNT32 (.en(E), .C(i32), .clr(C), .out(o32));  // open: ovf
  // Pins of 1 and 32 bits meet at o1
  // Pins of 1 and 32 bits meet at o2
  // Pins of 1 and 32 bits meet at o3
  // Pins of 1 and 32 bits meet at o4
  // Pins of 1 and 32 bits meet at o5
  // Pins of 1 and 32 bits meet at o6
  // Pins of 1 and 32 bits meet at o7
  // Pins of 1 and 32 bits meet at o8
  // Pins of 1 and 32 bits meet at o9
  // Pins of 1 and 32 bits meet at o10
  // Pins of 1 and 32 bits meet at o11
  // Pins of 1 and 32 bits meet at o12
endmodule
