// Digital circuit CSI.dig as structural Verilog
module CSI (
  input  I0,
  input  I1,
  input  I2,
  input  I3,
  output O0,
  output O1,
  output O2,
  output O3,
  output C
);

  wire and_1_out, and_2_out, and_3_out;

  not not_1 (O0, I0);
  xor xor_1 (O1, I0, I1);
  and and_1 (and_1_out, I0, I1);
  and and_2 (and_2_out, I3, I2);
  xor xor_2 (O2, and_1_out, I2);
  and and_3 (and_3_out, I2, and_1_out);
  and and_4 (C, and_1_out, and_2_out);
  xor xor_3 (O3, and_3_out, I3);
endmodule
