// Digital circuit HOLD-uART.dig as structural Verilog
module HOLD_uART (
  input  RX,
  input  ACK,
  input  OE,
  input  [7:0] DIN,
  input  STB,
  input  CLK,
  input  XTAL,
  input  CLEAR,
  output [7:0] DOUT,
  output RDY,
  output TX,
  output BUSY
);

  wire _74165_1_p18, _74393_1__1qd, _74393_1__2qa, _74393_1__2qd, _74393_2__1qb, _74393_2__1qd,
       _74393_2__2qd, _74595_1_q_a, and_1_out, CLK_t, d_ff_1_nq, d_ff_1_q, nand_1_out, nand_2_out,
       nand_4_out, nand_5_out, nand_6_out, nand_7_out, nand_8_out, nand_9_out, nand_10_out, nand_11_out,
       nand_12_out, nand_13_out, nand_14_out, nor_1_out, pulldown_3_out, pulldown_4_out, pullup_2_out,
       UART_CLK;
  wire [15:0] counter_1_out;

  Counter #(.Bits(16)) counter_1 (
    .en(1'b1), .C(CLK_t), .clr(1'b0), .out({counter_1_out[15:6], CLK, counter_1_out[4:0]}));  // open: ovf
  // Port port_1: pin names not known; wires that end beside it: 1'b1, CLK, RX
  // CntProbe cntprobe_1: pin names not known; wires that end beside it: CLK
  // CntProbe cntprobe_2: pin names not known; wires that end beside it: RX
  PullDown pulldown_1 (.out(STB));
  and and_1 (and_1_out, XTAL, CLEAR);
  PullUp pullup_1 (.out(RX));
  PullDown pulldown_2 (.out(ACK));
  xor xor_1 (UART_CLK, CLK, and_1_out);
  nand nand_1 (nand_1_out, STB, STB);
  nand nand_2 (nand_2_out, nand_10_out, _74393_1__1qd);
  // NAnd nand_3 has open pins: In_1=ACK, In_2=ACK, out=open
  nand nand_4 (nand_4_out, nand_2_out, nand_5_out);
  nand nand_5 (nand_5_out, nand_4_out, RX);
  nand nand_6 (nand_6_out, nand_1_out, nand_7_out);
  nand nand_7 (nand_7_out, nand_6_out, d_ff_1_nq);
  nor nor_1 (nor_1_out, ACK, CLEAR);
  D_FF d_ff_1 (.D(nand_6_out), .C(_74393_2__2qd), .Q(d_ff_1_q), .nQ(d_ff_1_nq));
  _74393 _74393_1 (
    .VCC(1'b1), .GND(1'b0), ._1A(UART_CLK), ._1CL(nand_4_out), ._2A(_74393_1__1qd), ._2CL(nand_4_out),
    ._1QD(_74393_1__1qd), ._2QA(_74393_1__2qa), ._2QD(_74393_1__2qd));  // open: _1QA, _1QB, _1QC, _2QB, _2QC
  // CntProbe cntprobe_3: pin names not known; wires that end beside it: nand_4_out, RDY
  // CntProbe cntprobe_4: pin names not known; wires that end beside it: nor_1_out
  RS_FF_AS rs_ff_as_1 (.S(~nand_4_out), .R(~nor_1_out), .Q(RDY));  // open: nQ
  nand nand_8 (nand_8_out, _74393_1__2qa, _74393_1__2qd);
  nand nand_9 (nand_9_out, nand_12_out, _74393_2__2qd);
  nand nand_10 (nand_10_out, nand_8_out, nand_8_out);
  // CntProbe cntprobe_5: pin names not known; wires that end beside it: RDY
  _74393 _74393_2 (
    .VCC(1'b1), .GND(1'b0), ._1A(nand_9_out), ._1CL(d_ff_1_q), ._2A(UART_CLK), ._2CL(1'b0),
    ._1QB(_74393_2__1qb), ._1QD(_74393_2__1qd), ._2QD(_74393_2__2qd));  // open: _1QA, _1QC, _2QA, _2QB, _2QC
  nand nand_11 (nand_11_out, OE, OE);
  PullDown pulldown_3 (.out(pulldown_3_out));
  PullUp pullup_2 (.out(pullup_2_out));
  nand nand_12 (nand_12_out, _74393_2__1qb, _74393_2__1qd);
  // _74165 _74165_1: pin names not known; wires that end beside it: pulldown_3_out, DIN[7], pullup_2_out, d_ff_1_nq, pulldown_3_out, 1'b0, _74393_2__2qd, 1'b1, DIN[6], DIN[5], DIN[4], DIN[3], DIN[2], DIN[1], DIN[0], 1'b1, 1'b0, _74165_1_p18
  _74595 _74595_1 (
    .SER(RX), .SCLK(_74393_1__1qd), .RCLK(nand_10_out), .nOE(nand_11_out), .nCLR(1'b1), .VCC(1'b1),
    .GND(1'b0), .Q_A(_74595_1_q_a), .Q_B(DOUT[6]), .Q_C(DOUT[5]), .Q_D(DOUT[4]), .Q_E(DOUT[3]),
    .Q_F(DOUT[2]), .Q_G(DOUT[1]), .Q_H(DOUT[0]));  // open: Q_HH
  nand nand_13 (nand_13_out, d_ff_1_nq, _74165_1_p18);
  PullUp pullup_3 (.out(DOUT[7]));
  PullDown pulldown_4 (.out(pulldown_4_out));
  nand nand_14 (nand_14_out, nand_12_out, nand_13_out);
  and and_2 (BUSY, ~CLEAR, nand_12_out);  // And
  or or_1 (TX, CLEAR, nand_14_out);

  // Other names for the same wires on the sheet: UART_DOUT[7:0] = DOUT; UART_ACK = ACK; CCC_C = CLEAR;
  //   UART_CLEAR = CLEAR; UART_OE = OE; UART_RDY = RDY; UART_RX = RX

  // Notes on the sheet:
  //   DOUT: 8 bits of parallel data from the received serial stream. Controlled by the OE input
  //   RDY: Goes high when a full byte of data has been received at the RX. Cleared at the rising edge of the ACK input
  //   RX: Serial data input
  //   ACK: Rising edge acknowledges that the received data has been read. Causes the RDY output to go low.
  //   TX: Serial data output
  //   OE: High level enables the parallel output on DOUT of of the received data
  //   DIN: 8 bit of parallel data to be sent, default 15
  //   BUSY: High while the TX output is transmidding start/data/stopbits.
  //   STB: Rising edge latches the parallel data at DIN and starts the serial output stream at TX
  //   CLK: 16 times the desired baudrate, default 15
  //   XTAL: High level enables the parallel output on DOUT of of the received data
  //   CLEAR: High level enables the parallel output on DOUT of of the received data
  //   Must be used if not the below
  //   Clock domain synchronizer
  //   10-counter, divide-by-16
  //   The Serial Receiver is based on
  //   http://digitarworld.uw.hu/circuits.html
  //   8N1
  //   7S1
  //   7M1
  //   2 pcs 7474 Dual D- Flip-Flop
  //   4 pcs 7400 Quad 2-input NAND
  //   2 pcs 74393 Dual 4-bit counter
  //   1 pcs 74165 PISO Shift register
  //   1 pcs 74595 SIPO Shift counter
endmodule
