// Digital circuit INC8.dig as structural Verilog
module INC8 (
  input  [11:0] IN,
  input  INC,
  input  OE,
  output [11:0] OUT,
  output C
);

  wire _74541_2_p18, _74541_2_p19, _74541_2_p20, and_1_out, and_2_out, and_3_out, and_4_out, and_5_out,
       and_6_out, and_7_out, and_8_out, and_9_out, and_10_out, and_11_out, and_12_out, not_1_out, xor_1_out,
       xor_2_out, xor_3_out, xor_4_out, xor_5_out, xor_6_out, xor_7_out, xor_8_out, xor_9_out, xor_10_out,
       xor_11_out, xor_12_out;
  wire [3:0] _74157_1_p16, _74157_2_p16, _74157_3_p16;

  not not_1 (not_1_out, OE);
  and and_1 (and_1_out, IN[0], IN[1]);
  and and_2 (and_2_out, IN[4], IN[5]);
  and and_3 (and_3_out, IN[8], IN[9]);
  xor xor_1 (xor_1_out, 1'b1, IN[0]);
  xor xor_2 (xor_2_out, IN[0], IN[1]);
  xor xor_3 (xor_3_out, 1'b1, IN[4]);
  xor xor_4 (xor_4_out, IN[4], IN[5]);
  xor xor_5 (xor_5_out, 1'b1, IN[8]);
  xor xor_6 (xor_6_out, IN[8], IN[9]);
  xor xor_7 (xor_7_out, and_1_out, IN[2]);
  and and_4 (and_4_out, IN[2], and_1_out);
  and and_5 (and_5_out, and_1_out, IN[3], IN[2]);
  xor xor_8 (xor_8_out, and_2_out, IN[6]);
  and and_6 (and_6_out, IN[6], and_2_out);
  and and_7 (and_7_out, and_2_out, IN[7], IN[6]);
  xor xor_9 (xor_9_out, and_3_out, IN[10]);
  and and_8 (and_8_out, IN[10], and_3_out);
  and and_9 (and_9_out, and_3_out, IN[11], IN[10]);
  xor xor_10 (xor_10_out, and_4_out, IN[3]);
  xor xor_11 (xor_11_out, and_6_out, IN[7]);
  xor xor_12 (xor_12_out, and_8_out, IN[11]);
  and and_10 (and_10_out, INC, and_5_out, and_7_out, and_9_out);
  // _74157 _74157_1: pin names not known; wires that end beside it: INC, IN[0], IN[1], IN[2], IN[3], xor_1_out, xor_2_out, xor_7_out, xor_10_out, 1'b0, 1'b1, 1'b0, _74157_1_p16[0], _74157_1_p16[1], _74157_1_p16[2], _74157_1_p16[3]
  and and_11 (and_11_out, INC, and_5_out);
  // _74157 _74157_2: pin names not known; wires that end beside it: and_11_out, IN[4], IN[5], IN[6], IN[7], xor_3_out, xor_4_out, xor_8_out, xor_11_out, 1'b0, 1'b1, 1'b0, _74157_2_p16[0], _74157_2_p16[1], _74157_2_p16[2], _74157_2_p16[3]
  and and_12 (and_12_out, 1'b1, INC, and_5_out, and_7_out);
  // _74157 _74157_3: pin names not known; wires that end beside it: and_12_out, IN[8], IN[9], IN[10], IN[11], xor_5_out, xor_6_out, xor_9_out, xor_12_out, 1'b0, 1'b1, 1'b0, _74157_3_p16[0], _74157_3_p16[1], _74157_3_p16[2], _74157_3_p16[3]
  // _74541 _74541_1: pin names not known; wires that end beside it: 1'b1, 1'b0, not_1_out, not_1_out, _74157_1_p16[0], _74157_1_p16[1], _74157_1_p16[2], _74157_1_p16[3], _74157_2_p16[0], _74157_2_p16[1], _74157_2_p16[2], _74157_2_p16[3], OUT[0], OUT[1], OUT[2], OUT[3], OUT[4], OUT[5], OUT[6], OUT[7]
  // _74541 _74541_2: pin names not known; wires that end beside it: 1'b1, 1'b0, not_1_out, not_1_out, _74157_3_p16[0], _74157_3_p16[1], _74157_3_p16[2], _74157_3_p16[3], and_10_out, 1'b0, 1'b0, 1'b0, OUT[8], OUT[9], OUT[10], OUT[11], C, _74541_2_p18, _74541_2_p19, _74541_2_p20, _74541_2_p18, _74541_2_p19, _74541_2_p20

  // Notes on the sheet:
  //   3 pcs Quad 2-input XOR
  //   1 pcs Triple 3-inout AND
  //   2 pcs Quad 2-input AND
  //   1 pcs Dual 4-input AND
  //   2 pcs 74541 Octal buffer 3-state
  //   1 pcs 7404 Hex inverter
  //   3 pcs 74154 Quad 2-to-1 mux
endmodule
