// Digital circuit INTERRUPT.dig as structural Verilog
module INTERRUPT (
  input  [2:0] IR_LEAST3,
  input  [11:0] AC,
  input  CK_AUTOINC1,
  input  CK_AUTOINC2,
  input  CK1,
  input  STB1,
  input  CK2,
  input  STB2,
  input  DEVCPU,
  input  LINK,
  input  IRQ_JMS,
  input  IRQ_BUS,
  input  CLEAR,
  output [11:0] STATUS12,
  output OR_STATUS12,
  output PC_CK,
  output AC_CK,
  output LINK_CK,
  output CLL,
  output CLA,
  output CLA_KCC,
  output ROT2AC,
  output FLAG_IRQDLY,
  output FLAG_GREATERTHAN,
  output FLAG_IRQINH,
  output FLAG_USER,
  output FLAG_ION,
  output RTF_ION,
  output RTF_LINK,
  output IOT_CAF
);

  wire and_1_out, and_2_out, and_3_out, and_4_out, and_5_out, and_6_out, and_7_out, and_8_out, and_9_out,
       and_15_out, and_16_out, IOT_GTF, IOT_IOF, IOT_ION, IOT_RTF, IOT_SGT, IOT_SKON, IOT_SRQ, IRQ_DELAY2_q,
       or_1_out, or_2_out, RTF_GREATERTANON, RTF_GREATERTHANOFF, RTF_USEROFF, RTF_USERON;

  and and_1 (and_1_out, IOT_ION, STB1);
  LED led_1 (.in(and_1_out));
  and and_2 (and_2_out, IOT_CAF, CK1);
  LED led_2 (.in(and_2_out));
  and and_3 (and_3_out, IOT_CAF, STB1);
  LED led_3 (.in(and_3_out));
  and and_4 (and_4_out, IOT_SKON, FLAG_ION, CK1);
  LED led_4 (.in(and_4_out));
  and and_5 (and_5_out, IOT_SKON, FLAG_ION, STB1);
  LED led_5 (.in(and_5_out));
  assign CLL = and_2_out ? and_2_out : 1'bz;  // Driver driver_1
  assign CLA = and_2_out ? and_2_out : 1'bz;  // Driver driver_2
  assign ROT2AC = and_2_out ? and_2_out : 1'bz;  // Driver driver_3
  assign AC_CK = and_3_out ? and_3_out : 1'bz;  // Driver driver_4
  assign LINK_CK = and_3_out ? and_3_out : 1'bz;  // Driver driver_5
  assign PC_CK = and_4_out ? and_4_out : 1'bz;  // Driver driver_6
  or or_1 (or_1_out, RTF_ION, and_1_out);
  or or_2 (or_2_out, IOT_IOF, CLEAR, IRQ_JMS, IOT_CAF, and_5_out);
  and and_6 (and_6_out, IOT_SRQ, CK1, IRQ_BUS);
  LED led_6 (.in(or_1_out));
  LED led_7 (.in(or_2_out));
  LED led_8 (.in(and_6_out));
  assign PC_CK = and_6_out ? and_6_out : 1'bz;  // Driver driver_7
  RS_FF_AS IRQ_DELAY1 (.S(or_1_out), .R(CK_AUTOINC2), .Q(FLAG_IRQDLY));  // open: nQ
  RS_FF_AS ION_FLAG (.S(or_1_out), .R(or_2_out), .Q(FLAG_ION));  // open: nQ
  LED led_9 (.in(FLAG_IRQDLY));
  LED led_10 (.in(FLAG_ION));
  and and_7 (and_7_out, ~FLAG_IRQDLY, CK_AUTOINC1);  // And
  LED led_11 (.in(and_7_out));
  RS_FF_AS IRQ_DELAY2 (.S(or_1_out), .R(and_7_out), .Q(IRQ_DELAY2_q));  // open: nQ
  LED led_12 (.in(IRQ_DELAY2_q));
  RS_FF_AS IRQ_INHIBIT (.S(1'b0), .R(1'b0), .Q(FLAG_IRQINH));  // open: nQ
  LED led_13 (.in(FLAG_IRQINH));
  and and_8 (and_8_out, IOT_GTF, CK2);
  and and_9 (and_9_out, IOT_GTF, STB2);
  // _74238 _74238_1: pin names not known; wires that end beside it: 1'b1, 1'b0, DEVCPU, 1'b0, 1'b0, IR_LEAST3[0], IR_LEAST3[1], IR_LEAST3[2], IOT_SKON, IOT_ION, IOT_IOF, IOT_SRQ, IOT_GTF, IOT_RTF, IOT_SGT, IOT_CAF
  // Probe on {LINK, FLAG_GREATERTHAN, IRQ_BUS, FLAG_IRQINH, FLAG_ION, FLAG_USER, {6{1'b0}}}
  LED led_14 (.in(and_8_out));
  LED led_15 (.in(and_9_out));
  assign ROT2AC = and_8_out ? and_8_out : 1'bz;  // Driver driver_8
  assign CLA_KCC = and_8_out ? and_8_out : 1'bz;  // Driver driver_9
  assign OR_STATUS12 = and_8_out ? and_8_out : 1'bz;  // Driver driver_10
  assign AC_CK = and_9_out ? and_9_out : 1'bz;  // Driver driver_11
  RS_FF_AS FLAG_GREATER_THAN (.S(RTF_GREATERTANON), .R(RTF_GREATERTHANOFF), .Q(FLAG_GREATERTHAN));  // open: nQ
  LED led_16 (.in(FLAG_GREATERTHAN));
  // Probe on AC
  RS_FF_AS USER_FLAG (.S(RTF_USEROFF), .R(RTF_USERON), .Q(FLAG_USER));  // open: nQ
  LED led_17 (.in(FLAG_USER));
  and and_10 (RTF_ION, IOT_RTF, CK1);
  and and_11 (RTF_USEROFF, IOT_RTF, CK1, ~AC[6]);  // And
  and and_12 (RTF_USERON, IOT_RTF, CK1, AC[6]);
  and and_13 (RTF_GREATERTHANOFF, IOT_RTF, CK1, ~AC[10]);  // And
  and and_14 (RTF_GREATERTANON, IOT_RTF, CK1, AC[10]);
  and and_15 (and_15_out, IOT_RTF, CK1);
  and and_16 (and_16_out, IOT_RTF, STB1);
  and and_17 (RTF_LINK, IOT_RTF, AC[11]);
  LED led_18 (.in(RTF_ION));
  LED led_19 (.in(RTF_USEROFF));
  LED led_20 (.in(RTF_USERON));
  LED led_21 (.in(RTF_GREATERTHANOFF));
  LED led_22 (.in(RTF_GREATERTANON));
  LED led_23 (.in(and_15_out));
  assign CLL = and_15_out ? and_15_out : 1'bz;  // Driver driver_12
  LED led_24 (.in(and_16_out));
  assign LINK_CK = and_16_out ? and_16_out : 1'bz;  // Driver driver_13
  LED led_25 (.in(RTF_LINK));

  assign STATUS12 = {LINK, FLAG_GREATERTHAN, IRQ_BUS, FLAG_IRQINH, FLAG_ION, FLAG_USER, {6{1'b0}}};

  // Other names for the same wires on the sheet: CCC_C = CLEAR; CK_1 = CK1; CK_2 = CK2; IOT_DEVCPU = DEVCPU;
  //   STB_1 = STB1; STB_2 = STB2

  // Notes on the sheet:
  //   Turn interrupt ON
  //   Turn interrupt OFF
  //   Clear All Flags
  //   Skip if interrupt ON, and turn OFF
  //   Skip interrupt request
  //   Skip on Greater Than flag
  //   Get interrupt flags
  //   600x
  //   CPU FLAGS & 
  //   INTERRUPT
  //   AC6..11 - Save field register
  //   AC5 - User flag
  //   AC4 - Interrupt Enable flip-flop
  //   AC3 - Interrupt inhibit flip-flop
  //   AC2 - Interrupt Request line
  //   AC1 - Greater than flag
  //   AC0 - LINK
  //   Restore interrupt flags
  //   HANDLES USER FLAG
  //   HANDLES GREATER THAN FLAG
  //   HANDLES LINK
endmodule
