// Digital circuit MQ.dig as structural Verilog
module MQ (
  input  LATCH,
  input  CLR,
  input  OE,
  input  [11:0] IN,
  input  HOLD,
  output [11:0] MQ,
  output [11:0] OUT
);

  wire _74373_1_p13, _74373_1_p14, _74373_1_p15, _74373_1_p16, _74373_1_p17, _74373_1_p18, _74373_1_p19,
       _74373_1_p20, _74373_2_p13, _74373_2_p14, _74373_2_p15, _74373_2_p16, _74374_2_p17, _74374_2_p18,
       _74374_2_p19, _74374_2_p20, _74374_4_p17, _74374_4_p18, _74374_4_p19, _74374_4_p20, and_1_out,
       and_2_out, and_3_out, and_4_out, and_5_out, and_6_out, and_7_out, and_8_out, and_9_out, and_10_out,
       and_11_out, and_12_out, not_1_out, not_2_out, not_3_out, not_4_out;

  not not_1 (not_1_out, HOLD);
  not not_2 (not_2_out, LATCH);
  not not_3 (not_3_out, CLR);
  not not_4 (not_4_out, OE);
  // _74373 _74373_1: pin names not known; wires that end beside it: 1'b0, not_1_out, IN[0], IN[1], IN[2], IN[3], IN[4], IN[5], IN[6], IN[7], 1'b1, 1'b0, _74373_1_p13, _74373_1_p14, _74373_1_p15, _74373_1_p16, _74373_1_p17, _74373_1_p18, _74373_1_p19, _74373_1_p20
  // _74373 _74373_2: pin names not known; wires that end beside it: 1'b0, not_1_out, IN[8], IN[9], IN[10], IN[11], 1'b0, 1'b0, 1'b0, 1'b0, 1'b1, 1'b0, _74373_2_p13, _74373_2_p14, _74373_2_p15, _74373_2_p16
  and and_1 (and_1_out, _74373_1_p13, not_3_out);
  and and_2 (and_2_out, _74373_1_p14, not_3_out);
  and and_3 (and_3_out, _74373_1_p15, not_3_out);
  and and_4 (and_4_out, _74373_1_p16, not_3_out);
  and and_5 (and_5_out, _74373_1_p17, not_3_out);
  and and_6 (and_6_out, _74373_1_p18, not_3_out);
  and and_7 (and_7_out, _74373_1_p19, not_3_out);
  and and_8 (and_8_out, _74373_1_p20, not_3_out);
  and and_9 (and_9_out, _74373_2_p13, not_3_out);
  and and_10 (and_10_out, _74373_2_p14, not_3_out);
  and and_11 (and_11_out, _74373_2_p15, not_3_out);
  and and_12 (and_12_out, _74373_2_p16, not_3_out);
  // _74374 _74374_1: pin names not known; wires that end beside it: 1'b0, not_2_out, and_1_out, and_2_out, and_3_out, and_4_out, and_5_out, and_6_out, and_7_out, and_8_out, 1'b1, 1'b0, MQ[0], MQ[1], MQ[2], MQ[3], MQ[4], MQ[5], MQ[6], MQ[7]
  // _74374 _74374_2: pin names not known; wires that end beside it: 1'b0, not_2_out, and_9_out, and_10_out, and_11_out, and_12_out, 1'b0, 1'b0, 1'b0, 1'b0, 1'b1, 1'b0, MQ[8], MQ[9], MQ[10], MQ[11], _74374_2_p17, _74374_2_p18, _74374_2_p19, _74374_2_p20, _74374_2_p17, _74374_2_p18, _74374_2_p19, _74374_2_p20
  // _74374 _74374_3: pin names not known; wires that end beside it: not_4_out, not_2_out, and_1_out, and_2_out, and_3_out, and_4_out, and_5_out, and_6_out, and_7_out, and_8_out, 1'b1, 1'b0, OUT[0], OUT[1], OUT[2], OUT[3], OUT[4], OUT[5], OUT[6], OUT[7]
  // _74374 _74374_4: pin names not known; wires that end beside it: not_4_out, not_2_out, and_9_out, and_10_out, and_11_out, and_12_out, 1'b0, 1'b0, 1'b0, 1'b0, 1'b1, 1'b0, OUT[8], OUT[9], OUT[10], OUT[11], _74374_4_p17, _74374_4_p18, _74374_4_p19, _74374_4_p20, _74374_4_p17, _74374_4_p18, _74374_4_p19, _74374_4_p20

  // Notes on the sheet:
  //   1 pcs 7404 Hex inverter
  //   3 pcs 7408 Quad 2-input AND
  //   2 pcs 74574 Octal  latch 3-state
endmodule
