// Digital circuit MultiLatchClr.dig as structural Verilog
module MultiLatchClr (
  input  CLR,
  input  [11:0] IN,
  input  LATCH,
  input  OE,
  input  OE1,
  input  OE2,
  output [11:0] OUT1,
  output [11:0] OUT2,
  output [11:0] mon
);

  wire not_1_out, not_2_out, not_3_out;

  not not_1 (not_1_out, OE);
  not not_2 (not_2_out, OE1);
  not not_3 (not_3_out, OE2);
  // _74173 _74173_1: pin names not known; wires that end beside it: 1'b1, 1'b0, IN[0], IN[1], IN[2], IN[3], 1'b0, 1'b0, LATCH, CLR, not_1_out, not_1_out, mon[0], mon[1], mon[2], mon[3]
  // _74173 _74173_2: pin names not known; wires that end beside it: 1'b1, 1'b0, IN[4], IN[5], IN[6], IN[7], 1'b0, 1'b0, LATCH, CLR, not_1_out, not_1_out, mon[4], mon[5], mon[6], mon[7]
  // _74173 _74173_3: pin names not known; wires that end beside it: 1'b1, 1'b0, IN[8], IN[9], IN[10], IN[11], 1'b0, 1'b0, LATCH, CLR, not_1_out, not_1_out, mon[8], mon[9], mon[10], mon[11]
  // _74541 _74541_1: pin names not known; wires that end beside it: 1'b1, 1'b0, not_2_out, not_2_out, mon[0], mon[1], mon[2], mon[3], mon[4], mon[5], mon[6], mon[7], OUT1[0], OUT1[1], OUT1[2], OUT1[3], OUT1[4], OUT1[5], OUT1[6], OUT1[7]
  // _74541 _74541_2: pin names not known; wires that end beside it: 1'b1, 1'b0, not_2_out, not_2_out, mon[8], mon[9], mon[10], mon[11], 1'b0, 1'b0, 1'b0, 1'b0, OUT1[8], OUT1[9], OUT1[10], OUT1[11]
  // _74541 _74541_3: pin names not known; wires that end beside it: 1'b1, 1'b0, not_3_out, not_3_out, mon[0], mon[1], mon[2], mon[3], mon[4], mon[5], mon[6], mon[7], OUT2[0], OUT2[1], OUT2[2], OUT2[3], OUT2[4], OUT2[5], OUT2[6], OUT2[7]
  // _74541 _74541_4: pin names not known; wires that end beside it: 1'b1, 1'b0, not_3_out, not_3_out, mon[8], mon[9], mon[10], mon[11], 1'b0, 1'b0, 1'b0, 1'b0, OUT2[8], OUT2[9], OUT2[10], OUT2[11]

  // Notes on the sheet:
  //   3 pcs 74173 Quad D-type FF with asynch CLR
endmodule
