// Digital circuit OC12.dig as structural Verilog
module OC12 (
  input  E,
  input  [6:0] I_L,
  input  [4:0] I_U,
  input  Z,
  output [6:0] O_L,
  output [4:0] O_U
);

  wire not_1_out;
  wire [4:0] multiplexer_1_out;

  Multiplexer #(.Bits(5)) multiplexer_1 (.sel(not_1_out), .in_0(I_U), .in_1({5{1'b0}}), .out(multiplexer_1_out));
  not not_1 (not_1_out, Z);
  PullDown pulldown_1 (.out(Z));
  PullDown pulldown_2 (.out(E));
  assign O_L[0] = E ? I_L[0] : 1'bz;  // Driver driver_1
  assign O_L[1] = E ? I_L[1] : 1'bz;  // Driver driver_2
  assign O_L[2] = E ? I_L[2] : 1'bz;  // Driver driver_3
  assign O_L[3] = E ? I_L[3] : 1'bz;  // Driver driver_4
  assign O_L[4] = E ? I_L[4] : 1'bz;  // Driver driver_5
  assign O_L[5] = E ? I_L[5] : 1'bz;  // Driver driver_6
  assign O_L[6] = E ? I_L[6] : 1'bz;  // Driver driver_7
  assign O_U[0] = E ? multiplexer_1_out[0] : 1'bz;  // Driver driver_8
  assign O_U[1] = E ? multiplexer_1_out[1] : 1'bz;  // Driver driver_9
  assign O_U[2] = E ? multiplexer_1_out[2] : 1'bz;  // Driver driver_10
  assign O_U[3] = E ? multiplexer_1_out[3] : 1'bz;  // Driver driver_11
  assign O_U[4] = E ? multiplexer_1_out[4] : 1'bz;  // Driver driver_12

  // Notes on the sheet:
  //   O_L: Lower 7 bits output
  //   O_U: Upper 5 bits output
  //   E: Enable
  //   I_L: Lower 7 bits input
  //   I_U: Upper 5 bits
  //   Z: Zero the 5 high order bits if low
endmodule
