// Digital circuit PC.dig as structural Verilog
module PC (
  input  [11:0] IN,
  input  CLK,
  input  LD,
  input  CLR,
  input  LATCH1,
  input  LATCH2,
  output [11:0] PC,
  output [11:0] LPC
);

  wire _74161_1_p12, _74161_2_p12, not_1_out, not_2_out, or_1_out;

  not not_1 (not_1_out, LD);
  not not_2 (not_2_out, CLR);
  or or_1 (or_1_out, LATCH1, LATCH2);
  // _74161 _74161_1: pin names not known; wires that end beside it: not_1_out, not_2_out, CLK, 1'b1, 1'b1, IN[0], IN[1], IN[2], IN[3], 1'b1, 1'b0, _74161_1_p12, PC[0], PC[1], PC[2], PC[3]
  // _74161 _74161_2: pin names not known; wires that end beside it: not_1_out, not_2_out, CLK, _74161_1_p12, _74161_1_p12, IN[4], IN[5], IN[6], IN[7], 1'b1, 1'b0, _74161_2_p12, PC[4], PC[5], PC[6], PC[7]
  // _74161 _74161_3: pin names not known; wires that end beside it: not_1_out, not_2_out, CLK, _74161_2_p12, _74161_2_p12, IN[8], IN[9], IN[10], IN[11], 1'b1, 1'b0, PC[8], PC[9], PC[10], PC[11]
  _74573 _74573_1 (
    ._0D(PC[0]), ._1D(PC[1]), ._2D(PC[2]), ._3D(PC[3]), ._4D(PC[4]), ._5D(PC[5]), ._6D(PC[6]), ._7D(PC[7]),
    .LE(or_1_out), .nOE(1'b0), .VCC(1'b1), .GND(1'b0), ._0Q(LPC[0]), ._1Q(LPC[1]), ._2Q(LPC[2]),
    ._3Q(LPC[3]), ._4Q(LPC[4]), ._5Q(LPC[5]), ._6Q(LPC[6]), ._7Q(LPC[7]));
  _74573 _74573_2 (
    ._0D(PC[8]), ._1D(PC[9]), ._2D(PC[10]), ._3D(PC[11]), ._4D(1'b0), ._5D(1'b0), ._6D(1'b0), ._7D(1'b0),
    .LE(or_1_out), .nOE(1'b0), .VCC(1'b1), .GND(1'b0), ._0Q(LPC[8]), ._1Q(LPC[9]), ._2Q(LPC[10]),
    ._3Q(LPC[11]));  // open: _4Q, _5Q, _6Q, _7Q

  // Notes on the sheet:
  //   CLK increments the count at rising edge if LD is low
  //   CLK loads the value from IN at rising edge if LD is high
  //   CLR asynchronously clears the counters 
  //   While LATCH is high the count value is transparently 
  //   transferred to LPC and  locked in at the falling edge 
  //   of LATCH
endmodule
