// Digital circuit PDP8-Focal69-newtty.dig as structural Verilog
module PDP8_Focal69_newtty (
  input  clk
);

  wire _74238_4_p12, _74238_4_p16, _74238_5_p12, _74238_5_p16, _74238_9_p12, _74238_9_p16, _74238_10_p12,
       _74238_10_p16, AC2RAMD, AC_CK, add_1_c_o, add_2_c_o, AND, and_1_out, and_3_out, and_4_out, and_5_out,
       and_6_out, and_13_out, and_14_out, and_15_out, and_16_out, and_28_out, and_29_out, and_30_out,
       and_40_out, and_41_out, and_42_out, and_43_out, and_51_out, and_52_out, and_53_out, and_54_out,
       and_55_out, and_56_out, and_57_out, and_58_out, and_59_out, and_60_out, and_61_out, and_62_out,
       and_63_out, and_64_out, and_65_out, and_66_out, and_67_out, and_68_out, and_69_out, and_70_out,
       and_71_out, and_72_out, and_73_out, and_74_out, and_75_out, and_76_out, and_77_out, and_78_out,
       and_79_out, and_80_out, and_81_out, and_82_out, and_88_out, and_89_out, and_91_out, and_92_out,
       and_93_out, and_94_out, and_95_out, and_96_out, and_97_out, and_98_out, and_99_out, and_100_out,
       and_101_out, and_102_out, and_103_out, and_104_out, and_105_out, and_106_out, and_107_out,
       and_108_out, and_109_out, and_110_out, and_111_out, and_112_out, and_113_out, and_114_out,
       and_115_out, and_116_out, and_117_out, and_118_out, and_119_out, and_120_out, and_121_out,
       and_122_out, and_123_out, and_124_out, and_125_out, and_126_out, and_127_out, and_128_out,
       and_129_out, and_130_out, and_131_out, and_132_out, and_133_out, and_134_out, and_135_out,
       and_154_out, and_155_out, and_156_out, and_157_out, and_158_out, and_159_out, and_160_out,
       and_161_out, and_162_out, CCC_BP1, CCC_BP2, CCC_BPI, CCC_BPICTRL, CCC_C, CCC_H, CCC_HLTCTRL, CCC_I,
       CCC_R, CCC_S, CCC_T, CK_1, CK_2, CK_3, CK_4, CK_5, CK_6, CK_AUTOINC1, CK_AUTOINC2, CK_FETCH,
       CK_INDIRECT, CLA, CLA_KCC, CLAx, CLK_t, CLL, cntprobe_1_p1, cntprobe_3_p1, comparator_1_eq,
       counter_1_ovf, counter_2_ovf, counter_3_ovf, d_ff_1_q, DATA_CK, DCA, delay_1_out, DIRECT, DONE,
       driver_10_out, FLAG_GREATERTHAN, FLAG_ION, FLAG_IRQDLY, FLAG_IRQINH, FLAG_KBD, FLAG_KBDIE,
       FLAG_PRNCOMPLETE, FLAG_USER, FORCE4000, HALT, i_cla, i_cll, i_cma, i_cml, i_hlt, i_iac, i_nop, i_osr,
       i_ral, i_rar, i_rtl, i_rtr, i_skp, i_sma, i_sna, i_snl, i_spa, i_sza, i_szl, IN_IR2PC, INC2RAMD,
       INCZERO, IND2INC, IND2PC, IND2RAMA, IND_CK, INDIRECT, INIR2RAMA, IOT, IOT_CAF, IOT_DEV5, IOT_DEV6,
       IOT_DEV7, IOT_DEVCPU, IOT_DEVHSP, IOT_DEVHSR, IOT_DEVKBD, IOT_DEVPRI, IOT_GTF, IOT_IOF, IOT_ION,
       IOT_KCC, IOT_KCF, IOT_KIE, IOT_KRB, IOT_KRS, IOT_KSF, IOT_RTF, IOT_SGT, IOT_SKON, IOT_SRQ, IOT_TCF,
       IOT_TFL, IOT_TLS, IOT_TPC, IOT_TSF, IOT_TSK, IR2PC, IR2RAMA, IR_CK, IRQ_BUS, IRQ_DELAY2_q, IRQ_JMS,
       ISZ, JMP, JMS, L_CAF, L_DEV5, L_DEV6, L_DEV7, L_DEVCPU, L_DEVHSP, L_DEVHSR, L_DEVKBD, L_DEVPRI,
       LD2INC, LINK, LINK_CK, monoflop_1_q, monoflop_2_q, MQ_CK, nor_1_out, nor_2_out, nor_3_out, nor_4_out,
       nor_5_out, nor_6_out, nor_7_out, nor_8_out, not_1_out, not_2_out, not_3_out, not_4_out, not_5_out,
       not_6_out, not_7_out, not_9_out, not_10_out, not_11_out, not_12_out, not_13_out, not_14_out, OPR1,
       OPR2, OPR3, OPR_CLL, OPR_CMA, OPR_CML, OPR_HLT, OPR_IAC, OPR_LEFT, OPR_NA1, OPR_O, OPR_OSR, OPR_RIGHT,
       OPR_SMASPA, OPR_SNLSZL, OPR_SZASNA, OPR_TSTINV, OPR_X2, or_1_out, or_2_out, or_4_out, or_5_out,
       or_6_out, or_7_out, or_8_out, or_9_out, or_12_out, or_13_out, or_14_out, or_15_out, or_16_out,
       or_17_out, or_18_out, or_20_out, or_21_out, or_22_out, OR_KBD, OR_STATUS12, PC2ADDR, PC2RAMD, PC_CK,
       PC_LD, PH_FIRST, PH_LAST, PH_STB, port_1_p3, RAM_OE, RAMA_HOLD, RAMD2AC_ADD, RAMD2AC_AND, RAMD2IND,
       RAMD2PC, ramspy_1_o, ramspy_2_o, ramspy_3_o, reset_1_out, risingedgedet_1_y, risingedgedet_2_y,
       risingedgedet_3_y, ROT2AC, rotater_focal69_1_p5, rs_ff_as_1_q, rs_ff_as_2_q, rs_ff_as_3_q,
       RTF_GREATERTANON, RTF_GREATERTHANOFF, RTF_ION, RTF_LINK, RTF_USEROFF, RTF_USERON, SETPC, SKIP, STB_1,
       STB_2, STB_3, STB_4, STB_5, STB_6, STB_AUTOINC1, STB_AUTOINC2, STB_FETCH, STB_INDIRECT, TAD_OVF_q,
       uart_1_busy, uart_1_rdy, uart_1_tx, xor_1_out, xor_3_out, xor_4_out, xor_5_out, xor_6_out;
  wire [3:0] CK_NUM;
  wire [4:0] add_3_s, counter_3_out, multiplexer_1_out;
  wire [5:0] counter_2_out, L_KBD, L_PRN;
  wire [7:0] KBD8;
  wire [7:1] L_CPU;
  wire [8:8] L_OPR1;
  wire [9:9] L_OPR2;
  wire [10:0] L_GEN;
  wire [11:0] AC, add_1_s, add_2_s, and_2_out, and_7_out, and_12_out, autospy_1__10, autospy_1__11,
       autospy_1__12, autospy_1__13, autospy_1__14, autospy_1__15, autospy_1__16, autospy_1__17,
       bitextender_1_out, bitextender_2_out, bitextender_3_out, BUS_IR, BUS_PC, DATA, dipswitch_1_out,
       driver_1_out, driver_22_out, INC_s, INDOUT, LATCHED_PC, LATCHEDDATA, MQ, not_8_out, or_3_out, PCIN,
       rotater_focal69_1_p4, xor_2_out;
  wire [11:8] driver_4_out;
  wire [12:0] L_OPR3;
  wire [15:0] counter_10_out;
  wire [19:0] counter_1_out;
  wire [24:0] DAW;
  wire [31:0] counter_4_out, counter_5_out, counter_6_out, counter_7_out, counter_8_out, counter_9_out,
       INSTCNT;

  // Probe on BUS_IR
  nor nor_1 (nor_1_out, BUS_IR[4], BUS_IR[5], BUS_IR[6]);
  nor nor_2 (nor_2_out, LATCHED_PC[7], LATCHED_PC[8], LATCHED_PC[9]);
  nor nor_3 (nor_3_out, LATCHED_PC[10], LATCHED_PC[11], 1'b0);
  and and_1 (and_1_out, BUS_IR[3], nor_1_out);
  Seven_Seg_Hex seven_seg_hex_1 (.d({1'b0, BUS_PC[11:9]}), .dp(1'b0));
  Seven_Seg_Hex seven_seg_hex_2 (.d({1'b0, BUS_IR[11:9]}), .dp(1'b0));
  Seven_Seg_Hex seven_seg_hex_3 (.d({1'b0, AC[11:9]}), .dp(1'b0));
  Seven_Seg_Hex seven_seg_hex_4 (.d({1'b0, MQ[11:9]}), .dp(1'b0));
  LED led_1 (.in(LINK));
  RAMSPY ramspy_1 (.A(12'h5b4), .O(ramspy_1_o), .DAW(DAW));
  RAMSPY ramspy_2 (.A(12'h5b5), .O(ramspy_2_o), .DAW(DAW));
  RAMSPY ramspy_3 (.A(12'h36), .O(ramspy_3_o), .DAW(DAW));
  AUTOSPY autospy_1 (
    .DAW(DAW), ._10(autospy_1__10), ._11(autospy_1__11), ._12(autospy_1__12), ._13(autospy_1__13),
    ._14(autospy_1__14), ._15(autospy_1__15), ._16(autospy_1__16), ._17(autospy_1__17));
  // Probe on DATA
  not not_1 (not_1_out, BUS_IR[7]);
  // _74238 _74238_1: pin names not known; wires that end beside it: 1'b1, 1'b0, 1'b1, 1'b0, 1'b0, BUS_IR[9], BUS_IR[10], BUS_IR[11], AND, L_GEN[10], ISZ, DCA, JMS, JMP, IOT, L_GEN[4]
  Seven_Seg_Hex seven_seg_hex_5 (.d({1'b0, BUS_PC[8:6]}), .dp(1'b0));
  Seven_Seg_Hex seven_seg_hex_6 (.d({1'b0, BUS_IR[8:6]}), .dp(1'b0));
  Seven_Seg_Hex seven_seg_hex_7 (.d({1'b0, AC[8:6]}), .dp(1'b0));
  Seven_Seg_Hex seven_seg_hex_8 (.d({1'b0, MQ[8:6]}), .dp(1'b0));
  assign and_2_out = AC & DATA;  // And and_2, 12 bits wide
  Add #(.Bits(12)) add_1 (.a(AC), .b(DATA), .c_i(1'b0), .s(add_1_s), .c_o(add_1_c_o));
  and and_3 (and_3_out, add_1_c_o, RAMD2AC_ADD);
  LED led_2 (.in(RAMD2AC_ADD));
  and and_4 (and_4_out, nor_2_out, nor_3_out, and_1_out);
  and and_5 (and_5_out, not_1_out, and_1_out);
  Seven_Seg_Hex seven_seg_hex_9 (.d({1'b0, BUS_PC[5:3]}), .dp(1'b0));
  Seven_Seg_Hex seven_seg_hex_10 (.d({1'b0, BUS_IR[5:3]}), .dp(1'b0));
  Seven_Seg_Hex seven_seg_hex_11 (.d({1'b0, AC[5:3]}), .dp(1'b0));
  Seven_Seg_Hex seven_seg_hex_12 (.d({1'b0, MQ[5:3]}), .dp(1'b0));
  // Probe on ramspy_1_o
  // Probe on ramspy_2_o
  // Probe on ramspy_3_o
  // Probe on autospy_1__10
  // Probe on autospy_1__11
  // Probe on autospy_1__12
  // Probe on autospy_1__13
  // Probe on autospy_1__14
  // Probe on autospy_1__15
  // Probe on autospy_1__16
  // Probe on autospy_1__17
  LED led_3 (.in(add_1_c_o));
  LED led_4 (.in(and_3_out));
  LED led_5 (.in(STB_1));
  not not_2 (not_2_out, 1'b0);
  not not_3 (not_3_out, 1'b0);
  not not_4 (not_4_out, 1'b0);
  Seven_Seg_Hex seven_seg_hex_13 (.d({1'b0, BUS_PC[2:0]}), .dp(1'b0));
  Seven_Seg_Hex seven_seg_hex_14 (.d({1'b0, BUS_IR[2:0]}), .dp(1'b0));
  Seven_Seg_Hex seven_seg_hex_15 (.d({1'b0, AC[2:0]}), .dp(1'b0));
  Seven_Seg_Hex seven_seg_hex_16 (.d({1'b0, MQ[2:0]}), .dp(1'b0));
  // Probe on AC
  // Probe on and_2_out
  // Probe on add_1_s
  // Probe on rotater_focal69_1_p4
  D_FF TAD_OVF (.D(and_3_out), .C(STB_1), .Q(TAD_OVF_q));  // open: nQ
  nor nor_4 (nor_4_out, and_4_out, 1'b0, and_5_out);
  nor nor_5 (nor_5_out, not_2_out, not_3_out, not_4_out);
  LED led_6 (.in(MQ_CK));
  LED led_7 (.in(TAD_OVF_q));
  LED led_8 (.in(L_OPR3[12]));
  LED led_9 (.in(L_OPR2[9]));
  LED led_10 (.in(i_nop));
  LED led_11 (.in(AND));
  LED led_12 (.in(AC[11]));
  LED led_13 (.in(MQ[11]));
  Seven_Seg_Hex seven_seg_hex_17 (.d(CK_NUM), .dp(1'b0));
  and and_6 (and_6_out, L_OPR3[7], MQ_CK);
  assign driver_1_out = RAMD2AC_AND ? and_2_out : 12'bz;  // Driver driver_1
  LED led_14 (.in(RAMD2AC_AND));
  assign driver_1_out = RAMD2AC_ADD ? add_1_s : 12'bz;  // Driver driver_2
  LED led_15 (.in(RAMD2AC_ADD));
  assign driver_1_out = ROT2AC ? rotater_focal69_1_p4 : 12'bz;  // Driver driver_3
  LED led_16 (.in(ROT2AC));
  xor xor_1 (xor_1_out, TAD_OVF_q, rotater_focal69_1_p5);
  not not_5 (not_5_out, nor_4_out);
  not not_6 (not_6_out, BUS_IR[8]);
  LED led_17 (.in(L_OPR3[11]));
  LED led_18 (.in(i_skp));
  LED led_19 (.in(L_OPR1[8]));
  LED led_20 (.in(L_GEN[10]));
  LED led_21 (.in(AC[10]));
  LED led_22 (.in(AC[9]));
  LED led_23 (.in(MQ[10]));
  LED led_24 (.in(MQ[9]));
  // Probe on LATCHED_PC
  // Probe on and_7_out
  LED led_25 (.in(and_6_out));
  // Probe on driver_1_out
  LED led_26 (.in(xor_1_out));
  nor nor_6 (nor_6_out, L_GEN[4], 1'b0, IOT);
  LED led_27 (.in(L_OPR3[10]));
  LED led_28 (.in(i_sma));
  LED led_29 (.in(i_cll));
  LED led_30 (.in(ISZ));
  LED led_31 (.in(AC[8]));
  LED led_32 (.in(AC[7]));
  LED led_33 (.in(MQ[8]));
  LED led_34 (.in(MQ[7]));
  LED led_35 (.in(PH_FIRST));
  assign and_7_out = AC & ~bitextender_1_out;  // And and_7, 12 bits wide
  D_FF #(.Bits(12)) u_AC (.D(driver_1_out), .C(AC_CK), .Q(AC));  // open: nQ
  LED led_36 (.in(AC_CK));
  D_FF u_LINK (.D(xor_1_out), .C(LINK_CK), .Q(LINK));  // open: nQ
  LED led_37 (.in(LINK_CK));
  and and_8 (L_GEN[1], nor_6_out, BUS_IR[8], not_5_out);
  and and_9 (INDIRECT, nor_6_out, BUS_IR[8], nor_4_out);
  and and_10 (DIRECT, nor_6_out, not_6_out);
  and and_11 (L_GEN[0], nor_6_out, BUS_IR[7]);
  LED led_38 (.in(L_OPR3[9]));
  LED led_39 (.in(L_OPR3[8]));
  LED led_40 (.in(i_sza));
  LED led_41 (.in(i_spa));
  LED led_42 (.in(i_cma));
  LED led_43 (.in(i_cml));
  LED led_44 (.in(DCA));
  LED led_45 (.in(JMS));
  LED led_46 (.in(AC[6]));
  LED led_47 (.in(AC[5]));
  LED led_48 (.in(MQ[6]));
  LED led_49 (.in(MQ[5]));
  LED led_50 (.in(PH_STB));
  LED led_51 (.in(PH_LAST));
  Button C (.out(CCC_C));
  D_FF #(.Bits(12)) u_MQ (.D(and_7_out), .C(and_6_out), .Q(MQ));  // open: nQ
  or or_1 (or_1_out, L_OPR1[8], L_OPR2[9], L_OPR3[11], L_OPR3[7], CLA, CLA_KCC);
  LED led_52 (.in(or_1_out));
  LED led_53 (.in(LINK));
  LED led_54 (.in(L_GEN[1]));
  LED led_55 (.in(INDIRECT));
  LED led_56 (.in(DIRECT));
  LED led_57 (.in(L_GEN[0]));
  LED led_58 (.in(L_OPR3[7]));
  LED led_59 (.in(i_sna));
  LED led_60 (.in(i_iac));
  LED led_61 (.in(JMP));
  LED led_62 (.in(AC[4]));
  LED led_63 (.in(AC[3]));
  LED led_64 (.in(MQ[4]));
  LED led_65 (.in(MQ[3]));
  // Probe MQ on MQ
  BitExtender #(.inputBits(1), .outputBits(12)) bitextender_1 (.in(L_OPR3[11]), .out(bitextender_1_out));
  // Probe AC on AC
  BitExtender #(.inputBits(1), .outputBits(12)) bitextender_2 (.in(or_1_out), .out(bitextender_2_out));
  // Probe LINK on LINK
  LED led_66 (.in(OPR_CLL));
  LED led_67 (.in(L_OPR3[6]));
  LED led_68 (.in(i_snl));
  LED led_69 (.in(i_rar));
  LED led_70 (.in(IOT));
  LED led_71 (.in(AC[2]));
  LED led_72 (.in(AC[1]));
  LED led_73 (.in(MQ[2]));
  LED led_74 (.in(MQ[1]));
  assign and_12_out = AC & ~bitextender_2_out;  // And and_12, 12 bits wide
  or or_2 (or_2_out, CLL, OPR_CLL);
  LED led_75 (.in(L_OPR3[5]));
  LED led_76 (.in(L_OPR3[4]));
  LED led_77 (.in(i_szl));
  LED led_78 (.in(i_osr));
  LED led_79 (.in(i_rtr));
  LED led_80 (.in(i_ral));
  LED led_81 (.in(L_GEN[4]));
  LED led_82 (.in(DIRECT));
  LED led_83 (.in(AC[0]));
  LED led_84 (.in(MQ[0]));
  assign {driver_4_out, KBD8} = L_OPR3[8] ? MQ : 12'bz;  // Driver driver_4
  LED led_85 (.in(L_OPR3[8]));
  // Probe on and_12_out
  and and_13 (and_13_out, LINK, ~or_2_out);  // And
  LED led_86 (.in(L_OPR3[3]));
  LED led_87 (.in(i_hlt));
  LED led_88 (.in(i_rtl));
  LED led_89 (.in(INDIRECT));
  assign or_3_out = {driver_4_out, KBD8} | and_12_out;  // Or or_3, 12 bits wide
  LED led_90 (.in(and_13_out));
  LED led_91 (.in(OPR_CML));
  LED led_92 (.in(IOT));
  and and_14 (and_14_out, IOT, CK_3);
  LED led_93 (.in(L_OPR3[2]));
  LED led_94 (.in(L_GEN[1]));
  // Probe on {LINK, FLAG_GREATERTHAN, IRQ_BUS, FLAG_IRQINH, FLAG_ION, FLAG_USER, {6{1'b0}}}
  assign {driver_4_out, KBD8} = OR_STATUS12 ? {LINK, FLAG_GREATERTHAN, IRQ_BUS, FLAG_IRQINH, FLAG_ION, FLAG_USER, {6{1'b0}}} : 12'bz;  // Driver driver_5
  LED led_95 (.in(OR_STATUS12));
  // Probe on not_8_out
  assign {driver_4_out, KBD8} = OPR_OSR ? not_8_out : 12'bz;  // Driver driver_6
  LED led_96 (.in(OPR_OSR));
  // Probe on {driver_4_out, KBD8}
  // Probe on or_3_out
  BitExtender #(.inputBits(1), .outputBits(12)) bitextender_3 (.in(OPR_CMA), .out(bitextender_3_out));
  LED led_97 (.in(OPR_CMA));
  or or_4 (or_4_out, RTF_LINK, OPR_CML);
  and and_15 (and_15_out, not_7_out, IOT);
  not not_7 (not_7_out, CK_FETCH);
  or or_5 (or_5_out, BUS_IR[8], BUS_IR[7], BUS_IR[6]);
  LED led_98 (.in(and_14_out));
  LED led_99 (.in(L_OPR3[1]));
  LED led_100 (.in(L_OPR3[0]));
  LED led_101 (.in(L_GEN[0]));
  Button S (.out(CCC_S));
  Button I (.out(CCC_I));
  Button R (.out(CCC_R));
  Button H (.out(CCC_H));
  Button T (.out(CCC_T));
  Button P (.out(SETPC));
  assign xor_2_out = or_3_out ^ bitextender_3_out;  // XOr xor_2, 12 bits wide
  xor xor_3 (xor_3_out, and_13_out, or_4_out);
  assign DONE = and_14_out ? and_14_out : 1'bz;  // Driver driver_7
  assign driver_4_out = 1'b0 ? 4'b0001 : 4'bz;  // Driver driver_8
  // Probe on xor_2_out
  LED led_102 (.in(xor_3_out));
  LED led_103 (.in(L_PRN[5]));
  LED led_104 (.in(L_KBD[5]));
  LED led_105 (.in(L_CPU[7]));
  LED led_106 (.in(FLAG_ION));
  DipSwitch dipswitch_1 (.out(dipswitch_1_out[11]));
  DipSwitch dipswitch_2 (.out(dipswitch_1_out[10]));
  assign not_8_out = ~dipswitch_1_out;  // Not not_8, 12 bits wide
  LED led_107 (.in(OPR_IAC));
  xor xor_4 (xor_4_out, and_16_out, xor_3_out);
  // _74238 _74238_2: pin names not known; wires that end beside it: 1'b1, 1'b0, and_15_out, 1'b0, or_5_out, BUS_IR[3], BUS_IR[4], BUS_IR[5], IOT_DEVCPU, IOT_DEVHSR, IOT_DEVHSP, IOT_DEVKBD, IOT_DEVPRI, IOT_DEV5, IOT_DEV6, IOT_DEV7
  Switch switch_1 (.A(1'b0), .B(IOT_DEVKBD));
  Switch switch_2 (.A(1'b0), .B(IOT_DEVPRI));
  LED led_108 (.in(L_PRN[4]));
  LED led_109 (.in(L_KBD[4]));
  LED led_110 (.in(L_CPU[6]));
  LED led_111 (.in(FLAG_IRQINH));
  Switch #(.Closed("true")) ENABLE (.A(HALT), .B(CCC_HLTCTRL));
  Switch ENABLE_2 (.A(CCC_BP1), .B(CCC_BP2));
  Switch ENABLE_3 (.A(CCC_BPI), .B(CCC_BPICTRL));
  DipSwitch dipswitch_3 (.out(dipswitch_1_out[9]));
  DipSwitch dipswitch_4 (.out(dipswitch_1_out[8]));
  DipSwitch dipswitch_5 (.out(dipswitch_1_out[7]));
  Add #(.Bits(12)) add_2 (.a(xor_2_out), .b({12{1'b0}}), .c_i(OPR_IAC), .s(add_2_s), .c_o(add_2_c_o));
  LED led_112 (.in(xor_4_out));
  LED led_113 (.in(L_PRN[3]));
  LED led_114 (.in(L_KBD[3]));
  LED led_115 (.in(L_CPU[5]));
  LED led_116 (.in(FLAG_IRQDLY));
  Switch KILL (.A(CCC_HLTCTRL), .B(1'b0));
  Switch KILL_2 (.A(CCC_BPICTRL), .B(1'b0));
  DipSwitch dipswitch_6 (.out(dipswitch_1_out[6]));
  DipSwitch dipswitch_7 (.out(dipswitch_1_out[5]));
  DipSwitch dipswitch_8 (.out(dipswitch_1_out[4]));
  // Probe on add_2_s
  and and_16 (and_16_out, add_2_c_o, OPR_IAC);
  LED led_117 (.in(add_2_c_o));
  LED led_118 (.in(L_PRN[2]));
  LED led_119 (.in(L_PRN[1]));
  LED led_120 (.in(L_KBD[2]));
  LED led_121 (.in(L_KBD[1]));
  LED led_122 (.in(L_CPU[4]));
  LED led_123 (.in(L_CPU[3]));
  LED led_124 (.in(IRQ_BUS));
  LED led_125 (.in(FLAG_KBDIE));
  // Probe on INSTCNT
  DipSwitch dipswitch_9 (.out(dipswitch_1_out[3]));
  DipSwitch dipswitch_10 (.out(dipswitch_1_out[2]));
  DipSwitch dipswitch_11 (.out(dipswitch_1_out[1]));
  LED led_126 (.in(and_16_out));
  // _74238 _74238_3: pin names not known; wires that end beside it: 1'b1, 1'b0, IOT_DEVCPU, 1'b0, 1'b0, BUS_IR[0], BUS_IR[1], BUS_IR[2], IOT_SKON, IOT_ION, IOT_IOF, IOT_SRQ, IOT_GTF, IOT_RTF, IOT_SGT, IOT_CAF
  // _74238 _74238_4: pin names not known; wires that end beside it: 1'b1, 1'b0, IOT_DEVKBD, 1'b0, 1'b0, BUS_IR[0], BUS_IR[1], BUS_IR[2], IOT_KCF, IOT_KSF, IOT_KCC, _74238_4_p12, IOT_KRS, IOT_KIE, IOT_KRB, _74238_4_p16, _74238_4_p12, _74238_4_p16
  // _74238 _74238_5: pin names not known; wires that end beside it: 1'b1, 1'b0, IOT_DEVPRI, 1'b0, 1'b0, BUS_IR[0], BUS_IR[1], BUS_IR[2], IOT_TFL, IOT_TSF, IOT_TCF, _74238_5_p12, IOT_TPC, IOT_TSK, IOT_TLS, _74238_5_p16, _74238_5_p12, _74238_5_p16
  LED led_127 (.in(L_PRN[0]));
  LED led_128 (.in(L_KBD[0]));
  LED led_129 (.in(L_CPU[2]));
  LED led_130 (.in(FLAG_KBD));
  DipSwitch dipswitch_12 (.out(dipswitch_1_out[0]));
  LED led_131 (.in(L_CPU[1]));
  LED led_132 (.in(FLAG_PRNCOMPLETE));
  Seven_Seg_Hex seven_seg_hex_18 (.d(CK_NUM), .dp(1'b0));
  // ROTATER_focal69 rotater_focal69_1: pin names not known; wires that end beside it: {OPR_RIGHT, OPR_LEFT, OPR_X2}, add_2_s, xor_4_out, rotater_focal69_1_p4, rotater_focal69_1_p5
  LED led_133 (.in(L_CAF));
  // Probe on LATCHED_PC
  LED led_134 (.in(PH_FIRST));
  // Probe on rotater_focal69_1_p4
  LED led_135 (.in(PH_STB));
  LED led_136 (.in(PH_LAST));
  LED led_137 (.in(L_GEN[4]));
  not not_9 (not_9_out, BUS_IR[8]);
  not not_10 (not_10_out, BUS_IR[0]);
  assign PCIN = SETPC ? 12'h80 : 12'bz;  // Driver driver_9
  assign driver_10_out = SETPC ? SETPC : 1'bz;  // Driver driver_10
  assign PC_LD = SETPC ? SETPC : 1'bz;  // Driver driver_11
  and and_17 (OPR1, not_9_out, 1'b1, L_GEN[4]);
  LED led_138 (.in(OPR1));
  and and_18 (OPR2, not_10_out, BUS_IR[8], L_GEN[4]);
  LED led_139 (.in(OPR2));
  and and_19 (OPR3, BUS_IR[8], BUS_IR[0], L_GEN[4]);
  LED led_140 (.in(OPR3));
  // OC12 oc12_1: pin names not known; wires that end beside it: BUS_IR[6:0], LATCHED_PC[11:7], L_GEN[0], IR2PC, PCIN[6:0], PCIN[11:7], PCIN
  LED led_141 (.in(IR2PC));
  // Probe PCIN on PCIN
  LED led_142 (.in(PC_CK));
  xor xor_5 (xor_5_out, PC_CK, driver_10_out);
  LED led_143 (.in(RAMD2PC));
  assign PCIN = RAMD2PC ? DATA : 12'bz;  // Driver driver_12
  LED led_144 (.in(IND2PC));
  assign PCIN = IND2PC ? INDOUT : 12'bz;  // Driver driver_13
  and and_20 (OPR_IAC, BUS_IR[0], OPR1);
  and and_21 (OPR_X2, BUS_IR[1], OPR1);
  and and_22 (OPR_LEFT, BUS_IR[2], OPR1);
  and and_23 (OPR_RIGHT, BUS_IR[3], OPR1);
  and and_24 (OPR_CML, BUS_IR[4], OPR1);
  and and_25 (OPR_CMA, BUS_IR[5], OPR1);
  and and_26 (OPR_CLL, BUS_IR[6], OPR1);
  and and_27 (L_OPR1[8], BUS_IR[7], OPR1);
  LED led_145 (.in(OPR1));
  xor xor_6 (xor_6_out, CK_FETCH, SETPC);
  not not_11 (not_11_out, xor_5_out);
  nor nor_7 (nor_7_out, AC[0], AC[1], AC[2], AC[3], AC[4], AC[5], AC[6], AC[7], AC[8], AC[9], AC[10], AC[11]);
  LED led_146 (.in(nor_7_out));
  LED led_147 (.in(OPR_IAC));
  LED led_148 (.in(OPR_X2));
  LED led_149 (.in(OPR_LEFT));
  LED led_150 (.in(OPR_RIGHT));
  LED led_151 (.in(OPR_CML));
  LED led_152 (.in(OPR_CMA));
  LED led_153 (.in(OPR_CLL));
  LED led_154 (.in(L_OPR1[8]));
  Counter #(.Bits(20)) counter_1 (.en(1'b1), .C(STB_AUTOINC2), .clr(1'b0), .out(counter_1_out), .ovf(counter_1_ovf));
  CounterPreset #(.Bits(12)) PC (
    .en(1'b1), .C(not_11_out), .dir(1'b0), .in(PCIN), .ld(PC_LD), .clr(reset_1_out), .out(BUS_PC));  // open: ovf
  LED led_155 (.in(PC_LD));
  // Probe on counter_1_out
  Register #(.Bits(12)) register_1 (.D(BUS_PC), .C(xor_6_out), .en(1'b1), .Q(LATCHED_PC));
  Reset #(.invertOutput("false")) reset_1 (.out(reset_1_out));
  and and_28 (and_28_out, nor_7_out, OPR_SZASNA);
  LED led_156 (.in(and_28_out));
  and and_29 (and_29_out, AC[11], OPR_SMASPA);
  LED led_157 (.in(and_29_out));
  and and_30 (and_30_out, LINK, OPR_SNLSZL);
  LED led_158 (.in(and_30_out));
  EEPROM #(.AddrBits(20), .Bits(12)) eeprom_1 (
    .A(counter_1_out), .CS(1'b1), .WE(STB_AUTOINC1), .OE(1'b0), .D(LATCHED_PC));
  // Probe PCOUT on BUS_PC
  or or_6 (or_6_out, and_28_out, and_29_out, and_30_out);
  // Probe PCLATCHED on LATCHED_PC
  // OC12 oc12_2: pin names not known; wires that end beside it: BUS_PC, BUS_IR[6:0], LATCHED_PC[11:7], L_GEN[0], IR2RAMA, DAW[18:12], DAW[23:19]
  LED led_159 (.in(IR2RAMA));
  LED led_160 (.in(or_6_out));
  and and_31 (OPR_NA1, BUS_IR[0], OPR2);
  and and_32 (OPR_HLT, BUS_IR[1], OPR2);
  and and_33 (OPR_OSR, BUS_IR[2], OPR2);
  and and_34 (OPR_TSTINV, BUS_IR[3], OPR2);
  and and_35 (OPR_SNLSZL, BUS_IR[4], OPR2);
  and and_36 (OPR_SZASNA, BUS_IR[5], OPR2);
  and and_37 (OPR_SMASPA, BUS_IR[6], OPR2);
  and and_38 (L_OPR2[9], BUS_IR[7], OPR2);
  LED led_161 (.in(OPR2));
  LED led_162 (.in(PC2ADDR));
  assign DAW[23:12] = PC2ADDR ? BUS_PC : 12'bz;  // Driver driver_14
  xor xor_7 (SKIP, or_6_out, OPR_TSTINV);
  LED led_163 (.in(SKIP));
  and and_39 (HALT, OPR_HLT, CK_1);
  LED led_164 (.in(HALT));
  LED led_165 (.in(OPR_NA1));
  LED led_166 (.in(OPR_HLT));
  LED led_167 (.in(OPR_OSR));
  LED led_168 (.in(OPR_TSTINV));
  LED led_169 (.in(OPR_SNLSZL));
  LED led_170 (.in(OPR_SZASNA));
  LED led_171 (.in(OPR_SMASPA));
  LED led_172 (.in(L_OPR2[9]));
  // Probe RAMA on DAW[23:12]
  LED led_173 (.in(DAW[24]));
  LED led_174 (.in(RAM_OE));
  LED led_175 (.in(IND2RAMA));
  assign DAW[23:12] = IND2RAMA ? INDOUT : 12'bz;  // Driver driver_15
  EEPROM #(.AddrBits(17), .isProgramMemory("true"), .Bits(12)) eeprom_2 (
    .A({5'b01100, DAW[23:12]}), .CS(1'b1), .WE(DAW[24]), .OE(RAM_OE), .D(DAW[11:0]));
  // Probe RAMD on DAW[11:0]
  or or_7 (or_7_out, CCC_I, counter_2_ovf);
  Counter #(.Bits(6)) counter_2 (.en(CCC_T), .C(clk), .clr(1'b0), .out(counter_2_out), .ovf(counter_2_ovf));
  LED led_176 (.in(OPR3));
  assign DATA = RAM_OE ? DAW[11:0] : 12'bz;  // Driver driver_16
  assign DAW[11:0] = DAW[24] ? DATA : 12'bz;  // Driver driver_17
  Monoflop monoflop_1 (.C(or_7_out), .R(1'b0), .Q(monoflop_1_q));  // open: nQ
  LED led_177 (.in(or_7_out));
  Monoflop monoflop_2 (.C(CCC_R), .R(1'b0), .Q(monoflop_2_q));  // open: nQ
  // Probe on counter_2_out
  Comparator #(.Bits(12)) comparator_1 (.a(BUS_PC), .b(12'h154), .eq(comparator_1_eq));  // open: gt, lt
  nor nor_8 (nor_8_out, BUS_IR[0], BUS_IR[1], BUS_IR[2], BUS_IR[3], BUS_IR[4], BUS_IR[5], BUS_IR[6], BUS_IR[7]);
  and and_40 (and_40_out, OPR3, BUS_IR[0]);
  LED led_178 (.in(and_40_out));
  and and_41 (and_41_out, OPR3, BUS_IR[1]);
  LED led_179 (.in(and_41_out));
  and and_42 (and_42_out, OPR3, BUS_IR[2]);
  LED led_180 (.in(and_42_out));
  and and_43 (and_43_out, OPR3, BUS_IR[3]);
  LED led_181 (.in(and_43_out));
  and and_44 (L_OPR3[7], OPR3, BUS_IR[4]);
  LED led_182 (.in(L_OPR3[7]));
  and and_45 (L_OPR3[10], OPR3, BUS_IR[5]);
  LED led_183 (.in(L_OPR3[10]));
  and and_46 (L_OPR3[8], OPR3, BUS_IR[6]);
  LED led_184 (.in(L_OPR3[8]));
  and and_47 (L_OPR3[11], OPR3, BUS_IR[7]);
  LED led_185 (.in(L_OPR3[11]));
  LED led_186 (.in(FORCE4000));
  assign DATA = FORCE4000 ? 12'h800 : 12'bz;  // Driver driver_18
  LED led_187 (.in(PC2RAMD));
  assign DATA = PC2RAMD ? BUS_PC : 12'bz;  // Driver driver_19
  and and_48 (CCC_BP1, comparator_1_eq, CK_FETCH);
  Comparator #(.Bits(32)) comparator_2 (.a(INSTCNT), .b(32'h681), .eq(CCC_BPI));  // open: gt, lt
  // Probe DATA on DATA
  LED led_188 (.in(AC2RAMD));
  assign DATA = AC2RAMD ? AC : 12'bz;  // Driver driver_20
  and and_49 (L_OPR3[12], nor_8_out, L_GEN[4]);
  and and_50 (L_OPR3[9], L_OPR3[7], L_OPR3[8]);
  not not_12 (not_12_out, IR_CK);
  LED led_189 (.in(IR_CK));
  LED led_190 (.in(INC2RAMD));
  assign DATA = INC2RAMD ? INC_s : 12'bz;  // Driver driver_21
  RS_FF_AS rs_ff_as_1 (.S(monoflop_2_q), .R(or_9_out), .Q(rs_ff_as_1_q));  // open: nQ
  LED led_191 (.in(L_OPR3[12]));
  // _74238 _74238_6: pin names not known; wires that end beside it: and_40_out, 1'b1, 1'b0, 1'b1, 1'b0, 1'b0, and_41_out, and_42_out, and_43_out, OPR_O, L_OPR3[0], L_OPR3[1], L_OPR3[2], L_OPR3[3], L_OPR3[4], L_OPR3[5], L_OPR3[6]
  LED led_192 (.in(L_OPR3[9]));
  // TRANSP_LATCH IR: pin names not known; wires that end beside it: DATA, DATA, not_12_out, BUS_IR, BUS_IR
  or or_8 (or_8_out, monoflop_1_q, monoflop_2_q, rs_ff_as_1_q);
  PullDown pulldown_1 (.out(CCC_HLTCTRL));
  PullDown pulldown_2 (.out(CCC_BP2));
  // Probe IR on BUS_IR
  LED led_193 (.in(or_8_out));
  or or_9 (or_9_out, CCC_H, CCC_HLTCTRL, CCC_BP2, CCC_BPICTRL);
  PullDown pulldown_3 (.out(CCC_BPICTRL));
  D_FF #(.Bits(12)) IND (.D(DATA), .C(IND_CK), .Q(INDOUT));  // open: nQ
  LED led_194 (.in(IND_CK));
  D_FF d_ff_1 (.D(DONE), .C(clk), .Q(d_ff_1_q));  // open: nQ
  LED led_195 (.in(or_9_out));
  LED led_196 (.in(OPR_O));
  LED led_197 (.in(L_OPR3[0]));
  LED led_198 (.in(L_OPR3[1]));
  LED led_199 (.in(L_OPR3[2]));
  LED led_200 (.in(L_OPR3[3]));
  LED led_201 (.in(L_OPR3[4]));
  LED led_202 (.in(L_OPR3[5]));
  LED led_203 (.in(L_OPR3[6]));
  RS_FF_AS rs_ff_as_2 (.S(or_8_out), .R(d_ff_1_q), .Q(rs_ff_as_2_q));  // open: nQ
  // Probe INDOUT on INDOUT
  and and_51 (and_51_out, rs_ff_as_2_q, clk);
  D_FF #(.Bits(12)) DATA_2 (.D(DATA), .C(DATA_CK), .Q(LATCHEDDATA));  // open: nQ
  LED led_204 (.in(DATA_CK));
  or or_10 (CLK_t, CCC_S, and_51_out);
  LED led_205 (.in(and_51_out));
  // Probe LATDATA on LATCHEDDATA
  LED led_206 (.in(CLK_t));
  Counter #(.Bits(32)) INSTRUCTION_COUNT (.en(1'b1), .C(CK_FETCH), .clr(1'b0), .out(INSTCNT));  // open: ovf
  LED led_207 (.in(IND2INC));
  assign driver_22_out = IND2INC ? INDOUT : 12'bz;  // Driver driver_22
  LED led_208 (.in(LD2INC));
  assign driver_22_out = LD2INC ? LATCHEDDATA : 12'bz;  // Driver driver_23
  Counter #(.Bits(5)) counter_3 (.en(1'b1), .C(CLK_t), .clr(DONE), .out(counter_3_out), .ovf(counter_3_ovf));
  PullDown pulldown_4 (.out(DONE));
  // Probe COUNT on INSTCNT
  and and_52 (and_52_out, IOT_ION, STB_1);
  Seven_Seg_Hex seven_seg_hex_19 (.d(CK_NUM), .dp(1'b0));
  LED led_209 (.in(PH_FIRST));
  LED led_210 (.in(PH_STB));
  // Probe AFTERINC on INC_s
  // Probe TOINC on driver_22_out
  LED led_211 (.in(and_52_out));
  and and_53 (and_53_out, IOT_CAF, CK_1);
  LED led_212 (.in(and_53_out));
  and and_54 (and_54_out, IOT_CAF, STB_1);
  LED led_213 (.in(and_54_out));
  and and_55 (and_55_out, IOT_SKON, FLAG_ION, CK_1);
  LED led_214 (.in(and_55_out));
  and and_56 (and_56_out, IOT_SKON, FLAG_ION, STB_1);
  LED led_215 (.in(and_56_out));
  LED led_216 (.in(PH_LAST));
  Add #(.Bits(12)) INC (.a({12{1'b0}}), .b(driver_22_out), .c_i(1'b1), .s(INC_s), .c_o(INCZERO));
  Add #(.Bits(5)) add_3 (.a(counter_3_out), .b(multiplexer_1_out), .c_i(1'b0), .s(add_3_s));  // open: c_o
  assign CLL = and_53_out ? and_53_out : 1'bz;  // Driver driver_24
  assign CLA = and_53_out ? and_53_out : 1'bz;  // Driver driver_25
  assign ROT2AC = and_53_out ? and_53_out : 1'bz;  // Driver driver_26
  assign AC_CK = and_54_out ? and_54_out : 1'bz;  // Driver driver_27
  assign LINK_CK = and_54_out ? and_54_out : 1'bz;  // Driver driver_28
  assign PC_CK = and_55_out ? and_55_out : 1'bz;  // Driver driver_29
  SEQUENCER sequencer_1 (
    .PH_FIRST(PH_FIRST), .PH_STB(PH_STB), .PH_LAST(PH_LAST),
    .STB_bits({STB_6, STB_5, STB_4, STB_3, STB_2, STB_1, STB_INDIRECT, STB_AUTOINC2, STB_AUTOINC1, STB_FETCH}),
    .CK_bits({CK_6, CK_5, CK_4, CK_3, CK_2, CK_1, CK_INDIRECT, CK_AUTOINC2, CK_AUTOINC1, CK_FETCH}),
    .CK_num(CK_NUM), .IN(add_3_s));
  Multiplexer #(.Selector_Bits(2), .Bits(5)) multiplexer_1 (
    .sel(2'b00), .in_0({5{1'b0}}), .in_1(5'b00001), .in_2(5'b00011), .in_3({5{1'b0}}), .out(multiplexer_1_out));
  or or_11 (IRQ_BUS, FLAG_PRNCOMPLETE, FLAG_KBD);
  LED led_217 (.in(IRQ_BUS));
  // Probe STEP on CK_NUM
  or or_12 (or_12_out, RTF_ION, and_52_out);
  or or_13 (or_13_out, IOT_IOF, 1'b0, IRQ_JMS, IOT_CAF, and_56_out);
  and and_57 (and_57_out, IOT_SRQ, CK_1, FLAG_KBDIE, IRQ_BUS);
  LED led_218 (.in(or_12_out));
  LED led_219 (.in(or_13_out));
  LED led_220 (.in(and_57_out));
  assign PC_CK = and_57_out ? and_57_out : 1'bz;  // Driver driver_30
  Delay delay_1 (.in(or_12_out), .out(delay_1_out));
  RS_FF_AS IRQ_DELAY1 (.S(or_12_out), .R(CK_AUTOINC2), .Q(FLAG_IRQDLY));  // open: nQ
  RS_FF_AS ION_FLAG (.S(delay_1_out), .R(or_13_out), .Q(FLAG_ION));  // open: nQ
  Counter #(.Bits(32)) counter_4 (.en(1'b1), .C(IOT_IOF), .clr(1'b0), .out(counter_4_out));  // open: ovf
  Counter #(.Bits(32)) counter_5 (.en(1'b1), .C(IRQ_JMS), .clr(1'b0), .out(counter_5_out));  // open: ovf
  Counter #(.Bits(32)) counter_6 (.en(1'b1), .C(IOT_CAF), .clr(1'b0), .out(counter_6_out));  // open: ovf
  Counter #(.Bits(32)) counter_7 (.en(1'b1), .C(and_56_out), .clr(1'b0), .out(counter_7_out));  // open: ovf
  LED led_221 (.in(FLAG_IRQDLY));
  LED led_222 (.in(FLAG_ION));
  // Probe on counter_4_out
  // Probe on counter_5_out
  // Probe on counter_6_out
  // Probe on counter_7_out
  or or_14 (or_14_out, AND, L_GEN[10], ISZ, DCA, JMS);
  and and_58 (and_58_out, or_14_out, INDIRECT, CK_INDIRECT);
  and and_59 (and_59_out, INDIRECT, or_14_out, STB_INDIRECT);
  and and_60 (and_60_out, IRQ_BUS, ~FLAG_IRQDLY, FLAG_ION);  // And
  and and_61 (and_61_out, ~FLAG_IRQDLY, CK_AUTOINC1);  // And
  LED led_223 (.in(and_58_out));
  LED led_224 (.in(and_59_out));
  LED led_225 (.in(and_60_out));
  LED led_226 (.in(and_61_out));
  Seven_Seg_Hex seven_seg_hex_20 (.d(CK_NUM), .dp(1'b0));
  assign IR2RAMA = and_58_out ? and_58_out : 1'bz;  // Driver driver_31
  assign RAMD2IND = and_58_out ? and_58_out : 1'bz;  // Driver driver_32
  assign RAM_OE = and_58_out ? and_58_out : 1'bz;  // Driver driver_33
  assign IND_CK = and_59_out ? and_59_out : 1'bz;  // Driver driver_34
  and and_62 (and_62_out, CK_FETCH, ~and_60_out);  // And
  and and_63 (and_63_out, CK_FETCH, and_60_out);
  RS_FF_AS IRQ_DELAY2 (.S(or_12_out), .R(and_61_out), .Q(IRQ_DELAY2_q));  // open: nQ
  // Probe on LATCHED_PC
  LED led_227 (.in(and_62_out));
  LED led_228 (.in(and_63_out));
  LED led_229 (.in(IRQ_DELAY2_q));
  LED led_230 (.in(PH_FIRST));
  LED led_231 (.in(PH_STB));
  RS_FF_AS IRQ_INHIBIT (.S(1'b0), .R(1'b0), .Q(FLAG_IRQINH));  // open: nQ
  assign PC2ADDR = and_62_out ? and_62_out : 1'bz;  // Driver driver_35
  assign RAM_OE = and_62_out ? and_62_out : 1'bz;  // Driver driver_36
  assign IR_CK = and_62_out ? and_62_out : 1'bz;  // Driver driver_37
  assign PC_CK = and_62_out ? and_62_out : 1'bz;  // Driver driver_38
  assign FORCE4000 = and_63_out ? and_63_out : 1'bz;  // Driver driver_39
  assign IR_CK = and_63_out ? and_63_out : 1'bz;  // Driver driver_40
  LED led_232 (.in(PH_LAST));
  LED led_233 (.in(FLAG_IRQINH));
  and and_64 (and_64_out, or_14_out, L_GEN[1], CK_INDIRECT);
  and and_65 (and_65_out, or_14_out, L_GEN[1], STB_INDIRECT);
  assign IRQ_JMS = and_76_out ? and_76_out : 1'bz;  // Driver driver_41
  and and_66 (and_66_out, or_14_out, L_GEN[1], CK_AUTOINC1);
  LED led_234 (.in(and_66_out));
  and and_67 (and_67_out, or_14_out, L_GEN[1], STB_AUTOINC1);
  LED led_235 (.in(and_67_out));
  and and_68 (and_68_out, or_14_out, L_GEN[1], CK_AUTOINC2);
  LED led_236 (.in(and_68_out));
  and and_69 (and_69_out, or_14_out, L_GEN[1], STB_AUTOINC2);
  LED led_237 (.in(and_69_out));
  LED led_238 (.in(and_64_out));
  LED led_239 (.in(and_65_out));
  assign IR2RAMA = and_66_out ? and_66_out : 1'bz;  // Driver driver_42
  assign RAM_OE = and_66_out ? and_66_out : 1'bz;  // Driver driver_43
  assign IND2INC = and_66_out ? and_66_out : 1'bz;  // Driver driver_44
  assign IND_CK = and_67_out ? and_67_out : 1'bz;  // Driver driver_45
  assign INC2RAMD = and_68_out ? and_68_out : 1'bz;  // Driver driver_46
  assign IND2INC = and_68_out ? and_68_out : 1'bz;  // Driver driver_47
  assign IR2RAMA = and_68_out ? and_68_out : 1'bz;  // Driver driver_48
  assign DAW[24] = and_69_out ? and_69_out : 1'bz;  // Driver driver_49
  assign IR2RAMA = and_64_out ? and_64_out : 1'bz;  // Driver driver_50
  assign RAMD2IND = and_64_out ? and_64_out : 1'bz;  // Driver driver_51
  assign RAM_OE = and_64_out ? and_64_out : 1'bz;  // Driver driver_52
  assign IND_CK = and_65_out ? and_65_out : 1'bz;  // Driver driver_53
  RS_FF_AS rs_ff_as_3 (.S(and_63_out), .R(STB_AUTOINC1), .Q(rs_ff_as_3_q));  // open: nQ
  and and_70 (and_70_out, DIRECT, IN_IR2PC);
  and and_71 (and_71_out, ~DIRECT, IN_IR2PC);  // And
  and and_72 (and_72_out, DIRECT, INIR2RAMA);
  and and_73 (and_73_out, ~DIRECT, INIR2RAMA);  // And
  and and_74 (and_74_out, IOT_GTF, CK_2);
  and and_75 (and_75_out, IOT_GTF, STB_2);
  Counter #(.Bits(32)) counter_8 (.en(1'b1), .C(and_63_out), .clr(1'b0), .out(counter_8_out));  // open: ovf
  Counter #(.Bits(32)) counter_9 (.en(1'b1), .C(and_63_out), .clr(1'b0), .out(counter_9_out));  // open: ovf
  and and_76 (and_76_out, CK_AUTOINC1, rs_ff_as_3_q);
  assign IR2PC = and_70_out ? and_70_out : 1'bz;  // Driver driver_54
  assign IND2PC = and_71_out ? and_71_out : 1'bz;  // Driver driver_55
  assign IR2RAMA = and_72_out ? and_72_out : 1'bz;  // Driver driver_56
  assign IND2RAMA = and_73_out ? and_73_out : 1'bz;  // Driver driver_57
  // Probe on {LINK, FLAG_GREATERTHAN, IRQ_BUS, FLAG_IRQINH, FLAG_ION, FLAG_USER, {6{1'b0}}}
  LED led_240 (.in(and_74_out));
  LED led_241 (.in(and_75_out));
  // Probe on counter_8_out
  // Probe on counter_9_out
  LED led_242 (.in(and_76_out));
  assign ROT2AC = and_74_out ? and_74_out : 1'bz;  // Driver driver_58
  assign CLA_KCC = and_74_out ? and_74_out : 1'bz;  // Driver driver_59
  assign OR_STATUS12 = and_74_out ? and_74_out : 1'bz;  // Driver driver_60
  assign AC_CK = and_75_out ? and_75_out : 1'bz;  // Driver driver_61
  RS_FF_AS FLAG_GREATER_THAN (.S(RTF_GREATERTANON), .R(RTF_GREATERTHANOFF), .Q(FLAG_GREATERTHAN));  // open: nQ
  LED led_243 (.in(FLAG_GREATERTHAN));
  and and_77 (and_77_out, AND, CK_1);
  and and_78 (and_78_out, AND, STB_1);
  and and_79 (and_79_out, AND, CK_2);
  LED led_244 (.in(and_77_out));
  LED led_245 (.in(and_78_out));
  LED led_246 (.in(and_79_out));
  and and_80 (and_80_out, JMP, DIRECT, CK_1);
  LED led_247 (.in(and_80_out));
  and and_81 (and_81_out, JMP, DIRECT, STB_1);
  LED led_248 (.in(and_81_out));
  and and_82 (and_82_out, JMP, DIRECT, CK_2);
  LED led_249 (.in(and_82_out));
  // Probe on AC
  assign INIR2RAMA = and_77_out ? and_77_out : 1'bz;  // Driver driver_62
  assign RAMD2AC_AND = and_77_out ? and_77_out : 1'bz;  // Driver driver_63
  assign RAM_OE = and_77_out ? and_77_out : 1'bz;  // Driver driver_64
  assign AC_CK = and_78_out ? and_78_out : 1'bz;  // Driver driver_65
  assign DONE = and_79_out ? and_79_out : 1'bz;  // Driver driver_66
  Seven_Seg_Hex seven_seg_hex_21 (.d(CK_NUM), .dp(1'b0));
  assign IR2PC = and_80_out ? and_80_out : 1'bz;  // Driver driver_67
  assign PC_LD = and_80_out ? and_80_out : 1'bz;  // Driver driver_68
  assign PC_CK = and_81_out ? and_81_out : 1'bz;  // Driver driver_69
  assign DONE = and_82_out ? and_82_out : 1'bz;  // Driver driver_70
  RS_FF_AS USER_FLAG (.S(RTF_USEROFF), .R(RTF_USERON), .Q(FLAG_USER));  // open: nQ
  // Probe on LATCHED_PC
  LED led_250 (.in(FLAG_USER));
  LED led_251 (.in(PH_FIRST));
  LED led_252 (.in(PH_STB));
  LED led_253 (.in(PH_LAST));
  and and_83 (RTF_ION, IOT_RTF, CK_1);
  and and_84 (RTF_USEROFF, IOT_RTF, CK_1, ~AC[6]);  // And
  and and_85 (RTF_USERON, IOT_RTF, CK_1, AC[6]);
  and and_86 (RTF_GREATERTHANOFF, IOT_RTF, CK_1, ~AC[10]);  // And
  and and_87 (RTF_GREATERTANON, IOT_RTF, CK_1, AC[10]);
  and and_88 (and_88_out, IOT_RTF, CK_1);
  and and_89 (and_89_out, IOT_RTF, STB_1);
  and and_90 (RTF_LINK, IOT_RTF, AC[11]);
  and and_91 (and_91_out, L_GEN[10], CK_1);
  and and_92 (and_92_out, L_GEN[10], STB_1);
  and and_93 (and_93_out, L_GEN[10], CK_2);
  LED led_254 (.in(RTF_ION));
  LED led_255 (.in(RTF_USEROFF));
  LED led_256 (.in(RTF_USERON));
  LED led_257 (.in(RTF_GREATERTHANOFF));
  LED led_258 (.in(RTF_GREATERTANON));
  LED led_259 (.in(and_88_out));
  assign CLL = and_88_out ? and_88_out : 1'bz;  // Driver driver_71
  LED led_260 (.in(and_89_out));
  assign LINK_CK = and_89_out ? and_89_out : 1'bz;  // Driver driver_72
  LED led_261 (.in(RTF_LINK));
  LED led_262 (.in(and_91_out));
  LED led_263 (.in(and_92_out));
  LED led_264 (.in(and_93_out));
  and and_94 (and_94_out, JMP, INDIRECT, CK_1);
  LED led_265 (.in(and_94_out));
  and and_95 (and_95_out, JMP, INDIRECT, STB_1);
  LED led_266 (.in(and_95_out));
  and and_96 (and_96_out, JMP, INDIRECT, CK_2);
  LED led_267 (.in(and_96_out));
  assign INIR2RAMA = and_91_out ? and_91_out : 1'bz;  // Driver driver_73
  assign RAMD2AC_ADD = and_91_out ? and_91_out : 1'bz;  // Driver driver_74
  assign RAM_OE = and_91_out ? and_91_out : 1'bz;  // Driver driver_75
  assign AC_CK = and_92_out ? and_92_out : 1'bz;  // Driver driver_76
  assign LINK_CK = and_92_out ? and_92_out : 1'bz;  // Driver driver_77
  assign DONE = and_93_out ? and_93_out : 1'bz;  // Driver driver_78
  assign IR2RAMA = and_94_out ? and_94_out : 1'bz;  // Driver driver_79
  assign RAMD2PC = and_94_out ? and_94_out : 1'bz;  // Driver driver_80
  assign RAM_OE = and_94_out ? and_94_out : 1'bz;  // Driver driver_81
  assign PC_LD = and_94_out ? and_94_out : 1'bz;  // Driver driver_82
  assign PC_CK = and_95_out ? and_95_out : 1'bz;  // Driver driver_83
  assign DONE = and_96_out ? and_96_out : 1'bz;  // Driver driver_84
  and and_97 (and_97_out, ISZ, CK_1);
  LED led_268 (.in(and_97_out));
  and and_98 (and_98_out, ISZ, STB_1);
  LED led_269 (.in(and_98_out));
  and and_99 (and_99_out, ISZ, CK_2);
  LED led_270 (.in(and_99_out));
  and and_100 (and_100_out, ISZ, CK_3);
  LED led_271 (.in(and_100_out));
  and and_101 (and_101_out, ISZ, INCZERO, CK_4);
  LED led_272 (.in(and_101_out));
  and and_102 (and_102_out, ISZ, CK_5);
  LED led_273 (.in(and_102_out));
  and and_103 (and_103_out, JMP, L_GEN[1], CK_1);
  and and_104 (and_104_out, JMP, L_GEN[1], STB_1);
  and and_105 (and_105_out, JMP, L_GEN[1], CK_2);
  assign INIR2RAMA = and_97_out ? and_97_out : 1'bz;  // Driver driver_85
  assign RAM_OE = and_97_out ? and_97_out : 1'bz;  // Driver driver_86
  assign INIR2RAMA = and_98_out ? and_98_out : 1'bz;  // Driver driver_87
  assign RAM_OE = and_98_out ? and_98_out : 1'bz;  // Driver driver_88
  assign DATA_CK = and_98_out ? and_98_out : 1'bz;  // Driver driver_89
  assign LD2INC = and_98_out ? and_98_out : 1'bz;  // Driver driver_90
  assign INIR2RAMA = and_99_out ? and_99_out : 1'bz;  // Driver driver_91
  assign DAW[24] = and_99_out ? and_99_out : 1'bz;  // Driver driver_92
  assign INC2RAMD = and_99_out ? and_99_out : 1'bz;  // Driver driver_93
  assign LD2INC = and_99_out ? and_99_out : 1'bz;  // Driver driver_94
  assign INIR2RAMA = and_100_out ? and_100_out : 1'bz;  // Driver driver_95
  assign RAM_OE = and_100_out ? and_100_out : 1'bz;  // Driver driver_96
  assign LD2INC = and_100_out ? and_100_out : 1'bz;  // Driver driver_97
  assign PC_CK = and_101_out ? and_101_out : 1'bz;  // Driver driver_98
  assign LD2INC = and_101_out ? and_101_out : 1'bz;  // Driver driver_99
  assign DONE = and_102_out ? and_102_out : 1'bz;  // Driver driver_100
  and and_106 (and_106_out, JMP, L_GEN[1], CK_AUTOINC1);
  LED led_274 (.in(and_106_out));
  and and_107 (and_107_out, JMP, L_GEN[1], STB_AUTOINC1);
  LED led_275 (.in(and_107_out));
  and and_108 (and_108_out, JMP, L_GEN[1], CK_AUTOINC2);
  LED led_276 (.in(and_108_out));
  and and_109 (and_109_out, JMP, L_GEN[1], STB_AUTOINC2);
  LED led_277 (.in(and_109_out));
  LED led_278 (.in(and_103_out));
  LED led_279 (.in(and_104_out));
  LED led_280 (.in(and_105_out));
  assign IR2RAMA = and_106_out ? and_106_out : 1'bz;  // Driver driver_101
  assign RAM_OE = and_106_out ? and_106_out : 1'bz;  // Driver driver_102
  assign IND2INC = and_106_out ? and_106_out : 1'bz;  // Driver driver_103
  assign IND_CK = and_107_out ? and_107_out : 1'bz;  // Driver driver_104
  assign INC2RAMD = and_108_out ? and_108_out : 1'bz;  // Driver driver_105
  assign IND2INC = and_108_out ? and_108_out : 1'bz;  // Driver driver_106
  assign IR2RAMA = and_108_out ? and_108_out : 1'bz;  // Driver driver_107
  assign DAW[24] = and_109_out ? and_109_out : 1'bz;  // Driver driver_108
  assign IR2RAMA = and_103_out ? and_103_out : 1'bz;  // Driver driver_109
  assign RAMD2PC = and_103_out ? and_103_out : 1'bz;  // Driver driver_110
  assign RAM_OE = and_103_out ? and_103_out : 1'bz;  // Driver driver_111
  assign PC_LD = and_103_out ? and_103_out : 1'bz;  // Driver driver_112
  assign PC_CK = and_104_out ? and_104_out : 1'bz;  // Driver driver_113
  assign DONE = and_105_out ? and_105_out : 1'bz;  // Driver driver_114
  or or_15 (or_15_out, IOT_TPC, IOT_TLS);
  LED led_281 (.in(or_15_out));
  or or_16 (or_16_out, FLAG_PRNCOMPLETE, FLAG_KBD);
  and and_110 (and_110_out, DCA, CK_1);
  and and_111 (and_111_out, DCA, STB_1);
  and and_112 (and_112_out, DCA, CK_2);
  and and_113 (and_113_out, DCA, CK_3);
  and and_114 (and_114_out, OPR1, CK_1);
  and and_115 (and_115_out, OPR1, STB_1);
  and and_116 (and_116_out, OPR1, CK_2);
  or or_17 (or_17_out, cntprobe_1_p1, IOT_TFL);
  or or_18 (or_18_out, IOT_TLS, IOT_TCF, IOT_CAF, CCC_C);
  and and_117 (and_117_out, IOT_TSF, CK_1, FLAG_PRNCOMPLETE);
  and and_118 (and_118_out, IOT_TSK, CK_1, or_16_out);
  LED led_282 (.in(and_110_out));
  LED led_283 (.in(and_111_out));
  LED led_284 (.in(and_112_out));
  LED led_285 (.in(and_113_out));
  LED led_286 (.in(and_114_out));
  LED led_287 (.in(and_115_out));
  LED led_288 (.in(and_116_out));
  LED led_289 (.in(or_17_out));
  LED led_290 (.in(or_18_out));
  LED led_291 (.in(and_117_out));
  LED led_292 (.in(and_118_out));
  assign INIR2RAMA = and_110_out ? and_110_out : 1'bz;  // Driver driver_115
  assign AC2RAMD = and_110_out ? and_110_out : 1'bz;  // Driver driver_116
  assign DAW[24] = and_111_out ? and_111_out : 1'bz;  // Driver driver_117
  assign CLA = and_111_out ? and_111_out : 1'bz;  // Driver driver_118
  assign CLAx = and_112_out ? and_112_out : 1'bz;  // Driver driver_119
  assign ROT2AC = and_112_out ? and_112_out : 1'bz;  // Driver driver_120
  assign AC_CK = and_112_out ? and_112_out : 1'bz;  // Driver driver_121
  assign DONE = and_113_out ? and_113_out : 1'bz;  // Driver driver_122
  assign ROT2AC = and_114_out ? and_114_out : 1'bz;  // Driver driver_123
  assign LINK_CK = and_115_out ? and_115_out : 1'bz;  // Driver driver_124
  assign AC_CK = and_115_out ? and_115_out : 1'bz;  // Driver driver_125
  assign DONE = and_116_out ? and_116_out : 1'bz;  // Driver driver_126
  RisingEdgeDet risingedgedet_1 (.A(or_17_out), .Y(risingedgedet_1_y));
  RisingEdgeDet risingedgedet_2 (.A(or_18_out), .Y(risingedgedet_2_y));
  assign PC_CK = and_117_out ? and_117_out : 1'bz;  // Driver driver_127
  assign PC_CK = and_118_out ? and_118_out : 1'bz;  // Driver driver_128
  // Probe on INSTCNT
  RS_FF_AS PRN (.S(risingedgedet_1_y), .R(risingedgedet_2_y), .Q(FLAG_PRNCOMPLETE));  // open: nQ
  LED led_293 (.in(FLAG_PRNCOMPLETE));
  and and_119 (and_119_out, OPR2, CK_1);
  and and_120 (and_120_out, OPR2, SKIP, STB_1);
  and and_121 (and_121_out, OPR2, CK_2);
  and and_122 (and_122_out, OPR2, STB_2);
  and and_123 (and_123_out, OPR2, CK_3);
  and and_124 (and_124_out, JMS, CK_1);
  LED led_294 (.in(and_124_out));
  and and_125 (and_125_out, JMS, CK_2);
  LED led_295 (.in(and_125_out));
  and and_126 (and_126_out, JMS, CK_3);
  LED led_296 (.in(and_126_out));
  and and_127 (and_127_out, JMS, CK_4);
  LED led_297 (.in(and_127_out));
  and and_128 (and_128_out, JMS, CK_5);
  LED led_298 (.in(and_128_out));
  and and_129 (and_129_out, JMS, CK_6);
  LED led_299 (.in(and_129_out));
  LED led_300 (.in(and_119_out));
  assign ROT2AC = and_119_out ? and_119_out : 1'bz;  // Driver driver_129
  LED led_301 (.in(and_120_out));
  assign PC_CK = and_120_out ? and_120_out : 1'bz;  // Driver driver_130
  assign ROT2AC = and_121_out ? and_121_out : 1'bz;  // Driver driver_131
  LED led_302 (.in(and_121_out));
  assign MQ_CK = and_121_out ? and_121_out : 1'bz;  // Driver driver_132
  LED led_303 (.in(and_122_out));
  assign AC_CK = and_122_out ? and_122_out : 1'bz;  // Driver driver_133
  LED led_304 (.in(and_123_out));
  assign DONE = and_123_out ? and_123_out : 1'bz;  // Driver driver_134
  // CntProbe cntprobe_1: pin names not known; wires that end beside it: cntprobe_1_p1
  // CntProbe cntprobe_2: pin names not known; wires that end beside it: or_15_out
  assign INIR2RAMA = and_124_out ? and_124_out : 1'bz;  // Driver driver_135
  assign PC2RAMD = and_124_out ? and_124_out : 1'bz;  // Driver driver_136
  assign INIR2RAMA = and_125_out ? and_125_out : 1'bz;  // Driver driver_137
  assign PC2RAMD = and_125_out ? and_125_out : 1'bz;  // Driver driver_138
  assign DAW[24] = and_125_out ? and_125_out : 1'bz;  // Driver driver_139
  assign PC_LD = and_125_out ? and_125_out : 1'bz;  // Driver driver_140
  assign IN_IR2PC = and_125_out ? and_125_out : 1'bz;  // Driver driver_141
  assign IN_IR2PC = and_126_out ? and_126_out : 1'bz;  // Driver driver_142
  assign PC_LD = and_126_out ? and_126_out : 1'bz;  // Driver driver_143
  assign PC_CK = and_126_out ? and_126_out : 1'bz;  // Driver driver_144
  assign IN_IR2PC = and_127_out ? and_127_out : 1'bz;  // Driver driver_145
  assign PC_LD = and_127_out ? and_127_out : 1'bz;  // Driver driver_146
  assign PC_CK = and_128_out ? and_128_out : 1'bz;  // Driver driver_147
  assign DONE = and_129_out ? and_129_out : 1'bz;  // Driver driver_148
  Counter #(.Bits(16)) counter_10 (.en(1'b1), .C(CLK_t), .clr(1'b0), .out(counter_10_out));  // open: ovf
  FallingEdgeDet fallingedgedet_1 (.A(uart_1_busy), .Y(cntprobe_1_p1));
  not not_13 (not_13_out, L_OPR3[9]);
  not not_14 (not_14_out, L_OPR3[9]);
  LED led_305 (.in(FLAG_ION));
  LED led_306 (.in(FLAG_IRQINH));
  and and_130 (and_130_out, OPR3, CK_1);
  and and_131 (and_131_out, OPR3, not_13_out, STB_1);
  and and_132 (and_132_out, OPR3, CK_2);
  and and_133 (and_133_out, OPR3, not_14_out, STB_2);
  and and_134 (and_134_out, OPR3, CK_3);
  and and_135 (and_135_out, OPR3, L_OPR3[9], STB_1);
  UART uart_1 (
    .RX(port_1_p3), .ACK(cntprobe_3_p1), .OE(OR_KBD), .DIN(AC[7:0]), .STB(or_15_out),
    .CLK(counter_10_out[5]), .XTAL(clk), .CLEAR(CCC_C), .DOUT(KBD8), .RDY(uart_1_rdy), .TX(uart_1_tx),
    .BUSY(uart_1_busy));
  LED led_307 (.in(FLAG_IRQDLY));
  LED led_308 (.in(and_130_out));
  LED led_309 (.in(and_131_out));
  LED led_310 (.in(and_132_out));
  LED led_311 (.in(and_133_out));
  LED led_312 (.in(and_134_out));
  LED led_313 (.in(and_135_out));
  LED led_314 (.in(IRQ_BUS));
  assign ROT2AC = and_130_out ? and_130_out : 1'bz;  // Driver driver_149
  assign MQ_CK = and_131_out ? and_131_out : 1'bz;  // Driver driver_150
  assign ROT2AC = and_132_out ? and_132_out : 1'bz;  // Driver driver_151
  assign AC_CK = and_133_out ? and_133_out : 1'bz;  // Driver driver_152
  assign DONE = and_134_out ? and_134_out : 1'bz;  // Driver driver_153
  assign MQ_CK = and_135_out ? and_135_out : 1'bz;  // Driver driver_154
  assign AC_CK = and_135_out ? and_135_out : 1'bz;  // Driver driver_155
  // Port port_1: pin names not known; wires that end beside it: uart_1_tx, counter_10_out[5], port_1_p3
  LED led_315 (.in(FLAG_KBDIE));
  LED led_316 (.in(FLAG_KBD));
  and and_136 (i_iac, OPR_IAC, 1'b1);
  and and_137 (i_cll, OPR_CLL, 1'b1);
  and and_138 (i_cma, OPR_CMA, 1'b1);
  and and_139 (i_cml, OPR_CML, 1'b1);
  and and_140 (i_osr, OPR_OSR, 1'b1);
  and and_141 (i_hlt, OPR_HLT, 1'b1);
  or or_19 (i_cla, L_OPR1[8], L_OPR2[9]);
  and and_142 (i_nop, L_OPR3[12], 1'b1);
  and and_143 (i_ral, OPR_LEFT, ~OPR_X2);  // And
  and and_144 (i_rar, OPR_RIGHT, ~OPR_X2);  // And
  and and_145 (i_rtl, OPR_LEFT, OPR_X2);
  and and_146 (i_rtr, OPR_RIGHT, OPR_X2);
  LED led_317 (.in(FLAG_PRNCOMPLETE));
  // CntProbe cntprobe_3: pin names not known; wires that end beside it: cntprobe_3_p1
  // CntProbe cntprobe_4: pin names not known; wires that end beside it: uart_1_rdy
  PullDown pulldown_5 (.out(IR2PC));
  PullDown pulldown_6 (.out(IND2PC));
  PullDown pulldown_7 (.out(RAMD2PC));
  PullDown pulldown_8 (.out(ROT2AC));
  PullDown pulldown_9 (.out(RAMD2AC_ADD));
  PullDown pulldown_10 (.out(PC_LD));
  PullDown pulldown_11 (.out(IND2RAMA));
  PullDown pulldown_12 (.out(INC2RAMD));
  PullDown pulldown_13 (.out(PC2RAMD));
  PullDown pulldown_14 (.out(IR2RAMA));
  PullDown pulldown_15 (.out(IND2INC));
  PullDown pulldown_16 (.out(LD2INC));
  PullDown pulldown_17 (.out(RAMA_HOLD));
  PullDown pulldown_18 (.out(DATA_CK));
  PullDown pulldown_19 (.out(IR_CK));
  PullDown pulldown_20 (.out(PC_CK));
  PullDown pulldown_21 (.out(AC_CK));
  PullDown pulldown_22 (.out(IND_CK));
  PullDown pulldown_23 (.out(LINK_CK));
  PullDown pulldown_24 (.out(DAW[24]));
  PullDown pulldown_25 (.out(RAM_OE));
  PullDown pulldown_26 (.out(MQ_CK));
  and and_147 (i_snl, OPR_SNLSZL, ~OPR_TSTINV);  // And
  and and_148 (i_sza, OPR_SZASNA, ~OPR_TSTINV);  // And
  and and_149 (i_sma, OPR_SMASPA, ~OPR_TSTINV);  // And
  and and_150 (i_szl, OPR_SNLSZL, OPR_TSTINV);
  and and_151 (i_sna, OPR_SZASNA, OPR_TSTINV);
  and and_152 (i_spa, OPR_SMASPA, OPR_TSTINV);
  and and_153 (i_skp, ~OPR_SNLSZL, ~OPR_SZASNA, ~OPR_SMASPA, OPR_TSTINV);  // And
  or or_20 (or_20_out, BUS_IR[8], BUS_IR[7], BUS_IR[6]);
  FallingEdgeDet fallingedgedet_2 (.A(FLAG_KBD), .Y(cntprobe_3_p1));
  RisingEdgeDet risingedgedet_3 (.A(uart_1_rdy), .Y(risingedgedet_3_y));
  LED led_318 (.in(IOT));
  // _74238 _74238_7: pin names not known; wires that end beside it: 1'b1, 1'b0, IOT, 1'b0, or_20_out, BUS_IR[3], BUS_IR[4], BUS_IR[5], L_DEVCPU, L_DEVHSR, L_DEVHSP, L_DEVKBD, L_DEVPRI, L_DEV5, L_DEV6, L_DEV7
  or or_21 (or_21_out, IOT_KCF, IOT_KCC, IOT_KRB, CCC_C);
  and and_154 (and_154_out, IOT_KCC, CK_1);
  and and_155 (and_155_out, IOT_KCC, STB_1);
  and and_156 (and_156_out, IOT_KRB, CK_1);
  and and_157 (and_157_out, IOT_KRB, STB_1);
  // CntProbe cntprobe_5: pin names not known; wires that end beside it: risingedgedet_3_y
  RS_FF_AS KBD (.S(risingedgedet_3_y), .R(or_21_out), .Q(FLAG_KBD));  // open: nQ
  LED led_319 (.in(or_21_out));
  LED led_320 (.in(and_154_out));
  assign ROT2AC = and_154_out ? and_154_out : 1'bz;  // Driver driver_156
  assign CLA_KCC = and_154_out ? and_154_out : 1'bz;  // Driver driver_157
  LED led_321 (.in(and_155_out));
  assign AC_CK = and_155_out ? and_155_out : 1'bz;  // Driver driver_158
  LED led_322 (.in(and_156_out));
  assign ROT2AC = and_156_out ? and_156_out : 1'bz;  // Driver driver_159
  assign OR_KBD = and_156_out ? and_156_out : 1'bz;  // Driver driver_160
  assign CLA_KCC = and_156_out ? and_156_out : 1'bz;  // Driver driver_161
  LED led_323 (.in(and_157_out));
  assign AC_CK = and_157_out ? and_157_out : 1'bz;  // Driver driver_162
  // CntProbe cntprobe_6: pin names not known; wires that end beside it: FLAG_KBD
  LED led_324 (.in(FLAG_KBD));
  // _74238 _74238_8: pin names not known; wires that end beside it: 1'b1, 1'b0, L_DEVCPU, 1'b0, 1'b0, BUS_IR[0], BUS_IR[1], BUS_IR[2], L_CPU[7], L_CPU[6], L_CPU[5], L_CPU[4], L_CPU[3], L_CPU[2], L_CPU[1], L_CAF
  // _74238 _74238_9: pin names not known; wires that end beside it: 1'b1, 1'b0, L_DEVKBD, 1'b0, 1'b0, BUS_IR[0], BUS_IR[1], BUS_IR[2], L_KBD[5], L_KBD[4], L_KBD[3], _74238_9_p12, L_KBD[2], L_KBD[1], L_KBD[0], _74238_9_p16, _74238_9_p12, _74238_9_p16
  // _74238 _74238_10: pin names not known; wires that end beside it: 1'b1, 1'b0, L_DEVPRI, 1'b0, 1'b0, BUS_IR[0], BUS_IR[1], BUS_IR[2], L_PRN[5], L_PRN[4], L_PRN[3], _74238_10_p12, L_PRN[2], L_PRN[1], L_PRN[0], _74238_10_p16, _74238_10_p12, _74238_10_p16
  and and_158 (and_158_out, IOT_KIE, AC[0]);
  LED led_325 (.in(and_158_out));
  and and_159 (and_159_out, IOT_KIE, ~AC[0]);  // And
  LED led_326 (.in(and_159_out));
  and and_160 (and_160_out, IOT_KSF, CK_1, FLAG_KBD);
  and and_161 (and_161_out, IOT_KRS, CK_1);
  and and_162 (and_162_out, IOT_KRS, STB_1);
  or or_22 (or_22_out, and_158_out, CCC_C, IOT_CAF);
  LED led_327 (.in(and_160_out));
  LED led_328 (.in(and_161_out));
  LED led_329 (.in(and_162_out));
  RS_FF_AS #(.Default(1)) KBD_IE (.S(or_22_out), .R(and_159_out), .Q(FLAG_KBDIE));  // open: nQ
  assign PC_CK = and_160_out ? and_160_out : 1'bz;  // Driver driver_163
  assign ROT2AC = and_161_out ? and_161_out : 1'bz;  // Driver driver_164
  assign OR_KBD = and_161_out ? and_161_out : 1'bz;  // Driver driver_165
  assign AC_CK = and_162_out ? and_162_out : 1'bz;  // Driver driver_166
  LED led_330 (.in(FLAG_KBDIE));
  // also tied to GND on the sheet: {counter_1_ovf, counter_3_ovf}

  // Other names for the same wires on the sheet: RAMADDR[11:0] = DAW[23:12]; AC0[2:0] = AC[2:0]; AC1[2:0] = AC[5:3];
  //   AC2[2:0] = AC[8:6]; AC3[2:0] = AC[11:9]; L_GEN (some bits) = {AND, ISZ, DCA, JMS, JMP, IOT, DIRECT, INDIRECT};
  //   IR0[2:0] = BUS_IR[2:0]; IR1[2:0] = BUS_IR[5:3]; IR2[2:0] = BUS_IR[8:6]; IR3[2:0] = BUS_IR[11:9];
  //   PC0[2:0] = BUS_PC[2:0]; PC1[2:0] = BUS_PC[5:3]; PC2[2:0] = BUS_PC[8:6]; PC3[2:0] = BUS_PC[11:9];
  //   STATUS12[11:6] = {LINK, FLAG_GREATERTHAN, IRQ_BUS, FLAG_IRQINH, FLAG_ION, FLAG_USER};
  //   L_IRQ[6:0] = {FLAG_ION, FLAG_IRQINH, FLAG_IRQDLY, IRQ_BUS, FLAG_KBDIE, FLAG_KBD, FLAG_PRNCOMPLETE};
  //   L_OPR1 (some bits) = {i_nop, i_cll, i_cma, i_cml, i_iac, i_rar, i_rtr, i_ral, i_rtl};
  //   L_OPR2[8:0] = {i_skp, i_sma, i_sza, i_spa, i_sna, i_snl, i_szl, i_osr, i_hlt}; L_CPU[0] = L_CAF;
  //   L_GTF = L_CPU[3]; L_IOF = L_CPU[5]; L_ION = L_CPU[6]; L_KCC = L_KBD[3]; L_KCF = L_KBD[5]; L_KIE = L_KBD[1];
  //   L_KRB = L_KBD[0]; L_KRS = L_KBD[2]; L_KSF = L_KBD[4]; L_RTF = L_CPU[2]; L_SGT = L_CPU[1]; L_SKON = L_CPU[7];
  //   L_SRQ = L_CPU[4]; L_TCF = L_PRN[3]; L_TFL = L_PRN[5]; L_TLS = L_PRN[0]; L_TPC = L_PRN[2]; L_TSF = L_PRN[4];
  //   L_TSK = L_PRN[1]; MP = L_GEN[0]; MQ0[2:0] = MQ[2:0]; MQ1[2:0] = MQ[5:3]; MQ2[2:0] = MQ[8:6];
  //   MQ3[2:0] = MQ[11:9]; OPR = L_GEN[4]; OPR_ASL = L_OPR3[5]; OPR_CLA1 = L_OPR1[8]; OPR_CLA2 = L_OPR2[9];
  //   OPR_CLA3 = L_OPR3[11]; OPR_DVI = L_OPR3[2]; OPR_LSR = L_OPR3[6]; OPR_MQA = L_OPR3[8]; OPR_MQL = L_OPR3[7];
  //   OPR_MUY = L_OPR3[1]; OPR_NMI = L_OPR3[3]; OPR_NOP = L_OPR3[12]; OPR_SCA = L_OPR3[10]; OPR_SCL = L_OPR3[0];
  //   OPR_SHL = L_OPR3[4]; OPR_SWP = L_OPR3[9]; plus__plus_INDIRECT = L_GEN[1]; RAM_WE = DAW[24];
  //   RAMDATA[11:0] = DAW[11:0]; TAD = L_GEN[10]; XTAL = clk

  // Notes on the sheet:
  //   clk: Hz: 1000000
  //   IR DECODER
  //   CP=0 PAGE ZERO
  //   CP=1 CURRENT PAGE
  //   IA=0 DIRECT
  //   IA=1 INDIRECT
  //   SEQ OPR 1 MICROCODES
  //   ------------------------------------
  //   1 CLA CLL
  //   2 CMA CML
  //   3 IAC
  //   4 RAR RAL RTR RTL BSW
  //   github.com/SmallRoomLabs/PDP8-X
  //   PC
  //   IR
  //   AC
  //   MQ
  //   ACCUMULATOR
  //   PDP-8/X v4
  //   LINK
  //   C
  //   Available softwares:
  //   ——————————
  //   000: printhelp.bin                PC:0200 (This help)
  //   001: D0AB-InstTest-1.pt           PC:0200 SR:7777 Watch:0121 cont@0147
  //   002: D0BB-InstTest-2.pt           PC:0200 SR:xxxx Watch:3747
  //   003: D0IB-JMPJMS.pt               PC:0200 SR:xxxx Watch:3571
  //   004: D0JB-JMPJMS-RANDOM.pt        PC:0200 SR:0000 Watch:0044
  //   005: D0DB-RandomAND.pt            PC:0200 SR:0000 Watch:0202
  //   006: D0EB-Random-TAD.pt           PC:0200 SR:0000 Watch:6776
  //   007: D0FC-Random-ISZ.pt           PC:0200 SR:0000 Watch:0175
  //   010: D0GC-Random-DCA.pt           PC:0200 SR:0000 Watch 0006/0011
  //   011: D0CC-AddTest.pt              PC:0200
  //   012: D1AA-Memory-Checkerboard.pt  PC:0200
  //   013: D1EA-Memory-Address.rim      PC:0200
  //   014: intIO.bin                    PC:0100
  //   015: intout.bin                   PC:0100
  //   016: tstest.bin                   PC:0100
  //   017: myfocal-noint.bin            PC:0200
  //   020: myfocal.bin                  PC:0200
  //   <end>
  //   OPR-3
  //   NOP
  //   OPR-2
  //   CLA
  //   OPR-1
  //   OPCODES
  //   AND
  //   -
  //   TAD
  //   1 pcs 7404 Hex inverter
  //   1 pcs 7408 Quad 2-input AND
  //   1 pcs 7411 Triple 3-input AND
  //   2 pcs 7427 Triple 3-input NOR
  //   1 pcs 74238 Decoder 3-to-8
  //   SKP
  //   SCA
  //   SMA
  //   CLL
  //   ISZ
  //   F
  //   SWP
  //   MQA
  //   SZA
  //   SPA
  //   CMA
  //   CML
  //   DCA
  //   JMS
  //   S
  //   L
  //   MQL
  //   SNA
  //   IAC
  //   JMP
  //   LSR
  //   SNL
  //   RAR
  //   IOT
  //   ASL
  //   SHL
  //   OSR
  //   SZL
  //   RTR
  //   RAL
  //   OPR
  //   DIR
  //   IOT DECODER
  //   NMI
  //   HLT
  //   RTL
  //   IND
  //   CPU COMMAND & CONTROL
  //   MEM BANK
  //   DVI
  //   AUTO
  //   IND
  //   STATE
  //   INSTR.
  //   RUN
  //   HALT
  //   TRACE
  //   PC.SET
  //   MUY
  //   SCL
  //   CURR
  //   PAGE
  //   BREAKPOINT - PC
  //   BREAKPOINT - INSTR. CNT
  //   600x
  //   CPU FLAGS & 
  //   INTERRUPT
  //   603x
  //   TTY KEYBOARD
  //   SLOW READER
  //   604x
  //   TTY PRINTER
  //   SLOW PUNCH
  //   IOT-PRINTER
  //   TFL
  //   IOT-KEYBOARD
  //   KCF
  //   IOT-CPU
  //   SKON
  //   INTERRUPT FLAGS
  //   GIE
  //   ROTATES
  //   TSF
  //   KSF
  //   ION
  //   IRQ
  //   IHBT
  //   TCF
  //   KCC
  //   IOF
  //   IRQ
  //   DLY
  //   TPC
  //   TSK
  //   KRS
  //   KIE
  //   SRQ
  //   GTF
  //   TTY
  //   IE
  //   INT
  //   BUS
  //   TLS
  //   KRB
  //   RTF
  //   TTY
  //   KBD
  //   SGT
  //   TTY
  //   PRN
  //   LATCHED PC
  //   CAF
  //   OPR DECODER
  //   OPR1
  //   OPR2
  //   OPR3
  //   SEQ OPR 2 MICROCODES
  //   ------------------------------------
  //   1 SMA SPA SZA SZN SNK SZL SKP
  //   2 CLA
  //   3 OSR
  //   4 HLT
  //   PCIN
  //   SKIP LOGIC
  //   AC=0
  //   AC negative
  //   LINK<>0
  //   contents of eeprom_1 (hex, n*v repeats v):
  //   80,8f9,8fa,8fb,8fc,8fd,8fe,8ff,900,901,902,903,904,905,903,904,905,903,904,905,903,
  //   904,905,903,904,905,903,904,905,903,904,905,903,904,905,903,904,905,903,904,905,903,
  //   904,905,903,904,905,903,904,905,903,904,905,903,904,905,903,904,906,907,97a,97b,152,
  //   153,154,155,149,14a,14b,14c,14d,14e,150,156,157,158,159,15a,149,14a,14b,14c,14d,14e,
  //   150,15b,31f,320,321,322,323,324,325,326,331,332,333,334,335,337,338,339,33a,33b,33c,
  //   33d,33e,33f,340,d01,d02,d03,d04,d05,d07,d08,d09,d0a,d0b,d0e,d0f,d10,d11,d12,d13,d14,
  //   d15,d17,d18,d19,d1a,d1b,d1c,d1d,d1e,d1f,d20,d21,d22,d37,d38,d39,d3a,d3b,d3c,d3d,d3e,
  //   d3f,d40,d41,d3e,d3f,d40,d41,d3e,d3f,d40,d42,d01,d02,d03,d04,d05,d07,d08,d09,d0a,d0b,
  //   d0e,d0f,d10,d11,d12,d13,d14,d15,d17,d18,d19,d1a,d1b,d1c,d1d,d1e,d1f,d20,d21,d23,d24,
  //   d25,d26,d27,d35,d36,d3b,d3c,d3d,d3e,d3f,d40,d41,d3e,d3f,d40,d41,d3e,d3f,d40,d42,d01,
  //   d02,d03,d04,d05,d06,343,344,375,376,377,97d,97e,97f,908,909,90a,90b,90c,90d,90e,90f,
  //   916,917,918,919,91a,91c,91d,91e,91f,920,926,927,928,92a,92b,92c,92d,94a,94b,94c,94d,
  //   94e,152,153,154,155,149,14a,14b,14c,14d,14e,150,156,157,158,159,15a,149,14a,14b,14c,
  //   14d,14e,150,15b,111,112,140,141,142,149,14a,14b,14c,14d,14e,150,143,144,145,146,149,
  //   14a,14b,14c,14d,14e,150,147,113,15d,15e,15f,160,161,162,149,14a,14b,14c,14d,14e,150,
  //   163,164,165,166,167,168,165,166,167,168,165,166,167,169,16a,149,14a,14b,14c,14d,14e,
  //   150,16b,115,15d,15e,15f,160,161,162,149,14a,14b,14c,14d,14e,150,163,164,165,166,167,
  //   168,165,166,167,168,165,166,167,169,16a,149,14a,14b,14c,14d,14e,150,16b,117,118,11a,
  //   4a3,4a4,4a5,4a6,4a7,4a8,4a9,4aa,4ab,4ac,4ad,4b6,4b7,4b8,4b9,4ba,4bb,11c,11d,11e,11f,
  //   1e5,1e6,1e7,1e8,1e9,1ea,1eb,1ec,1ed,121,152,153,154,155,149,14a,14b,14c,14d,14e,150,
  //   156,157,158,159,15a,149,14a,14b,14c,14d,14e,150,15b,186,187,188,4bd,4d9,4da,4e5,4e6,
  //   4e7,4e8,4e9,4ea,4eb,4ec,4ed,4dc,4dd,4de,4df,4e0,4e2,4e3,4e4,4be,4bf,4c0,4c1,4c2,4c4,
  //   4c5,4c6,4c7,4c8,4ca,189,18a,18b,18d,1d2,1d3,1d4,1d5,1d7,1d8,1d9,1da,1d4,1d5,1d7,1d8,
  //   1d9,1da,1d4,1d5,1d7,1d8,1d9,1da,1d4,1d5,1d7,1d8,1d9,1da,1d4,1d5,1d6,1e0,1e1,1e2,1e3,
  //   190,191,192,140,141,142,149,14a,14b,14c,14d,14e,150,143,144,145,146,149,14a,14b,14c,
  //   14d,14e,150,147,193,4bd,4d9,4db,4dc,4dd,4de,4df,4e0,4e2,4e3,4e4,4be,4c0,4c1,4c2,4c4,
  //   4c5,4c6,4c7,4c8,4ca,194,1d2,1d3,1d4,1d5,1d7,1d8,1d9,1da,1d4,1d5,1d7,1d8,1d9,1da,1d4,
  //   1d5,1d7,1d8,1d9,1da,1d4,1d5,1d7,1d8,1d9,1da,1d4,1d5,1d6,1e0,1e1,1e2,1e3,197,193,4bd,
  //   4d9,4da,4e5,4e6,4e7,4e8,4e9,4ea,4eb,4ec,4ed,4dc,4dd,4de,4df,4e0,4e2,4e3,4e4,4be,4bf,
  //   4c0,4c1,4c2,4c4,4c5,4c6,4c7,4c8,4ca,194,1d2,1d3,1d4,1d5,1d7,1d8,1d9,1da,1d4,1d5,1d7,
  //   1d8,1d9,1da,1d4,1d5,1d7,1d8,1d9,1da,1d4,1d5,1d7,1d8,1d9,1da,1d4,1d5,1d6,1e0,1e1,1e2,
  //   1e3,197,193,4bd,4d9,4db,4dc,4dd,4de,4df,4e0,4e2,4e3,4e4,4be,4bf,4c0,4c1,4c2,4c4,4c5,
  //   4c6,4c7,4c8,4ca,194,1d2,1d3,1d4,1d5,1d7,1d8,1d9,1da,1d4,1d5,1d7,1d8,1d9,1da,1d4,1d5,
  //   1d7,1d8,1d9,1da,1d4,1d5,1d7,1d8,1d9,1da,1d4,1d5,1d6,1e0,1e1,1e2,1e3,197,193,4bd,4d9,
  //   4da,4e5,4e6,4e7,4e8,4e9,4ea,4eb,4ec,4ed,4dc,4dd,4de,4df,4e0,4e2,4e3,4e4,4be,4bf,4c0,
  //   4c1,4c2,4c4,4c5,4c6,4c7,4c8,4ca,194,1d2,1d3,1d4,1d5,1d7,1d8,1d9,1da,1d4,1d5,1d7,1d8,
  //   1d9,1da,1d4,1d5,1d7,1d8,1d9,1da,1d4,1d5,1d7,1d8,1d9,1da,1d4,1d5,1d6,1e0,1e1,1e2,1e3,
  //   197,193,4bd,4d9,4db,4dc,4dd,4de,4df,4e0,4e2,4e3,4e4,4be,4bf,4c0,4c1,4c2,4c4,4c5,1,
  //   583,584,585,586,588,589,58a,58b,58c,595,596,5a6,5a7,5aa,5ab,5ac,5ad,5ae,5af,5b0,5b1,
  //   4c5,4c6,4c7,4c8,4ca,194,1d2,1d3,1d4,1d5,1d7,1d8,1d9,1da,1d4,1d5,1d7,1d8,1d9,1da,1d4,
  //   1d5,1d7,1d8,1d9,1da,1d4,1d5,1d7,1d8,1d9,1da,1d4,1d5,1d6,1e0,1e1,1e2,1e3,197,193,4bd,
  //   4d9,4da,4e5,4e6,4e7,4e8,4e9,4ea,4eb,4ec,4ed,4dc,4dd,4de,4df,4e0,4e2,4e3,4e4,4be,4bf,
  //   4c0,4c1,4c2,4c4,4c5,4c6,4c7,4c8,4ca,194,1d2,1d3,1d4,1d5,1d7,1d8,1d9,1da,1d4,1d5,1d7,
  //   1d8,1d9,1da,1d4,1d5,1d7,1d8,1d9,1da,1d4,1d5,1d7,1d8,1d9,1da,1d4,1d5,1d6,1e0,1e1,1e2,
  //   1e3,197,193,4bd,4d9,4db,4dc,4dd,4de,4df,4e0,4e2,4e3,4e4,4be,4c0,4c1,4c2,4c4,4c5,4c6,
  //   4c7,4c8,4ca,194,1d2,1d3,1d4,1d5,1d7,1d8,1d9,1da,1d4,1d5,1d7,1d8,1d9,1db,1dc,1dd,1de,
  //   1df,1e1,1e2,1e3,196,198,199,2cd,2cf,2d0,2d1,2d2,2d3,2d4,2d5,2d7,2d8,2d9,2d4,2d5,2d7,
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  //   PCOUT
  //   SMA      7500  skip on minus AC
  //   SPA      7510  skip on plus AC
  //   SZA      7440  skip on zero AC
  //   SNA      7450  skip on non-zero AC
  //   SNL      7420  skip on non-zero link
  //   SZL      7430  skip on zero link
  //   MAIN DATA-PATHS
  //   RAMADDR
  //   contents of eeprom_2 (hex, n*v repeats v):
  //   0,e00,e00,b00,f02,f02,f02,f02,9b,f02,f02,f02,f02,f02,f02,f02,f02,f02,f02,f02,f02,
  //   f02,f02,f02,f02,f02,f02,f02,f02,f02,f02,f02,f02,f02,f02,f02,f02,f02,f02,f02,f02,f02,
  //   f02,f02,f02,f02,f02,f02,f02,f02,f02,f02,f02,f02,f02,f02,f02,f02,f02,f02,f02,f02,f02,
  //   f02,c07,c1d,e01,a41,e00,e00,c02,e00,e00,c01,e00,e00,c04,e00,e00,c02,e00,e00,c05,e00,
  //   e00,e00,e00,a58,e00,e00,e00,bff,c1a,c19,a5d,c1e,c26,c21,a61,c26,c21,a64,c26,c21,a67,
  //   a5d,e80,c26,c21,a6c,e01,a6b,f02,f02,f02,f02,f02,f02,f02,f02,f02,f02,f02,f02,f02,f02,
  //   f02,82,e00,a82,c20,e80,308,f28,a86,889,a83,0,c21,a8a,c26,b89,ed0,e04,f18,a95,49b,
  //   a92,a8f,e08,f18,a8f,49b,a98,a95,0,d,a,d,a,c1,f6,e1,e9,ec,e1,e2,ec,e5,a0,f3,ef,e6,
  //   f4,f7,e1,f2,e5,f3,ba,d,a,ad,ad,ad,ad,ad,ad,ad,ad,ad,ad,ad,ad,ad,ad,ad,ad,ad,ad,ad,
  //   ad,d,a,30,30,30,3a,20,70,72,69,6e,74,68,65,6c,70,2e,62,69,6e,20,20,20,20,20,20,20,
  //   20,20,20,20,20,20,20,20,20,50,43,3a,30,32,30,30,20,28,54,68,69,73,20,68,65,6c,70,
  //   29,a,d,30,30,31,3a,20,44,30,41,42,2d,49,6e,73,74,54,65,73,74,2d,31,2e,70,74,20,20,
  //   20,20,20,20,20,20,20,20,20,50,43,3a,30,32,30,30,20,53,52,3a,37,37,37,37,20,57,61,
  //   74,63,68,3a,30,31,32,31,20,63,6f,6e,74,40,30,31,34,37,a,d,30,30,32,3a,20,44,30,42,
  //   42,2d,49,6e,73,74,54,65,73,74,2d,32,2e,70,74,20,20,20,20,20,20,20,20,20,20,20,50,
  //   43,3a,30,32,30,30,20,53,52,3a,78,78,78,78,20,57,61,74,63,68,3a,33,37,34,37,a,d,30,
  //   30,33,3a,20,44,30,49,42,2d,4a,4d,50,4a,4d,53,2e,70,74,20,20,20,20,20,20,20,20,20,
  //   20,20,20,20,20,20,50,43,3a,30,32,30,30,20,53,52,3a,78,78,78,78,20,57,61,74,63,68,
  //   3a,33,35,37,31,a,d,30,30,34,3a,20,44,30,4a,42,2d,4a,4d,50,4a,4d,53,2d,52,41,4e,44,
  //   4f,4d,2e,70,74,20,20,20,20,20,20,20,20,50,43,3a,30,32,30,30,20,53,52,3a,30,30,30,
  //   30,20,57,61,74,63,68,3a,30,30,34,33,2f,30,30,34,34,5c,72,5c,6e,20,20,20,20,20,20,
  //   20,20,20,20,20,20,20,20,20,20,20,20,20,20,20,20,20,20,20,20,20,20,20,57,72,61,70,
  //   73,20,61,74,20,30,37,37,37,37,2f,30,37,37,37,37,20,70,72,69,6e,74,73,20,4a,42,a,d,
  //   30,30,35,3a,20,44,30,44,42,2d,52,61,6e,64,6f,6d,41,4e,44,2e,70,74,20,20,20,20,20,
  //   20,20,20,20,20,20,20,50,43,3a,30,32,30,30,20,53,52,3a,30,30,30,30,20,57,61,74,63,
  //   68,3a,30,32,30,32,a,d,30,30,36,3a,20,44,30,45,42,2d,52,61,6e,64,6f,6d,2d,54,41,44,
  //   2e,70,74,20,20,20,20,20,20,20,20,20,20,20,50,43,3a,30,32,30,30,20,53,52,3a,30,30,
  //   30,30,20,57,61,74,63,68,3a,36,37,37,36,a,d,30,30,37,3a,20,44,30,46,43,2d,52,61,6e,
  //   64,6f,6d,2d,49,53,5a,2e,70,74,20,20,20,20,20,20,20,20,20,20,20,50,43,3a,30,32,30,
  //   30,20,53,52,3a,30,30,30,30,20,57,61,74,63,68,3a,30,31,37,35,a,d,30,31,30,3a,20,44,
  //   30,47,43,2d,52,61,6e,64,6f,6d,2d,44,43,41,2e,70,74,20,20,20,20,20,20,20,20,20,20,
  //   20,50,43,3a,30,32,30,30,20,53,52,3a,30,30,30,30,20,57,61,74,63,68,20,30,30,30,36,
  //   2f,30,30,31,31,a,d,30,31,31,3a,20,44,30,43,43,2d,41,64,64,54,65,73,74,2e,70,74,20,
  //   20,20,20,20,20,20,20,20,20,20,20,20,20,50,43,3a,30,32,30,30,a,d,30,31,32,3a,20,44,
  //   31,41,41,2d,4d,65,6d,6f,72,79,2d,43,68,65,63,6b,65,72,62,6f,61,72,64,2e,70,74,20,
  //   20,50,43,3a,30,32,30,30,a,d,30,31,33,3a,20,44,31,45,41,2d,4d,65,6d,6f,72,79,2d,41,
  //   64,64,72,65,73,73,2e,72,69,6d,20,20,20,20,20,20,50,43,3a,30,32,30,30,a,d,30,31,34,
  //   3a,20,66,6f,63,61,6c,2d,38,2e,62,69,6e,20,20,20,20,20,20,20,20,20,20,20,20,20,20,
  //   20,20,20,20,50,43,3a,30,32,30,30,a,d,30,31,35,3a,20,49,6e,74,49,4f,2e,62,69,6e,20,
  //   20,20,20,20,20,20,20,20,20,20,20,20,20,20,20,20,20,20,20,50,43,3a,30,31,30,30,a,d,
  //   30,31,36,3a,20,49,6e,74,6f,75,74,2e,62,69,6e,20,20,20,20,20,20,20,20,20,20,20,20,
  //   20,20,20,20,20,20,20,50,43,3a,30,31,30,30,a,d,30,31,37,3a,20,74,73,74,65,73,74,2e,
  //   62,69,6e,20,20,20,20,20,20,20,20,20,20,20,20,20,20,20,20,20,20,20,50,43,3a,30,31,
  //   30,30,a,d,bc,e5,ee,e4,be,d,0,f02,f02,f02,f02,f02,f02,f02,f02,f02,f02,f02,f02,f02,
  //   f02,f02,f02,f02,f02,f02,f02,f02,f02,f02,f02,f02,f02,f02,f02,f02,f02,f02,f02,f02,f02,
  //   f02,f02,f02,f02,f02,f02,f02,f02,f02,f02,f02,f02,f02,f02,f02,f02,f02,f02,f02,f02,f02,
  //   f02,f02,f02,f02,f02,f02,f02,f02,f02,f02,f02,f02,f02,f02,f02,f02,f02,f02,f02,f02,f02,
  //   f02,f02,f02,f02,f02,f02,f02,f02,f02,f02,f02,f02,f02,f02,f02,f02,f02,f02,f02,f02,f02,
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  //   CLOCK CYCLE CONTROLLER
  //   RAMDATA
  //   PC 
  //   BREAKPOINT
  //   DATA
  //   INSTRUCTION
  //   1 pcs 7404 Hex inverter
  //   7 pcs 7408 Quad 2-input AND
  //   1 pcs 7411 Triple 3-input AND
  //   1 pcs 8-input NOR (***REPLACE***)
  //   1 pcs 74238 Decoder 3-to-8
  //   INST COUNT
  //   BREAKPOINT
  //   INDOUT
  //   600x - INTERRUPT INSTRUCTIONS
  //   LATCHED
  //   DATA
  //   Turn interrupt ON
  //   Turn interrupt OFF
  //   Clear All Flags
  //   Skip if interrupt ON, and turn OFF
  //   Skip interrupt request
  //   External IRQ
  //   sources
  //   INC
  //   Skip on Greater Than flag
  //   IND
  //   STEP1
  //   IND
  //   STEP2
  //   FETCH OP &
  //   INCREMENT PC
  //   FORCE 4000 (JMS 0)
  //   TO IR AS INTERRUPT
  //   iAuto 1
  //   iAuto 2
  //   iAuto 3
  //   iAuto 4
  //   Get interrupt flags
  //   AC6..11 - Save field register
  //   AC5 - User flag
  //   AC4 - Interrupt Enable flip-flop
  //   AC3 - Interrupt inhibit flip-flop
  //   AC2 - Interrupt Request line
  //   AC1 - Greater than flag
  //   AC0 - LINK
  //   Prepare to set
  //   new PC
  //   Actually set
  //   new PC
  //   Restore interrupt flags
  //   HANDLES USER FLAG
  //   HANDLES GREATER THAN FLAG
  //   HANDLES LINK
  //   TAD
  //   STEP1
  //   TAD
  //   STEP2
  //   Prepare to set PC
  //   with new vector
  //   JMP i
  //   AUTOINDEX
  //   604x - IOT Printer
  //   TPC: The least significant 8-bits of the accumulator 
  //   is copied to the print buffer, initiating output.
  //   Save value
  //   from IND
  //   indo LATDAT
  //   JMP i-auto
  //   SKIP IF
  //   AC=ZERO
  //   Teleprinter Print Character
  //   Teleprinter Load and Start
  //   Teleprinter Flag set (aka SPF)
  //   Teleprinter Clear Flag
  //   Teleprinter Skip if Flag
  //   Teleprinter Skip (aka SPI)
  //   TFL: The printer flag, signalling output complete, is set.
  //   OPR 1
  //   TSK: If either the print flag or the keyboard flag are 
  //   set, the next instruction in sequence is skipped.
  //   TSF: If the printer flag is set, indicating output 
  //   is complete, the next instruction in sequence is 
  //   skipped.
  //   KIE: The accumulator is loaded into the device 
  //   control register (the interrupt enable and status 
  //   report control bits).
  //   OPR 2
  //   Prepate to store 
  //   return addr
  //   to [ind]
  //   Store return addr
  //   to [ind]
  //   Actually increment
  //   PC
  //   Pause to accept
  //   new PC inc clk
  //   KRS: The 8-bit character in the keyboard buffer 
  //   is ored with the accumulator.
  //   OPR 3
  //   OPR_SWP
  //   CONNECTORS & DECODERS FOR LED/DISPLAYS
  //   [LED] IOT DECODER
  //   603x - IOT Keyboard
  //   KCF: The keyboard flag, signalling input data ready, 
  //   is cleared.
  //   Keyboard Clear Flags
  //   Keyboard and AC Clear
  //   Keyboard Read and 
  //   Begin next read
  //   KRB: The 8 bit character in the keyboard buffer is 
  //   transferred to the accumulator, and the keyboard 
  //   flag is cleared, allowing the reading of the next 
  //   character to begin. In effect, this operation combines 
  //   the KCC and KRS operations;
  //   Keyboard Skip if Flag
  //   Keyboard Clear and read Character
  //   Keyboard Read Static
  //   Keyboard Interrupt Enable
  //   Keyboard Read and Begin next read
  //   KSF: If the keyboard flag is set, indicating that input 
  //   data is ready, the next instruction in sequence is 
  //   skipped.
endmodule
