// Digital circuit PDP8-X-backup1.dig as structural Verilog
module PDP8_X_backup1 (
  input  clk
);

  wire AC2RAMD, AC_CK, add_1_c_o, add_2_c_o, AND, and_1_out, and_2_out, and_4_out, and_6_out, and_8_out,
       and_9_out, and_10_out, and_12_out, and_13_out, and_14_out, and_15_out, and_16_out, and_17_out,
       and_19_out, and_21_out, and_23_out, and_26_out, and_27_out, and_28_out, and_30_out, and_31_out,
       and_32_out, and_33_out, and_34_out, and_35_out, and_37_out, and_38_out, and_39_out, and_40_out,
       and_41_out, and_42_out, and_43_out, and_45_out, and_46_out, and_47_out, and_48_out, and_49_out,
       and_50_out, and_52_out, and_53_out, and_54_out, and_55_out, and_57_out, and_58_out, and_60_out,
       and_62_out, and_63_out, and_64_out, and_65_out, and_66_out, and_68_out, and_69_out, and_70_out,
       and_72_out, and_73_out, and_74_out, and_75_out, and_76_out, and_77_out, and_79_out, and_80_out,
       and_81_out, and_82_out, and_83_out, and_84_out, and_85_out, and_86_out, and_87_out, and_89_out,
       and_91_out, and_93_out, and_94_out, and_95_out, and_96_out, and_98_out, and_100_out, and_101_out,
       and_102_out, AUTOIND, BP_ENABLED_b, CLA, CLAx, CNT_AND, CNT_AND_I, CNT_AND_IA, CNT_DCA, CNT_DCA_I,
       CNT_DCA_IA, CNT_ISZ, CNT_ISZ_I, CNT_ISZ_IA, CNT_JMP, CNT_JMP_I, CNT_JMP_IA, CNT_JMS, CNT_JMS_I,
       CNT_JMS_IA, CNT_OPR1, CNT_OPR2, CNT_TAD, CNT_TAD_I, CNT_TAD_IA, comparator_1_eq, comparator_2_eq,
       counter_1_o1, counter_1_o2, counter_1_o3, counter_1_o4, counter_1_o5, counter_1_o6, counter_1_o7,
       counter_1_o8, counter_1_o9, counter_1_o10, counter_1_o11, counter_1_o12, counter_1_o13, counter_1_o14,
       counter_1_o15, counter_1_o16, counter_1_o17, counter_1_o18, counter_1_o19, counter_1_o20,
       counter_1_o21, counter_1_o22, counter_1_o23, counter_1_o24, counter_1_o25, counter_1_o26,
       counter_1_o27, counter_1_o28, counter_1_o29, counter_1_o30, counter_1_o31, counter_1_o32, d_ff_1_q,
       DCA, demultiplexer_1_out_0, demultiplexer_1_out_1, demultiplexer_1_out_2, demultiplexer_1_out_3,
       demultiplexer_1_out_4, demultiplexer_1_out_5, demultiplexer_1_out_6, demultiplexer_1_out_7,
       demultiplexer_2_out_3, demultiplexer_2_out_7, demultiplexer_3_out_3, demultiplexer_3_out_7,
       demultiplexer_4_out_10, demultiplexer_4_out_11, demultiplexer_4_out_12, demultiplexer_4_out_13,
       demultiplexer_4_out_14, demultiplexer_4_out_15, demultiplexer_4_out_16, demultiplexer_4_out_17,
       demultiplexer_4_out_18, demultiplexer_4_out_19, demultiplexer_4_out_20, demultiplexer_4_out_21,
       demultiplexer_4_out_22, demultiplexer_4_out_23, demultiplexer_4_out_24, demultiplexer_4_out_25,
       demultiplexer_4_out_26, demultiplexer_4_out_27, demultiplexer_4_out_28, demultiplexer_4_out_29,
       demultiplexer_4_out_30, demultiplexer_4_out_31, demultiplexer_4_out_32, demultiplexer_4_out_33,
       demultiplexer_4_out_34, demultiplexer_4_out_35, demultiplexer_4_out_36, demultiplexer_4_out_37,
       demultiplexer_4_out_38, demultiplexer_4_out_39, demultiplexer_4_out_40, demultiplexer_4_out_41,
       demultiplexer_4_out_42, demultiplexer_4_out_43, demultiplexer_4_out_44, demultiplexer_4_out_45,
       demultiplexer_4_out_46, demultiplexer_4_out_47, demultiplexer_4_out_48, demultiplexer_4_out_49,
       demultiplexer_4_out_50, demultiplexer_4_out_51, demultiplexer_4_out_52, demultiplexer_4_out_53,
       demultiplexer_4_out_54, demultiplexer_4_out_55, demultiplexer_4_out_56, demultiplexer_4_out_57,
       demultiplexer_4_out_58, demultiplexer_4_out_59, demultiplexer_4_out_60, demultiplexer_4_out_61,
       demultiplexer_4_out_62, demultiplexer_4_out_63, driver_21_out, driver_22_out, driver_50_out,
       driver_51_out, driver_52_out, driver_56_out, driver_57_out, driver_60_out, driver_61_out,
       driver_62_out, driver_89_out, driver_90_out, driver_254_out, driver_255_out, driver_260_out,
       driver_263_out, driver_264_out, driver_265_out, driver_269_out, driver_270_out, driver_273_out,
       driver_274_out, driver_275_out, driver_279_out, driver_280_out, driver_285_out, driver_288_out,
       driver_289_out, driver_290_out, driver_295_out, driver_299_out, driver_300_out, driver_301_out,
       driver_302_out, driver_303_out, driver_304_out, driver_305_out, driver_307_out, driver_308_out,
       driver_309_out, driver_314_out, driver_315_out, driver_320_out, driver_324_out, driver_325_out,
       driver_335_out, driver_338_out, driver_339_out, driver_340_out, driver_342_out, driver_343_out,
       driver_344_out, driver_348_out, driver_349_out, driver_350_out, driver_354_out, driver_355_out,
       driver_358_out, driver_359_out, driver_360_out, driver_364_out, driver_365_out, driver_370_out,
       driver_374_out, driver_375_out, driver_385_out, driver_388_out, driver_389_out, driver_390_out,
       driver_392_out, driver_393_out, driver_394_out, driver_397_out, driver_398_out, driver_399_out,
       driver_400_out, driver_404_out, driver_405_out, driver_409_out, driver_410_out, driver_418_out,
       driver_419_out, driver_420_out, driver_424_out, driver_425_out, driver_428_out, driver_429_out,
       driver_430_out, driver_434_out, driver_435_out, FLAG_PRNRDY, H_out, HALT, HLT_ENABLED_b, I_out,
       INC2RAMD, INCZERO, IND, IND2PC, IND2RAMA, IND_CK, INST_KCC, INST_KCF, INST_KIE, INST_KRB, INST_KRS,
       INST_KSF, INST_TCF, INST_TFL, INST_TLS, INST_TPC, INST_TSF, INST_TSK, IOT, IOT_1x, IOT_2x, IOT_3x,
       IOT_4x, IOT_5, IOT_5x, IOT_6, IOT_6x, IOT_7, IOT_8, IOT_9, IOT_DEVCPU, IOT_DEVHSP, IOT_DEVHSR,
       IOT_DEVKBD, IOT_DEVPRI, IR2PC, IR2RAMA, IR_CK, ISZ, JMP, JMS, LINK, LINK_CK, monoflop_1_nq,
       monoflop_1_q, monoflop_2_q, monoflop_3_q, monoflop_4_q, monoflop_5_q, NOIND, nor_1_out, NOTNOP, OPR,
       OPR1, OPR2, OPR_CLA1, OPR_CLA2, OPR_CLL, OPR_CMA, OPR_CML, OPR_HLT, OPR_IAC, OPR_LEFT, OPR_NA1,
       OPR_NOP, OPR_OSR, OPR_RIGHT, OPR_SMA, OPR_SNL, OPR_SZA, OPR_TSTINV, OPR_X2, or_1_out, or_2_out,
       or_3_out, or_4_out, or_5_out, or_6_out, or_7_out, or_9_out, or_10_out, or_11_out, PC2RAMA, PC2RAMD,
       PC_CK, PC_eq_200, PC_LD, PH00, PH01, PH02, PH03, PH04, PH05, PH06, PH07, PH08, PH09, PH10, PH11, PH12,
       PH13, PH14, PH15, R_out, RAM_OE, RAM_WE, RAMA_HOLD, RAMD2AC_ADD, RAMD2AC_AND, RAMD2IND, RAMD2PC,
       reset_1_out, ROT2AC, rotater_1_p5, rs_ff_as_2_q, rs_ff_as_3_q, S_out, SKIP, TAD, xor_1_out, xor_2_out;
  wire [2:0] DA0, DA1, DA2, DA3, IND0, IND1, IND2, IND3, RA0, RA1, RA2, RA3;
  wire [3:0] counter_2_out;
  wire [11:0] AC, add_1_s, add_2_s, and_18_out, and_22_out, and_24_out, autocapture_1__10, autocapture_1__11,
       autocapture_1__12, autocapture_1__13, autocapture_1__14, autocapture_1__15, autocapture_1__16,
       autocapture_1__17, bitextender_1_out, bitextender_2_out, bitextender_3_out, BUS_IR, BUS_PC,
       dipswitch_1_out, driver_83_out, INC_s, not_1_out, or_8_out, PCIN, RAMDATA, register_1_q, rotater_1_p4,
       transp_latch_1_p4, xor_3_out;
  wire [31:0] COUNT_out, INSTRUCTION_COUNT_out;

  Comparator #(.Bits(12)) comparator_1 (.a({RA3, RA2, RA1, RA0}), .b(12'h1), .eq(comparator_1_eq));  // open: gt, lt
  and and_1 (and_1_out, comparator_1_eq, RAM_WE);
  COUNTER counter_1 (
    .i1(CNT_AND), .i2(CNT_AND_I), .i3(CNT_AND_IA), .i4(CNT_TAD), .i5(CNT_TAD_I), .i6(CNT_TAD_IA),
    .i7(CNT_ISZ), .i8(CNT_ISZ_I), .i9(CNT_ISZ_IA), .i10(CNT_DCA), .i11(CNT_DCA_I), .i12(CNT_DCA_IA),
    .i13(CNT_JMS), .i14(CNT_JMS_I), .i15(CNT_JMS_IA), .i16(CNT_JMP), .i17(CNT_JMP_I), .i18(CNT_JMP_IA),
    .i19(CNT_OPR1), .i20(CNT_OPR2), .i21(IOT_DEVCPU), .i22(IOT_DEVHSR), .i23(IOT_DEVHSP), .i24(IOT_DEVKBD),
    .i25(IOT_DEVPRI), .i26(IOT_5), .i27(IOT_6), .i28(IOT_7), .i29(IOT_8), .i30(IOT_9), .i31(IOT_1x),
    .i32(IOT_2x), .C(1'b0), .E(PH02), .o1(counter_1_o1), .o2(counter_1_o2), .o3(counter_1_o3),
    .o4(counter_1_o4), .o5(counter_1_o5), .o6(counter_1_o6), .o7(counter_1_o7), .o8(counter_1_o8),
    .o9(counter_1_o9), .o10(counter_1_o10), .o11(counter_1_o11), .o12(counter_1_o12), .o13(counter_1_o13),
    .o14(counter_1_o14), .o15(counter_1_o15), .o16(counter_1_o16), .o17(counter_1_o17), .o18(counter_1_o18),
    .o19(counter_1_o19), .o20(counter_1_o20), .o21(counter_1_o21), .o22(counter_1_o22), .o23(counter_1_o23),
    .o24(counter_1_o24), .o25(counter_1_o25), .o26(counter_1_o26), .o27(counter_1_o27), .o28(counter_1_o28),
    .o29(counter_1_o29), .o30(counter_1_o30), .o31(counter_1_o31), .o32(counter_1_o32));
  AUTOCAPTURE autocapture_1 (
    .D(RAMDATA), .A({RA3, RA2, RA1, RA0}), .WR(RAM_WE), ._10(autocapture_1__10), ._11(autocapture_1__11),
    ._12(autocapture_1__12), ._13(autocapture_1__13), ._14(autocapture_1__14), ._15(autocapture_1__15),
    ._16(autocapture_1__16), ._17(autocapture_1__17));
  Register #(.Bits(12)) register_1 (.D(RAMDATA), .C(and_1_out), .en(1'b1), .Q(register_1_q));
  // Probe on counter_1_o1
  // Probe on counter_1_o2
  // Probe on counter_1_o3
  // Probe on counter_1_o4
  // Probe on counter_1_o5
  // Probe on counter_1_o6
  // Probe on counter_1_o7
  // Probe on counter_1_o8
  // Probe on counter_1_o9
  // Probe on counter_1_o10
  // Probe on counter_1_o11
  // Probe on counter_1_o12
  // Probe on counter_1_o13
  // Probe on counter_1_o14
  // Probe on counter_1_o15
  // Probe on counter_1_o16
  // Probe on counter_1_o17
  // Probe on counter_1_o18
  // Probe on counter_1_o19
  // Probe on counter_1_o20
  // Probe on counter_1_o21
  // Probe on counter_1_o22
  // Probe on counter_1_o23
  // Probe on counter_1_o24
  // Probe on counter_1_o25
  // Probe on counter_1_o26
  // Probe on counter_1_o27
  // Probe on counter_1_o28
  // Probe on counter_1_o29
  // Probe on counter_1_o30
  // Probe on counter_1_o31
  // Probe on counter_1_o32
  // Probe on autocapture_1__10
  // Probe on autocapture_1__11
  // Probe on autocapture_1__12
  // Probe on autocapture_1__13
  // Probe on autocapture_1__14
  // Probe on autocapture_1__15
  // Probe on autocapture_1__16
  // Probe on autocapture_1__17
  // Probe on register_1_q
  Seven_Seg_Hex seven_seg_hex_1 (.d({1'b0, BUS_PC[11:9]}), .dp(1'b0));
  Seven_Seg_Hex seven_seg_hex_2 (.d({1'b0, BUS_IR[11:9]}), .dp(1'b0));
  Seven_Seg_Hex seven_seg_hex_3 (.d({1'b0, AC[11:9]}), .dp(1'b0));
  Seven_Seg_Hex seven_seg_hex_4 (.d({1'b0, IND3}), .dp(1'b0));
  Seven_Seg_Hex seven_seg_hex_5 (.d({1'b0, RA3}), .dp(1'b0));
  Seven_Seg_Hex seven_seg_hex_6 (.d({1'b0, RAMDATA[11:9]}), .dp(1'b0));
  Seven_Seg_Hex seven_seg_hex_7 (.d({1'b0, PCIN[11:9]}), .dp(1'b0));
  Seven_Seg_Hex seven_seg_hex_8 (.d({1'b0, DA3}), .dp(1'b0));
  or or_1 (or_1_out, INST_TPC, INST_TLS);
  Seven_Seg_Hex seven_seg_hex_9 (.d({1'b0, BUS_PC[8:6]}), .dp(1'b0));
  Seven_Seg_Hex seven_seg_hex_10 (.d({1'b0, BUS_IR[8:6]}), .dp(1'b0));
  Seven_Seg_Hex seven_seg_hex_11 (.d({1'b0, AC[8:6]}), .dp(1'b0));
  Seven_Seg_Hex seven_seg_hex_12 (.d({1'b0, IND2}), .dp(1'b0));
  Seven_Seg_Hex seven_seg_hex_13 (.d({1'b0, RA2}), .dp(1'b0));
  Seven_Seg_Hex seven_seg_hex_14 (.d({1'b0, RAMDATA[8:6]}), .dp(1'b0));
  Seven_Seg_Hex seven_seg_hex_15 (.d({1'b0, PCIN[8:6]}), .dp(1'b0));
  Seven_Seg_Hex seven_seg_hex_16 (.d({1'b0, DA2}), .dp(1'b0));
  Seven_Seg_Hex seven_seg_hex_17 (.d({1'b0, BUS_PC[5:3]}), .dp(1'b0));
  Seven_Seg_Hex seven_seg_hex_18 (.d({1'b0, BUS_IR[5:3]}), .dp(1'b0));
  Seven_Seg_Hex seven_seg_hex_19 (.d({1'b0, AC[5:3]}), .dp(1'b0));
  Seven_Seg_Hex seven_seg_hex_20 (.d({1'b0, IND1}), .dp(1'b0));
  Seven_Seg_Hex seven_seg_hex_21 (.d({1'b0, RA1}), .dp(1'b0));
  Seven_Seg_Hex seven_seg_hex_22 (.d({1'b0, RAMDATA[5:3]}), .dp(1'b0));
  Seven_Seg_Hex seven_seg_hex_23 (.d({1'b0, PCIN[5:3]}), .dp(1'b0));
  Seven_Seg_Hex seven_seg_hex_24 (.d({1'b0, DA1}), .dp(1'b0));
  Counter #(.Bits(32)) INSTRUCTION_COUNT (.en(1'b1), .C(PH01), .clr(1'b0), .out(INSTRUCTION_COUNT_out));  // open: ovf
  Monoflop #(.timerDelay(300)) monoflop_1 (.C(or_1_out), .R(1'b0), .Q(monoflop_1_q), .nQ(monoflop_1_nq));
  Seven_Seg_Hex seven_seg_hex_25 (.d({1'b0, BUS_PC[2:0]}), .dp(1'b0));
  Seven_Seg_Hex seven_seg_hex_26 (.d({1'b0, BUS_IR[2:0]}), .dp(1'b0));
  Seven_Seg_Hex seven_seg_hex_27 (.d({1'b0, AC[2:0]}), .dp(1'b0));
  Seven_Seg_Hex seven_seg_hex_28 (.d({1'b0, IND0}), .dp(1'b0));
  Seven_Seg_Hex seven_seg_hex_29 (.d({1'b0, RA0}), .dp(1'b0));
  Seven_Seg_Hex seven_seg_hex_30 (.d({1'b0, RAMDATA[2:0]}), .dp(1'b0));
  Seven_Seg_Hex seven_seg_hex_31 (.d({1'b0, PCIN[2:0]}), .dp(1'b0));
  Seven_Seg_Hex seven_seg_hex_32 (.d({1'b0, DA0}), .dp(1'b0));
  // Probe on INSTRUCTION_COUNT_out
  Counter #(.Bits(32)) COUNT (.en(1'b1), .C(or_1_out), .clr(1'b0), .out(COUNT_out));  // open: ovf
  Terminal #(.termWidth(20), .termHeight(10)) PRN (.D(AC[7:0]), .C(or_1_out), .en(1'b1));
  LED led_1 (.in(LINK));
  // Probe on COUNT_out
  LED led_2 (.in(INST_KCF));
  LED led_3 (.in(OPR_CLA1));
  LED led_4 (.in(AND));
  Monoflop monoflop_2 (.C(monoflop_1_q), .R(1'b0), .Q(monoflop_2_q));  // open: nQ
  Monoflop monoflop_3 (.C(monoflop_1_nq), .R(1'b0), .Q(monoflop_3_q));  // open: nQ
  assign PCIN = PC_eq_200 ? 12'h80 : 12'bz;  // Driver driver_1
  assign PC_CK = PC_eq_200 ? PC_eq_200 : 1'bz;  // Driver driver_2
  assign PC_LD = PC_eq_200 ? PC_eq_200 : 1'bz;  // Driver driver_3
  LED led_5 (.in(INST_KSF));
  LED led_6 (.in(OPR_CLL));
  LED led_7 (.in(TAD));
  or or_2 (or_2_out, INST_TFL, monoflop_2_q);
  or or_3 (or_3_out, monoflop_3_q, INST_TCF);
  LED led_8 (.in(IR2PC));
  LED led_9 (.in(INST_KCC));
  LED led_10 (.in(INST_KRS));
  LED led_11 (.in(OPR_CMA));
  LED led_12 (.in(OPR_CML));
  LED led_13 (.in(ISZ));
  LED led_14 (.in(DCA));
  RS_FF_AS rs_ff_as_1 (.S(or_2_out), .R(or_3_out), .nQ(FLAG_PRNRDY));  // open: Q
  // OC12 oc12_1: pin names not known; wires that end beside it: BUS_IR[6:0], BUS_PC[11:7], BUS_IR[7], IR2PC, PCIN[6:0], PCIN[11:7], PCIN
  LED led_15 (.in(INST_KIE));
  LED led_16 (.in(OPR_IAC));
  LED led_17 (.in(JMS));
  LED led_18 (.in(INST_KRB));
  LED led_19 (.in(OPR_RIGHT));
  LED led_20 (.in(JMP));
  Button S (.out(S_out));
  Button I (.out(I_out));
  Button R (.out(R_out));
  Button H (.out(H_out));
  Button _2 (.out(PC_eq_200));
  // Probe on PCIN
  LED led_21 (.in(PC_CK));
  LED led_22 (.in(PC_LD));
  LED led_23 (.in(RAMD2PC));
  assign PCIN = RAMD2PC ? {DA3, DA2, DA1, DA0} : 12'bz;  // Driver driver_4
  LED led_24 (.in(IND2PC));
  assign PCIN = IND2PC ? {IND3, IND2, IND1, IND0} : 12'bz;  // Driver driver_5
  LED led_25 (.in(INST_TFL));
  LED led_26 (.in(OPR_LEFT));
  LED led_27 (.in(OPR_X2));
  LED led_28 (.in(IOT));
  LED led_29 (.in(OPR));
  Monoflop #(.timerDelay(2)) monoflop_4 (.C(I_out), .R(1'b0), .Q(monoflop_4_q));  // open: nQ
  Monoflop monoflop_5 (.C(R_out), .R(1'b0), .Q(monoflop_5_q));  // open: nQ
  Comparator #(.Bits(12)) comparator_2 (.a(BUS_PC), .b(12'heb), .eq(comparator_2_eq));  // open: gt, lt
  CounterPreset #(.Bits(12)) PC (
    .en(1'b1), .C(PC_CK), .dir(1'b0), .in(PCIN), .ld(PC_LD), .clr(reset_1_out), .out(BUS_PC));  // open: ovf
  Reset #(.invertOutput("false")) reset_1 (.out(reset_1_out));
  LED led_30 (.in(INST_TSF));
  LED led_31 (.in(OPR_CLA2));
  Switch #(.Closed("true")) HLT_ENABLED (.A(HALT), .B(HLT_ENABLED_b));
  LED led_32 (.in(INST_TCF));
  LED led_33 (.in(OPR_SMA));
  LED led_34 (.in(NOIND));
  LED led_35 (.in(IND));
  RS_FF_AS rs_ff_as_2 (.S(monoflop_5_q), .R(or_5_out), .Q(rs_ff_as_2_q));  // open: nQ
  PullDown pulldown_1 (.out(HLT_ENABLED_b));
  Switch BP_ENABLED (.A(comparator_2_eq), .B(BP_ENABLED_b));
  // Probe on BUS_PC
  LED led_36 (.in(INST_TPC));
  LED led_37 (.in(INST_TSK));
  LED led_38 (.in(OPR_SZA));
  LED led_39 (.in(OPR_SNL));
  LED led_40 (.in(AUTOIND));
  or or_4 (or_4_out, monoflop_4_q, monoflop_5_q, rs_ff_as_2_q);
  or or_5 (or_5_out, H_out, BP_ENABLED_b, HLT_ENABLED_b);
  // OC12 oc12_2: pin names not known; wires that end beside it: BUS_PC, BUS_IR[6:0], BUS_PC[11:7], BUS_IR[7], IR2RAMA, {RA2[0], RA1, RA0}, {RA3, RA2[2:1]}
  LED led_41 (.in(IR2RAMA));
  LED led_42 (.in(INST_TLS));
  LED led_43 (.in(OPR_TSTINV));
  LED led_44 (.in(BUS_IR[7]));
  LED led_45 (.in(or_4_out));
  LED led_46 (.in(or_5_out));
  PullDown pulldown_2 (.out(BP_ENABLED_b));
  and and_2 (and_2_out, INST_TSF, FLAG_PRNRDY, PH04);
  and and_3 (HALT, OPR_HLT, PH02);
  LED led_47 (.in(PC2RAMA));
  assign {RA3, RA2, RA1, RA0} = PC2RAMA ? BUS_PC : 12'bz;  // Driver driver_6
  LED led_48 (.in(OPR_OSR));
  D_FF d_ff_1 (.D(PH12), .C(clk), .Q(d_ff_1_q));  // open: nQ
  LED led_49 (.in(and_2_out));
  LED led_50 (.in(HALT));
  // Probe on {RA3, RA2, RA1, RA0}
  LED led_51 (.in(OPR_HLT));
  LED led_52 (.in(OPR_NA1));
  assign IR_CK = and_2_out ? and_2_out : 1'bz;  // Driver driver_7
  assign PC_CK = and_2_out ? and_2_out : 1'bz;  // Driver driver_8
  Driver driver_9 (.in(and_2_out), .en(and_2_out));  // open: out
  Driver driver_10 (.in(and_2_out), .en(and_2_out));  // open: out
  Driver driver_11 (.in(and_2_out), .en(and_2_out));  // open: out
  LED led_53 (.in(RAMA_HOLD));
  LED led_54 (.in(IND2RAMA));
  assign {RA3, RA2, RA1, RA0} = IND2RAMA ? {IND3, IND2, IND1, IND0} : 12'bz;  // Driver driver_12
  LED led_55 (.in(OPR_NOP));
  RS_FF_AS rs_ff_as_3 (.S(or_4_out), .R(d_ff_1_q), .Q(rs_ff_as_3_q));  // open: nQ
  // TRANSP_LATCH transp_latch_1: pin names not known; wires that end beside it: {RA3, RA2, RA1, RA0}, {RA3, RA2, RA1, RA0}, RAMA_HOLD, transp_latch_1_p4, RAMDATA
  and and_4 (and_4_out, rs_ff_as_3_q, clk);
  LED led_56 (.in(and_4_out));
  // Probe on transp_latch_1_p4
  EEPROM #(.AddrBits(12), .isProgramMemory("true"), .Bits(12)) eeprom_1 (
    .A(transp_latch_1_p4), .CS(1'b1), .WE(RAM_WE), .OE(RAM_OE), .D(RAMDATA));
  LED led_57 (.in(RAM_WE));
  LED led_58 (.in(RAM_OE));
  or or_6 (or_6_out, S_out, and_4_out);
  Counter #(.Bits(4)) counter_2 (.en(1'b1), .C(or_6_out), .clr(PH12), .out(counter_2_out));  // open: ovf
  LED led_59 (.in(or_6_out));
  // Probe on RAMDATA
  Seven_Seg_Hex seven_seg_hex_33 (.d(counter_2_out), .dp(1'b0));
  Decoder #(.Selector_Bits(4)) decoder_1 (
    .sel(counter_2_out), .out_0(PH00), .out_1(PH01), .out_2(PH02), .out_3(PH03), .out_4(PH04), .out_5(PH05),
    .out_6(PH06), .out_7(PH07), .out_8(PH08), .out_9(PH09), .out_10(PH10), .out_11(PH11), .out_12(PH12),
    .out_13(PH13), .out_14(PH14), .out_15(PH15));
  assign {DA3, DA2, DA1, DA0} = RAM_OE ? RAMDATA : 12'bz;  // Driver driver_13
  assign RAMDATA = RAM_WE ? {DA3, DA2, DA1, DA0} : 12'bz;  // Driver driver_14
  LED led_60 (.in(PC2RAMD));
  // Probe on {DA3, DA2, DA1, DA0}
  assign {DA3, DA2, DA1, DA0} = PC2RAMD ? BUS_PC : 12'bz;  // Driver driver_15
  D_FF #(.Bits(12)) IR (.D({DA3, DA2, DA1, DA0}), .C(IR_CK), .Q(BUS_IR));  // open: nQ
  LED led_61 (.in(IR_CK));
  LED led_62 (.in(INC2RAMD));
  assign {DA3, DA2, DA1, DA0} = INC2RAMD ? INC_s : 12'bz;  // Driver driver_16
  LED led_63 (.in(AC2RAMD));
  assign {DA3, DA2, DA1, DA0} = AC2RAMD ? AC : 12'bz;  // Driver driver_17
  // Probe on BUS_IR
  and and_5 (CNT_AND, AND, NOIND, PH02);
  and and_6 (and_6_out, AND, NOIND, PH03);
  D_FF #(.Bits(12)) u_IND (.D({DA3, DA2, DA1, DA0}), .C(IND_CK), .Q({IND3, IND2, IND1, IND0}));  // open: nQ
  LED led_64 (.in(IND_CK));
  LED led_65 (.in(CNT_AND));
  LED led_66 (.in(and_6_out));
  assign IR2RAMA = CNT_AND ? CNT_AND : 1'bz;  // Driver driver_18
  assign RAMD2AC_AND = CNT_AND ? CNT_AND : 1'bz;  // Driver driver_19
  assign RAM_OE = CNT_AND ? CNT_AND : 1'bz;  // Driver driver_20
  assign driver_21_out = CNT_AND ? CNT_AND : 1'bz;  // Driver driver_21
  assign driver_22_out = CNT_AND ? CNT_AND : 1'bz;  // Driver driver_22
  assign IR2RAMA = and_6_out ? and_6_out : 1'bz;  // Driver driver_23
  assign RAMD2AC_AND = and_6_out ? and_6_out : 1'bz;  // Driver driver_24
  assign RAM_OE = and_6_out ? and_6_out : 1'bz;  // Driver driver_25
  assign AC_CK = and_6_out ? and_6_out : 1'bz;  // Driver driver_26
  Driver driver_27 (.in(and_6_out), .en(and_6_out));  // open: out
  // Probe on {IND3, IND2, IND1, IND0}
  Add #(.Bits(12)) INC (.a({12{1'b0}}), .b({IND3, IND2, IND1, IND0}), .c_i(1'b1), .s(INC_s), .c_o(INCZERO));
  and and_7 (CNT_AND_I, AND, IND, PH02);
  LED led_67 (.in(CNT_AND_I));
  and and_8 (and_8_out, AND, IND, PH03);
  LED led_68 (.in(and_8_out));
  and and_9 (and_9_out, AND, IND, PH04);
  LED led_69 (.in(and_9_out));
  and and_10 (and_10_out, AND, IND, PH05);
  LED led_70 (.in(and_10_out));
  assign IR2RAMA = CNT_AND_I ? CNT_AND_I : 1'bz;  // Driver driver_28
  assign RAMD2IND = CNT_AND_I ? CNT_AND_I : 1'bz;  // Driver driver_29
  assign RAM_OE = CNT_AND_I ? CNT_AND_I : 1'bz;  // Driver driver_30
  Driver driver_31 (.in(CNT_AND_I), .en(CNT_AND_I));  // open: out
  Driver driver_32 (.in(CNT_AND_I), .en(CNT_AND_I));  // open: out
  assign IR2RAMA = and_8_out ? and_8_out : 1'bz;  // Driver driver_33
  assign RAMD2IND = and_8_out ? and_8_out : 1'bz;  // Driver driver_34
  assign RAM_OE = and_8_out ? and_8_out : 1'bz;  // Driver driver_35
  assign IND_CK = and_8_out ? and_8_out : 1'bz;  // Driver driver_36
  Driver driver_37 (.in(and_8_out), .en(and_8_out));  // open: out
  assign IND2RAMA = and_9_out ? and_9_out : 1'bz;  // Driver driver_38
  assign RAMD2AC_AND = and_9_out ? and_9_out : 1'bz;  // Driver driver_39
  assign RAM_OE = and_9_out ? and_9_out : 1'bz;  // Driver driver_40
  Driver driver_41 (.in(and_9_out), .en(and_9_out));  // open: out
  Driver driver_42 (.in(and_9_out), .en(and_9_out));  // open: out
  assign IND2RAMA = and_10_out ? and_10_out : 1'bz;  // Driver driver_43
  assign RAMD2AC_AND = and_10_out ? and_10_out : 1'bz;  // Driver driver_44
  assign RAM_OE = and_10_out ? and_10_out : 1'bz;  // Driver driver_45
  assign AC_CK = and_10_out ? and_10_out : 1'bz;  // Driver driver_46
  Driver driver_47 (.in(and_10_out), .en(and_10_out));  // open: out
  and and_11 (CNT_AND_IA, AND, AUTOIND, PH02);
  and and_12 (and_12_out, AND, AUTOIND, PH03);
  and and_13 (and_13_out, AND, AUTOIND, PH04);
  and and_14 (and_14_out, AND, AUTOIND, PH05);
  and and_15 (and_15_out, AND, AUTOIND, PH06);
  and and_16 (and_16_out, AND, AUTOIND, PH07);
  and and_17 (and_17_out, AND, AUTOIND, PH08);
  Add #(.Bits(12)) add_1 (.a(AC), .b({DA3, DA2, DA1, DA0}), .c_i(1'b0), .s(add_1_s), .c_o(add_1_c_o));
  assign and_18_out = AC & {DA3, DA2, DA1, DA0};  // And and_18, 12 bits wide
  LED led_71 (.in(CNT_AND_IA));
  LED led_72 (.in(and_12_out));
  LED led_73 (.in(and_13_out));
  LED led_74 (.in(and_14_out));
  LED led_75 (.in(and_15_out));
  LED led_76 (.in(and_16_out));
  LED led_77 (.in(and_17_out));
  assign IR2RAMA = CNT_AND_IA ? CNT_AND_IA : 1'bz;  // Driver driver_48
  assign RAM_OE = CNT_AND_IA ? CNT_AND_IA : 1'bz;  // Driver driver_49
  assign driver_50_out = CNT_AND_IA ? CNT_AND_IA : 1'bz;  // Driver driver_50
  assign driver_51_out = CNT_AND_IA ? CNT_AND_IA : 1'bz;  // Driver driver_51
  assign driver_52_out = CNT_AND_IA ? CNT_AND_IA : 1'bz;  // Driver driver_52
  assign IR2RAMA = and_12_out ? and_12_out : 1'bz;  // Driver driver_53
  assign IND_CK = and_12_out ? and_12_out : 1'bz;  // Driver driver_54
  assign RAM_OE = and_12_out ? and_12_out : 1'bz;  // Driver driver_55
  assign driver_56_out = and_12_out ? and_12_out : 1'bz;  // Driver driver_56
  assign driver_57_out = and_12_out ? and_12_out : 1'bz;  // Driver driver_57
  assign INC2RAMD = and_13_out ? and_13_out : 1'bz;  // Driver driver_58
  assign RAM_WE = and_13_out ? and_13_out : 1'bz;  // Driver driver_59
  assign driver_60_out = and_13_out ? and_13_out : 1'bz;  // Driver driver_60
  assign driver_61_out = and_13_out ? and_13_out : 1'bz;  // Driver driver_61
  assign driver_62_out = and_13_out ? and_13_out : 1'bz;  // Driver driver_62
  assign IR2RAMA = and_14_out ? and_14_out : 1'bz;  // Driver driver_63
  assign RAMD2IND = and_14_out ? and_14_out : 1'bz;  // Driver driver_64
  assign RAM_OE = and_14_out ? and_14_out : 1'bz;  // Driver driver_65
  Driver driver_66 (.in(and_14_out), .en(and_14_out));  // open: out
  Driver driver_67 (.in(and_14_out), .en(and_14_out));  // open: out
  assign IR2RAMA = and_15_out ? and_15_out : 1'bz;  // Driver driver_68
  assign RAMD2IND = and_15_out ? and_15_out : 1'bz;  // Driver driver_69
  assign RAM_OE = and_15_out ? and_15_out : 1'bz;  // Driver driver_70
  assign IND_CK = and_15_out ? and_15_out : 1'bz;  // Driver driver_71
  Driver driver_72 (.in(and_15_out), .en(and_15_out));  // open: out
  assign IND2RAMA = and_16_out ? and_16_out : 1'bz;  // Driver driver_73
  assign RAMD2AC_AND = and_16_out ? and_16_out : 1'bz;  // Driver driver_74
  assign RAM_OE = and_16_out ? and_16_out : 1'bz;  // Driver driver_75
  Driver driver_76 (.in(and_16_out), .en(and_16_out));  // open: out
  Driver driver_77 (.in(and_16_out), .en(and_16_out));  // open: out
  assign IND2RAMA = and_17_out ? and_17_out : 1'bz;  // Driver driver_78
  assign RAMD2AC_AND = and_17_out ? and_17_out : 1'bz;  // Driver driver_79
  assign RAM_OE = and_17_out ? and_17_out : 1'bz;  // Driver driver_80
  assign AC_CK = and_17_out ? and_17_out : 1'bz;  // Driver driver_81
  Driver driver_82 (.in(and_17_out), .en(and_17_out));  // open: out
  // Probe on AC
  // Probe on add_1_s
  // Probe on and_18_out
  // Probe on rotater_1_p4
  and and_19 (and_19_out, add_1_c_o, RAMD2AC_ADD);
  xor xor_1 (xor_1_out, and_19_out, rotater_1_p5);
  assign driver_83_out = RAMD2AC_ADD ? add_1_s : 12'bz;  // Driver driver_83
  LED led_78 (.in(RAMD2AC_ADD));
  assign driver_83_out = RAMD2AC_AND ? and_18_out : 12'bz;  // Driver driver_84
  LED led_79 (.in(RAMD2AC_AND));
  assign driver_83_out = ROT2AC ? rotater_1_p4 : 12'bz;  // Driver driver_85
  LED led_80 (.in(ROT2AC));
  // Probe on driver_83_out
  D_FF u_LINK (.D(xor_1_out), .C(LINK_CK), .Q(LINK));  // open: nQ
  LED led_81 (.in(LINK_CK));
  and and_20 (CNT_TAD, TAD, NOIND, PH02);
  LED led_82 (.in(CNT_TAD));
  and and_21 (and_21_out, TAD, NOIND, PH03);
  LED led_83 (.in(and_21_out));
  D_FF #(.Bits(12)) u_AC (.D(driver_83_out), .C(AC_CK), .Q(AC));  // open: nQ
  LED led_84 (.in(AC_CK));
  assign IR2RAMA = CNT_TAD ? CNT_TAD : 1'bz;  // Driver driver_86
  assign RAMD2AC_ADD = CNT_TAD ? CNT_TAD : 1'bz;  // Driver driver_87
  assign RAM_OE = CNT_TAD ? CNT_TAD : 1'bz;  // Driver driver_88
  assign driver_89_out = CNT_TAD ? CNT_TAD : 1'bz;  // Driver driver_89
  assign driver_90_out = CNT_TAD ? CNT_TAD : 1'bz;  // Driver driver_90
  assign IR2RAMA = and_21_out ? and_21_out : 1'bz;  // Driver driver_91
  assign RAMD2AC_ADD = and_21_out ? and_21_out : 1'bz;  // Driver driver_92
  assign RAM_OE = and_21_out ? and_21_out : 1'bz;  // Driver driver_93
  assign AC_CK = and_21_out ? and_21_out : 1'bz;  // Driver driver_94
  assign LINK_CK = and_21_out ? and_21_out : 1'bz;  // Driver driver_95
  // Probe on AC
  or or_7 (or_7_out, OPR_CLA2, OPR_CLA1, CLAx);
  BitExtender #(.inputBits(1), .outputBits(12)) bitextender_1 (.in(or_7_out), .out(bitextender_1_out));
  LED led_85 (.in(or_7_out));
  assign and_22_out = AC & ~bitextender_1_out;  // And and_22, 12 bits wide
  and and_23 (and_23_out, LINK, ~OPR_CLL);  // And
  DipSwitch #(.dipDefault("true")) dipswitch_1 (.out(dipswitch_1_out[11]));
  DipSwitch #(.dipDefault("true")) dipswitch_2 (.out(dipswitch_1_out[10]));
  DipSwitch #(.dipDefault("true")) dipswitch_3 (.out(dipswitch_1_out[9]));
  assign or_8_out = and_24_out | and_22_out;  // Or or_8, 12 bits wide
  LED led_86 (.in(and_23_out));
  DipSwitch dipswitch_4 (.out(dipswitch_1_out[8]));
  DipSwitch dipswitch_5 (.out(dipswitch_1_out[7]));
  DipSwitch dipswitch_6 (.out(dipswitch_1_out[6]));
  BitExtender #(.inputBits(1), .outputBits(12)) bitextender_2 (.in(OPR_CMA), .out(bitextender_2_out));
  xor xor_2 (xor_2_out, and_23_out, OPR_CML);
  DipSwitch dipswitch_7 (.out(dipswitch_1_out[5]));
  DipSwitch dipswitch_8 (.out(dipswitch_1_out[4]));
  DipSwitch dipswitch_9 (.out(dipswitch_1_out[3]));
  assign and_24_out = bitextender_3_out & not_1_out;  // And and_24, 12 bits wide
  assign xor_3_out = or_8_out ^ bitextender_2_out;  // XOr xor_3, 12 bits wide
  LED led_87 (.in(xor_2_out));
  and and_25 (CNT_TAD_I, TAD, IND, PH02);
  and and_26 (and_26_out, TAD, IND, PH03);
  LED led_88 (.in(and_26_out));
  and and_27 (and_27_out, TAD, IND, PH04);
  LED led_89 (.in(and_27_out));
  and and_28 (and_28_out, TAD, IND, PH05);
  LED led_90 (.in(and_28_out));
  DipSwitch #(.dipDefault("true")) dipswitch_10 (.out(dipswitch_1_out[2]));
  DipSwitch #(.dipDefault("true")) dipswitch_11 (.out(dipswitch_1_out[1]));
  DipSwitch #(.dipDefault("true")) dipswitch_12 (.out(dipswitch_1_out[0]));
  assign not_1_out = ~dipswitch_1_out;  // Not not_1, 12 bits wide
  // Probe on not_1_out
  BitExtender #(.inputBits(1), .outputBits(12)) bitextender_3 (.in(OPR_OSR), .out(bitextender_3_out));
  assign IR2RAMA = CNT_TAD_I ? CNT_TAD_I : 1'bz;  // Driver driver_96
  LED led_91 (.in(CNT_TAD_I));
  assign RAMD2IND = CNT_TAD_I ? CNT_TAD_I : 1'bz;  // Driver driver_97
  assign RAM_OE = CNT_TAD_I ? CNT_TAD_I : 1'bz;  // Driver driver_98
  Driver driver_99 (.in(CNT_TAD_I), .en(CNT_TAD_I));  // open: out
  Driver driver_100 (.in(CNT_TAD_I), .en(CNT_TAD_I));  // open: out
  assign IR2RAMA = and_26_out ? and_26_out : 1'bz;  // Driver driver_101
  assign RAMD2IND = and_26_out ? and_26_out : 1'bz;  // Driver driver_102
  assign RAM_OE = and_26_out ? and_26_out : 1'bz;  // Driver driver_103
  assign IND_CK = and_26_out ? and_26_out : 1'bz;  // Driver driver_104
  Driver driver_105 (.in(and_26_out), .en(and_26_out));  // open: out
  assign IND2RAMA = and_27_out ? and_27_out : 1'bz;  // Driver driver_106
  assign RAMD2AC_ADD = and_27_out ? and_27_out : 1'bz;  // Driver driver_107
  assign RAM_OE = and_27_out ? and_27_out : 1'bz;  // Driver driver_108
  Driver driver_109 (.in(and_27_out), .en(and_27_out));  // open: out
  Driver driver_110 (.in(and_27_out), .en(and_27_out));  // open: out
  assign IND2RAMA = and_28_out ? and_28_out : 1'bz;  // Driver driver_111
  assign RAMD2AC_ADD = and_28_out ? and_28_out : 1'bz;  // Driver driver_112
  assign RAM_OE = and_28_out ? and_28_out : 1'bz;  // Driver driver_113
  assign AC_CK = and_28_out ? and_28_out : 1'bz;  // Driver driver_114
  assign LINK_CK = and_28_out ? and_28_out : 1'bz;  // Driver driver_115
  Add #(.Bits(12)) add_2 (.a(xor_3_out), .b({12{1'b0}}), .c_i(OPR_IAC), .s(add_2_s), .c_o(add_2_c_o));
  or or_9 (or_9_out, add_2_c_o, xor_2_out);
  LED led_92 (.in(or_9_out));
  // ROTATER rotater_1: pin names not known; wires that end beside it: {OPR_RIGHT, OPR_LEFT, OPR_X2}, add_2_s, or_9_out, rotater_1_p4, rotater_1_p5
  and and_29 (CNT_TAD_IA, TAD, AUTOIND, PH02);
  and and_30 (and_30_out, TAD, AUTOIND, PH03);
  and and_31 (and_31_out, TAD, AUTOIND, PH04);
  and and_32 (and_32_out, TAD, AUTOIND, PH05);
  and and_33 (and_33_out, TAD, AUTOIND, PH06);
  and and_34 (and_34_out, TAD, AUTOIND, PH07);
  and and_35 (and_35_out, TAD, AUTOIND, PH08);
  // Probe on rotater_1_p4
  LED led_93 (.in(CNT_TAD_IA));
  LED led_94 (.in(and_30_out));
  LED led_95 (.in(and_31_out));
  LED led_96 (.in(and_32_out));
  LED led_97 (.in(and_33_out));
  LED led_98 (.in(and_34_out));
  LED led_99 (.in(and_35_out));
  assign IR2RAMA = CNT_TAD_IA ? CNT_TAD_IA : 1'bz;  // Driver driver_116
  assign RAM_OE = CNT_TAD_IA ? CNT_TAD_IA : 1'bz;  // Driver driver_117
  Driver driver_118 (.in(CNT_TAD_IA), .en(CNT_TAD_IA));  // open: out
  Driver driver_119 (.in(CNT_TAD_IA), .en(CNT_TAD_IA));  // open: out
  Driver driver_120 (.in(CNT_TAD_IA), .en(CNT_TAD_IA));  // open: out
  assign IR2RAMA = and_30_out ? and_30_out : 1'bz;  // Driver driver_121
  assign IND_CK = and_30_out ? and_30_out : 1'bz;  // Driver driver_122
  assign RAM_OE = and_30_out ? and_30_out : 1'bz;  // Driver driver_123
  Driver driver_124 (.in(and_30_out), .en(and_30_out));  // open: out
  Driver driver_125 (.in(and_30_out), .en(and_30_out));  // open: out
  assign INC2RAMD = and_31_out ? and_31_out : 1'bz;  // Driver driver_126
  assign RAM_WE = and_31_out ? and_31_out : 1'bz;  // Driver driver_127
  Driver driver_128 (.in(and_31_out), .en(and_31_out));  // open: out
  Driver driver_129 (.in(and_31_out), .en(and_31_out));  // open: out
  Driver driver_130 (.in(and_31_out), .en(and_31_out));  // open: out
  assign IR2RAMA = and_32_out ? and_32_out : 1'bz;  // Driver driver_131
  assign RAMD2IND = and_32_out ? and_32_out : 1'bz;  // Driver driver_132
  assign RAM_OE = and_32_out ? and_32_out : 1'bz;  // Driver driver_133
  Driver driver_134 (.in(and_32_out), .en(and_32_out));  // open: out
  Driver driver_135 (.in(and_32_out), .en(and_32_out));  // open: out
  assign IR2RAMA = and_33_out ? and_33_out : 1'bz;  // Driver driver_136
  assign RAMD2IND = and_33_out ? and_33_out : 1'bz;  // Driver driver_137
  assign RAM_OE = and_33_out ? and_33_out : 1'bz;  // Driver driver_138
  assign IND_CK = and_33_out ? and_33_out : 1'bz;  // Driver driver_139
  Driver driver_140 (.in(and_33_out), .en(and_33_out));  // open: out
  assign IND2RAMA = and_34_out ? and_34_out : 1'bz;  // Driver driver_141
  assign RAMD2AC_ADD = and_34_out ? and_34_out : 1'bz;  // Driver driver_142
  assign RAM_OE = and_34_out ? and_34_out : 1'bz;  // Driver driver_143
  Driver driver_144 (.in(and_34_out), .en(and_34_out));  // open: out
  Driver driver_145 (.in(and_34_out), .en(and_34_out));  // open: out
  assign IND2RAMA = and_35_out ? and_35_out : 1'bz;  // Driver driver_146
  assign RAMD2AC_ADD = and_35_out ? and_35_out : 1'bz;  // Driver driver_147
  assign RAM_OE = and_35_out ? and_35_out : 1'bz;  // Driver driver_148
  assign AC_CK = and_35_out ? and_35_out : 1'bz;  // Driver driver_149
  assign LINK_CK = and_35_out ? and_35_out : 1'bz;  // Driver driver_150
  and and_36 (CNT_ISZ, ISZ, NOIND, PH02);
  and and_37 (and_37_out, ISZ, NOIND, PH03);
  and and_38 (and_38_out, ISZ, NOIND, PH04);
  and and_39 (and_39_out, ISZ, NOIND, PH05);
  and and_40 (and_40_out, ISZ, NOIND, INCZERO, PH06);
  LED led_100 (.in(CNT_ISZ));
  LED led_101 (.in(and_37_out));
  LED led_102 (.in(and_38_out));
  LED led_103 (.in(and_39_out));
  LED led_104 (.in(and_40_out));
  nor nor_1 (nor_1_out, AC[0], AC[1], AC[2], AC[3], AC[4], AC[5], AC[6], AC[7], AC[8], AC[9], AC[10], AC[11]);
  LED led_105 (.in(nor_1_out));
  assign IR2RAMA = CNT_ISZ ? CNT_ISZ : 1'bz;  // Driver driver_151
  assign RAM_OE = CNT_ISZ ? CNT_ISZ : 1'bz;  // Driver driver_152
  Driver driver_153 (.in(CNT_ISZ), .en(CNT_ISZ));  // open: out
  Driver driver_154 (.in(CNT_ISZ), .en(CNT_ISZ));  // open: out
  Driver driver_155 (.in(CNT_ISZ), .en(CNT_ISZ));  // open: out
  assign IR2RAMA = and_37_out ? and_37_out : 1'bz;  // Driver driver_156
  assign RAM_OE = and_37_out ? and_37_out : 1'bz;  // Driver driver_157
  assign IND_CK = and_37_out ? and_37_out : 1'bz;  // Driver driver_158
  Driver driver_159 (.in(and_37_out), .en(and_37_out));  // open: out
  Driver driver_160 (.in(and_37_out), .en(and_37_out));  // open: out
  assign IR2RAMA = and_38_out ? and_38_out : 1'bz;  // Driver driver_161
  assign INC2RAMD = and_38_out ? and_38_out : 1'bz;  // Driver driver_162
  Driver driver_163 (.in(and_38_out), .en(and_38_out));  // open: out
  Driver driver_164 (.in(and_38_out), .en(and_38_out));  // open: out
  Driver driver_165 (.in(and_38_out), .en(and_38_out));  // open: out
  assign IR2RAMA = and_39_out ? and_39_out : 1'bz;  // Driver driver_166
  assign INC2RAMD = and_39_out ? and_39_out : 1'bz;  // Driver driver_167
  assign RAM_WE = and_39_out ? and_39_out : 1'bz;  // Driver driver_168
  Driver driver_169 (.in(and_39_out), .en(and_39_out));  // open: out
  Driver driver_170 (.in(and_39_out), .en(and_39_out));  // open: out
  assign PC_CK = and_40_out ? and_40_out : 1'bz;  // Driver driver_171
  Driver driver_172 (.in(and_40_out), .en(and_40_out));  // open: out
  Driver driver_173 (.in(and_40_out), .en(and_40_out));  // open: out
  Driver driver_174 (.in(and_40_out), .en(and_40_out));  // open: out
  Driver driver_175 (.in(and_40_out), .en(and_40_out));  // open: out
  and and_41 (and_41_out, nor_1_out, OPR_SZA);
  and and_42 (and_42_out, AC[11], OPR_SMA);
  and and_43 (and_43_out, OPR_SNL, LINK);
  LED led_106 (.in(and_41_out));
  LED led_107 (.in(and_42_out));
  LED led_108 (.in(and_43_out));
  or or_10 (or_10_out, and_41_out, and_42_out, and_43_out);
  and and_44 (CNT_ISZ_I, ISZ, IND, PH02);
  and and_45 (and_45_out, ISZ, IND, PH03);
  and and_46 (and_46_out, ISZ, IND, PH04);
  and and_47 (and_47_out, ISZ, IND, PH05);
  and and_48 (and_48_out, ISZ, IND, PH06);
  and and_49 (and_49_out, ISZ, IND, PH07);
  and and_50 (and_50_out, ISZ, IND, INCZERO, PH08);
  LED led_109 (.in(or_10_out));
  LED led_110 (.in(CNT_ISZ_I));
  LED led_111 (.in(and_45_out));
  LED led_112 (.in(and_46_out));
  LED led_113 (.in(and_47_out));
  LED led_114 (.in(and_48_out));
  LED led_115 (.in(and_49_out));
  LED led_116 (.in(and_50_out));
  xor xor_4 (SKIP, or_10_out, OPR_TSTINV);
  LED led_117 (.in(SKIP));
  assign IR2RAMA = CNT_ISZ_I ? CNT_ISZ_I : 1'bz;  // Driver driver_176
  assign RAMD2IND = CNT_ISZ_I ? CNT_ISZ_I : 1'bz;  // Driver driver_177
  assign RAM_OE = CNT_ISZ_I ? CNT_ISZ_I : 1'bz;  // Driver driver_178
  Driver driver_179 (.in(CNT_ISZ_I), .en(CNT_ISZ_I));  // open: out
  Driver driver_180 (.in(CNT_ISZ_I), .en(CNT_ISZ_I));  // open: out
  assign IR2RAMA = and_45_out ? and_45_out : 1'bz;  // Driver driver_181
  assign RAMD2IND = and_45_out ? and_45_out : 1'bz;  // Driver driver_182
  assign RAM_OE = and_45_out ? and_45_out : 1'bz;  // Driver driver_183
  assign IND_CK = and_45_out ? and_45_out : 1'bz;  // Driver driver_184
  Driver driver_185 (.in(and_45_out), .en(and_45_out));  // open: out
  Driver driver_186 (.in(and_46_out), .en(and_46_out));  // open: out
  Driver driver_187 (.in(and_46_out), .en(and_46_out));  // open: out
  Driver driver_188 (.in(and_46_out), .en(and_46_out));  // open: out
  Driver driver_189 (.in(and_46_out), .en(and_46_out));  // open: out
  Driver driver_190 (.in(and_46_out), .en(and_46_out));  // open: out
  Driver driver_191 (.in(and_47_out), .en(and_47_out));  // open: out
  Driver driver_192 (.in(and_47_out), .en(and_47_out));  // open: out
  Driver driver_193 (.in(and_47_out), .en(and_47_out));  // open: out
  Driver driver_194 (.in(and_47_out), .en(and_47_out));  // open: out
  Driver driver_195 (.in(and_47_out), .en(and_47_out));  // open: out
  Driver driver_196 (.in(and_48_out), .en(and_48_out));  // open: out
  Driver driver_197 (.in(and_48_out), .en(and_48_out));  // open: out
  Driver driver_198 (.in(and_48_out), .en(and_48_out));  // open: out
  Driver driver_199 (.in(and_48_out), .en(and_48_out));  // open: out
  Driver driver_200 (.in(and_48_out), .en(and_48_out));  // open: out
  Driver driver_201 (.in(and_49_out), .en(and_49_out));  // open: out
  Driver driver_202 (.in(and_49_out), .en(and_49_out));  // open: out
  Driver driver_203 (.in(and_49_out), .en(and_49_out));  // open: out
  Driver driver_204 (.in(and_49_out), .en(and_49_out));  // open: out
  Driver driver_205 (.in(and_49_out), .en(and_49_out));  // open: out
  Driver driver_206 (.in(and_50_out), .en(and_50_out));  // open: out
  Driver driver_207 (.in(and_50_out), .en(and_50_out));  // open: out
  Driver driver_208 (.in(and_50_out), .en(and_50_out));  // open: out
  Driver driver_209 (.in(and_50_out), .en(and_50_out));  // open: out
  Driver driver_210 (.in(and_50_out), .en(and_50_out));  // open: out
  and and_51 (CNT_ISZ_IA, ISZ, AUTOIND, PH02);
  and and_52 (and_52_out, ISZ, AUTOIND, PH03);
  and and_53 (and_53_out, ISZ, AUTOIND, PH04);
  and and_54 (and_54_out, ISZ, AUTOIND, PH05);
  and and_55 (and_55_out, ISZ, AUTOIND, PH06);
  assign IR2RAMA = CNT_ISZ_IA ? CNT_ISZ_IA : 1'bz;  // Driver driver_211
  LED led_118 (.in(CNT_ISZ_IA));
  assign RAM_OE = CNT_ISZ_IA ? CNT_ISZ_IA : 1'bz;  // Driver driver_212
  Driver driver_213 (.in(CNT_ISZ_IA), .en(CNT_ISZ_IA));  // open: out
  Driver driver_214 (.in(CNT_ISZ_IA), .en(CNT_ISZ_IA));  // open: out
  Driver driver_215 (.in(CNT_ISZ_IA), .en(CNT_ISZ_IA));  // open: out
  assign IR2RAMA = and_52_out ? and_52_out : 1'bz;  // Driver driver_216
  LED led_119 (.in(and_52_out));
  assign IND_CK = and_52_out ? and_52_out : 1'bz;  // Driver driver_217
  assign RAM_OE = and_52_out ? and_52_out : 1'bz;  // Driver driver_218
  Driver driver_219 (.in(and_52_out), .en(and_52_out));  // open: out
  Driver driver_220 (.in(and_52_out), .en(and_52_out));  // open: out
  assign INC2RAMD = and_53_out ? and_53_out : 1'bz;  // Driver driver_221
  LED led_120 (.in(and_53_out));
  assign RAM_WE = and_53_out ? and_53_out : 1'bz;  // Driver driver_222
  Driver driver_223 (.in(and_53_out), .en(and_53_out));  // open: out
  Driver driver_224 (.in(and_53_out), .en(and_53_out));  // open: out
  Driver driver_225 (.in(and_53_out), .en(and_53_out));  // open: out
  assign IR2RAMA = and_54_out ? and_54_out : 1'bz;  // Driver driver_226
  LED led_121 (.in(and_54_out));
  assign RAMD2IND = and_54_out ? and_54_out : 1'bz;  // Driver driver_227
  assign RAM_OE = and_54_out ? and_54_out : 1'bz;  // Driver driver_228
  Driver driver_229 (.in(and_54_out), .en(and_54_out));  // open: out
  Driver driver_230 (.in(and_54_out), .en(and_54_out));  // open: out
  assign IR2RAMA = and_55_out ? and_55_out : 1'bz;  // Driver driver_231
  LED led_122 (.in(and_55_out));
  assign RAMD2IND = and_55_out ? and_55_out : 1'bz;  // Driver driver_232
  assign RAM_OE = and_55_out ? and_55_out : 1'bz;  // Driver driver_233
  assign IND_CK = and_55_out ? and_55_out : 1'bz;  // Driver driver_234
  Driver driver_235 (.in(and_55_out), .en(and_55_out));  // open: out
  and and_56 (CNT_DCA, DCA, NOIND, PH02);
  and and_57 (and_57_out, DCA, NOIND, PH03);
  and and_58 (and_58_out, DCA, NOIND, PH04);
  LED led_123 (.in(CNT_DCA));
  LED led_124 (.in(and_57_out));
  LED led_125 (.in(and_58_out));
  assign IR2RAMA = CNT_DCA ? CNT_DCA : 1'bz;  // Driver driver_236
  assign AC2RAMD = CNT_DCA ? CNT_DCA : 1'bz;  // Driver driver_237
  Driver driver_238 (.in(CNT_DCA), .en(CNT_DCA));  // open: out
  Driver driver_239 (.in(CNT_DCA), .en(CNT_DCA));  // open: out
  Driver driver_240 (.in(CNT_DCA), .en(CNT_DCA));  // open: out
  assign IR2RAMA = and_57_out ? and_57_out : 1'bz;  // Driver driver_241
  assign AC2RAMD = and_57_out ? and_57_out : 1'bz;  // Driver driver_242
  assign RAM_WE = and_57_out ? and_57_out : 1'bz;  // Driver driver_243
  assign CLA = and_57_out ? and_57_out : 1'bz;  // Driver driver_244
  Driver driver_245 (.in(and_57_out), .en(and_57_out));  // open: out
  assign CLAx = and_58_out ? and_58_out : 1'bz;  // Driver driver_246
  assign ROT2AC = and_58_out ? and_58_out : 1'bz;  // Driver driver_247
  assign AC_CK = and_58_out ? and_58_out : 1'bz;  // Driver driver_248
  Driver driver_249 (.in(and_58_out), .en(and_58_out));  // open: out
  Driver driver_250 (.in(and_58_out), .en(and_58_out));  // open: out
  and and_59 (CNT_DCA_I, DCA, IND, PH02);
  and and_60 (and_60_out, DCA, IND, PH03);
  LED led_126 (.in(CNT_DCA_I));
  LED led_127 (.in(and_60_out));
  assign IR2RAMA = CNT_DCA_I ? CNT_DCA_I : 1'bz;  // Driver driver_251
  assign RAMD2IND = CNT_DCA_I ? CNT_DCA_I : 1'bz;  // Driver driver_252
  assign RAM_OE = CNT_DCA_I ? CNT_DCA_I : 1'bz;  // Driver driver_253
  assign driver_254_out = CNT_DCA_I ? CNT_DCA_I : 1'bz;  // Driver driver_254
  assign driver_255_out = CNT_DCA_I ? CNT_DCA_I : 1'bz;  // Driver driver_255
  assign IR2RAMA = and_60_out ? and_60_out : 1'bz;  // Driver driver_256
  assign RAMD2IND = and_60_out ? and_60_out : 1'bz;  // Driver driver_257
  assign RAM_OE = and_60_out ? and_60_out : 1'bz;  // Driver driver_258
  assign IND_CK = and_60_out ? and_60_out : 1'bz;  // Driver driver_259
  assign driver_260_out = and_60_out ? and_60_out : 1'bz;  // Driver driver_260
  and and_61 (CNT_DCA_IA, DCA, AUTOIND, PH02);
  and and_62 (and_62_out, DCA, AUTOIND, PH03);
  and and_63 (and_63_out, DCA, AUTOIND, PH04);
  and and_64 (and_64_out, DCA, AUTOIND, PH05);
  and and_65 (and_65_out, DCA, AUTOIND, PH06);
  LED led_128 (.in(CNT_DCA_IA));
  LED led_129 (.in(and_62_out));
  LED led_130 (.in(and_63_out));
  LED led_131 (.in(and_64_out));
  LED led_132 (.in(and_65_out));
  assign IR2RAMA = CNT_DCA_IA ? CNT_DCA_IA : 1'bz;  // Driver driver_261
  assign RAM_OE = CNT_DCA_IA ? CNT_DCA_IA : 1'bz;  // Driver driver_262
  assign driver_263_out = CNT_DCA_IA ? CNT_DCA_IA : 1'bz;  // Driver driver_263
  assign driver_264_out = CNT_DCA_IA ? CNT_DCA_IA : 1'bz;  // Driver driver_264
  assign driver_265_out = CNT_DCA_IA ? CNT_DCA_IA : 1'bz;  // Driver driver_265
  assign IR2RAMA = and_62_out ? and_62_out : 1'bz;  // Driver driver_266
  assign IND_CK = and_62_out ? and_62_out : 1'bz;  // Driver driver_267
  assign RAM_OE = and_62_out ? and_62_out : 1'bz;  // Driver driver_268
  assign driver_269_out = and_62_out ? and_62_out : 1'bz;  // Driver driver_269
  assign driver_270_out = and_62_out ? and_62_out : 1'bz;  // Driver driver_270
  assign INC2RAMD = and_63_out ? and_63_out : 1'bz;  // Driver driver_271
  assign RAM_WE = and_63_out ? and_63_out : 1'bz;  // Driver driver_272
  assign driver_273_out = and_63_out ? and_63_out : 1'bz;  // Driver driver_273
  assign driver_274_out = and_63_out ? and_63_out : 1'bz;  // Driver driver_274
  assign driver_275_out = and_63_out ? and_63_out : 1'bz;  // Driver driver_275
  assign IR2RAMA = and_64_out ? and_64_out : 1'bz;  // Driver driver_276
  assign RAMD2IND = and_64_out ? and_64_out : 1'bz;  // Driver driver_277
  assign RAM_OE = and_64_out ? and_64_out : 1'bz;  // Driver driver_278
  assign driver_279_out = and_64_out ? and_64_out : 1'bz;  // Driver driver_279
  assign driver_280_out = and_64_out ? and_64_out : 1'bz;  // Driver driver_280
  assign IR2RAMA = and_65_out ? and_65_out : 1'bz;  // Driver driver_281
  assign RAMD2IND = and_65_out ? and_65_out : 1'bz;  // Driver driver_282
  assign RAM_OE = and_65_out ? and_65_out : 1'bz;  // Driver driver_283
  assign IND_CK = and_65_out ? and_65_out : 1'bz;  // Driver driver_284
  assign driver_285_out = and_65_out ? and_65_out : 1'bz;  // Driver driver_285
  and and_66 (and_66_out, JMS, NOIND, PH03);
  and and_67 (CNT_JMS, JMS, NOIND, PH02);
  LED led_133 (.in(CNT_JMS));
  LED led_134 (.in(and_66_out));
  and and_68 (and_68_out, JMS, NOIND, PH04);
  LED led_135 (.in(and_68_out));
  and and_69 (and_69_out, JMS, NOIND, PH05);
  LED led_136 (.in(and_69_out));
  and and_70 (and_70_out, JMS, NOIND, PH06);
  LED led_137 (.in(and_70_out));
  assign PC2RAMD = CNT_JMS ? CNT_JMS : 1'bz;  // Driver driver_286
  assign IR2RAMA = CNT_JMS ? CNT_JMS : 1'bz;  // Driver driver_287
  assign driver_288_out = CNT_JMS ? CNT_JMS : 1'bz;  // Driver driver_288
  assign driver_289_out = CNT_JMS ? CNT_JMS : 1'bz;  // Driver driver_289
  assign driver_290_out = CNT_JMS ? CNT_JMS : 1'bz;  // Driver driver_290
  assign PC2RAMD = and_66_out ? and_66_out : 1'bz;  // Driver driver_291
  assign IR2RAMA = and_66_out ? and_66_out : 1'bz;  // Driver driver_292
  assign RAM_WE = and_66_out ? and_66_out : 1'bz;  // Driver driver_293
  assign IR2PC = and_66_out ? and_66_out : 1'bz;  // Driver driver_294
  assign driver_295_out = and_66_out ? and_66_out : 1'bz;  // Driver driver_295
  assign IR2PC = and_68_out ? and_68_out : 1'bz;  // Driver driver_296
  assign PC_LD = and_68_out ? and_68_out : 1'bz;  // Driver driver_297
  assign PC_CK = and_68_out ? and_68_out : 1'bz;  // Driver driver_298
  assign driver_299_out = and_68_out ? and_68_out : 1'bz;  // Driver driver_299
  assign driver_300_out = and_68_out ? and_68_out : 1'bz;  // Driver driver_300
  assign driver_301_out = and_69_out ? and_69_out : 1'bz;  // Driver driver_301
  assign driver_302_out = and_69_out ? and_69_out : 1'bz;  // Driver driver_302
  assign driver_303_out = and_69_out ? and_69_out : 1'bz;  // Driver driver_303
  assign driver_304_out = and_69_out ? and_69_out : 1'bz;  // Driver driver_304
  assign driver_305_out = and_69_out ? and_69_out : 1'bz;  // Driver driver_305
  assign PC_CK = and_70_out ? and_70_out : 1'bz;  // Driver driver_306
  assign driver_307_out = and_70_out ? and_70_out : 1'bz;  // Driver driver_307
  assign driver_308_out = and_70_out ? and_70_out : 1'bz;  // Driver driver_308
  assign driver_309_out = and_70_out ? and_70_out : 1'bz;  // Driver driver_309
  Driver driver_310 (.in(and_70_out), .en(and_70_out));  // open: out
  and and_71 (CNT_JMS_I, JMS, IND, PH02);
  and and_72 (and_72_out, JMS, IND, PH03);
  and and_73 (and_73_out, JMS, IND, PH04);
  and and_74 (and_74_out, JMS, IND, PH05);
  and and_75 (and_75_out, JMS, IND, PH06);
  and and_76 (and_76_out, JMS, IND, PH07);
  and and_77 (and_77_out, JMS, IND, PH08);
  LED led_138 (.in(CNT_JMS_I));
  LED led_139 (.in(and_72_out));
  LED led_140 (.in(and_73_out));
  LED led_141 (.in(and_74_out));
  LED led_142 (.in(and_75_out));
  LED led_143 (.in(and_76_out));
  LED led_144 (.in(and_77_out));
  assign IR2RAMA = CNT_JMS_I ? CNT_JMS_I : 1'bz;  // Driver driver_311
  assign RAMD2IND = CNT_JMS_I ? CNT_JMS_I : 1'bz;  // Driver driver_312
  assign RAM_OE = CNT_JMS_I ? CNT_JMS_I : 1'bz;  // Driver driver_313
  assign driver_314_out = CNT_JMS_I ? CNT_JMS_I : 1'bz;  // Driver driver_314
  assign driver_315_out = CNT_JMS_I ? CNT_JMS_I : 1'bz;  // Driver driver_315
  assign IR2RAMA = and_72_out ? and_72_out : 1'bz;  // Driver driver_316
  assign RAMD2IND = and_72_out ? and_72_out : 1'bz;  // Driver driver_317
  assign RAM_OE = and_72_out ? and_72_out : 1'bz;  // Driver driver_318
  assign IND_CK = and_72_out ? and_72_out : 1'bz;  // Driver driver_319
  assign driver_320_out = and_72_out ? and_72_out : 1'bz;  // Driver driver_320
  assign IND2RAMA = and_73_out ? and_73_out : 1'bz;  // Driver driver_321
  assign PC2RAMD = and_73_out ? and_73_out : 1'bz;  // Driver driver_322
  Driver driver_323 (.in(and_73_out), .en(and_73_out));  // open: out
  assign driver_324_out = and_73_out ? and_73_out : 1'bz;  // Driver driver_324
  assign driver_325_out = and_73_out ? and_73_out : 1'bz;  // Driver driver_325
  assign IND2RAMA = and_74_out ? and_74_out : 1'bz;  // Driver driver_326
  assign PC2RAMD = and_74_out ? and_74_out : 1'bz;  // Driver driver_327
  assign RAM_WE = and_74_out ? and_74_out : 1'bz;  // Driver driver_328
  assign PC_LD = and_74_out ? and_74_out : 1'bz;  // Driver driver_329
  assign IND2PC = and_74_out ? and_74_out : 1'bz;  // Driver driver_330
  assign IND2PC = and_75_out ? and_75_out : 1'bz;  // Driver driver_331
  assign PC_LD = and_75_out ? and_75_out : 1'bz;  // Driver driver_332
  assign PC_CK = and_75_out ? and_75_out : 1'bz;  // Driver driver_333
  Driver driver_334 (.in(and_75_out), .en(and_75_out));  // open: out
  assign driver_335_out = and_75_out ? and_75_out : 1'bz;  // Driver driver_335
  Driver driver_336 (.in(and_76_out), .en(and_76_out));  // open: out
  Driver driver_337 (.in(and_76_out), .en(and_76_out));  // open: out
  assign driver_338_out = and_76_out ? and_76_out : 1'bz;  // Driver driver_338
  assign driver_339_out = and_76_out ? and_76_out : 1'bz;  // Driver driver_339
  assign driver_340_out = and_76_out ? and_76_out : 1'bz;  // Driver driver_340
  assign PC_CK = and_77_out ? and_77_out : 1'bz;  // Driver driver_341
  assign driver_342_out = and_77_out ? and_77_out : 1'bz;  // Driver driver_342
  assign driver_343_out = and_77_out ? and_77_out : 1'bz;  // Driver driver_343
  assign driver_344_out = and_77_out ? and_77_out : 1'bz;  // Driver driver_344
  Driver driver_345 (.in(and_77_out), .en(and_77_out));  // open: out
  and and_78 (CNT_JMS_IA, JMS, AUTOIND, PH02);
  and and_79 (and_79_out, JMS, AUTOIND, PH03);
  and and_80 (and_80_out, JMS, AUTOIND, PH04);
  and and_81 (and_81_out, JMS, AUTOIND, PH05);
  and and_82 (and_82_out, JMS, AUTOIND, PH06);
  and and_83 (and_83_out, JMS, AUTOIND, PH07);
  and and_84 (and_84_out, JMS, AUTOIND, PH08);
  and and_85 (and_85_out, JMS, AUTOIND, PH09);
  and and_86 (and_86_out, JMS, AUTOIND, PH10);
  and and_87 (and_87_out, JMS, AUTOIND, PH11);
  assign IR2RAMA = CNT_JMS_IA ? CNT_JMS_IA : 1'bz;  // Driver driver_346
  LED led_145 (.in(CNT_JMS_IA));
  assign RAM_OE = CNT_JMS_IA ? CNT_JMS_IA : 1'bz;  // Driver driver_347
  assign driver_348_out = CNT_JMS_IA ? CNT_JMS_IA : 1'bz;  // Driver driver_348
  assign driver_349_out = CNT_JMS_IA ? CNT_JMS_IA : 1'bz;  // Driver driver_349
  assign driver_350_out = CNT_JMS_IA ? CNT_JMS_IA : 1'bz;  // Driver driver_350
  assign IR2RAMA = and_79_out ? and_79_out : 1'bz;  // Driver driver_351
  LED led_146 (.in(and_79_out));
  assign IND_CK = and_79_out ? and_79_out : 1'bz;  // Driver driver_352
  assign RAM_OE = and_79_out ? and_79_out : 1'bz;  // Driver driver_353
  assign driver_354_out = and_79_out ? and_79_out : 1'bz;  // Driver driver_354
  assign driver_355_out = and_79_out ? and_79_out : 1'bz;  // Driver driver_355
  assign INC2RAMD = and_80_out ? and_80_out : 1'bz;  // Driver driver_356
  LED led_147 (.in(and_80_out));
  assign RAM_WE = and_80_out ? and_80_out : 1'bz;  // Driver driver_357
  assign driver_358_out = and_80_out ? and_80_out : 1'bz;  // Driver driver_358
  assign driver_359_out = and_80_out ? and_80_out : 1'bz;  // Driver driver_359
  assign driver_360_out = and_80_out ? and_80_out : 1'bz;  // Driver driver_360
  assign IR2RAMA = and_81_out ? and_81_out : 1'bz;  // Driver driver_361
  LED led_148 (.in(and_81_out));
  assign RAMD2IND = and_81_out ? and_81_out : 1'bz;  // Driver driver_362
  assign RAM_OE = and_81_out ? and_81_out : 1'bz;  // Driver driver_363
  assign driver_364_out = and_81_out ? and_81_out : 1'bz;  // Driver driver_364
  assign driver_365_out = and_81_out ? and_81_out : 1'bz;  // Driver driver_365
  assign IR2RAMA = and_82_out ? and_82_out : 1'bz;  // Driver driver_366
  LED led_149 (.in(and_82_out));
  assign RAMD2IND = and_82_out ? and_82_out : 1'bz;  // Driver driver_367
  assign RAM_OE = and_82_out ? and_82_out : 1'bz;  // Driver driver_368
  assign IND_CK = and_82_out ? and_82_out : 1'bz;  // Driver driver_369
  assign driver_370_out = and_82_out ? and_82_out : 1'bz;  // Driver driver_370
  assign IND2RAMA = and_83_out ? and_83_out : 1'bz;  // Driver driver_371
  LED led_150 (.in(and_83_out));
  assign PC2RAMD = and_83_out ? and_83_out : 1'bz;  // Driver driver_372
  Driver driver_373 (.in(and_83_out), .en(and_83_out));  // open: out
  assign driver_374_out = and_83_out ? and_83_out : 1'bz;  // Driver driver_374
  assign driver_375_out = and_83_out ? and_83_out : 1'bz;  // Driver driver_375
  assign IND2RAMA = and_84_out ? and_84_out : 1'bz;  // Driver driver_376
  LED led_151 (.in(and_84_out));
  assign PC2RAMD = and_84_out ? and_84_out : 1'bz;  // Driver driver_377
  assign RAM_WE = and_84_out ? and_84_out : 1'bz;  // Driver driver_378
  assign PC_LD = and_84_out ? and_84_out : 1'bz;  // Driver driver_379
  assign IND2PC = and_84_out ? and_84_out : 1'bz;  // Driver driver_380
  assign IND2PC = and_85_out ? and_85_out : 1'bz;  // Driver driver_381
  LED led_152 (.in(and_85_out));
  assign PC_LD = and_85_out ? and_85_out : 1'bz;  // Driver driver_382
  assign PC_CK = and_85_out ? and_85_out : 1'bz;  // Driver driver_383
  Driver driver_384 (.in(and_85_out), .en(and_85_out));  // open: out
  assign driver_385_out = and_85_out ? and_85_out : 1'bz;  // Driver driver_385
  Driver driver_386 (.in(and_86_out), .en(and_86_out));  // open: out
  LED led_153 (.in(and_86_out));
  Driver driver_387 (.in(and_86_out), .en(and_86_out));  // open: out
  assign driver_388_out = and_86_out ? and_86_out : 1'bz;  // Driver driver_388
  assign driver_389_out = and_86_out ? and_86_out : 1'bz;  // Driver driver_389
  assign driver_390_out = and_86_out ? and_86_out : 1'bz;  // Driver driver_390
  assign PC_CK = and_87_out ? and_87_out : 1'bz;  // Driver driver_391
  LED led_154 (.in(and_87_out));
  assign driver_392_out = and_87_out ? and_87_out : 1'bz;  // Driver driver_392
  assign driver_393_out = and_87_out ? and_87_out : 1'bz;  // Driver driver_393
  assign driver_394_out = and_87_out ? and_87_out : 1'bz;  // Driver driver_394
  Driver driver_395 (.in(and_87_out), .en(and_87_out));  // open: out
  and and_88 (CNT_JMP, JMP, NOIND, PH02);
  LED led_155 (.in(CNT_JMP));
  and and_89 (and_89_out, JMP, NOIND, PH03);
  LED led_156 (.in(and_89_out));
  assign IR2PC = CNT_JMP ? CNT_JMP : 1'bz;  // Driver driver_396
  assign driver_397_out = CNT_JMP ? CNT_JMP : 1'bz;  // Driver driver_397
  assign driver_398_out = CNT_JMP ? CNT_JMP : 1'bz;  // Driver driver_398
  assign driver_399_out = CNT_JMP ? CNT_JMP : 1'bz;  // Driver driver_399
  assign driver_400_out = CNT_JMP ? CNT_JMP : 1'bz;  // Driver driver_400
  assign IR2PC = and_89_out ? and_89_out : 1'bz;  // Driver driver_401
  assign PC_LD = and_89_out ? and_89_out : 1'bz;  // Driver driver_402
  assign PC_CK = and_89_out ? and_89_out : 1'bz;  // Driver driver_403
  assign driver_404_out = and_89_out ? and_89_out : 1'bz;  // Driver driver_404
  assign driver_405_out = and_89_out ? and_89_out : 1'bz;  // Driver driver_405
  and and_90 (CNT_JMP_I, JMP, IND, PH02);
  and and_91 (and_91_out, JMP, IND, PH03);
  LED led_157 (.in(CNT_JMP_I));
  LED led_158 (.in(and_91_out));
  assign IR2RAMA = CNT_JMP_I ? CNT_JMP_I : 1'bz;  // Driver driver_406
  assign RAMD2PC = CNT_JMP_I ? CNT_JMP_I : 1'bz;  // Driver driver_407
  assign RAM_OE = CNT_JMP_I ? CNT_JMP_I : 1'bz;  // Driver driver_408
  assign driver_409_out = CNT_JMP_I ? CNT_JMP_I : 1'bz;  // Driver driver_409
  assign driver_410_out = CNT_JMP_I ? CNT_JMP_I : 1'bz;  // Driver driver_410
  assign IR2RAMA = and_91_out ? and_91_out : 1'bz;  // Driver driver_411
  assign RAMD2PC = and_91_out ? and_91_out : 1'bz;  // Driver driver_412
  assign RAM_OE = and_91_out ? and_91_out : 1'bz;  // Driver driver_413
  assign PC_LD = and_91_out ? and_91_out : 1'bz;  // Driver driver_414
  assign PC_CK = and_91_out ? and_91_out : 1'bz;  // Driver driver_415
  and and_92 (CNT_JMP_IA, JMP, AUTOIND, PH02);
  and and_93 (and_93_out, JMP, AUTOIND, PH03);
  and and_94 (and_94_out, JMP, AUTOIND, PH04);
  and and_95 (and_95_out, JMP, AUTOIND, PH05);
  and and_96 (and_96_out, JMP, AUTOIND, PH06);
  LED led_159 (.in(CNT_JMP_IA));
  LED led_160 (.in(and_93_out));
  LED led_161 (.in(and_94_out));
  LED led_162 (.in(and_95_out));
  LED led_163 (.in(and_96_out));
  assign IR2RAMA = CNT_JMP_IA ? CNT_JMP_IA : 1'bz;  // Driver driver_416
  assign RAM_OE = CNT_JMP_IA ? CNT_JMP_IA : 1'bz;  // Driver driver_417
  assign driver_418_out = CNT_JMP_IA ? CNT_JMP_IA : 1'bz;  // Driver driver_418
  assign driver_419_out = CNT_JMP_IA ? CNT_JMP_IA : 1'bz;  // Driver driver_419
  assign driver_420_out = CNT_JMP_IA ? CNT_JMP_IA : 1'bz;  // Driver driver_420
  assign IR2RAMA = and_93_out ? and_93_out : 1'bz;  // Driver driver_421
  assign IND_CK = and_93_out ? and_93_out : 1'bz;  // Driver driver_422
  assign RAM_OE = and_93_out ? and_93_out : 1'bz;  // Driver driver_423
  assign driver_424_out = and_93_out ? and_93_out : 1'bz;  // Driver driver_424
  assign driver_425_out = and_93_out ? and_93_out : 1'bz;  // Driver driver_425
  assign INC2RAMD = and_94_out ? and_94_out : 1'bz;  // Driver driver_426
  assign RAM_WE = and_94_out ? and_94_out : 1'bz;  // Driver driver_427
  assign driver_428_out = and_94_out ? and_94_out : 1'bz;  // Driver driver_428
  assign driver_429_out = and_94_out ? and_94_out : 1'bz;  // Driver driver_429
  assign driver_430_out = and_94_out ? and_94_out : 1'bz;  // Driver driver_430
  assign IR2RAMA = and_95_out ? and_95_out : 1'bz;  // Driver driver_431
  assign RAMD2PC = and_95_out ? and_95_out : 1'bz;  // Driver driver_432
  assign RAM_OE = and_95_out ? and_95_out : 1'bz;  // Driver driver_433
  assign driver_434_out = and_95_out ? and_95_out : 1'bz;  // Driver driver_434
  assign driver_435_out = and_95_out ? and_95_out : 1'bz;  // Driver driver_435
  assign IR2RAMA = and_96_out ? and_96_out : 1'bz;  // Driver driver_436
  assign RAMD2PC = and_96_out ? and_96_out : 1'bz;  // Driver driver_437
  assign RAM_OE = and_96_out ? and_96_out : 1'bz;  // Driver driver_438
  assign PC_LD = and_96_out ? and_96_out : 1'bz;  // Driver driver_439
  assign PC_CK = and_96_out ? and_96_out : 1'bz;  // Driver driver_440
  and and_97 (CNT_OPR1, OPR1, NOTNOP, PH02);
  LED led_164 (.in(CNT_OPR1));
  and and_98 (and_98_out, OPR1, 1'b1, PH03);
  LED led_165 (.in(and_98_out));
  assign ROT2AC = CNT_OPR1 ? CNT_OPR1 : 1'bz;  // Driver driver_441
  Driver driver_442 (.in(CNT_OPR1), .en(CNT_OPR1));  // open: out
  Driver driver_443 (.in(CNT_OPR1), .en(CNT_OPR1));  // open: out
  Driver driver_444 (.in(CNT_OPR1), .en(CNT_OPR1));  // open: out
  Driver driver_445 (.in(CNT_OPR1), .en(CNT_OPR1));  // open: out
  assign AC_CK = and_98_out ? and_98_out : 1'bz;  // Driver driver_446
  assign LINK_CK = and_98_out ? and_98_out : 1'bz;  // Driver driver_447
  assign ROT2AC = and_98_out ? and_98_out : 1'bz;  // Driver driver_448
  Driver driver_449 (.in(and_98_out), .en(and_98_out));  // open: out
  Driver driver_450 (.in(and_98_out), .en(and_98_out));  // open: out
  Driver driver_451 (.in(and_98_out), .en(and_98_out));  // open: out
  and and_99 (CNT_OPR2, OPR2, NOTNOP, PH02);
  and and_100 (and_100_out, OPR2, 1'b1, PH03);
  and and_101 (and_101_out, OPR2, SKIP, PH04);
  LED led_166 (.in(CNT_OPR2));
  LED led_167 (.in(and_100_out));
  LED led_168 (.in(and_101_out));
  assign ROT2AC = CNT_OPR2 ? CNT_OPR2 : 1'bz;  // Driver driver_452
  Driver driver_453 (.in(CNT_OPR2), .en(CNT_OPR2));  // open: out
  Driver driver_454 (.in(CNT_OPR2), .en(CNT_OPR2));  // open: out
  Driver driver_455 (.in(CNT_OPR2), .en(CNT_OPR2));  // open: out
  Driver driver_456 (.in(CNT_OPR2), .en(CNT_OPR2));  // open: out
  assign AC_CK = and_100_out ? and_100_out : 1'bz;  // Driver driver_457
  assign ROT2AC = and_100_out ? and_100_out : 1'bz;  // Driver driver_458
  Driver driver_459 (.in(and_100_out), .en(and_100_out));  // open: out
  Driver driver_460 (.in(and_100_out), .en(and_100_out));  // open: out
  Driver driver_461 (.in(and_100_out), .en(and_100_out));  // open: out
  assign IR_CK = and_101_out ? and_101_out : 1'bz;  // Driver driver_462
  assign PC_CK = and_101_out ? and_101_out : 1'bz;  // Driver driver_463
  Driver driver_464 (.in(and_101_out), .en(and_101_out));  // open: out
  Driver driver_465 (.in(and_101_out), .en(and_101_out));  // open: out
  Driver driver_466 (.in(and_101_out), .en(and_101_out));  // open: out
  Demultiplexer #(.Selector_Bits(3)) demultiplexer_1 (
    .sel(BUS_IR[2:0]), .in(IOT_DEVHSR), .out_0(demultiplexer_1_out_0), .out_1(demultiplexer_1_out_1),
    .out_2(demultiplexer_1_out_2), .out_3(demultiplexer_1_out_3), .out_4(demultiplexer_1_out_4),
    .out_5(demultiplexer_1_out_5), .out_6(demultiplexer_1_out_6), .out_7(demultiplexer_1_out_7));
  LED led_169 (.in(IOT_DEVHSR));
  or or_11 (or_11_out, PH02, PH03, PH04, PH05, PH06, PH07, PH08, PH09, PH10, PH11);
  LED led_170 (.in(IOT));
  // Probe on BUS_IR[2:0]
  // Probe on BUS_IR[8:3]
  and and_102 (and_102_out, or_11_out, IOT);
  Demultiplexer #(.Selector_Bits(3)) demultiplexer_2 (
    .sel(BUS_IR[2:0]), .in(IOT_DEVKBD), .out_0(INST_KCF), .out_1(INST_KSF), .out_2(INST_KCC),
    .out_3(demultiplexer_2_out_3), .out_4(INST_KRS), .out_5(INST_KIE), .out_6(INST_KRB),
    .out_7(demultiplexer_2_out_7));
  LED led_171 (.in(IOT_DEVKBD));
  Demultiplexer #(.Selector_Bits(3)) demultiplexer_3 (
    .sel(BUS_IR[2:0]), .in(IOT_DEVPRI), .out_0(INST_TFL), .out_1(INST_TSF), .out_2(INST_TCF),
    .out_3(demultiplexer_3_out_3), .out_4(INST_TPC), .out_5(INST_TSK), .out_6(INST_TLS),
    .out_7(demultiplexer_3_out_7));
  LED led_172 (.in(IOT_DEVPRI));
  Demultiplexer #(.Selector_Bits(6)) demultiplexer_4 (
    .sel(BUS_IR[8:3]), .in(and_102_out), .out_0(IOT_DEVCPU), .out_1(IOT_DEVHSR), .out_2(IOT_DEVHSP),
    .out_3(IOT_DEVKBD), .out_4(IOT_DEVPRI), .out_5(IOT_5), .out_6(IOT_6), .out_7(IOT_7), .out_8(IOT_8),
    .out_9(IOT_9), .out_10(demultiplexer_4_out_10), .out_11(demultiplexer_4_out_11),
    .out_12(demultiplexer_4_out_12), .out_13(demultiplexer_4_out_13), .out_14(demultiplexer_4_out_14),
    .out_15(demultiplexer_4_out_15), .out_16(demultiplexer_4_out_16), .out_17(demultiplexer_4_out_17),
    .out_18(demultiplexer_4_out_18), .out_19(demultiplexer_4_out_19), .out_20(demultiplexer_4_out_20),
    .out_21(demultiplexer_4_out_21), .out_22(demultiplexer_4_out_22), .out_23(demultiplexer_4_out_23),
    .out_24(demultiplexer_4_out_24), .out_25(demultiplexer_4_out_25), .out_26(demultiplexer_4_out_26),
    .out_27(demultiplexer_4_out_27), .out_28(demultiplexer_4_out_28), .out_29(demultiplexer_4_out_29),
    .out_30(demultiplexer_4_out_30), .out_31(demultiplexer_4_out_31), .out_32(demultiplexer_4_out_32),
    .out_33(demultiplexer_4_out_33), .out_34(demultiplexer_4_out_34), .out_35(demultiplexer_4_out_35),
    .out_36(demultiplexer_4_out_36), .out_37(demultiplexer_4_out_37), .out_38(demultiplexer_4_out_38),
    .out_39(demultiplexer_4_out_39), .out_40(demultiplexer_4_out_40), .out_41(demultiplexer_4_out_41),
    .out_42(demultiplexer_4_out_42), .out_43(demultiplexer_4_out_43), .out_44(demultiplexer_4_out_44),
    .out_45(demultiplexer_4_out_45), .out_46(demultiplexer_4_out_46), .out_47(demultiplexer_4_out_47),
    .out_48(demultiplexer_4_out_48), .out_49(demultiplexer_4_out_49), .out_50(demultiplexer_4_out_50),
    .out_51(demultiplexer_4_out_51), .out_52(demultiplexer_4_out_52), .out_53(demultiplexer_4_out_53),
    .out_54(demultiplexer_4_out_54), .out_55(demultiplexer_4_out_55), .out_56(demultiplexer_4_out_56),
    .out_57(demultiplexer_4_out_57), .out_58(demultiplexer_4_out_58), .out_59(demultiplexer_4_out_59),
    .out_60(demultiplexer_4_out_60), .out_61(demultiplexer_4_out_61), .out_62(demultiplexer_4_out_62),
    .out_63(demultiplexer_4_out_63));
  or or_12 (IOT_5x, demultiplexer_4_out_50, demultiplexer_4_out_51, demultiplexer_4_out_52, demultiplexer_4_out_53, demultiplexer_4_out_54, demultiplexer_4_out_56, demultiplexer_4_out_57, demultiplexer_4_out_58, demultiplexer_4_out_59, demultiplexer_4_out_55);
  or or_13 (IOT_6x, demultiplexer_4_out_60, demultiplexer_4_out_61, demultiplexer_4_out_63, demultiplexer_4_out_62);
  assign PC2RAMA = PH00 ? PH00 : 1'bz;  // Driver driver_467
  assign RAM_OE = PH00 ? PH00 : 1'bz;  // Driver driver_468
  assign PC2RAMA = PH01 ? PH01 : 1'bz;  // Driver driver_469
  assign RAM_OE = PH01 ? PH01 : 1'bz;  // Driver driver_470
  assign IR_CK = PH01 ? PH01 : 1'bz;  // Driver driver_471
  assign PC_CK = PH01 ? PH01 : 1'bz;  // Driver driver_472
  or or_14 (IOT_3x, demultiplexer_4_out_30, demultiplexer_4_out_31, demultiplexer_4_out_32, demultiplexer_4_out_33, demultiplexer_4_out_34, demultiplexer_4_out_36, demultiplexer_4_out_37, demultiplexer_4_out_38, demultiplexer_4_out_39, demultiplexer_4_out_35);
  or or_15 (IOT_4x, demultiplexer_4_out_40, demultiplexer_4_out_41, demultiplexer_4_out_42, demultiplexer_4_out_43, demultiplexer_4_out_44, demultiplexer_4_out_46, demultiplexer_4_out_47, demultiplexer_4_out_48, demultiplexer_4_out_49, demultiplexer_4_out_45);
  or or_16 (IOT_1x, demultiplexer_4_out_10, demultiplexer_4_out_11, demultiplexer_4_out_12, demultiplexer_4_out_13, demultiplexer_4_out_14, demultiplexer_4_out_16, demultiplexer_4_out_17, demultiplexer_4_out_18, demultiplexer_4_out_19, demultiplexer_4_out_15);
  or or_17 (IOT_2x, demultiplexer_4_out_20, demultiplexer_4_out_21, demultiplexer_4_out_22, demultiplexer_4_out_23, demultiplexer_4_out_24, demultiplexer_4_out_26, demultiplexer_4_out_27, demultiplexer_4_out_28, demultiplexer_4_out_29, demultiplexer_4_out_25);
  LED led_173 (.in(OPR));
  LED led_174 (.in(OPR1));
  LED led_175 (.in(OPR2));
  // Probe on BUS_IR
  Demultiplexer #(.Selector_Bits(3)) demultiplexer_5 (
    .sel(BUS_IR[11:9]), .in(1'b1), .out_0(AND), .out_1(TAD), .out_2(ISZ), .out_3(DCA), .out_4(JMS),
    .out_5(JMP), .out_6(IOT), .out_7(OPR));
  Demultiplexer demultiplexer_6 (.sel(BUS_IR[8]), .in(OPR), .out_0(OPR1), .out_1(OPR2));
  and and_103 (AUTOIND, BUS_IR[3], ~BUS_IR[4], ~BUS_IR[5], ~BUS_IR[6], ~BUS_IR[7], BUS_IR[8]);  // And
  not not_2 (NOIND, BUS_IR[8]);
  LED led_176 (.in(AUTOIND));
  nor nor_2 (IND, AUTOIND, NOIND);
  LED led_177 (.in(IND));
  and and_104 (OPR_IAC, BUS_IR[0], OPR1);
  LED led_178 (.in(OPR_IAC));
  and and_105 (OPR_X2, BUS_IR[1], OPR1);
  LED led_179 (.in(OPR_X2));
  and and_106 (OPR_LEFT, BUS_IR[2], OPR1);
  LED led_180 (.in(OPR_LEFT));
  and and_107 (OPR_RIGHT, BUS_IR[3], OPR1);
  LED led_181 (.in(OPR_RIGHT));
  and and_108 (OPR_CML, BUS_IR[4], OPR1);
  LED led_182 (.in(OPR_CML));
  and and_109 (OPR_CMA, BUS_IR[5], OPR1);
  LED led_183 (.in(OPR_CMA));
  and and_110 (OPR_CLL, BUS_IR[6], OPR1);
  LED led_184 (.in(OPR_CLL));
  and and_111 (OPR_CLA1, BUS_IR[7], OPR1);
  LED led_185 (.in(OPR_CLA1));
  and and_112 (OPR_NA1, BUS_IR[0], OPR2);
  LED led_186 (.in(OPR_NA1));
  and and_113 (OPR_HLT, BUS_IR[1], OPR2);
  LED led_187 (.in(OPR_HLT));
  and and_114 (OPR_OSR, BUS_IR[2], OPR2);
  LED led_188 (.in(OPR_OSR));
  and and_115 (OPR_TSTINV, BUS_IR[3], OPR2);
  LED led_189 (.in(OPR_TSTINV));
  and and_116 (OPR_SNL, BUS_IR[4], OPR2);
  LED led_190 (.in(OPR_SNL));
  and and_117 (OPR_SZA, BUS_IR[5], OPR2);
  LED led_191 (.in(OPR_SZA));
  and and_118 (OPR_SMA, BUS_IR[6], OPR2);
  LED led_192 (.in(OPR_SMA));
  and and_119 (OPR_CLA2, BUS_IR[7], OPR2);
  LED led_193 (.in(OPR_CLA2));
  or or_18 (NOTNOP, BUS_IR[0], BUS_IR[1], BUS_IR[2], BUS_IR[3], BUS_IR[4], BUS_IR[5], BUS_IR[6], BUS_IR[7]);
  and and_120 (OPR_NOP, NOTNOP, OPR);
  LED led_194 (.in(OPR_NOP));
  PullDown pulldown_3 (.out(PC_LD));
  PullDown pulldown_4 (.out(IR2PC));
  PullDown pulldown_5 (.out(IR2PC));
  PullDown pulldown_6 (.out(IND_CK));
  PullDown pulldown_7 (.out(IND2PC));
  PullDown pulldown_8 (.out(IR2RAMA));
  PullDown pulldown_9 (.out(IR2RAMA));
  PullDown pulldown_10 (.out(AC_CK));
  PullDown pulldown_11 (.out(LINK_CK));
  PullDown pulldown_12 (.out(RAMD2PC));
  PullDown pulldown_13 (.out(IND2RAMA));
  PullDown pulldown_14 (.out(INC2RAMD));
  PullDown pulldown_15 (.out(IR_CK));
  PullDown pulldown_16 (.out(RAM_WE));
  PullDown pulldown_17 (.out(PC_CK));
  PullDown pulldown_18 (.out(PC2RAMD));
  PullDown pulldown_19 (.out(ROT2AC));
  PullDown pulldown_20 (.out(RAMD2AC_ADD));
  PullDown pulldown_21 (.out(RAM_OE));
  PullDown pulldown_22 (.out(RAMA_HOLD));

  // Other names for the same wires on the sheet: RAMADDR[11:0] = {RA3, RA2, RA1, RA0}; PI0[2:0] = PCIN[2:0];
  //   PI1[2:0] = PCIN[5:3]; PI2[2:0] = PCIN[8:6]; PI3[2:0] = PCIN[11:9]; AC0[2:0] = AC[2:0]; AC1[2:0] = AC[5:3];
  //   AC2[2:0] = AC[8:6]; AC3[2:0] = AC[11:9]; IR0[2:0] = BUS_IR[2:0]; IR1[2:0] = BUS_IR[5:3]; IR2[2:0] = BUS_IR[8:6];
  //   MP = BUS_IR[7]; IR3[2:0] = BUS_IR[11:9]; PC0[2:0] = BUS_PC[2:0]; PC1[2:0] = BUS_PC[5:3]; PC2[2:0] = BUS_PC[8:6];
  //   PC3[2:0] = BUS_PC[11:9]; DATA[11:0] = {DA3, DA2, DA1, DA0}; INDOUT[11:0] = {IND3, IND2, IND1, IND0};
  //   RD0[2:0] = RAMDATA[2:0]; RD1[2:0] = RAMDATA[5:3]; RD2[2:0] = RAMDATA[8:6]; RD3[2:0] = RAMDATA[11:9]

  // Notes on the sheet:
  //   clk: Hz: 100
  //   PC
  //   IR
  //   AC
  //   IND
  //   RAM-A
  //   RAM-D
  //   PC-IN
  //   DATA
  //   KCF
  //   CLA
  //   AND
  //   KSF
  //   CLL
  //   TAD
  //   KCC
  //   KRS
  //   CMA
  //   CMI
  //   ISZ
  //   DCA
  //   KIE
  //   IAC
  //   JMS
  //   STATE
  //   INSTRUCTION
  //   RUN
  //   HALT
  //   PC=0200
  //   BREAKPOINT
  //   PCIN
  //   KRB
  //   ROR
  //   JMP
  //   TFL
  //   ROL
  //   x2
  //   IOT
  //   OPR
  //   TSF
  //   START/STOP/STEP
  //   CLOCK CYCLE CONTROLLER
  //   TCF
  //   SMA
  //   DIR
  //   PCOUT
  //   TPC
  //   TSK
  //   SZA
  //   SNL
  //   AUTO
  //   IND
  //   TLS
  //   INV
  //   CURR
  //   PAGE
  //   OSR
  //   RAMADDR
  //   HLT
  //   -
  //   NOP
  //   contents of eeprom_1 (hex, n*v repeats v):
  //   a13,13,29d,bff,f02,f02,f02,f02,a6,38,43,ad,f02,f02,f02,f02,29,9f,2,e80,601,e80,201,
  //   f02,e00,bfe,bff,401,e80,201,f02,e00,a22,bff,401,e80,201,f02,e00,b10,bff,401,e80,201,
  //   f02,e00,b11,bff,3f,401,e80,201,f02,e00,b30,bff,401,e80,201,f02,e00,9fd,830,90a,90b,
  //   bfc,bff,40,401,e80,201,f02,e00,b43,bff,f02,f02,f02,f02,f02,f02,f02,f02,f02,f02,f02,
  //   f02,f02,f02,f02,f02,f02,f02,f02,f02,f02,f02,f02,f02,f02,f02,f02,f02,f02,f02,f02,f02,
  //   f02,f02,f02,f02,f02,f02,f02,f02,f02,f02,f02,f02,f02,f02,f02,f02,f02,b5,8f,80,fc0,
  //   401,e80,201,f02,e00,a98,bff,96,401,e80,201,f02,e00,b87,bff,3e,401,e80,201,f02,e00,
  //   887,b8f,bff,401,e80,201,f02,e00,a1b,bff,401,e80,201,f02,e00,b08,bff,401,e80,201,f02,
  //   e00,b09,bff,41,401,e80,201,f02,e00,bad,bff,401,e80,201,f02,e00,e80,2fe,e21,201,f28,
  //   ac1,bff,401,e80,201,f02,e00,e80,2fe,e21,201,f20,acd,bff,401,e80,201,f02,e00,e80,2fe,
  //   e21,201,f28,ad9,ada,bff,401,e80,201,f02,e00,e80,2fd,e21,201,f20,ae6,ae7,bff,401,e80,
  //   201,f02,402,aee,bff,e80,2fc,e21,202,f28,bfb,bff,f02,f02,f02,f02,f02,f02,100,29d,11,
  //   e,fc0,401,e80,201,f02,512,a87,bff,e80,2fe,e21,202,f28,a8e,bff,bfd,f02,f02,f02,f02,
  //   f02,f02,f02,f02,f02,f02,f02,f02,f02,f02,f02,f02,f02,f02,f02,f02,f02,f02,f02,f02,f02,
  //   f02,f02,f02,f02,f02,f02,f02,f02,f02,f02,f02,f02,f02,f02,f02,f02,f02,f02,f02,f02,f02,
  //   f02,f02,f02,f02,f02,f02,f02,f02,f02,f02,f02,f02,f02,f02,f02,f02,f02,f02,f02,f02,f02,
  //   f02,f02,f02,f02,f02,f02,f02,f02,f02,f02,f02,f02,f02,f02,f02,f02,f02,f02,f02,f02,f02,
  //   f02,f02,f02,f02,f02,f02,f02,f02,f02,f02,f02,f02,f02,f02,f02,f02,f02,f02,f02,f02,f02,
  //   f02,aa8,29e,fc0,f02,f02,f02,f02,f02,f02,f02,f02,f02,f02,f02,f02,f02,f02,f02,f02,f02,
  //   f02,f02,f02,f02,f02,f02,f02,f02,f02,f02,f02,f02,f02,f02,f02,f02,f02,f02,f02,f02,f02,
  //   f02,f02,f02,f02,f02,f02,f02,f02,f02,f02,f02,f02,f02,f02,f02,f02,f02,f02,f02,f02,f02,
  //   f02,f02,f02,f02,f02,f02,f02,f02,f02,f02,f02,f02,f02,f02,f02,f02,f02,f02,f02,f02,f02,
  //   f02,f02,f02,f02,f02,f02,f02,f02,f02,f02,f02,f02,f02,f02,f02,f02,f02,f02,f02,f02,f02,
  //   f02,f02,f02,f02,f02,f02,f02,f02,f02,f02,f02,f02,f02,f02,f02,f02,f02,f02,f02,f02,f02,
  //   f02,f02,f02,f02,f02,f02,f02,f02,f02,f02,f02,f02,f02,f02,f02,f02,f02,f02,f02,f02,f02,
  //   f02,f02,f02,f02,f02,f02,f02,f02,f02,f02,f02,f02,f02,f02,f02,f02,f02,f02,f02,f02,f02,
  //   f02,f02,f02,f02,f02,f02,f02,f02,f02,f02,f02,f02,f02,f02,f02,f02,f02,f02,f02,f02,f02,
  //   f02,f02,f02,f02,f02,f02,f02,f02,f02,f02,f02,f02,f02,f02,f02,f02,f02,f02,f02,f02,f02,
  //   f02,f02,f02,f02,f02,f02,f02,f02,f02,f02,f02,f02,f02,f02,f02,f02,f02,f02,f02,f02,f02,
  //   f02,f02,f02,f02,f02,f02,f02,f02,f02,f02,f02,f02,f02,f02,f02,f02,f02,f02,f02,f02,f02,
  //   f02,f02,f02,f02,f02,f02,f02,f02,f02,f02,f02,f02,f02,f02,f02,f02,f02,f02,f02,f02,f02,
  //   f02,f02,f02,f02,f02,f02,f02,f02,f02,f02,f02,f02,f02,f02,f02,f02,f02,f02,f02,f02,f02,
  //   f02,f02,f02,f02,f02,f02,f02,f02,f02,f02,f02,f02,f02,f02,f02,f02,f02,f02,f02,f02,f02,
  //   f02,f02,f02,f02,f02,f02,f02,f02,f02,f02,f02,f02,f02,f02,f02,f02,f02,f02,f02,f02,f02,
  //   f02,f02,f02,f02,f02,f02,f02,f02,f02,f02,f02,f02,f02,f02,f02,f02,f02,f02,f02,f02,f02,
  //   f02,f02,f02,f02,f02,f02,f02,f02,f02,f02,f02,f02,f02,f02,f02,f02,f02,f02,f02,f02,f02,
  //   f02,f02,f02,f02,f02,f02,f02,f02,f02,f02,f02,f02,f02,f02,f02,f02,f02,f02,f02,f02,f02,
  //   f02,f02,f02,f02,f02,f02,f02,f02,f02,f02,f02,f02,f02,f02,f02,f02,f02,f02,f02,f02,f02,
  //   f02,f02,f02,f02,f02,f02,f02,f02,f02,f02,f02,f02,f02,f02,f02,f02,f02,f02,f02,f02,f02,
  //   f02,f02,f02,f02,f02,f02,f02,f02,f02,f02,f02,f02,f02,f02,f02,f02,f02,f02,f02,f02,f02,
  //   f02,f02,f02,f02,f02,f02,f02,f02,f02,f02,f02,f02,f02,f02,f02,f02,f02,f02,f02,f02,f02,
  //   f02,f02,f02,f02,f02,f02,f02,f02,f02,f02,f02,f02,f02,f02,f02,f02,f02,f02,f02,f02,f02,
  //   f02,f02,f02,f02,f02,f02,f02,f02,f02,f02,f02,f02,f02,f02,f02,f02,f02,f02,f02,f02,f02,
  //   f02,f02,f02,f02,f02,f02,f02,f02,f02,f02,f02,f02,f02,f02,f02,f02,f02,f02,f02,f02,f02,
  //   f02,f02,f02,f02,f02,f02,f02,f02,f02,f02,f02,f02,f02,f02,f02,f02,f02,f02,f02,f02,f02,
  //   f02,f02,f02,f02,f02,f02,f02,f02,f02,f02,f02,f02,f02,f02,f02,f02,f02,f02,f02,f02,f02,
  //   f02,f02,f02,f02,f02,f02,f02,f02,f02,f02,f02,f02,f02,f02,f02,f02,f02,f02,f02,f02,f02,
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  //   RAMDATA
  //   AND
  //   STEP1
  //   INDOUT
  //   AND i
  //   IND
  //   STEP1
  //   IND
  //   STEP2
  //   AND
  //   STEP2
  //   AND-i-auto
  //   iAuto 1
  //   iAuto 2
  //   iAuto 3
  //   TAD
  //   STEP1
  //   TAD
  //   STEP2
  //   CML
  //   TAD i
  //   TAD-i-auto
  //   Put M addr
  //   into IND
  //   SKIP IF
  //   AC=ZERO
  //   Get address
  //   of M
  //   ISZ i
  //   ISZ-i-auto
  //   DCA i
  //   DCA-i-auto
  //   Prepare to store
  //   return address
  //   Actually store
  //   return address
  //   Pause to accept
  //   new PC inc clk
  //   Actually increment
  //   PC
  //   Actually set
  //   PC
  //   Prepate to store 
  //   return addr
  //   to [ind]
  //   Store return addr
  //   to [ind]
  //   JMS i
  //   JMS i-auto
  //   Prepare to set
  //   new PC
  //   Actually set
  //   new PC
  //   Prepare to set PC
  //   with new vector
  //   JMP i
  //   JMP i-auto
  //   OPR 1
  //   OPR 2
  //   IOT DECODER
  //   PH0 & PH1
  //   IR DECODER
  //   OPR DECODER
endmodule
