// Digital circuit PDP8-X.dig as structural Verilog
module PDP8_X (
  input  clk
);

  wire AC2RAMD, AC_CK, add_1_c_o, add_2_c_o, AND, and_1_out, and_3_out, and_4_out, and_7_out, and_8_out,
       and_9_out, and_10_out, and_11_out, and_12_out, and_14_out, and_17_out, and_18_out, and_19_out,
       and_20_out, and_21_out, and_22_out, and_23_out, and_24_out, and_25_out, and_26_out, and_28_out,
       and_29_out, and_30_out, and_31_out, and_33_out, and_34_out, and_35_out, and_36_out, and_37_out,
       and_38_out, and_39_out, and_40_out, and_41_out, and_42_out, and_43_out, and_44_out, and_45_out,
       and_46_out, and_47_out, and_48_out, and_49_out, and_50_out, and_52_out, and_53_out, and_54_out,
       and_55_out, and_56_out, and_58_out, and_59_out, and_60_out, and_61_out, and_62_out, and_63_out,
       and_64_out, and_67_out, and_68_out, and_70_out, and_71_out, and_72_out, and_74_out, and_75_out,
       and_76_out, and_77_out, and_79_out, and_80_out, and_81_out, and_82_out, and_83_out, and_84_out,
       and_85_out, and_86_out, and_87_out, and_88_out, and_89_out, and_90_out, and_91_out, and_93_out,
       and_94_out, and_95_out, and_97_out, and_98_out, and_100_out, and_101_out, and_102_out, and_103_out,
       and_105_out, and_106_out, and_107_out, and_108_out, and_109_out, and_110_out, and_111_out,
       and_112_out, and_114_out, and_115_out, and_116_out, and_117_out, and_119_out, and_120_out,
       and_121_out, and_122_out, and_123_out, and_124_out, and_125_out, and_126_out, and_127_out,
       and_128_out, and_129_out, and_130_out, and_131_out, and_133_out, and_134_out, and_135_out,
       and_137_out, and_139_out, and_140_out, and_141_out, and_143_out, and_144_out, and_145_out,
       and_147_out, and_149_out, and_150_out, and_151_out, and_153_out, and_154_out, and_155_out,
       and_156_out, and_157_out, and_158_out, and_179_out, and_183_out, and_185_out, AUTOIND, BP_ENABLED_b,
       CK0, CK1, CK2, CK3, CK4, CK5, CK6, CK7, CK8, CK9, CLA, CLA_KCC, CLAx, CLL, CNT_AND, CNT_AND_I,
       CNT_AND_IA, CNT_DCA, CNT_DCA_I, CNT_DCA_IA, CNT_ISZ, CNT_ISZ_I, CNT_ISZ_IA, CNT_JMP, CNT_JMP_I,
       CNT_JMP_IA, CNT_JMS, CNT_JMS_I, CNT_JMS_IA, CNT_OPR1, CNT_OPR2, CNT_OPR3, CNT_TAD, CNT_TAD_I,
       CNT_TAD_IA, comparator_1_eq, comparator_2_eq, counter_1_o1, counter_1_o2, counter_1_o3, counter_1_o4,
       counter_1_o5, counter_1_o6, counter_1_o7, counter_1_o8, counter_1_o9, counter_1_o10, counter_1_o11,
       counter_1_o12, counter_1_o13, counter_1_o14, counter_1_o15, counter_1_o16, counter_1_o17,
       counter_1_o18, counter_1_o19, counter_1_o20, counter_1_o21, counter_1_o22, counter_1_o23,
       counter_1_o24, counter_1_o25, counter_1_o26, counter_1_o27, counter_1_o28, counter_1_o29,
       counter_1_o30, counter_1_o31, counter_1_o32, counter_2_ovf, d_ff_1_q, d_ff_as_2_q, d_ff_as_3_q,
       DATA_CK, DCA, demultiplexer_1_out_3, demultiplexer_1_out_7, demultiplexer_2_out_3,
       demultiplexer_2_out_7, demultiplexer_4_out_10, demultiplexer_4_out_11, demultiplexer_4_out_12,
       demultiplexer_4_out_13, demultiplexer_4_out_14, demultiplexer_4_out_15, demultiplexer_4_out_16,
       demultiplexer_4_out_17, demultiplexer_4_out_18, demultiplexer_4_out_19, demultiplexer_4_out_20,
       demultiplexer_4_out_21, demultiplexer_4_out_22, demultiplexer_4_out_23, demultiplexer_4_out_24,
       demultiplexer_4_out_25, demultiplexer_4_out_26, demultiplexer_4_out_27, demultiplexer_4_out_28,
       demultiplexer_4_out_29, demultiplexer_4_out_30, demultiplexer_4_out_31, demultiplexer_4_out_32,
       demultiplexer_4_out_33, demultiplexer_4_out_34, demultiplexer_4_out_35, demultiplexer_4_out_36,
       demultiplexer_4_out_37, demultiplexer_4_out_38, demultiplexer_4_out_39, demultiplexer_4_out_40,
       demultiplexer_4_out_41, demultiplexer_4_out_42, demultiplexer_4_out_43, demultiplexer_4_out_44,
       demultiplexer_4_out_45, demultiplexer_4_out_46, demultiplexer_4_out_47, demultiplexer_4_out_48,
       demultiplexer_4_out_49, demultiplexer_4_out_50, demultiplexer_4_out_51, demultiplexer_4_out_52,
       demultiplexer_4_out_53, demultiplexer_4_out_54, demultiplexer_4_out_55, demultiplexer_4_out_56,
       demultiplexer_4_out_57, demultiplexer_4_out_58, demultiplexer_4_out_59, demultiplexer_4_out_60,
       demultiplexer_4_out_61, demultiplexer_4_out_62, demultiplexer_4_out_63, demultiplexer_6_out_0,
       demultiplexer_6_out_1, demultiplexer_7_out_3, demultiplexer_7_out_7, demultiplexer_8_out_3,
       demultiplexer_8_out_7, demultiplexer_10_out_10, demultiplexer_10_out_11, demultiplexer_10_out_12,
       demultiplexer_10_out_13, demultiplexer_10_out_14, demultiplexer_10_out_15, demultiplexer_10_out_16,
       demultiplexer_10_out_17, demultiplexer_10_out_18, demultiplexer_10_out_19, demultiplexer_10_out_20,
       demultiplexer_10_out_21, demultiplexer_10_out_22, demultiplexer_10_out_23, demultiplexer_10_out_24,
       demultiplexer_10_out_25, demultiplexer_10_out_26, demultiplexer_10_out_27, demultiplexer_10_out_28,
       demultiplexer_10_out_29, demultiplexer_10_out_30, demultiplexer_10_out_31, demultiplexer_10_out_32,
       demultiplexer_10_out_33, demultiplexer_10_out_34, demultiplexer_10_out_35, demultiplexer_10_out_36,
       demultiplexer_10_out_37, demultiplexer_10_out_38, demultiplexer_10_out_39, demultiplexer_10_out_40,
       demultiplexer_10_out_41, demultiplexer_10_out_42, demultiplexer_10_out_43, demultiplexer_10_out_44,
       demultiplexer_10_out_45, demultiplexer_10_out_46, demultiplexer_10_out_47, demultiplexer_10_out_48,
       demultiplexer_10_out_49, demultiplexer_10_out_50, demultiplexer_10_out_51, demultiplexer_10_out_52,
       demultiplexer_10_out_53, demultiplexer_10_out_54, demultiplexer_10_out_55, demultiplexer_10_out_56,
       demultiplexer_10_out_57, demultiplexer_10_out_58, demultiplexer_10_out_59, demultiplexer_10_out_60,
       demultiplexer_10_out_61, demultiplexer_10_out_62, demultiplexer_10_out_63, driver_2_out,
       driver_96_out, driver_97_out, driver_287_out, driver_288_out, driver_293_out, driver_312_out,
       driver_313_out, driver_318_out, driver_346_out, driver_349_out, driver_350_out, driver_351_out,
       driver_355_out, driver_356_out, driver_360_out, driver_361_out, driver_363_out, driver_364_out,
       driver_365_out, driver_370_out, driver_371_out, driver_376_out, driver_380_out, driver_381_out,
       driver_391_out, driver_394_out, driver_395_out, driver_396_out, driver_398_out, driver_399_out,
       driver_400_out, driver_413_out, driver_414_out, driver_419_out, driver_423_out, driver_424_out,
       driver_434_out, driver_437_out, driver_438_out, driver_439_out, driver_441_out, driver_442_out,
       driver_443_out, driver_452_out, driver_462_out, driver_484_out, FLAG_GIE, FLAG_KBD, FLAG_KBDIE,
       FLAG_PRN, FORCE4000, H_out, HALT, HLT_ENABLED_b, i_cla, i_cll, i_cma, i_cml, i_hlt, i_iac, i_nop,
       i_osr, I_out, i_ral, i_rar, i_rtl, i_rtr, i_skp, i_sma, i_sna, i_snl, i_spa, i_sza, i_szl, INC2RAMD,
       INCZERO, IND, IND2INC, IND2PC, IND2RAMA, IND_CK, IOT, IOT_CAF, IOT_DEV1x, IOT_DEV2x, IOT_DEV3x,
       IOT_DEV4x, IOT_DEV5, IOT_DEV5x, IOT_DEV6, IOT_DEV6x, IOT_DEV7, IOT_DEV8, IOT_DEV9, IOT_DEVCPU,
       IOT_DEVHSP, IOT_DEVHSR, IOT_DEVKBD, IOT_DEVPRI, IOT_GTF, IOT_IOF, IOT_ION, IOT_KCC, IOT_KCF, IOT_KIE,
       IOT_KRB, IOT_KRS, IOT_KSF, IOT_RTF, IOT_SGT, IOT_SKON, IOT_SRQ, IOT_TCF, IOT_TFL, IOT_TLS, IOT_TPC,
       IOT_TSF, IOT_TSK, IR2PC, IR2RAMA, IR_CK, IRQ_BUS, IRQ_INHIBIT, IRQ_JMP, ISZ, JMP, JMS, KEYBOARD_av,
       L_CAF, L_DEV1x, L_DEV2x, L_DEV3x, L_DEV4x, L_DEV5, L_DEV5x, L_DEV6, L_DEV6x, L_DEV7, L_DEV8, L_DEV9,
       L_DEVCPU, L_DEVHSP, L_DEVHSR, L_DEVKBD, L_DEVPRI, L_GTF, L_IOF, L_ION, L_KCC, L_KCF, L_KIE, L_KRB,
       L_KRS, L_KSF, L_RTF, L_SGT, L_SKON, L_SRQ, L_TCF, L_TFL, L_TLS, L_TPC, L_TSF, L_TSK, LD2INC, LINK,
       LINK_CK, monoflop_1_q, monoflop_2_q, monoflop_3_nq, monoflop_4_q, MP, MQ_CK, nand_1_out, NOIND,
       nor_1_out, nor_2_out, nor_3_out, nor_4_out, not_1_out, not_2_out, not_4_out, not_5_out, not_6_out,
       OPR, OPR1, OPR2, OPR3, OPR_ASL, OPR_CLA1, OPR_CLA2, OPR_CLA3, OPR_CLL, OPR_CMA, OPR_CML, OPR_DVI,
       OPR_HLT, OPR_IAC, OPR_LEFT, OPR_LSR, OPR_MQA, OPR_MQL, OPR_MUY, OPR_NA1, OPR_NMI, OPR_NOP,
       OPR_OPERATION, OPR_OSR, OPR_RIGHT, OPR_SCA, OPR_SCL, OPR_SHL, OPR_SMASPA, OPR_SNLSZL, OPR_SWP,
       OPR_SZASNA, OPR_TSTINV, OPR_X2, or_1_out, or_2_out, or_3_out, or_4_out, or_6_out, or_7_out, or_8_out,
       or_9_out, or_10_out, or_11_out, or_12_out, or_14_out, or_15_out, or_16_out, or_17_out, or_18_out,
       or_19_out, or_20_out, OR_KBD12, OR_STATUS12, PC2ADDR, PC2RAMD, PC_CK, PC_eq_200, PC_LD, PH_FIRST,
       PH_LAST, PH_STB, R_out, RAM_OE, RAM_WE, RAMA_HOLD, RAMD2AC_ADD, RAMD2AC_AND, RAMD2IND, RAMD2PC,
       reset_1_out, ROT2AC, rotater_1_p5, rs_ff_as_1_q, rs_ff_as_2_q, RTF_IOF, RTF_ION, RTF_LINK, S_out,
       SKIP, STB0, STB1, STB2, STB3, STB4, STB5, STB6, STB7, STB8, STB9, TAD, TAD_OVF_q, xor_1_out,
       xor_2_out, xor_3_out, xor_4_out, xor_6_out;
  wire [2:0] and_180_out, DA0, DA1, DA2, DA3, IND0, IND1, IND2, IND3, RA0, RA1, RA2, RA3;
  wire [3:0] CK_NUM;
  wire [4:0] counter_2_out;
  wire [11:0] AC, add_1_s, add_2_s, and_2_out, and_5_out, and_6_out, autocapture_1__10, autocapture_1__11,
       autocapture_1__12, autocapture_1__13, autocapture_1__14, autocapture_1__15, autocapture_1__16,
       autocapture_1__17, bitextender_1_out, bitextender_2_out, bitextender_3_out, BUS_IR, BUS_PC,
       dipswitch_1_out, driver_6_out, driver_15_out, driver_21_out, INC_s, KBD12, LATCHED_PC, LATCHEDDATA,
       MQ, not_3_out, or_5_out, PCIN, RAMDATA, register_1_q, rotater_1_p4, xor_5_out;
  wire [15:0] KEYBOARD_d;
  wire [31:0] INSTRUCTION_COUNT_out;

  Comparator #(.Bits(12)) comparator_1 (.a({RA3, RA2, RA1, RA0}), .b(12'h779), .eq(comparator_1_eq));  // open: gt, lt
  xor xor_1 (xor_1_out, CK0, PC_eq_200);
  and and_1 (and_1_out, comparator_1_eq, RAM_WE);
  assign PCIN = PC_eq_200 ? 12'h80 : 12'bz;  // Driver driver_1
  assign driver_2_out = PC_eq_200 ? PC_eq_200 : 1'bz;  // Driver driver_2
  assign PC_LD = PC_eq_200 ? PC_eq_200 : 1'bz;  // Driver driver_3
  COUNTER counter_1 (
    .i1(CNT_AND), .i2(CNT_AND_I), .i3(CNT_AND_IA), .i4(CNT_TAD), .i5(CNT_TAD_I), .i6(CNT_TAD_IA),
    .i7(CNT_ISZ), .i8(CNT_ISZ_I), .i9(CNT_ISZ_IA), .i10(CNT_DCA), .i11(CNT_DCA_I), .i12(CNT_DCA_IA),
    .i13(CNT_JMS), .i14(CNT_JMS_I), .i15(CNT_JMS_IA), .i16(CNT_JMP), .i17(CNT_JMP_I), .i18(CNT_JMP_IA),
    .i19(CNT_OPR1), .i20(CNT_OPR2), .i21(IOT_DEVCPU), .i22(IOT_DEVHSR), .i23(IOT_DEVHSP), .i24(IOT_DEVKBD),
    .i25(IOT_DEVPRI), .i26(IOT_DEV5), .i27(IOT_DEV6), .i28(IOT_DEV7), .i29(IOT_DEV8), .i30(IOT_DEV9),
    .i31(IOT_DEV1x), .i32(IOT_DEV2x), .C(1'b0), .E(1'b1), .o1(counter_1_o1), .o2(counter_1_o2),
    .o3(counter_1_o3), .o4(counter_1_o4), .o5(counter_1_o5), .o6(counter_1_o6), .o7(counter_1_o7),
    .o8(counter_1_o8), .o9(counter_1_o9), .o10(counter_1_o10), .o11(counter_1_o11), .o12(counter_1_o12),
    .o13(counter_1_o13), .o14(counter_1_o14), .o15(counter_1_o15), .o16(counter_1_o16), .o17(counter_1_o17),
    .o18(counter_1_o18), .o19(counter_1_o19), .o20(counter_1_o20), .o21(counter_1_o21), .o22(counter_1_o22),
    .o23(counter_1_o23), .o24(counter_1_o24), .o25(counter_1_o25), .o26(counter_1_o26), .o27(counter_1_o27),
    .o28(counter_1_o28), .o29(counter_1_o29), .o30(counter_1_o30), .o31(counter_1_o31), .o32(counter_1_o32));
  AUTOCAPTURE autocapture_1 (
    .D(RAMDATA), .A({RA3, RA2, RA1, RA0}), .WR(RAM_WE), ._10(autocapture_1__10), ._11(autocapture_1__11),
    ._12(autocapture_1__12), ._13(autocapture_1__13), ._14(autocapture_1__14), ._15(autocapture_1__15),
    ._16(autocapture_1__16), ._17(autocapture_1__17));
  Counter #(.Bits(32)) INSTRUCTION_COUNT (.en(1'b1), .C(CK0), .clr(1'b0), .out(INSTRUCTION_COUNT_out));  // open: ovf
  Register #(.Bits(12)) register_1 (.D(RAMDATA), .C(and_1_out), .en(1'b1), .Q(register_1_q));
  Register #(.Bits(12)) register_2 (.D(BUS_PC), .C(xor_1_out), .en(1'b1), .Q(LATCHED_PC));
  // OC12 oc12_1: pin names not known; wires that end beside it: BUS_IR[6:0], BUS_PC[11:7], MP, IR2PC, PCIN[6:0], PCIN[11:7], PCIN
  LED led_1 (.in(IR2PC));
  // Probe on counter_1_o1
  // Probe on counter_1_o2
  // Probe on counter_1_o3
  // Probe on counter_1_o4
  // Probe on counter_1_o5
  // Probe on counter_1_o6
  // Probe on counter_1_o7
  // Probe on counter_1_o8
  // Probe on counter_1_o9
  // Probe on counter_1_o10
  // Probe on counter_1_o11
  // Probe on counter_1_o12
  // Probe on counter_1_o13
  // Probe on counter_1_o14
  // Probe on counter_1_o15
  // Probe on counter_1_o16
  // Probe on counter_1_o17
  // Probe on counter_1_o18
  // Probe on counter_1_o19
  // Probe on counter_1_o20
  // Probe on counter_1_o21
  // Probe on counter_1_o22
  // Probe on counter_1_o23
  // Probe on counter_1_o24
  // Probe on counter_1_o25
  // Probe on counter_1_o26
  // Probe on counter_1_o27
  // Probe on counter_1_o28
  // Probe on counter_1_o29
  // Probe on counter_1_o30
  // Probe on counter_1_o31
  // Probe on counter_1_o32
  // Probe on autocapture_1__10
  // Probe on autocapture_1__11
  // Probe on autocapture_1__12
  // Probe on autocapture_1__13
  // Probe on autocapture_1__14
  // Probe on autocapture_1__15
  // Probe on autocapture_1__16
  // Probe on autocapture_1__17
  // Probe on INSTRUCTION_COUNT_out
  // Probe on register_1_q
  // Probe on PCIN
  LED led_2 (.in(RAMD2PC));
  assign PCIN = RAMD2PC ? {DA3, DA2, DA1, DA0} : 12'bz;  // Driver driver_4
  LED led_3 (.in(IND2PC));
  assign PCIN = IND2PC ? {IND3, IND2, IND1, IND0} : 12'bz;  // Driver driver_5
  LED led_4 (.in(LINK));
  LED led_5 (.in(PC_CK));
  xor xor_2 (xor_2_out, PC_CK, driver_2_out);
  Seven_Seg_Hex seven_seg_hex_1 (.d({1'b0, BUS_PC[11:9]}), .dp(1'b0));
  Seven_Seg_Hex seven_seg_hex_2 (.d({1'b0, BUS_IR[11:9]}), .dp(1'b0));
  Seven_Seg_Hex seven_seg_hex_3 (.d({1'b0, AC[11:9]}), .dp(1'b0));
  Seven_Seg_Hex seven_seg_hex_4 (.d({1'b0, MQ[11:9]}), .dp(1'b0));
  Seven_Seg_Hex seven_seg_hex_5 (.d({1'b0, IND3}), .dp(1'b0));
  Seven_Seg_Hex seven_seg_hex_6 (.d({1'b0, RA3}), .dp(1'b0));
  Seven_Seg_Hex seven_seg_hex_7 (.d({1'b0, RAMDATA[11:9]}), .dp(1'b0));
  Seven_Seg_Hex seven_seg_hex_8 (.d({1'b0, PCIN[11:9]}), .dp(1'b0));
  Seven_Seg_Hex seven_seg_hex_9 (.d({1'b0, DA3}), .dp(1'b0));
  // Probe on {DA3, DA2, DA1, DA0}
  not not_1 (not_1_out, xor_2_out);
  LED led_6 (.in(PC_LD));
  Seven_Seg_Hex seven_seg_hex_10 (.d({1'b0, BUS_PC[8:6]}), .dp(1'b0));
  Seven_Seg_Hex seven_seg_hex_11 (.d({1'b0, BUS_IR[8:6]}), .dp(1'b0));
  Seven_Seg_Hex seven_seg_hex_12 (.d({1'b0, AC[8:6]}), .dp(1'b0));
  Seven_Seg_Hex seven_seg_hex_13 (.d({1'b0, MQ[8:6]}), .dp(1'b0));
  Seven_Seg_Hex seven_seg_hex_14 (.d({1'b0, IND2}), .dp(1'b0));
  Seven_Seg_Hex seven_seg_hex_15 (.d({1'b0, RA2}), .dp(1'b0));
  Seven_Seg_Hex seven_seg_hex_16 (.d({1'b0, RAMDATA[8:6]}), .dp(1'b0));
  Seven_Seg_Hex seven_seg_hex_17 (.d({1'b0, PCIN[8:6]}), .dp(1'b0));
  Seven_Seg_Hex seven_seg_hex_18 (.d({1'b0, DA2}), .dp(1'b0));
  LED led_7 (.in(RAMD2AC_ADD));
  CounterPreset #(.Bits(12)) PC (
    .en(1'b1), .C(not_1_out), .dir(1'b0), .in(PCIN), .ld(PC_LD), .clr(reset_1_out), .out(BUS_PC));  // open: ovf
  Seven_Seg_Hex seven_seg_hex_19 (.d({1'b0, BUS_PC[5:3]}), .dp(1'b0));
  Seven_Seg_Hex seven_seg_hex_20 (.d({1'b0, BUS_IR[5:3]}), .dp(1'b0));
  Seven_Seg_Hex seven_seg_hex_21 (.d({1'b0, AC[5:3]}), .dp(1'b0));
  Seven_Seg_Hex seven_seg_hex_22 (.d({1'b0, MQ[5:3]}), .dp(1'b0));
  Seven_Seg_Hex seven_seg_hex_23 (.d({1'b0, IND1}), .dp(1'b0));
  Seven_Seg_Hex seven_seg_hex_24 (.d({1'b0, RA1}), .dp(1'b0));
  Seven_Seg_Hex seven_seg_hex_25 (.d({1'b0, RAMDATA[5:3]}), .dp(1'b0));
  Seven_Seg_Hex seven_seg_hex_26 (.d({1'b0, PCIN[5:3]}), .dp(1'b0));
  Seven_Seg_Hex seven_seg_hex_27 (.d({1'b0, DA1}), .dp(1'b0));
  assign and_2_out = AC & {DA3, DA2, DA1, DA0};  // And and_2, 12 bits wide
  Add #(.Bits(12)) add_1 (.a(AC), .b({DA3, DA2, DA1, DA0}), .c_i(1'b0), .s(add_1_s), .c_o(add_1_c_o));
  and and_3 (and_3_out, add_1_c_o, RAMD2AC_ADD);
  LED led_8 (.in(and_3_out));
  Reset #(.invertOutput("false")) reset_1 (.out(reset_1_out));
  Seven_Seg_Hex seven_seg_hex_28 (.d({1'b0, BUS_PC[2:0]}), .dp(1'b0));
  Seven_Seg_Hex seven_seg_hex_29 (.d({1'b0, BUS_IR[2:0]}), .dp(1'b0));
  Seven_Seg_Hex seven_seg_hex_30 (.d({1'b0, AC[2:0]}), .dp(1'b0));
  Seven_Seg_Hex seven_seg_hex_31 (.d({1'b0, MQ[2:0]}), .dp(1'b0));
  Seven_Seg_Hex seven_seg_hex_32 (.d({1'b0, IND0}), .dp(1'b0));
  Seven_Seg_Hex seven_seg_hex_33 (.d({1'b0, RA0}), .dp(1'b0));
  Seven_Seg_Hex seven_seg_hex_34 (.d({1'b0, RAMDATA[2:0]}), .dp(1'b0));
  Seven_Seg_Hex seven_seg_hex_35 (.d({1'b0, PCIN[2:0]}), .dp(1'b0));
  Seven_Seg_Hex seven_seg_hex_36 (.d({1'b0, DA0}), .dp(1'b0));
  // Probe on AC
  // Probe on and_2_out
  // Probe on add_1_s
  LED led_9 (.in(add_1_c_o));
  // Probe on rotater_1_p4
  D_FF TAD_OVF (.D(and_3_out), .C(STB1), .Q(TAD_OVF_q));  // open: nQ
  LED led_10 (.in(STB1));
  // Probe on BUS_PC
  LED led_11 (.in(MQ_CK));
  LED led_12 (.in(TAD_OVF_q));
  // OC12 oc12_2: pin names not known; wires that end beside it: BUS_PC, BUS_IR[6:0], BUS_PC[11:7], MP, IR2RAMA, {RA2[0], RA1, RA0}, {RA3, RA2[2:1]}
  LED led_13 (.in(IR2RAMA));
  LED led_14 (.in(L_SKON));
  LED led_15 (.in(i_nop));
  LED led_16 (.in(AND));
  and and_4 (and_4_out, OPR_MQL, MQ_CK);
  assign driver_6_out = RAMD2AC_AND ? and_2_out : 12'bz;  // Driver driver_6
  LED led_17 (.in(RAMD2AC_AND));
  assign driver_6_out = RAMD2AC_ADD ? add_1_s : 12'bz;  // Driver driver_7
  LED led_18 (.in(RAMD2AC_ADD));
  assign driver_6_out = ROT2AC ? rotater_1_p4 : 12'bz;  // Driver driver_8
  LED led_19 (.in(ROT2AC));
  xor xor_3 (xor_3_out, TAD_OVF_q, rotater_1_p5);
  LED led_20 (.in(PC2ADDR));
  assign {RA3, RA2, RA1, RA0} = PC2ADDR ? BUS_PC : 12'bz;  // Driver driver_9
  LED led_21 (.in(L_ION));
  LED led_22 (.in(i_cla));
  LED led_23 (.in(TAD));
  // Probe on and_5_out
  LED led_24 (.in(and_4_out));
  // Probe on driver_6_out
  LED led_25 (.in(xor_3_out));
  // Probe on {RA3, RA2, RA1, RA0}
  LED led_26 (.in(IND2RAMA));
  LED led_27 (.in(L_IOF));
  LED led_28 (.in(L_SRQ));
  LED led_29 (.in(i_cll));
  LED led_30 (.in(ISZ));
  LED led_31 (.in(DCA));
  Button S (.out(S_out));
  Button I (.out(I_out));
  Button R (.out(R_out));
  Button H (.out(H_out));
  Button P (.out(PC_eq_200));
  assign and_5_out = AC & ~bitextender_1_out;  // And and_5, 12 bits wide
  LED led_32 (.in(AC_CK));
  D_FF u_LINK (.D(xor_3_out), .C(LINK_CK), .Q(LINK));  // open: nQ
  LED led_33 (.in(LINK_CK));
  LED led_34 (.in(RAM_WE));
  LED led_35 (.in(RAM_OE));
  assign {RA3, RA2, RA1, RA0} = IND2RAMA ? {IND3, IND2, IND1, IND0} : 12'bz;  // Driver driver_10
  LED led_36 (.in(L_GTF));
  LED led_37 (.in(i_cma));
  LED led_38 (.in(JMS));
  Monoflop #(.timerDelay(2)) monoflop_1 (.C(I_out), .R(1'b0), .Q(monoflop_1_q));  // open: nQ
  Monoflop monoflop_2 (.C(R_out), .R(1'b0), .Q(monoflop_2_q));  // open: nQ
  D_FF #(.Bits(12)) u_MQ (.D(and_5_out), .C(and_4_out), .Q(MQ));  // open: nQ
  D_FF #(.Bits(12)) u_AC (.D(driver_6_out), .C(AC_CK), .Q(AC));  // open: nQ
  or or_1 (or_1_out, OPR_CLA1, OPR_CLA2, OPR_CLA3, OPR_MQL, CLA, CLA_KCC);
  LED led_39 (.in(LINK));
  EEPROM #(.AddrBits(15), .isProgramMemory("true"), .Bits(12)) eeprom_1 (
    .A({3'b011, RA3, RA2, RA1, RA0}), .CS(1'b1), .WE(RAM_WE), .OE(RAM_OE), .D(RAMDATA));
  LED led_40 (.in(L_RTF));
  LED led_41 (.in(i_cml));
  LED led_42 (.in(JMP));
  Comparator #(.Bits(12)) comparator_2 (.a(BUS_PC), .b(12'h771), .eq(comparator_2_eq));  // open: gt, lt
  // Probe on MQ
  BitExtender #(.inputBits(1), .outputBits(12)) bitextender_1 (.in(OPR_CLA3), .out(bitextender_1_out));
  // Probe on AC
  BitExtender #(.inputBits(1), .outputBits(12)) bitextender_2 (.in(or_1_out), .out(bitextender_2_out));
  LED led_43 (.in(or_1_out));
  // Probe on RAMDATA
  LED led_44 (.in(L_SGT));
  LED led_45 (.in(L_CAF));
  LED led_46 (.in(i_iac));
  LED led_47 (.in(IOT));
  LED led_48 (.in(OPR));
  Switch #(.Closed("true")) HLT_ENABLED (.A(HALT), .B(HLT_ENABLED_b));
  assign and_6_out = AC & ~bitextender_2_out;  // And and_6, 12 bits wide
  or or_2 (or_2_out, CLL, OPR_CLL);
  LED led_49 (.in(OPR_CLL));
  assign {DA3, DA2, DA1, DA0} = RAM_OE ? RAMDATA : 12'bz;  // Driver driver_11
  assign RAMDATA = RAM_WE ? {DA3, DA2, DA1, DA0} : 12'bz;  // Driver driver_12
  LED led_50 (.in(i_rar));
  LED led_51 (.in(i_rtr));
  RS_FF_AS rs_ff_as_1 (.S(monoflop_2_q), .R(or_4_out), .Q(rs_ff_as_1_q));  // open: nQ
  PullDown pulldown_1 (.out(HLT_ENABLED_b));
  Switch #(.Closed("true")) BP_ENABLED (.A(comparator_2_eq), .B(BP_ENABLED_b));
  // Probe on and_6_out
  and and_7 (and_7_out, LINK, ~or_2_out);  // And
  LED led_52 (.in(FORCE4000));
  assign {DA3, DA2, DA1, DA0} = FORCE4000 ? 12'h800 : 12'bz;  // Driver driver_13
  LED led_53 (.in(PC2RAMD));
  assign {DA3, DA2, DA1, DA0} = PC2RAMD ? BUS_PC : 12'bz;  // Driver driver_14
  LED led_54 (.in(L_KCF));
  LED led_55 (.in(i_ral));
  LED led_56 (.in(NOIND));
  LED led_57 (.in(IND));
  or or_3 (or_3_out, monoflop_1_q, monoflop_2_q, rs_ff_as_1_q);
  or or_4 (or_4_out, H_out, BP_ENABLED_b, HLT_ENABLED_b);
  PullDown pulldown_2 (.out(BP_ENABLED_b));
  assign driver_15_out = OPR_MQA ? MQ : 12'bz;  // Driver driver_15
  LED led_58 (.in(OPR_MQA));
  LED led_59 (.in(and_7_out));
  // Probe on {DA3, DA2, DA1, DA0}
  LED led_60 (.in(INC2RAMD));
  assign {DA3, DA2, DA1, DA0} = INC2RAMD ? INC_s : 12'bz;  // Driver driver_16
  LED led_61 (.in(AC2RAMD));
  assign {DA3, DA2, DA1, DA0} = AC2RAMD ? AC : 12'bz;  // Driver driver_17
  LED led_62 (.in(L_KSF));
  LED led_63 (.in(L_KCC));
  LED led_64 (.in(i_rtl));
  LED led_65 (.in(AUTOIND));
  LED led_66 (.in(or_3_out));
  LED led_67 (.in(or_4_out));
  assign driver_15_out = OR_STATUS12 ? {LINK, 1'b0, IRQ_BUS, IRQ_INHIBIT, FLAG_GIE, {7{1'b0}}} : 12'bz;  // Driver driver_18
  LED led_68 (.in(OR_STATUS12));
  assign driver_15_out = OR_KBD12 ? KBD12 : 12'bz;  // Driver driver_19
  LED led_69 (.in(OR_KBD12));
  assign driver_15_out = OPR_OSR ? not_3_out : 12'bz;  // Driver driver_20
  LED led_70 (.in(OPR_OSR));
  // Probe on driver_15_out
  assign or_5_out = driver_15_out | and_6_out;  // Or or_5, 12 bits wide
  BitExtender #(.inputBits(1), .outputBits(12)) bitextender_3 (.in(OPR_CMA), .out(bitextender_3_out));
  LED led_71 (.in(OPR_CMA));
  or or_6 (or_6_out, RTF_LINK, OPR_CML);
  LED led_72 (.in(OPR_CML));
  not not_2 (not_2_out, IR_CK);
  LED led_73 (.in(IR_CK));
  LED led_74 (.in(L_KRS));
  LED led_75 (.in(i_skp));
  LED led_76 (.in(MP));
  D_FF d_ff_1 (.D(counter_2_ovf), .C(clk), .Q(d_ff_1_q));  // open: nQ
  // Probe on {LINK, 1'b0, IRQ_BUS, IRQ_INHIBIT, FLAG_GIE, {7{1'b0}}}
  // Probe on KBD12
  // Probe on not_3_out
  // Probe on or_5_out
  xor xor_4 (xor_4_out, and_7_out, or_6_out);
  // TRANSP_LATCH IR: pin names not known; wires that end beside it: {DA3, DA2, DA1, DA0}, {DA3, DA2, DA1, DA0}, not_2_out, BUS_IR, BUS_IR
  LED led_77 (.in(L_KIE));
  LED led_78 (.in(i_sza));
  LED led_79 (.in(i_sma));
  RS_FF_AS rs_ff_as_2 (.S(or_3_out), .R(d_ff_1_q), .Q(rs_ff_as_2_q));  // open: nQ
  assign xor_5_out = or_5_out ^ bitextender_3_out;  // XOr xor_5, 12 bits wide
  LED led_80 (.in(xor_4_out));
  // Probe on BUS_IR
  LED led_81 (.in(L_KRB));
  LED led_82 (.in(i_spa));
  and and_8 (and_8_out, rs_ff_as_2_q, clk);
  DipSwitch #(.dipDefault("true")) dipswitch_1 (.out(dipswitch_1_out[11]));
  assign not_3_out = ~dipswitch_1_out;  // Not not_3, 12 bits wide
  // Probe on xor_5_out
  LED led_83 (.in(OPR_IAC));
  xor xor_6 (xor_6_out, and_9_out, xor_4_out);
  D_FF #(.Bits(12)) u_IND (.D({DA3, DA2, DA1, DA0}), .C(IND_CK), .Q({IND3, IND2, IND1, IND0}));  // open: nQ
  LED led_84 (.in(IND_CK));
  LED led_85 (.in(L_TFL));
  LED led_86 (.in(i_sna));
  DipSwitch #(.dipDefault("true")) dipswitch_2 (.out(dipswitch_1_out[10]));
  DipSwitch #(.dipDefault("true")) dipswitch_3 (.out(dipswitch_1_out[9]));
  DipSwitch #(.dipDefault("true")) dipswitch_4 (.out(dipswitch_1_out[8]));
  Add #(.Bits(12)) add_2 (.a(xor_5_out), .b({12{1'b0}}), .c_i(OPR_IAC), .s(add_2_s), .c_o(add_2_c_o));
  LED led_87 (.in(xor_6_out));
  LED led_88 (.in(L_TSF));
  LED led_89 (.in(i_szl));
  LED led_90 (.in(i_snl));
  or or_7 (or_7_out, S_out, and_8_out);
  LED led_91 (.in(or_7_out));
  DipSwitch #(.dipDefault("true")) dipswitch_5 (.out(dipswitch_1_out[7]));
  DipSwitch #(.dipDefault("true")) dipswitch_6 (.out(dipswitch_1_out[6]));
  DipSwitch #(.dipDefault("true")) dipswitch_7 (.out(dipswitch_1_out[5]));
  // Probe on add_2_s
  and and_9 (and_9_out, add_2_c_o, OPR_IAC);
  LED led_92 (.in(add_2_c_o));
  // Probe on {IND3, IND2, IND1, IND0}
  LED led_93 (.in(DATA_CK));
  LED led_94 (.in(L_TCF));
  LED led_95 (.in(L_TPC));
  LED led_96 (.in(i_osr));
  Counter #(.Bits(5)) counter_2 (
    .en(1'b1), .C(or_7_out), .clr(counter_2_ovf), .out(counter_2_out), .ovf(counter_2_ovf));
  PullDown pulldown_3 (.out(counter_2_ovf));
  DipSwitch #(.dipDefault("true")) dipswitch_8 (.out(dipswitch_1_out[4]));
  DipSwitch #(.dipDefault("true")) dipswitch_9 (.out(dipswitch_1_out[3]));
  DipSwitch #(.dipDefault("true")) dipswitch_10 (.out(dipswitch_1_out[2]));
  LED led_97 (.in(and_9_out));
  D_FF #(.Bits(12)) DATA (.D({DA3, DA2, DA1, DA0}), .C(DATA_CK), .Q(LATCHEDDATA));  // open: nQ
  LED led_98 (.in(L_TSK));
  LED led_99 (.in(i_hlt));
  DipSwitch #(.dipDefault("true")) dipswitch_11 (.out(dipswitch_1_out[1]));
  DipSwitch #(.dipDefault("true")) dipswitch_12 (.out(dipswitch_1_out[0]));
  // Probe on LATCHEDDATA
  LED led_100 (.in(L_TLS));
  SEQUENCER sequencer_1 (
    .PH_FIRST(PH_FIRST), .PH_STB(PH_STB), .PH_LAST(PH_LAST),
    .STB_bits({STB9, STB8, STB7, STB6, STB5, STB4, STB3, STB2, STB1, STB0}),
    .CK_bits({CK9, CK8, CK7, CK6, CK5, CK4, CK3, CK2, CK1, CK0}), .CK_num(CK_NUM), .IN(counter_2_out));
  Seven_Seg_Hex seven_seg_hex_37 (.d(CK_NUM), .dp(1'b0));
  // ROTATER rotater_1: pin names not known; wires that end beside it: {OPR_RIGHT, OPR_LEFT, OPR_X2}, add_2_s, xor_6_out, rotater_1_p4, rotater_1_p5
  LED led_101 (.in(IND2INC));
  assign driver_21_out = IND2INC ? {IND3, IND2, IND1, IND0} : 12'bz;  // Driver driver_21
  LED led_102 (.in(LD2INC));
  assign driver_21_out = LD2INC ? LATCHEDDATA : 12'bz;  // Driver driver_22
  // Probe on LATCHED_PC
  // Probe on rotater_1_p4
  Seven_Seg_Hex seven_seg_hex_38 (.d(CK_NUM), .dp(1'b0));
  LED led_103 (.in(PH_FIRST));
  LED led_104 (.in(PH_STB));
  // Probe on INC_s
  // Probe on driver_21_out
  Seven_Seg_Hex seven_seg_hex_39 (.d(CK_NUM), .dp(1'b0));
  LED led_105 (.in(PH_FIRST));
  LED led_106 (.in(PH_STB));
  LED led_107 (.in(PH_FIRST));
  LED led_108 (.in(PH_STB));
  LED led_109 (.in(PH_LAST));
  Add #(.Bits(12)) INC (.a({12{1'b0}}), .b(driver_21_out), .c_i(1'b1), .s(INC_s), .c_o(INCZERO));
  LED led_110 (.in(PH_LAST));
  LED led_111 (.in(PH_LAST));
  nor nor_1 (nor_1_out, AC[0], AC[1], AC[2], AC[3], AC[4], AC[5], AC[6], AC[7], AC[8], AC[9], AC[10], AC[11]);
  LED led_112 (.in(nor_1_out));
  and and_10 (and_10_out, nor_1_out, OPR_SZASNA);
  and and_11 (and_11_out, AC[11], OPR_SMASPA);
  and and_12 (and_12_out, LINK, OPR_SNLSZL);
  and and_13 (CNT_AND, AND, NOIND, CK1);
  LED led_113 (.in(CNT_AND));
  and and_14 (and_14_out, AND, NOIND, STB1);
  LED led_114 (.in(and_14_out));
  LED led_115 (.in(and_10_out));
  LED led_116 (.in(and_11_out));
  LED led_117 (.in(and_12_out));
  assign IR2RAMA = CNT_AND ? CNT_AND : 1'bz;  // Driver driver_23
  assign RAMD2AC_AND = CNT_AND ? CNT_AND : 1'bz;  // Driver driver_24
  assign RAM_OE = CNT_AND ? CNT_AND : 1'bz;  // Driver driver_25
  assign AC_CK = and_14_out ? and_14_out : 1'bz;  // Driver driver_26
  or or_8 (or_8_out, and_10_out, and_11_out, and_12_out);
  xor xor_7 (SKIP, or_8_out, OPR_TSTINV);
  LED led_118 (.in(or_8_out));
  and and_15 (HALT, OPR_HLT, CK1);
  LED led_119 (.in(SKIP));
  LED led_120 (.in(HALT));
  and and_16 (CNT_AND_I, AND, IND, CK1);
  and and_17 (and_17_out, AND, IND, STB1);
  and and_18 (and_18_out, AND, IND, CK2);
  and and_19 (and_19_out, AND, IND, STB2);
  D_FF d_ff_2 (.D(FLAG_GIE), .C(CK1));  // open: Q, nQ
  assign IR2RAMA = CNT_AND_I ? CNT_AND_I : 1'bz;  // Driver driver_27
  LED led_121 (.in(CNT_AND_I));
  assign RAMD2IND = CNT_AND_I ? CNT_AND_I : 1'bz;  // Driver driver_28
  assign RAM_OE = CNT_AND_I ? CNT_AND_I : 1'bz;  // Driver driver_29
  Driver driver_30 (.in(CNT_AND_I), .en(CNT_AND_I));  // open: out
  Driver driver_31 (.in(CNT_AND_I), .en(CNT_AND_I));  // open: out
  Driver driver_32 (.in(and_17_out), .en(and_17_out));  // open: out
  LED led_122 (.in(and_17_out));
  Driver driver_33 (.in(and_17_out), .en(and_17_out));  // open: out
  Driver driver_34 (.in(and_17_out), .en(and_17_out));  // open: out
  assign IND_CK = and_17_out ? and_17_out : 1'bz;  // Driver driver_35
  Driver driver_36 (.in(and_17_out), .en(and_17_out));  // open: out
  assign IND2RAMA = and_18_out ? and_18_out : 1'bz;  // Driver driver_37
  LED led_123 (.in(and_18_out));
  assign RAMD2AC_AND = and_18_out ? and_18_out : 1'bz;  // Driver driver_38
  assign RAM_OE = and_18_out ? and_18_out : 1'bz;  // Driver driver_39
  Driver driver_40 (.in(and_18_out), .en(and_18_out));  // open: out
  Driver driver_41 (.in(and_18_out), .en(and_18_out));  // open: out
  Driver driver_42 (.in(and_19_out), .en(and_19_out));  // open: out
  LED led_124 (.in(and_19_out));
  Driver driver_43 (.in(and_19_out), .en(and_19_out));  // open: out
  Driver driver_44 (.in(and_19_out), .en(and_19_out));  // open: out
  assign AC_CK = and_19_out ? and_19_out : 1'bz;  // Driver driver_45
  Driver driver_46 (.in(and_19_out), .en(and_19_out));  // open: out
  and and_20 (and_20_out, IRQ_BUS, FLAG_GIE);
  LED led_125 (.in(and_20_out));
  and and_21 (and_21_out, CK0, 1'b1, ~and_20_out);  // And
  and and_22 (and_22_out, CK0, 1'b1, and_20_out);
  LED led_126 (.in(and_21_out));
  LED led_127 (.in(and_22_out));
  assign PC2ADDR = and_21_out ? and_21_out : 1'bz;  // Driver driver_47
  assign RAM_OE = and_21_out ? and_21_out : 1'bz;  // Driver driver_48
  assign IR_CK = and_21_out ? and_21_out : 1'bz;  // Driver driver_49
  assign PC_CK = and_21_out ? and_21_out : 1'bz;  // Driver driver_50
  assign IRQ_JMP = and_22_out ? and_22_out : 1'bz;  // Driver driver_51
  assign FORCE4000 = and_22_out ? and_22_out : 1'bz;  // Driver driver_52
  assign IR_CK = and_22_out ? and_22_out : 1'bz;  // Driver driver_53
  and and_23 (and_23_out, AND, AUTOIND, CK3);
  and and_24 (and_24_out, AND, AUTOIND, STB3);
  and and_25 (and_25_out, AND, AUTOIND, CK4);
  and and_26 (and_26_out, AND, AUTOIND, STB4);
  and and_27 (CNT_AND_IA, AND, AUTOIND, CK1);
  and and_28 (and_28_out, AND, AUTOIND, STB1);
  and and_29 (and_29_out, AND, AUTOIND, CK2);
  and and_30 (and_30_out, AND, AUTOIND, STB2);
  LED led_128 (.in(and_23_out));
  LED led_129 (.in(and_24_out));
  LED led_130 (.in(and_25_out));
  LED led_131 (.in(and_26_out));
  assign IR2RAMA = CNT_AND_IA ? CNT_AND_IA : 1'bz;  // Driver driver_54
  LED led_132 (.in(CNT_AND_IA));
  assign RAM_OE = CNT_AND_IA ? CNT_AND_IA : 1'bz;  // Driver driver_55
  assign IND2INC = CNT_AND_IA ? CNT_AND_IA : 1'bz;  // Driver driver_56
  LED led_133 (.in(and_28_out));
  assign IND_CK = and_28_out ? and_28_out : 1'bz;  // Driver driver_57
  assign INC2RAMD = and_29_out ? and_29_out : 1'bz;  // Driver driver_58
  LED led_134 (.in(and_29_out));
  assign IND2INC = and_29_out ? and_29_out : 1'bz;  // Driver driver_59
  assign IR2RAMA = and_29_out ? and_29_out : 1'bz;  // Driver driver_60
  LED led_135 (.in(and_30_out));
  assign RAM_WE = and_30_out ? and_30_out : 1'bz;  // Driver driver_61
  assign IR2RAMA = and_23_out ? and_23_out : 1'bz;  // Driver driver_62
  assign RAMD2IND = and_23_out ? and_23_out : 1'bz;  // Driver driver_63
  assign RAM_OE = and_23_out ? and_23_out : 1'bz;  // Driver driver_64
  Driver driver_65 (.in(and_23_out), .en(and_23_out));  // open: out
  Driver driver_66 (.in(and_23_out), .en(and_23_out));  // open: out
  Driver driver_67 (.in(and_24_out), .en(and_24_out));  // open: out
  Driver driver_68 (.in(and_24_out), .en(and_24_out));  // open: out
  Driver driver_69 (.in(and_24_out), .en(and_24_out));  // open: out
  assign IND_CK = and_24_out ? and_24_out : 1'bz;  // Driver driver_70
  Driver driver_71 (.in(and_24_out), .en(and_24_out));  // open: out
  assign IND2RAMA = and_25_out ? and_25_out : 1'bz;  // Driver driver_72
  assign RAMD2AC_AND = and_25_out ? and_25_out : 1'bz;  // Driver driver_73
  assign RAM_OE = and_25_out ? and_25_out : 1'bz;  // Driver driver_74
  Driver driver_75 (.in(and_25_out), .en(and_25_out));  // open: out
  Driver driver_76 (.in(and_25_out), .en(and_25_out));  // open: out
  Driver driver_77 (.in(and_26_out), .en(and_26_out));  // open: out
  Driver driver_78 (.in(and_26_out), .en(and_26_out));  // open: out
  Driver driver_79 (.in(and_26_out), .en(and_26_out));  // open: out
  assign AC_CK = and_26_out ? and_26_out : 1'bz;  // Driver driver_80
  Driver driver_81 (.in(and_26_out), .en(and_26_out));  // open: out
  or or_9 (or_9_out, IOT_ION, RTF_ION);
  and and_31 (and_31_out, CK1, or_9_out);
  LED led_136 (.in(or_9_out));
  Keyboard KEYBOARD (.C(clk), .en(KEYBOARD_av), .D(KEYBOARD_d), .av(KEYBOARD_av));
  LED led_137 (.in(and_31_out));
  // Probe on KEYBOARD_d[11:0]
  and and_32 (CNT_TAD, TAD, NOIND, CK1);
  and and_33 (and_33_out, TAD, NOIND, STB1);
  D_FF_AS d_ff_as_1 (.Set(1'b0), .D(and_31_out), .C(STB1), .Clr(IOT_IOF), .Q(IRQ_INHIBIT));  // open: nQ
  Register #(.Bits(12)) register_3 (.D(KEYBOARD_d[11:0]), .C(clk), .en(KEYBOARD_av), .Q(KBD12));
  or or_10 (or_10_out, KEYBOARD_av, 1'b0, 1'b0, 1'b0, 1'b0);
  or or_11 (or_11_out, IOT_KCF, IOT_KCC, IOT_KRB, 1'b0, 1'b0);
  and and_34 (and_34_out, IOT_KCC, CK1);
  and and_35 (and_35_out, IOT_KCC, STB1);
  and and_36 (and_36_out, IOT_KSF, CK1, FLAG_KBD);
  and and_37 (and_37_out, IOT_KRS, CK1);
  and and_38 (and_38_out, IOT_KRS, STB1);
  and and_39 (and_39_out, IOT_KRB, CK1);
  and and_40 (and_40_out, IOT_KRB, STB1);
  and and_41 (and_41_out, IOT_KIE, AC[0]);
  and and_42 (and_42_out, IOT_KIE, ~AC[0]);  // And
  LED led_138 (.in(CNT_TAD));
  LED led_139 (.in(and_33_out));
  and and_43 (and_43_out, IOT_CAF, CK1);
  LED led_140 (.in(and_43_out));
  and and_44 (and_44_out, IOT_CAF, STB1);
  LED led_141 (.in(and_44_out));
  and and_45 (and_45_out, IOT_SKON, FLAG_GIE, CK1);
  LED led_142 (.in(and_45_out));
  and and_46 (and_46_out, IOT_SKON, FLAG_GIE, STB1);
  LED led_143 (.in(and_46_out));
  and and_47 (and_47_out, IOT_SRQ, CK1, IRQ_BUS);
  LED led_144 (.in(and_47_out));
  and and_48 (and_48_out, FLAG_KBDIE, FLAG_PRN);
  LED led_145 (.in(and_48_out));
  and and_49 (and_49_out, FLAG_KBDIE, FLAG_KBD);
  LED led_146 (.in(and_49_out));
  // Probe on KBD12
  LED led_147 (.in(or_10_out));
  RS_FF_AS KBD (.S(or_10_out), .R(or_11_out), .Q(FLAG_KBD));  // open: nQ
  LED led_148 (.in(or_11_out));
  LED led_149 (.in(and_34_out));
  assign ROT2AC = and_34_out ? and_34_out : 1'bz;  // Driver driver_82
  assign CLA_KCC = and_34_out ? and_34_out : 1'bz;  // Driver driver_83
  LED led_150 (.in(and_35_out));
  assign AC_CK = and_35_out ? and_35_out : 1'bz;  // Driver driver_84
  LED led_151 (.in(and_36_out));
  assign PC_CK = and_36_out ? and_36_out : 1'bz;  // Driver driver_85
  LED led_152 (.in(and_37_out));
  assign ROT2AC = and_37_out ? and_37_out : 1'bz;  // Driver driver_86
  assign OR_KBD12 = and_37_out ? and_37_out : 1'bz;  // Driver driver_87
  LED led_153 (.in(and_38_out));
  assign AC_CK = and_38_out ? and_38_out : 1'bz;  // Driver driver_88
  LED led_154 (.in(and_39_out));
  assign ROT2AC = and_39_out ? and_39_out : 1'bz;  // Driver driver_89
  assign OR_KBD12 = and_39_out ? and_39_out : 1'bz;  // Driver driver_90
  assign CLA_KCC = and_39_out ? and_39_out : 1'bz;  // Driver driver_91
  LED led_155 (.in(and_40_out));
  assign AC_CK = and_40_out ? and_40_out : 1'bz;  // Driver driver_92
  LED led_156 (.in(and_41_out));
  LED led_157 (.in(and_42_out));
  assign IR2RAMA = CNT_TAD ? CNT_TAD : 1'bz;  // Driver driver_93
  assign RAMD2AC_ADD = CNT_TAD ? CNT_TAD : 1'bz;  // Driver driver_94
  assign RAM_OE = CNT_TAD ? CNT_TAD : 1'bz;  // Driver driver_95
  assign driver_96_out = CNT_TAD ? CNT_TAD : 1'bz;  // Driver driver_96
  assign driver_97_out = CNT_TAD ? CNT_TAD : 1'bz;  // Driver driver_97
  Driver driver_98 (.in(and_33_out), .en(and_33_out));  // open: out
  Driver driver_99 (.in(and_33_out), .en(and_33_out));  // open: out
  Driver driver_100 (.in(and_33_out), .en(and_33_out));  // open: out
  assign AC_CK = and_33_out ? and_33_out : 1'bz;  // Driver driver_101
  assign LINK_CK = and_33_out ? and_33_out : 1'bz;  // Driver driver_102
  D_FF_AS d_ff_as_2 (.Set(1'b0), .D(IRQ_INHIBIT), .C(STB1), .Clr(IOT_IOF), .Q(d_ff_as_2_q));  // open: nQ
  assign CLL = and_43_out ? and_43_out : 1'bz;  // Driver driver_103
  assign CLA = and_43_out ? and_43_out : 1'bz;  // Driver driver_104
  assign ROT2AC = and_43_out ? and_43_out : 1'bz;  // Driver driver_105
  assign AC_CK = and_44_out ? and_44_out : 1'bz;  // Driver driver_106
  assign LINK_CK = and_44_out ? and_44_out : 1'bz;  // Driver driver_107
  assign PC_CK = and_45_out ? and_45_out : 1'bz;  // Driver driver_108
  assign PC_CK = and_47_out ? and_47_out : 1'bz;  // Driver driver_109
  LED led_158 (.in(FLAG_KBD));
  or or_12 (or_12_out, and_41_out, IOT_CAF);
  or or_13 (IRQ_BUS, and_48_out, and_49_out, 1'b0, 1'b0, 1'b0);
  RS_FF_AS KBD_IE (.S(or_12_out), .R(and_42_out), .Q(FLAG_KBDIE));  // open: nQ
  D_FF_AS d_ff_as_3 (.Set(1'b0), .D(d_ff_as_2_q), .C(STB1), .Clr(IOT_IOF), .Q(d_ff_as_3_q));  // open: nQ
  LED led_159 (.in(IRQ_BUS));
  LED led_160 (.in(FLAG_KBDIE));
  and and_50 (and_50_out, d_ff_as_2_q, CK0);
  LED led_161 (.in(and_50_out));
  or or_14 (or_14_out, d_ff_as_2_q, 1'b0, 1'b0, 1'b0, 1'b0);
  or or_15 (or_15_out, IOT_CAF, IOT_IOF, RTF_IOF, IRQ_JMP, and_46_out);
  and and_51 (CNT_TAD_I, TAD, IND, CK1);
  and and_52 (and_52_out, TAD, IND, STB1);
  and and_53 (and_53_out, TAD, IND, CK2);
  and and_54 (and_54_out, TAD, IND, STB2);
  LED led_162 (.in(or_14_out));
  RS_FF_AS GIE (.S(or_14_out), .R(or_15_out), .Q(FLAG_GIE));  // open: nQ
  LED led_163 (.in(or_15_out));
  LED led_164 (.in(CNT_TAD_I));
  Driver driver_110 (.in(and_52_out), .en(and_52_out));  // open: out
  LED led_165 (.in(and_52_out));
  Driver driver_111 (.in(and_52_out), .en(and_52_out));  // open: out
  Driver driver_112 (.in(and_52_out), .en(and_52_out));  // open: out
  assign IND_CK = and_52_out ? and_52_out : 1'bz;  // Driver driver_113
  Driver driver_114 (.in(and_52_out), .en(and_52_out));  // open: out
  assign IND2RAMA = and_53_out ? and_53_out : 1'bz;  // Driver driver_115
  LED led_166 (.in(and_53_out));
  assign RAMD2AC_ADD = and_53_out ? and_53_out : 1'bz;  // Driver driver_116
  assign RAM_OE = and_53_out ? and_53_out : 1'bz;  // Driver driver_117
  Driver driver_118 (.in(and_53_out), .en(and_53_out));  // open: out
  Driver driver_119 (.in(and_53_out), .en(and_53_out));  // open: out
  Driver driver_120 (.in(and_54_out), .en(and_54_out));  // open: out
  LED led_167 (.in(and_54_out));
  Driver driver_121 (.in(and_54_out), .en(and_54_out));  // open: out
  Driver driver_122 (.in(and_54_out), .en(and_54_out));  // open: out
  assign AC_CK = and_54_out ? and_54_out : 1'bz;  // Driver driver_123
  assign LINK_CK = and_54_out ? and_54_out : 1'bz;  // Driver driver_124
  LED led_168 (.in(FLAG_GIE));
  assign IR2RAMA = CNT_TAD_I ? CNT_TAD_I : 1'bz;  // Driver driver_125
  assign RAMD2IND = CNT_TAD_I ? CNT_TAD_I : 1'bz;  // Driver driver_126
  assign RAM_OE = CNT_TAD_I ? CNT_TAD_I : 1'bz;  // Driver driver_127
  Driver driver_128 (.in(CNT_TAD_I), .en(CNT_TAD_I));  // open: out
  Driver driver_129 (.in(CNT_TAD_I), .en(CNT_TAD_I));  // open: out
  or or_16 (or_16_out, IOT_TPC, IOT_TLS);
  LED led_169 (.in(or_16_out));
  and and_55 (and_55_out, IOT_GTF, CK2);
  and and_56 (and_56_out, IOT_GTF, STB2);
  LED led_170 (.in(and_55_out));
  LED led_171 (.in(and_56_out));
  // Probe on {LINK, 1'b0, IRQ_BUS, IRQ_INHIBIT, FLAG_GIE, {7{1'b0}}}
  Terminal #(.termWidth(20), .termHeight(10)) PRINTER (.D({1'b0, AC[6:0]}), .C(or_16_out), .en(1'b1));
  and and_57 (CNT_TAD_IA, TAD, AUTOIND, CK1);
  and and_58 (and_58_out, TAD, AUTOIND, STB1);
  and and_59 (and_59_out, TAD, AUTOIND, CK2);
  and and_60 (and_60_out, TAD, AUTOIND, STB2);
  and and_61 (and_61_out, TAD, AUTOIND, CK3);
  and and_62 (and_62_out, TAD, AUTOIND, STB3);
  LED led_172 (.in(and_62_out));
  and and_63 (and_63_out, TAD, AUTOIND, CK4);
  LED led_173 (.in(and_63_out));
  and and_64 (and_64_out, TAD, AUTOIND, STB4);
  LED led_174 (.in(and_64_out));
  assign ROT2AC = and_55_out ? and_55_out : 1'bz;  // Driver driver_130
  assign CLA_KCC = and_55_out ? and_55_out : 1'bz;  // Driver driver_131
  assign OR_STATUS12 = and_55_out ? and_55_out : 1'bz;  // Driver driver_132
  assign AC_CK = and_56_out ? and_56_out : 1'bz;  // Driver driver_133
  and and_65 (RTF_IOF, IOT_RTF, CK1, AC[7]);
  and and_66 (RTF_ION, IOT_RTF, CK1, ~AC[7]);  // And
  and and_67 (and_67_out, IOT_RTF, CK1);
  and and_68 (and_68_out, IOT_RTF, STB1);
  and and_69 (RTF_LINK, IOT_RTF, AC[11]);
  Monoflop #(.timerDelay(50)) monoflop_3 (.C(or_16_out), .R(1'b0), .nQ(monoflop_3_nq));  // open: Q
  Monoflop #(.timerDelay(51)) monoflop_4 (.C(or_16_out), .R(1'b0), .Q(monoflop_4_q));  // open: nQ
  or or_17 (or_17_out, FLAG_PRN, FLAG_KBD);
  LED led_175 (.in(CNT_TAD_IA));
  LED led_176 (.in(and_58_out));
  LED led_177 (.in(and_59_out));
  LED led_178 (.in(and_60_out));
  assign IR2RAMA = and_61_out ? and_61_out : 1'bz;  // Driver driver_134
  LED led_179 (.in(and_61_out));
  assign RAMD2IND = and_61_out ? and_61_out : 1'bz;  // Driver driver_135
  assign RAM_OE = and_61_out ? and_61_out : 1'bz;  // Driver driver_136
  Driver driver_137 (.in(and_61_out), .en(and_61_out));  // open: out
  Driver driver_138 (.in(and_61_out), .en(and_61_out));  // open: out
  Driver driver_139 (.in(and_62_out), .en(and_62_out));  // open: out
  Driver driver_140 (.in(and_62_out), .en(and_62_out));  // open: out
  Driver driver_141 (.in(and_62_out), .en(and_62_out));  // open: out
  assign IND_CK = and_62_out ? and_62_out : 1'bz;  // Driver driver_142
  Driver driver_143 (.in(and_62_out), .en(and_62_out));  // open: out
  assign IND2RAMA = and_63_out ? and_63_out : 1'bz;  // Driver driver_144
  assign RAMD2AC_ADD = and_63_out ? and_63_out : 1'bz;  // Driver driver_145
  assign RAM_OE = and_63_out ? and_63_out : 1'bz;  // Driver driver_146
  Driver driver_147 (.in(and_63_out), .en(and_63_out));  // open: out
  Driver driver_148 (.in(and_63_out), .en(and_63_out));  // open: out
  Driver driver_149 (.in(and_64_out), .en(and_64_out));  // open: out
  Driver driver_150 (.in(and_64_out), .en(and_64_out));  // open: out
  Driver driver_151 (.in(and_64_out), .en(and_64_out));  // open: out
  assign AC_CK = and_64_out ? and_64_out : 1'bz;  // Driver driver_152
  assign LINK_CK = and_64_out ? and_64_out : 1'bz;  // Driver driver_153
  LED led_180 (.in(RTF_IOF));
  LED led_181 (.in(RTF_ION));
  LED led_182 (.in(and_67_out));
  LED led_183 (.in(and_68_out));
  LED led_184 (.in(RTF_LINK));
  and and_70 (and_70_out, monoflop_3_nq, monoflop_4_q);
  or or_18 (or_18_out, and_70_out, IOT_TFL, 1'b0, 1'b0, 1'b0);
  or or_19 (or_19_out, IOT_TCF, IOT_CAF, IOT_TLS, 1'b0, 1'b0);
  and and_71 (and_71_out, IOT_TSF, CK1, FLAG_PRN);
  and and_72 (and_72_out, IOT_TSK, CK1, or_17_out);
  assign IR2RAMA = CNT_TAD_IA ? CNT_TAD_IA : 1'bz;  // Driver driver_154
  assign RAM_OE = CNT_TAD_IA ? CNT_TAD_IA : 1'bz;  // Driver driver_155
  assign IND2INC = CNT_TAD_IA ? CNT_TAD_IA : 1'bz;  // Driver driver_156
  assign IND_CK = and_58_out ? and_58_out : 1'bz;  // Driver driver_157
  assign INC2RAMD = and_59_out ? and_59_out : 1'bz;  // Driver driver_158
  assign IND2INC = and_59_out ? and_59_out : 1'bz;  // Driver driver_159
  assign IR2RAMA = and_59_out ? and_59_out : 1'bz;  // Driver driver_160
  assign RAM_WE = and_60_out ? and_60_out : 1'bz;  // Driver driver_161
  assign CLL = and_67_out ? and_67_out : 1'bz;  // Driver driver_162
  assign LINK_CK = and_68_out ? and_68_out : 1'bz;  // Driver driver_163
  LED led_185 (.in(or_18_out));
  RS_FF_AS PRN (.S(or_18_out), .R(or_19_out), .Q(FLAG_PRN));  // open: nQ
  LED led_186 (.in(or_19_out));
  LED led_187 (.in(and_71_out));
  LED led_188 (.in(and_72_out));
  LED led_189 (.in(FLAG_PRN));
  assign PC_CK = and_71_out ? and_71_out : 1'bz;  // Driver driver_164
  assign PC_CK = and_72_out ? and_72_out : 1'bz;  // Driver driver_165
  // Probe on LATCHED_PC
  Seven_Seg_Hex seven_seg_hex_40 (.d(CK_NUM), .dp(1'b0));
  LED led_190 (.in(PH_FIRST));
  // Probe on AC
  LED led_191 (.in(LINK));
  LED led_192 (.in(FLAG_KBDIE));
  and and_73 (CNT_ISZ, ISZ, NOIND, CK1);
  and and_74 (and_74_out, ISZ, NOIND, STB1);
  and and_75 (and_75_out, ISZ, NOIND, CK2);
  and and_76 (and_76_out, ISZ, NOIND, CK3);
  and and_77 (and_77_out, ISZ, NOIND, INCZERO, CK4);
  LED led_193 (.in(PH_STB));
  LED led_194 (.in(PH_LAST));
  LED led_195 (.in(CNT_ISZ));
  LED led_196 (.in(and_74_out));
  LED led_197 (.in(and_75_out));
  LED led_198 (.in(and_76_out));
  LED led_199 (.in(and_77_out));
  assign IR2RAMA = CNT_ISZ ? CNT_ISZ : 1'bz;  // Driver driver_166
  assign RAM_OE = CNT_ISZ ? CNT_ISZ : 1'bz;  // Driver driver_167
  Driver driver_168 (.in(CNT_ISZ), .en(CNT_ISZ));  // open: out
  Driver driver_169 (.in(CNT_ISZ), .en(CNT_ISZ));  // open: out
  Driver driver_170 (.in(CNT_ISZ), .en(CNT_ISZ));  // open: out
  Driver driver_171 (.in(and_74_out), .en(and_74_out));  // open: out
  Driver driver_172 (.in(and_74_out), .en(and_74_out));  // open: out
  assign DATA_CK = and_74_out ? and_74_out : 1'bz;  // Driver driver_173
  assign LD2INC = and_74_out ? and_74_out : 1'bz;  // Driver driver_174
  Driver driver_175 (.in(and_74_out), .en(and_74_out));  // open: out
  assign IR2RAMA = and_75_out ? and_75_out : 1'bz;  // Driver driver_176
  assign RAM_WE = and_75_out ? and_75_out : 1'bz;  // Driver driver_177
  assign INC2RAMD = and_75_out ? and_75_out : 1'bz;  // Driver driver_178
  assign LD2INC = and_75_out ? and_75_out : 1'bz;  // Driver driver_179
  Driver driver_180 (.in(and_75_out), .en(and_75_out));  // open: out
  assign IR2RAMA = and_76_out ? and_76_out : 1'bz;  // Driver driver_181
  assign RAM_OE = and_76_out ? and_76_out : 1'bz;  // Driver driver_182
  assign LD2INC = and_76_out ? and_76_out : 1'bz;  // Driver driver_183
  Driver driver_184 (.in(and_76_out), .en(and_76_out));  // open: out
  Driver driver_185 (.in(and_76_out), .en(and_76_out));  // open: out
  assign PC_CK = and_77_out ? and_77_out : 1'bz;  // Driver driver_186
  assign LD2INC = and_77_out ? and_77_out : 1'bz;  // Driver driver_187
  Driver driver_188 (.in(and_77_out), .en(and_77_out));  // open: out
  Driver driver_189 (.in(and_77_out), .en(and_77_out));  // open: out
  Driver driver_190 (.in(and_77_out), .en(and_77_out));  // open: out
  Seven_Seg_Hex seven_seg_hex_41 (.d(CK_NUM), .dp(1'b0));
  // Probe on LATCHED_PC
  LED led_200 (.in(PH_FIRST));
  LED led_201 (.in(PH_STB));
  LED led_202 (.in(PH_LAST));
  and and_78 (CNT_ISZ_I, ISZ, IND, CK1);
  LED led_203 (.in(CNT_ISZ_I));
  and and_79 (and_79_out, ISZ, IND, STB1);
  LED led_204 (.in(and_79_out));
  and and_80 (and_80_out, ISZ, IND, CK2);
  LED led_205 (.in(and_80_out));
  and and_81 (and_81_out, ISZ, IND, STB2);
  LED led_206 (.in(and_81_out));
  and and_82 (and_82_out, ISZ, IND, CK3);
  LED led_207 (.in(and_82_out));
  and and_83 (and_83_out, ISZ, IND, CK4);
  LED led_208 (.in(and_83_out));
  and and_84 (and_84_out, ISZ, IND, INCZERO, CK5);
  LED led_209 (.in(and_84_out));
  assign IR2RAMA = CNT_ISZ_I ? CNT_ISZ_I : 1'bz;  // Driver driver_191
  assign RAMD2IND = CNT_ISZ_I ? CNT_ISZ_I : 1'bz;  // Driver driver_192
  assign RAM_OE = CNT_ISZ_I ? CNT_ISZ_I : 1'bz;  // Driver driver_193
  Driver driver_194 (.in(CNT_ISZ_I), .en(CNT_ISZ_I));  // open: out
  Driver driver_195 (.in(CNT_ISZ_I), .en(CNT_ISZ_I));  // open: out
  Driver driver_196 (.in(and_79_out), .en(and_79_out));  // open: out
  Driver driver_197 (.in(and_79_out), .en(and_79_out));  // open: out
  Driver driver_198 (.in(and_79_out), .en(and_79_out));  // open: out
  assign IND_CK = and_79_out ? and_79_out : 1'bz;  // Driver driver_199
  Driver driver_200 (.in(and_79_out), .en(and_79_out));  // open: out
  assign IND2RAMA = and_80_out ? and_80_out : 1'bz;  // Driver driver_201
  assign RAM_OE = and_80_out ? and_80_out : 1'bz;  // Driver driver_202
  Driver driver_203 (.in(and_80_out), .en(and_80_out));  // open: out
  Driver driver_204 (.in(and_80_out), .en(and_80_out));  // open: out
  Driver driver_205 (.in(and_80_out), .en(and_80_out));  // open: out
  Driver driver_206 (.in(and_81_out), .en(and_81_out));  // open: out
  Driver driver_207 (.in(and_81_out), .en(and_81_out));  // open: out
  assign DATA_CK = and_81_out ? and_81_out : 1'bz;  // Driver driver_208
  assign LD2INC = and_81_out ? and_81_out : 1'bz;  // Driver driver_209
  Driver driver_210 (.in(and_81_out), .en(and_81_out));  // open: out
  assign IND2RAMA = and_82_out ? and_82_out : 1'bz;  // Driver driver_211
  assign RAM_WE = and_82_out ? and_82_out : 1'bz;  // Driver driver_212
  assign INC2RAMD = and_82_out ? and_82_out : 1'bz;  // Driver driver_213
  assign LD2INC = and_82_out ? and_82_out : 1'bz;  // Driver driver_214
  Driver driver_215 (.in(and_82_out), .en(and_82_out));  // open: out
  assign IND2RAMA = and_83_out ? and_83_out : 1'bz;  // Driver driver_216
  assign RAM_OE = and_83_out ? and_83_out : 1'bz;  // Driver driver_217
  assign LD2INC = and_83_out ? and_83_out : 1'bz;  // Driver driver_218
  Driver driver_219 (.in(and_83_out), .en(and_83_out));  // open: out
  Driver driver_220 (.in(and_83_out), .en(and_83_out));  // open: out
  assign PC_CK = and_84_out ? and_84_out : 1'bz;  // Driver driver_221
  assign LD2INC = and_84_out ? and_84_out : 1'bz;  // Driver driver_222
  Driver driver_223 (.in(and_84_out), .en(and_84_out));  // open: out
  Driver driver_224 (.in(and_84_out), .en(and_84_out));  // open: out
  Driver driver_225 (.in(and_84_out), .en(and_84_out));  // open: out
  and and_85 (and_85_out, ISZ, AUTOIND, CK3);
  and and_86 (and_86_out, ISZ, AUTOIND, STB3);
  and and_87 (and_87_out, ISZ, AUTOIND, CK4);
  and and_88 (and_88_out, ISZ, AUTOIND, STB4);
  and and_89 (and_89_out, ISZ, AUTOIND, CK5);
  and and_90 (and_90_out, ISZ, AUTOIND, CK6);
  and and_91 (and_91_out, ISZ, AUTOIND, INCZERO, CK7);
  and and_92 (CNT_ISZ_IA, ISZ, AUTOIND, CK1);
  and and_93 (and_93_out, ISZ, AUTOIND, STB1);
  and and_94 (and_94_out, ISZ, AUTOIND, CK2);
  and and_95 (and_95_out, ISZ, AUTOIND, STB2);
  LED led_210 (.in(and_85_out));
  LED led_211 (.in(and_86_out));
  LED led_212 (.in(and_87_out));
  LED led_213 (.in(and_88_out));
  assign IND2RAMA = and_89_out ? and_89_out : 1'bz;  // Driver driver_226
  LED led_214 (.in(and_89_out));
  assign RAM_WE = and_89_out ? and_89_out : 1'bz;  // Driver driver_227
  assign INC2RAMD = and_89_out ? and_89_out : 1'bz;  // Driver driver_228
  assign LD2INC = and_89_out ? and_89_out : 1'bz;  // Driver driver_229
  Driver driver_230 (.in(and_89_out), .en(and_89_out));  // open: out
  assign IND2RAMA = and_90_out ? and_90_out : 1'bz;  // Driver driver_231
  LED led_215 (.in(and_90_out));
  assign RAM_OE = and_90_out ? and_90_out : 1'bz;  // Driver driver_232
  assign LD2INC = and_90_out ? and_90_out : 1'bz;  // Driver driver_233
  Driver driver_234 (.in(and_90_out), .en(and_90_out));  // open: out
  Driver driver_235 (.in(and_90_out), .en(and_90_out));  // open: out
  assign PC_CK = and_91_out ? and_91_out : 1'bz;  // Driver driver_236
  LED led_216 (.in(and_91_out));
  assign LD2INC = and_91_out ? and_91_out : 1'bz;  // Driver driver_237
  Driver driver_238 (.in(and_91_out), .en(and_91_out));  // open: out
  Driver driver_239 (.in(and_91_out), .en(and_91_out));  // open: out
  Driver driver_240 (.in(and_91_out), .en(and_91_out));  // open: out
  LED led_217 (.in(CNT_ISZ_IA));
  LED led_218 (.in(and_93_out));
  LED led_219 (.in(and_94_out));
  LED led_220 (.in(and_95_out));
  assign IR2RAMA = and_85_out ? and_85_out : 1'bz;  // Driver driver_241
  assign RAMD2IND = and_85_out ? and_85_out : 1'bz;  // Driver driver_242
  assign RAM_OE = and_85_out ? and_85_out : 1'bz;  // Driver driver_243
  Driver driver_244 (.in(and_85_out), .en(and_85_out));  // open: out
  Driver driver_245 (.in(and_85_out), .en(and_85_out));  // open: out
  Driver driver_246 (.in(and_86_out), .en(and_86_out));  // open: out
  Driver driver_247 (.in(and_86_out), .en(and_86_out));  // open: out
  Driver driver_248 (.in(and_86_out), .en(and_86_out));  // open: out
  assign IND_CK = and_86_out ? and_86_out : 1'bz;  // Driver driver_249
  Driver driver_250 (.in(and_86_out), .en(and_86_out));  // open: out
  assign IND2RAMA = and_87_out ? and_87_out : 1'bz;  // Driver driver_251
  assign RAM_OE = and_87_out ? and_87_out : 1'bz;  // Driver driver_252
  Driver driver_253 (.in(and_87_out), .en(and_87_out));  // open: out
  Driver driver_254 (.in(and_87_out), .en(and_87_out));  // open: out
  Driver driver_255 (.in(and_87_out), .en(and_87_out));  // open: out
  assign IND2RAMA = and_88_out ? and_88_out : 1'bz;  // Driver driver_256
  assign RAM_OE = and_88_out ? and_88_out : 1'bz;  // Driver driver_257
  assign DATA_CK = and_88_out ? and_88_out : 1'bz;  // Driver driver_258
  assign LD2INC = and_88_out ? and_88_out : 1'bz;  // Driver driver_259
  Driver driver_260 (.in(and_88_out), .en(and_88_out));  // open: out
  assign IR2RAMA = CNT_ISZ_IA ? CNT_ISZ_IA : 1'bz;  // Driver driver_261
  assign RAM_OE = CNT_ISZ_IA ? CNT_ISZ_IA : 1'bz;  // Driver driver_262
  assign IND2INC = CNT_ISZ_IA ? CNT_ISZ_IA : 1'bz;  // Driver driver_263
  assign IND_CK = and_93_out ? and_93_out : 1'bz;  // Driver driver_264
  assign INC2RAMD = and_94_out ? and_94_out : 1'bz;  // Driver driver_265
  assign IND2INC = and_94_out ? and_94_out : 1'bz;  // Driver driver_266
  assign IR2RAMA = and_94_out ? and_94_out : 1'bz;  // Driver driver_267
  assign RAM_WE = and_95_out ? and_95_out : 1'bz;  // Driver driver_268
  and and_96 (CNT_DCA, DCA, NOIND, CK1);
  LED led_221 (.in(CNT_DCA));
  and and_97 (and_97_out, DCA, NOIND, STB1);
  LED led_222 (.in(and_97_out));
  and and_98 (and_98_out, DCA, NOIND, CK2);
  LED led_223 (.in(and_98_out));
  assign IR2RAMA = CNT_DCA ? CNT_DCA : 1'bz;  // Driver driver_269
  assign AC2RAMD = CNT_DCA ? CNT_DCA : 1'bz;  // Driver driver_270
  Driver driver_271 (.in(CNT_DCA), .en(CNT_DCA));  // open: out
  Driver driver_272 (.in(CNT_DCA), .en(CNT_DCA));  // open: out
  Driver driver_273 (.in(CNT_DCA), .en(CNT_DCA));  // open: out
  Driver driver_274 (.in(and_97_out), .en(and_97_out));  // open: out
  Driver driver_275 (.in(and_97_out), .en(and_97_out));  // open: out
  assign RAM_WE = and_97_out ? and_97_out : 1'bz;  // Driver driver_276
  assign CLA = and_97_out ? and_97_out : 1'bz;  // Driver driver_277
  Driver driver_278 (.in(and_97_out), .en(and_97_out));  // open: out
  assign CLAx = and_98_out ? and_98_out : 1'bz;  // Driver driver_279
  assign ROT2AC = and_98_out ? and_98_out : 1'bz;  // Driver driver_280
  assign AC_CK = and_98_out ? and_98_out : 1'bz;  // Driver driver_281
  Driver driver_282 (.in(and_98_out), .en(and_98_out));  // open: out
  Driver driver_283 (.in(and_98_out), .en(and_98_out));  // open: out
  and and_99 (CNT_DCA_I, DCA, IND, CK1);
  and and_100 (and_100_out, DCA, IND, STB1);
  and and_101 (and_101_out, DCA, IND, CK2);
  and and_102 (and_102_out, DCA, IND, STB2);
  and and_103 (and_103_out, DCA, IND, CK3);
  LED led_224 (.in(CNT_DCA_I));
  LED led_225 (.in(and_100_out));
  LED led_226 (.in(and_101_out));
  LED led_227 (.in(and_102_out));
  LED led_228 (.in(and_103_out));
  assign IR2RAMA = CNT_DCA_I ? CNT_DCA_I : 1'bz;  // Driver driver_284
  assign RAMD2IND = CNT_DCA_I ? CNT_DCA_I : 1'bz;  // Driver driver_285
  assign RAM_OE = CNT_DCA_I ? CNT_DCA_I : 1'bz;  // Driver driver_286
  assign driver_287_out = CNT_DCA_I ? CNT_DCA_I : 1'bz;  // Driver driver_287
  assign driver_288_out = CNT_DCA_I ? CNT_DCA_I : 1'bz;  // Driver driver_288
  assign IR2RAMA = and_100_out ? and_100_out : 1'bz;  // Driver driver_289
  assign RAMD2IND = and_100_out ? and_100_out : 1'bz;  // Driver driver_290
  assign RAM_OE = and_100_out ? and_100_out : 1'bz;  // Driver driver_291
  assign IND_CK = and_100_out ? and_100_out : 1'bz;  // Driver driver_292
  assign driver_293_out = and_100_out ? and_100_out : 1'bz;  // Driver driver_293
  assign IND2RAMA = and_101_out ? and_101_out : 1'bz;  // Driver driver_294
  assign AC2RAMD = and_101_out ? and_101_out : 1'bz;  // Driver driver_295
  Driver driver_296 (.in(and_101_out), .en(and_101_out));  // open: out
  Driver driver_297 (.in(and_101_out), .en(and_101_out));  // open: out
  Driver driver_298 (.in(and_101_out), .en(and_101_out));  // open: out
  Driver driver_299 (.in(and_102_out), .en(and_102_out));  // open: out
  Driver driver_300 (.in(and_102_out), .en(and_102_out));  // open: out
  assign RAM_WE = and_102_out ? and_102_out : 1'bz;  // Driver driver_301
  assign CLA = and_102_out ? and_102_out : 1'bz;  // Driver driver_302
  Driver driver_303 (.in(and_102_out), .en(and_102_out));  // open: out
  assign CLAx = and_103_out ? and_103_out : 1'bz;  // Driver driver_304
  assign ROT2AC = and_103_out ? and_103_out : 1'bz;  // Driver driver_305
  assign AC_CK = and_103_out ? and_103_out : 1'bz;  // Driver driver_306
  Driver driver_307 (.in(and_103_out), .en(and_103_out));  // open: out
  Driver driver_308 (.in(and_103_out), .en(and_103_out));  // open: out
  and and_104 (CNT_DCA_IA, DCA, AUTOIND, CK1);
  and and_105 (and_105_out, DCA, AUTOIND, STB1);
  and and_106 (and_106_out, DCA, AUTOIND, CK2);
  and and_107 (and_107_out, DCA, AUTOIND, STB2);
  and and_108 (and_108_out, DCA, AUTOIND, CK3);
  and and_109 (and_109_out, DCA, AUTOIND, STB3);
  and and_110 (and_110_out, DCA, AUTOIND, CK4);
  LED led_229 (.in(and_110_out));
  and and_111 (and_111_out, DCA, AUTOIND, STB4);
  LED led_230 (.in(and_111_out));
  and and_112 (and_112_out, DCA, AUTOIND, CK5);
  LED led_231 (.in(and_112_out));
  LED led_232 (.in(CNT_DCA_IA));
  LED led_233 (.in(and_105_out));
  LED led_234 (.in(and_106_out));
  LED led_235 (.in(and_107_out));
  assign IR2RAMA = and_108_out ? and_108_out : 1'bz;  // Driver driver_309
  LED led_236 (.in(and_108_out));
  assign RAMD2IND = and_108_out ? and_108_out : 1'bz;  // Driver driver_310
  assign RAM_OE = and_108_out ? and_108_out : 1'bz;  // Driver driver_311
  assign driver_312_out = and_108_out ? and_108_out : 1'bz;  // Driver driver_312
  assign driver_313_out = and_108_out ? and_108_out : 1'bz;  // Driver driver_313
  Driver driver_314 (.in(and_109_out), .en(and_109_out));  // open: out
  LED led_237 (.in(and_109_out));
  Driver driver_315 (.in(and_109_out), .en(and_109_out));  // open: out
  Driver driver_316 (.in(and_109_out), .en(and_109_out));  // open: out
  assign IND_CK = and_109_out ? and_109_out : 1'bz;  // Driver driver_317
  assign driver_318_out = and_109_out ? and_109_out : 1'bz;  // Driver driver_318
  assign IND2RAMA = and_110_out ? and_110_out : 1'bz;  // Driver driver_319
  assign AC2RAMD = and_110_out ? and_110_out : 1'bz;  // Driver driver_320
  Driver driver_321 (.in(and_110_out), .en(and_110_out));  // open: out
  Driver driver_322 (.in(and_110_out), .en(and_110_out));  // open: out
  Driver driver_323 (.in(and_110_out), .en(and_110_out));  // open: out
  Driver driver_324 (.in(and_111_out), .en(and_111_out));  // open: out
  Driver driver_325 (.in(and_111_out), .en(and_111_out));  // open: out
  assign RAM_WE = and_111_out ? and_111_out : 1'bz;  // Driver driver_326
  assign CLA = and_111_out ? and_111_out : 1'bz;  // Driver driver_327
  Driver driver_328 (.in(and_111_out), .en(and_111_out));  // open: out
  assign CLAx = and_112_out ? and_112_out : 1'bz;  // Driver driver_329
  assign ROT2AC = and_112_out ? and_112_out : 1'bz;  // Driver driver_330
  assign AC_CK = and_112_out ? and_112_out : 1'bz;  // Driver driver_331
  Driver driver_332 (.in(and_112_out), .en(and_112_out));  // open: out
  Driver driver_333 (.in(and_112_out), .en(and_112_out));  // open: out
  assign IR2RAMA = CNT_DCA_IA ? CNT_DCA_IA : 1'bz;  // Driver driver_334
  assign RAM_OE = CNT_DCA_IA ? CNT_DCA_IA : 1'bz;  // Driver driver_335
  assign IND2INC = CNT_DCA_IA ? CNT_DCA_IA : 1'bz;  // Driver driver_336
  assign IND_CK = and_105_out ? and_105_out : 1'bz;  // Driver driver_337
  assign INC2RAMD = and_106_out ? and_106_out : 1'bz;  // Driver driver_338
  assign IND2INC = and_106_out ? and_106_out : 1'bz;  // Driver driver_339
  assign IR2RAMA = and_106_out ? and_106_out : 1'bz;  // Driver driver_340
  assign RAM_WE = and_107_out ? and_107_out : 1'bz;  // Driver driver_341
  and and_113 (CNT_JMS, JMS, NOIND, CK1);
  and and_114 (and_114_out, JMS, NOIND, STB1);
  and and_115 (and_115_out, JMS, NOIND, CK2);
  and and_116 (and_116_out, JMS, NOIND, STB2);
  and and_117 (and_117_out, JMS, NOIND, STB3);
  LED led_238 (.in(CNT_JMS));
  Driver driver_342 (.in(and_114_out), .en(and_114_out));  // open: out
  LED led_239 (.in(and_114_out));
  Driver driver_343 (.in(and_114_out), .en(and_114_out));  // open: out
  assign RAM_WE = and_114_out ? and_114_out : 1'bz;  // Driver driver_344
  assign IR2PC = and_114_out ? and_114_out : 1'bz;  // Driver driver_345
  assign driver_346_out = and_114_out ? and_114_out : 1'bz;  // Driver driver_346
  LED led_240 (.in(and_115_out));
  LED led_241 (.in(and_116_out));
  LED led_242 (.in(and_117_out));
  assign PC2RAMD = CNT_JMS ? CNT_JMS : 1'bz;  // Driver driver_347
  assign IR2RAMA = CNT_JMS ? CNT_JMS : 1'bz;  // Driver driver_348
  assign driver_349_out = CNT_JMS ? CNT_JMS : 1'bz;  // Driver driver_349
  assign driver_350_out = CNT_JMS ? CNT_JMS : 1'bz;  // Driver driver_350
  assign driver_351_out = CNT_JMS ? CNT_JMS : 1'bz;  // Driver driver_351
  assign IR2PC = and_115_out ? and_115_out : 1'bz;  // Driver driver_352
  assign PC_LD = and_115_out ? and_115_out : 1'bz;  // Driver driver_353
  Driver driver_354 (.in(and_115_out), .en(and_115_out));  // open: out
  assign driver_355_out = and_115_out ? and_115_out : 1'bz;  // Driver driver_355
  assign driver_356_out = and_115_out ? and_115_out : 1'bz;  // Driver driver_356
  Driver driver_357 (.in(and_116_out), .en(and_116_out));  // open: out
  Driver driver_358 (.in(and_116_out), .en(and_116_out));  // open: out
  assign PC_CK = and_116_out ? and_116_out : 1'bz;  // Driver driver_359
  assign driver_360_out = and_116_out ? and_116_out : 1'bz;  // Driver driver_360
  assign driver_361_out = and_116_out ? and_116_out : 1'bz;  // Driver driver_361
  assign PC_CK = and_117_out ? and_117_out : 1'bz;  // Driver driver_362
  assign driver_363_out = and_117_out ? and_117_out : 1'bz;  // Driver driver_363
  assign driver_364_out = and_117_out ? and_117_out : 1'bz;  // Driver driver_364
  assign driver_365_out = and_117_out ? and_117_out : 1'bz;  // Driver driver_365
  Driver driver_366 (.in(and_117_out), .en(and_117_out));  // open: out
  and and_118 (CNT_JMS_I, JMS, IND, CK1);
  and and_119 (and_119_out, JMS, IND, STB1);
  and and_120 (and_120_out, JMS, IND, CK2);
  and and_121 (and_121_out, JMS, IND, CK3);
  and and_122 (and_122_out, JMS, IND, CK4);
  and and_123 (and_123_out, JMS, IND, CK5);
  and and_124 (and_124_out, JMS, IND, CK6);
  LED led_243 (.in(CNT_JMS_I));
  LED led_244 (.in(and_119_out));
  LED led_245 (.in(and_120_out));
  LED led_246 (.in(and_121_out));
  LED led_247 (.in(and_122_out));
  LED led_248 (.in(and_123_out));
  LED led_249 (.in(and_124_out));
  assign IR2RAMA = CNT_JMS_I ? CNT_JMS_I : 1'bz;  // Driver driver_367
  assign RAMD2IND = CNT_JMS_I ? CNT_JMS_I : 1'bz;  // Driver driver_368
  assign RAM_OE = CNT_JMS_I ? CNT_JMS_I : 1'bz;  // Driver driver_369
  assign driver_370_out = CNT_JMS_I ? CNT_JMS_I : 1'bz;  // Driver driver_370
  assign driver_371_out = CNT_JMS_I ? CNT_JMS_I : 1'bz;  // Driver driver_371
  Driver driver_372 (.in(and_119_out), .en(and_119_out));  // open: out
  Driver driver_373 (.in(and_119_out), .en(and_119_out));  // open: out
  Driver driver_374 (.in(and_119_out), .en(and_119_out));  // open: out
  assign IND_CK = and_119_out ? and_119_out : 1'bz;  // Driver driver_375
  assign driver_376_out = and_119_out ? and_119_out : 1'bz;  // Driver driver_376
  assign IND2RAMA = and_120_out ? and_120_out : 1'bz;  // Driver driver_377
  assign PC2RAMD = and_120_out ? and_120_out : 1'bz;  // Driver driver_378
  Driver driver_379 (.in(and_120_out), .en(and_120_out));  // open: out
  assign driver_380_out = and_120_out ? and_120_out : 1'bz;  // Driver driver_380
  assign driver_381_out = and_120_out ? and_120_out : 1'bz;  // Driver driver_381
  assign IND2RAMA = and_121_out ? and_121_out : 1'bz;  // Driver driver_382
  assign PC2RAMD = and_121_out ? and_121_out : 1'bz;  // Driver driver_383
  assign RAM_WE = and_121_out ? and_121_out : 1'bz;  // Driver driver_384
  assign PC_LD = and_121_out ? and_121_out : 1'bz;  // Driver driver_385
  assign IND2PC = and_121_out ? and_121_out : 1'bz;  // Driver driver_386
  assign IND2PC = and_122_out ? and_122_out : 1'bz;  // Driver driver_387
  assign PC_LD = and_122_out ? and_122_out : 1'bz;  // Driver driver_388
  assign PC_CK = and_122_out ? and_122_out : 1'bz;  // Driver driver_389
  Driver driver_390 (.in(and_122_out), .en(and_122_out));  // open: out
  assign driver_391_out = and_122_out ? and_122_out : 1'bz;  // Driver driver_391
  assign IND2PC = and_123_out ? and_123_out : 1'bz;  // Driver driver_392
  assign PC_LD = and_123_out ? and_123_out : 1'bz;  // Driver driver_393
  assign driver_394_out = and_123_out ? and_123_out : 1'bz;  // Driver driver_394
  assign driver_395_out = and_123_out ? and_123_out : 1'bz;  // Driver driver_395
  assign driver_396_out = and_123_out ? and_123_out : 1'bz;  // Driver driver_396
  assign PC_CK = and_124_out ? and_124_out : 1'bz;  // Driver driver_397
  assign driver_398_out = and_124_out ? and_124_out : 1'bz;  // Driver driver_398
  assign driver_399_out = and_124_out ? and_124_out : 1'bz;  // Driver driver_399
  assign driver_400_out = and_124_out ? and_124_out : 1'bz;  // Driver driver_400
  Driver driver_401 (.in(and_124_out), .en(and_124_out));  // open: out
  and and_125 (and_125_out, JMS, AUTOIND, CK3);
  and and_126 (and_126_out, JMS, AUTOIND, STB3);
  and and_127 (and_127_out, JMS, AUTOIND, CK4);
  and and_128 (and_128_out, JMS, AUTOIND, CK5);
  and and_129 (and_129_out, JMS, AUTOIND, CK6);
  and and_130 (and_130_out, JMS, AUTOIND, CK7);
  and and_131 (and_131_out, JMS, AUTOIND, CK8);
  and and_132 (CNT_JMS_IA, JMS, AUTOIND, CK1);
  and and_133 (and_133_out, JMS, AUTOIND, STB1);
  and and_134 (and_134_out, JMS, AUTOIND, CK2);
  and and_135 (and_135_out, JMS, AUTOIND, STB2);
  LED led_250 (.in(and_125_out));
  LED led_251 (.in(and_126_out));
  LED led_252 (.in(and_127_out));
  LED led_253 (.in(and_128_out));
  LED led_254 (.in(and_129_out));
  LED led_255 (.in(and_130_out));
  LED led_256 (.in(and_131_out));
  assign IR2RAMA = CNT_JMS_IA ? CNT_JMS_IA : 1'bz;  // Driver driver_402
  LED led_257 (.in(CNT_JMS_IA));
  assign RAM_OE = CNT_JMS_IA ? CNT_JMS_IA : 1'bz;  // Driver driver_403
  assign IND2INC = CNT_JMS_IA ? CNT_JMS_IA : 1'bz;  // Driver driver_404
  LED led_258 (.in(and_133_out));
  assign IND_CK = and_133_out ? and_133_out : 1'bz;  // Driver driver_405
  assign INC2RAMD = and_134_out ? and_134_out : 1'bz;  // Driver driver_406
  LED led_259 (.in(and_134_out));
  assign IND2INC = and_134_out ? and_134_out : 1'bz;  // Driver driver_407
  assign IR2RAMA = and_134_out ? and_134_out : 1'bz;  // Driver driver_408
  LED led_260 (.in(and_135_out));
  assign RAM_WE = and_135_out ? and_135_out : 1'bz;  // Driver driver_409
  assign IR2RAMA = and_125_out ? and_125_out : 1'bz;  // Driver driver_410
  assign RAMD2IND = and_125_out ? and_125_out : 1'bz;  // Driver driver_411
  assign RAM_OE = and_125_out ? and_125_out : 1'bz;  // Driver driver_412
  assign driver_413_out = and_125_out ? and_125_out : 1'bz;  // Driver driver_413
  assign driver_414_out = and_125_out ? and_125_out : 1'bz;  // Driver driver_414
  Driver driver_415 (.in(and_126_out), .en(and_126_out));  // open: out
  Driver driver_416 (.in(and_126_out), .en(and_126_out));  // open: out
  Driver driver_417 (.in(and_126_out), .en(and_126_out));  // open: out
  assign IND_CK = and_126_out ? and_126_out : 1'bz;  // Driver driver_418
  assign driver_419_out = and_126_out ? and_126_out : 1'bz;  // Driver driver_419
  assign IND2RAMA = and_127_out ? and_127_out : 1'bz;  // Driver driver_420
  assign PC2RAMD = and_127_out ? and_127_out : 1'bz;  // Driver driver_421
  Driver driver_422 (.in(and_127_out), .en(and_127_out));  // open: out
  assign driver_423_out = and_127_out ? and_127_out : 1'bz;  // Driver driver_423
  assign driver_424_out = and_127_out ? and_127_out : 1'bz;  // Driver driver_424
  assign IND2RAMA = and_128_out ? and_128_out : 1'bz;  // Driver driver_425
  assign PC2RAMD = and_128_out ? and_128_out : 1'bz;  // Driver driver_426
  assign RAM_WE = and_128_out ? and_128_out : 1'bz;  // Driver driver_427
  assign PC_LD = and_128_out ? and_128_out : 1'bz;  // Driver driver_428
  assign IND2PC = and_128_out ? and_128_out : 1'bz;  // Driver driver_429
  assign IND2PC = and_129_out ? and_129_out : 1'bz;  // Driver driver_430
  assign PC_LD = and_129_out ? and_129_out : 1'bz;  // Driver driver_431
  assign PC_CK = and_129_out ? and_129_out : 1'bz;  // Driver driver_432
  Driver driver_433 (.in(and_129_out), .en(and_129_out));  // open: out
  assign driver_434_out = and_129_out ? and_129_out : 1'bz;  // Driver driver_434
  Driver driver_435 (.in(and_130_out), .en(and_130_out));  // open: out
  Driver driver_436 (.in(and_130_out), .en(and_130_out));  // open: out
  assign driver_437_out = and_130_out ? and_130_out : 1'bz;  // Driver driver_437
  assign driver_438_out = and_130_out ? and_130_out : 1'bz;  // Driver driver_438
  assign driver_439_out = and_130_out ? and_130_out : 1'bz;  // Driver driver_439
  assign PC_CK = and_131_out ? and_131_out : 1'bz;  // Driver driver_440
  assign driver_441_out = and_131_out ? and_131_out : 1'bz;  // Driver driver_441
  assign driver_442_out = and_131_out ? and_131_out : 1'bz;  // Driver driver_442
  assign driver_443_out = and_131_out ? and_131_out : 1'bz;  // Driver driver_443
  Driver driver_444 (.in(and_131_out), .en(and_131_out));  // open: out
  and and_136 (CNT_JMP, JMP, NOIND, CK1);
  and and_137 (and_137_out, JMP, NOIND, STB1);
  LED led_261 (.in(CNT_JMP));
  LED led_262 (.in(and_137_out));
  assign IR2PC = CNT_JMP ? CNT_JMP : 1'bz;  // Driver driver_445
  assign PC_LD = CNT_JMP ? CNT_JMP : 1'bz;  // Driver driver_446
  assign PC_CK = and_137_out ? and_137_out : 1'bz;  // Driver driver_447
  and and_138 (CNT_JMP_I, JMP, IND, CK1);
  and and_139 (and_139_out, JMP, IND, STB1);
  LED led_263 (.in(CNT_JMP_I));
  LED led_264 (.in(and_139_out));
  assign IR2RAMA = CNT_JMP_I ? CNT_JMP_I : 1'bz;  // Driver driver_448
  assign RAMD2PC = CNT_JMP_I ? CNT_JMP_I : 1'bz;  // Driver driver_449
  assign RAM_OE = CNT_JMP_I ? CNT_JMP_I : 1'bz;  // Driver driver_450
  assign PC_LD = CNT_JMP_I ? CNT_JMP_I : 1'bz;  // Driver driver_451
  assign driver_452_out = CNT_JMP_I ? CNT_JMP_I : 1'bz;  // Driver driver_452
  Driver driver_453 (.in(and_139_out), .en(and_139_out));  // open: out
  Driver driver_454 (.in(and_139_out), .en(and_139_out));  // open: out
  Driver driver_455 (.in(and_139_out), .en(and_139_out));  // open: out
  assign PC_LD = and_139_out ? and_139_out : 1'bz;  // Driver driver_456
  assign PC_CK = and_139_out ? and_139_out : 1'bz;  // Driver driver_457
  and and_140 (and_140_out, JMP, AUTOIND, CK3);
  and and_141 (and_141_out, JMP, AUTOIND, STB3);
  and and_142 (CNT_JMP_IA, JMP, AUTOIND, CK1);
  and and_143 (and_143_out, JMP, AUTOIND, STB1);
  and and_144 (and_144_out, JMP, AUTOIND, CK2);
  and and_145 (and_145_out, JMP, AUTOIND, STB2);
  LED led_265 (.in(and_140_out));
  LED led_266 (.in(and_141_out));
  LED led_267 (.in(CNT_JMP_IA));
  LED led_268 (.in(and_143_out));
  LED led_269 (.in(and_144_out));
  LED led_270 (.in(and_145_out));
  assign IR2RAMA = and_140_out ? and_140_out : 1'bz;  // Driver driver_458
  assign RAMD2PC = and_140_out ? and_140_out : 1'bz;  // Driver driver_459
  assign RAM_OE = and_140_out ? and_140_out : 1'bz;  // Driver driver_460
  assign PC_LD = and_140_out ? and_140_out : 1'bz;  // Driver driver_461
  assign driver_462_out = and_140_out ? and_140_out : 1'bz;  // Driver driver_462
  Driver driver_463 (.in(and_141_out), .en(and_141_out));  // open: out
  Driver driver_464 (.in(and_141_out), .en(and_141_out));  // open: out
  Driver driver_465 (.in(and_141_out), .en(and_141_out));  // open: out
  Driver driver_466 (.in(and_141_out), .en(and_141_out));  // open: out
  assign PC_CK = and_141_out ? and_141_out : 1'bz;  // Driver driver_467
  assign IR2RAMA = CNT_JMP_IA ? CNT_JMP_IA : 1'bz;  // Driver driver_468
  assign RAM_OE = CNT_JMP_IA ? CNT_JMP_IA : 1'bz;  // Driver driver_469
  assign IND2INC = CNT_JMP_IA ? CNT_JMP_IA : 1'bz;  // Driver driver_470
  assign IND_CK = and_143_out ? and_143_out : 1'bz;  // Driver driver_471
  assign INC2RAMD = and_144_out ? and_144_out : 1'bz;  // Driver driver_472
  assign IND2INC = and_144_out ? and_144_out : 1'bz;  // Driver driver_473
  assign IR2RAMA = and_144_out ? and_144_out : 1'bz;  // Driver driver_474
  assign RAM_WE = and_145_out ? and_145_out : 1'bz;  // Driver driver_475
  and and_146 (CNT_OPR1, OPR1, 1'b1, CK1);
  and and_147 (and_147_out, OPR1, 1'b1, STB1);
  LED led_271 (.in(CNT_OPR1));
  LED led_272 (.in(and_147_out));
  assign ROT2AC = CNT_OPR1 ? CNT_OPR1 : 1'bz;  // Driver driver_476
  assign LINK_CK = and_147_out ? and_147_out : 1'bz;  // Driver driver_477
  assign AC_CK = and_147_out ? and_147_out : 1'bz;  // Driver driver_478
  and and_148 (CNT_OPR2, OPR2, 1'b1, CK1);
  and and_149 (and_149_out, OPR2, SKIP, STB1);
  and and_150 (and_150_out, OPR2, 1'b1, CK2);
  LED led_273 (.in(and_150_out));
  and and_151 (and_151_out, OPR2, 1'b1, STB2);
  assign ROT2AC = CNT_OPR2 ? CNT_OPR2 : 1'bz;  // Driver driver_479
  LED led_274 (.in(CNT_OPR2));
  Driver driver_480 (.in(CNT_OPR2), .en(CNT_OPR2));  // open: out
  Driver driver_481 (.in(CNT_OPR2), .en(CNT_OPR2));  // open: out
  Driver driver_482 (.in(CNT_OPR2), .en(CNT_OPR2));  // open: out
  Driver driver_483 (.in(CNT_OPR2), .en(CNT_OPR2));  // open: out
  assign driver_484_out = and_149_out ? and_149_out : 1'bz;  // Driver driver_484
  LED led_275 (.in(and_149_out));
  assign PC_CK = and_149_out ? and_149_out : 1'bz;  // Driver driver_485
  Driver driver_486 (.in(and_149_out), .en(and_149_out));  // open: out
  Driver driver_487 (.in(and_149_out), .en(and_149_out));  // open: out
  Driver driver_488 (.in(and_149_out), .en(and_149_out));  // open: out
  assign ROT2AC = and_150_out ? and_150_out : 1'bz;  // Driver driver_489
  Driver driver_490 (.in(and_150_out), .en(and_150_out));  // open: out
  Driver driver_491 (.in(and_150_out), .en(and_150_out));  // open: out
  Driver driver_492 (.in(and_150_out), .en(and_150_out));  // open: out
  Driver driver_493 (.in(and_150_out), .en(and_150_out));  // open: out
  Driver driver_494 (.in(and_151_out), .en(and_151_out));  // open: out
  LED led_276 (.in(and_151_out));
  assign AC_CK = and_151_out ? and_151_out : 1'bz;  // Driver driver_495
  Driver driver_496 (.in(and_151_out), .en(and_151_out));  // open: out
  Driver driver_497 (.in(and_151_out), .en(and_151_out));  // open: out
  Driver driver_498 (.in(and_151_out), .en(and_151_out));  // open: out
  not not_4 (not_4_out, OPR_SWP);
  not not_5 (not_5_out, OPR_SWP);
  and and_152 (CNT_OPR3, OPR3, 1'b1, CK1);
  and and_153 (and_153_out, OPR3, not_4_out, STB1);
  and and_154 (and_154_out, OPR3, 1'b1, CK2);
  and and_155 (and_155_out, OPR3, not_5_out, STB2);
  LED led_277 (.in(CNT_OPR3));
  LED led_278 (.in(and_153_out));
  LED led_279 (.in(and_154_out));
  LED led_280 (.in(and_155_out));
  assign ROT2AC = CNT_OPR3 ? CNT_OPR3 : 1'bz;  // Driver driver_499
  Driver driver_500 (.in(CNT_OPR3), .en(CNT_OPR3));  // open: out
  Driver driver_501 (.in(CNT_OPR3), .en(CNT_OPR3));  // open: out
  Driver driver_502 (.in(CNT_OPR3), .en(CNT_OPR3));  // open: out
  Driver driver_503 (.in(CNT_OPR3), .en(CNT_OPR3));  // open: out
  Driver driver_504 (.in(and_153_out), .en(and_153_out));  // open: out
  Driver driver_505 (.in(and_153_out), .en(and_153_out));  // open: out
  assign MQ_CK = and_153_out ? and_153_out : 1'bz;  // Driver driver_506
  Driver driver_507 (.in(and_153_out), .en(and_153_out));  // open: out
  Driver driver_508 (.in(and_153_out), .en(and_153_out));  // open: out
  Driver driver_509 (.in(and_153_out), .en(and_153_out));  // open: out
  assign ROT2AC = and_154_out ? and_154_out : 1'bz;  // Driver driver_510
  Driver driver_511 (.in(and_154_out), .en(and_154_out));  // open: out
  Driver driver_512 (.in(and_154_out), .en(and_154_out));  // open: out
  Driver driver_513 (.in(and_154_out), .en(and_154_out));  // open: out
  Driver driver_514 (.in(and_154_out), .en(and_154_out));  // open: out
  Driver driver_515 (.in(and_155_out), .en(and_155_out));  // open: out
  assign AC_CK = and_155_out ? and_155_out : 1'bz;  // Driver driver_516
  Driver driver_517 (.in(and_155_out), .en(and_155_out));  // open: out
  Driver driver_518 (.in(and_155_out), .en(and_155_out));  // open: out
  Driver driver_519 (.in(and_155_out), .en(and_155_out));  // open: out
  or or_20 (or_20_out, CK1, CK2, CK3, CK4, CK5, CK6, CK7, CK8, CK9);
  LED led_281 (.in(IOT));
  Demultiplexer #(.Selector_Bits(3)) demultiplexer_1 (
    .sel(BUS_IR[2:0]), .in(IOT_DEVPRI), .out_0(IOT_TFL), .out_1(IOT_TSF), .out_2(IOT_TCF),
    .out_3(demultiplexer_1_out_3), .out_4(IOT_TPC), .out_5(IOT_TSK), .out_6(IOT_TLS),
    .out_7(demultiplexer_1_out_7));
  LED led_282 (.in(IOT_DEVPRI));
  Demultiplexer #(.Selector_Bits(3)) demultiplexer_2 (
    .sel(BUS_IR[2:0]), .in(IOT_DEVKBD), .out_0(IOT_KCF), .out_1(IOT_KSF), .out_2(IOT_KCC),
    .out_3(demultiplexer_2_out_3), .out_4(IOT_KRS), .out_5(IOT_KIE), .out_6(IOT_KRB),
    .out_7(demultiplexer_2_out_7));
  LED led_283 (.in(IOT_DEVKBD));
  Demultiplexer #(.Selector_Bits(3)) demultiplexer_3 (
    .sel(BUS_IR[2:0]), .in(IOT_DEVCPU), .out_0(IOT_SKON), .out_1(IOT_ION), .out_2(IOT_IOF), .out_3(IOT_SRQ),
    .out_4(IOT_GTF), .out_5(IOT_RTF), .out_6(IOT_SGT), .out_7(IOT_CAF));
  LED led_284 (.in(IOT_DEVCPU));
  // Probe on BUS_IR[2:0]
  // Probe on BUS_IR[8:3]
  and and_156 (and_156_out, or_20_out, IOT);
  Demultiplexer #(.Selector_Bits(6)) demultiplexer_4 (
    .sel(BUS_IR[8:3]), .in(and_156_out), .out_0(IOT_DEVCPU), .out_1(IOT_DEVHSR), .out_2(IOT_DEVHSP),
    .out_3(IOT_DEVKBD), .out_4(IOT_DEVPRI), .out_5(IOT_DEV5), .out_6(IOT_DEV6), .out_7(IOT_DEV7),
    .out_8(IOT_DEV8), .out_9(IOT_DEV9), .out_10(demultiplexer_4_out_10), .out_11(demultiplexer_4_out_11),
    .out_12(demultiplexer_4_out_12), .out_13(demultiplexer_4_out_13), .out_14(demultiplexer_4_out_14),
    .out_15(demultiplexer_4_out_15), .out_16(demultiplexer_4_out_16), .out_17(demultiplexer_4_out_17),
    .out_18(demultiplexer_4_out_18), .out_19(demultiplexer_4_out_19), .out_20(demultiplexer_4_out_20),
    .out_21(demultiplexer_4_out_21), .out_22(demultiplexer_4_out_22), .out_23(demultiplexer_4_out_23),
    .out_24(demultiplexer_4_out_24), .out_25(demultiplexer_4_out_25), .out_26(demultiplexer_4_out_26),
    .out_27(demultiplexer_4_out_27), .out_28(demultiplexer_4_out_28), .out_29(demultiplexer_4_out_29),
    .out_30(demultiplexer_4_out_30), .out_31(demultiplexer_4_out_31), .out_32(demultiplexer_4_out_32),
    .out_33(demultiplexer_4_out_33), .out_34(demultiplexer_4_out_34), .out_35(demultiplexer_4_out_35),
    .out_36(demultiplexer_4_out_36), .out_37(demultiplexer_4_out_37), .out_38(demultiplexer_4_out_38),
    .out_39(demultiplexer_4_out_39), .out_40(demultiplexer_4_out_40), .out_41(demultiplexer_4_out_41),
    .out_42(demultiplexer_4_out_42), .out_43(demultiplexer_4_out_43), .out_44(demultiplexer_4_out_44),
    .out_45(demultiplexer_4_out_45), .out_46(demultiplexer_4_out_46), .out_47(demultiplexer_4_out_47),
    .out_48(demultiplexer_4_out_48), .out_49(demultiplexer_4_out_49), .out_50(demultiplexer_4_out_50),
    .out_51(demultiplexer_4_out_51), .out_52(demultiplexer_4_out_52), .out_53(demultiplexer_4_out_53),
    .out_54(demultiplexer_4_out_54), .out_55(demultiplexer_4_out_55), .out_56(demultiplexer_4_out_56),
    .out_57(demultiplexer_4_out_57), .out_58(demultiplexer_4_out_58), .out_59(demultiplexer_4_out_59),
    .out_60(demultiplexer_4_out_60), .out_61(demultiplexer_4_out_61), .out_62(demultiplexer_4_out_62),
    .out_63(demultiplexer_4_out_63));
  or or_21 (IOT_DEV5x, demultiplexer_4_out_50, demultiplexer_4_out_51, demultiplexer_4_out_52, demultiplexer_4_out_53, demultiplexer_4_out_54, demultiplexer_4_out_56, demultiplexer_4_out_57, demultiplexer_4_out_58, demultiplexer_4_out_59, demultiplexer_4_out_55);
  or or_22 (IOT_DEV6x, demultiplexer_4_out_60, demultiplexer_4_out_61, demultiplexer_4_out_63, demultiplexer_4_out_62);
  and and_157 (and_157_out, OPR3, OPR_SWP, STB1);
  or or_23 (IOT_DEV3x, demultiplexer_4_out_30, demultiplexer_4_out_31, demultiplexer_4_out_32, demultiplexer_4_out_33, demultiplexer_4_out_34, demultiplexer_4_out_36, demultiplexer_4_out_37, demultiplexer_4_out_38, demultiplexer_4_out_39, demultiplexer_4_out_35);
  or or_24 (IOT_DEV4x, demultiplexer_4_out_40, demultiplexer_4_out_41, demultiplexer_4_out_42, demultiplexer_4_out_43, demultiplexer_4_out_44, demultiplexer_4_out_46, demultiplexer_4_out_47, demultiplexer_4_out_48, demultiplexer_4_out_49, demultiplexer_4_out_45);
  LED led_285 (.in(and_157_out));
  Seven_Seg_Hex seven_seg_hex_42 (.d(CK_NUM), .dp(1'b0));
  or or_25 (IOT_DEV1x, demultiplexer_4_out_10, demultiplexer_4_out_11, demultiplexer_4_out_12, demultiplexer_4_out_13, demultiplexer_4_out_14, demultiplexer_4_out_16, demultiplexer_4_out_17, demultiplexer_4_out_18, demultiplexer_4_out_19, demultiplexer_4_out_15);
  or or_26 (IOT_DEV2x, demultiplexer_4_out_20, demultiplexer_4_out_21, demultiplexer_4_out_22, demultiplexer_4_out_23, demultiplexer_4_out_24, demultiplexer_4_out_26, demultiplexer_4_out_27, demultiplexer_4_out_28, demultiplexer_4_out_29, demultiplexer_4_out_25);
  assign MQ_CK = and_157_out ? and_157_out : 1'bz;  // Driver driver_520
  assign AC_CK = and_157_out ? and_157_out : 1'bz;  // Driver driver_521
  Driver driver_522 (.in(and_157_out), .en(and_157_out));  // open: out
  Driver driver_523 (.in(and_157_out), .en(and_157_out));  // open: out
  Driver driver_524 (.in(and_157_out), .en(and_157_out));  // open: out
  // Probe on LATCHED_PC
  LED led_286 (.in(PH_FIRST));
  LED led_287 (.in(PH_STB));
  LED led_288 (.in(PH_LAST));
  // Probe on BUS_IR
  Demultiplexer #(.Selector_Bits(3)) demultiplexer_5 (
    .sel(BUS_IR[11:9]), .in(1'b1), .out_0(AND), .out_1(TAD), .out_2(ISZ), .out_3(DCA), .out_4(JMS),
    .out_5(JMP), .out_6(IOT), .out_7(OPR));
  LED led_289 (.in(OPR));
  Demultiplexer #(.Selector_Bits(2)) demultiplexer_6 (
    .sel({BUS_IR[8], BUS_IR[0]}), .in(OPR), .out_0(demultiplexer_6_out_0), .out_1(demultiplexer_6_out_1),
    .out_2(OPR2), .out_3(OPR3));
  and and_158 (and_158_out, BUS_IR[3], ~BUS_IR[4], ~BUS_IR[5], ~BUS_IR[6], ~BUS_IR[7], BUS_IR[8]);  // And
  LED led_290 (.in(and_158_out));
  not not_6 (not_6_out, BUS_IR[8]);
  or or_27 (OPR1, demultiplexer_6_out_0, demultiplexer_6_out_1);
  nor nor_2 (nor_2_out, and_158_out, not_6_out);
  LED led_291 (.in(OPR1));
  LED led_292 (.in(nor_2_out));
  nor nor_3 (nor_3_out, OPR, IOT);
  nor nor_4 (nor_4_out, BUS_IR[0], BUS_IR[1], BUS_IR[2], BUS_IR[3], BUS_IR[4], BUS_IR[5], BUS_IR[6], BUS_IR[7]);
  and and_159 (AUTOIND, nor_3_out, and_158_out);
  and and_160 (IND, nor_3_out, nor_2_out);
  and and_161 (NOIND, nor_3_out, not_6_out);
  and and_162 (MP, nor_3_out, BUS_IR[7]);
  and and_163 (OPR_IAC, BUS_IR[0], OPR1);
  LED led_293 (.in(OPR_IAC));
  and and_164 (OPR_X2, BUS_IR[1], OPR1);
  LED led_294 (.in(OPR_X2));
  and and_165 (OPR_LEFT, BUS_IR[2], OPR1);
  LED led_295 (.in(OPR_LEFT));
  and and_166 (OPR_RIGHT, BUS_IR[3], OPR1);
  LED led_296 (.in(OPR_RIGHT));
  and and_167 (OPR_CML, BUS_IR[4], OPR1);
  LED led_297 (.in(OPR_CML));
  and and_168 (OPR_CMA, BUS_IR[5], OPR1);
  LED led_298 (.in(OPR_CMA));
  and and_169 (OPR_CLL, BUS_IR[6], OPR1);
  LED led_299 (.in(OPR_CLL));
  and and_170 (OPR_CLA1, BUS_IR[7], OPR1);
  LED led_300 (.in(OPR_CLA1));
  and and_171 (OPR_NA1, BUS_IR[0], OPR2);
  LED led_301 (.in(OPR_NA1));
  and and_172 (OPR_HLT, BUS_IR[1], OPR2);
  LED led_302 (.in(OPR_HLT));
  and and_173 (OPR_OSR, BUS_IR[2], OPR2);
  LED led_303 (.in(OPR_OSR));
  and and_174 (OPR_TSTINV, BUS_IR[3], OPR2);
  LED led_304 (.in(OPR_TSTINV));
  and and_175 (OPR_SNLSZL, BUS_IR[4], OPR2);
  LED led_305 (.in(OPR_SNLSZL));
  and and_176 (OPR_SZASNA, BUS_IR[5], OPR2);
  LED led_306 (.in(OPR_SZASNA));
  and and_177 (OPR_SMASPA, BUS_IR[6], OPR2);
  LED led_307 (.in(OPR_SMASPA));
  and and_178 (OPR_CLA2, BUS_IR[7], OPR2);
  LED led_308 (.in(OPR_CLA2));
  and and_179 (and_179_out, OPR3, BUS_IR[0]);
  and and_180 (and_180_out[0], OPR3, BUS_IR[1]);
  and and_181 (and_180_out[1], OPR3, BUS_IR[2]);
  and and_182 (and_180_out[2], OPR3, BUS_IR[3]);
  and and_183 (and_183_out, OPR3, BUS_IR[4]);
  and and_184 (OPR_SCA, OPR3, BUS_IR[5]);
  and and_185 (and_185_out, OPR3, BUS_IR[6]);
  and and_186 (OPR_CLA3, OPR3, BUS_IR[7]);
  LED led_309 (.in(AUTOIND));
  LED led_310 (.in(IND));
  LED led_311 (.in(NOIND));
  LED led_312 (.in(MP));
  LED led_313 (.in(OPR3));
  LED led_314 (.in(and_179_out));
  LED led_315 (.in(and_180_out[0]));
  LED led_316 (.in(and_180_out[1]));
  LED led_317 (.in(and_180_out[2]));
  LED led_318 (.in(and_183_out));
  LED led_319 (.in(OPR_SCA));
  LED led_320 (.in(and_185_out));
  LED led_321 (.in(OPR_CLA3));
  and and_187 (OPR_NOP, nor_4_out, OPR);
  LED led_322 (.in(OPR1));
  LED led_323 (.in(OPR2));
  nand nand_1 (nand_1_out, and_183_out, and_185_out);
  LED led_324 (.in(OPR_NOP));
  LED led_325 (.in(nand_1_out));
  Seven_Seg_Hex seven_seg_hex_43 (.d(CK_NUM), .dp(1'b0));
  and and_188 (OPR_MQL, and_183_out, and_183_out);
  not not_7 (OPR_SWP, nand_1_out);
  and and_189 (OPR_MQA, and_185_out, and_185_out);
  // Probe on LATCHED_PC
  LED led_326 (.in(PH_FIRST));
  LED led_327 (.in(OPR_MQL));
  LED led_328 (.in(OPR_MQA));
  LED led_329 (.in(PH_STB));
  LED led_330 (.in(PH_LAST));
  Decoder #(.Selector_Bits(3)) decoder_1 (
    .sel(and_180_out), .out_0(OPR_OPERATION), .out_1(OPR_SCL), .out_2(OPR_MUY), .out_3(OPR_DVI),
    .out_4(OPR_NMI), .out_5(OPR_SHL), .out_6(OPR_ASL), .out_7(OPR_LSR));
  LED led_331 (.in(OPR_OPERATION));
  LED led_332 (.in(OPR_SCL));
  LED led_333 (.in(OPR_MUY));
  LED led_334 (.in(OPR_DVI));
  LED led_335 (.in(OPR_NMI));
  LED led_336 (.in(OPR_SHL));
  LED led_337 (.in(OPR_ASL));
  LED led_338 (.in(OPR_LSR));
  Demultiplexer #(.Selector_Bits(3)) demultiplexer_7 (
    .sel(BUS_IR[2:0]), .in(L_DEVPRI), .out_0(L_TFL), .out_1(L_TSF), .out_2(L_TCF),
    .out_3(demultiplexer_7_out_3), .out_4(L_TPC), .out_5(L_TSK), .out_6(L_TLS), .out_7(demultiplexer_7_out_7));
  LED led_339 (.in(L_DEVPRI));
  Demultiplexer #(.Selector_Bits(3)) demultiplexer_8 (
    .sel(BUS_IR[2:0]), .in(L_DEVKBD), .out_0(L_KCF), .out_1(L_KSF), .out_2(L_KCC),
    .out_3(demultiplexer_8_out_3), .out_4(L_KRS), .out_5(L_KIE), .out_6(L_KRB), .out_7(demultiplexer_8_out_7));
  LED led_340 (.in(L_DEVKBD));
  Demultiplexer #(.Selector_Bits(3)) demultiplexer_9 (
    .sel(BUS_IR[2:0]), .in(L_DEVCPU), .out_0(L_SKON), .out_1(L_ION), .out_2(L_IOF), .out_3(L_SRQ),
    .out_4(L_GTF), .out_5(L_RTF), .out_6(L_SGT), .out_7(L_CAF));
  LED led_341 (.in(L_DEVCPU));
  // Probe on BUS_IR[2:0]
  // Probe on BUS_IR[8:3]
  LED led_342 (.in(IOT));
  Demultiplexer #(.Selector_Bits(6)) demultiplexer_10 (
    .sel(BUS_IR[8:3]), .in(IOT), .out_0(L_DEVCPU), .out_1(L_DEVHSR), .out_2(L_DEVHSP), .out_3(L_DEVKBD),
    .out_4(L_DEVPRI), .out_5(L_DEV5), .out_6(L_DEV6), .out_7(L_DEV7), .out_8(L_DEV8), .out_9(L_DEV9),
    .out_10(demultiplexer_10_out_10), .out_11(demultiplexer_10_out_11), .out_12(demultiplexer_10_out_12),
    .out_13(demultiplexer_10_out_13), .out_14(demultiplexer_10_out_14), .out_15(demultiplexer_10_out_15),
    .out_16(demultiplexer_10_out_16), .out_17(demultiplexer_10_out_17), .out_18(demultiplexer_10_out_18),
    .out_19(demultiplexer_10_out_19), .out_20(demultiplexer_10_out_20), .out_21(demultiplexer_10_out_21),
    .out_22(demultiplexer_10_out_22), .out_23(demultiplexer_10_out_23), .out_24(demultiplexer_10_out_24),
    .out_25(demultiplexer_10_out_25), .out_26(demultiplexer_10_out_26), .out_27(demultiplexer_10_out_27),
    .out_28(demultiplexer_10_out_28), .out_29(demultiplexer_10_out_29), .out_30(demultiplexer_10_out_30),
    .out_31(demultiplexer_10_out_31), .out_32(demultiplexer_10_out_32), .out_33(demultiplexer_10_out_33),
    .out_34(demultiplexer_10_out_34), .out_35(demultiplexer_10_out_35), .out_36(demultiplexer_10_out_36),
    .out_37(demultiplexer_10_out_37), .out_38(demultiplexer_10_out_38), .out_39(demultiplexer_10_out_39),
    .out_40(demultiplexer_10_out_40), .out_41(demultiplexer_10_out_41), .out_42(demultiplexer_10_out_42),
    .out_43(demultiplexer_10_out_43), .out_44(demultiplexer_10_out_44), .out_45(demultiplexer_10_out_45),
    .out_46(demultiplexer_10_out_46), .out_47(demultiplexer_10_out_47), .out_48(demultiplexer_10_out_48),
    .out_49(demultiplexer_10_out_49), .out_50(demultiplexer_10_out_50), .out_51(demultiplexer_10_out_51),
    .out_52(demultiplexer_10_out_52), .out_53(demultiplexer_10_out_53), .out_54(demultiplexer_10_out_54),
    .out_55(demultiplexer_10_out_55), .out_56(demultiplexer_10_out_56), .out_57(demultiplexer_10_out_57),
    .out_58(demultiplexer_10_out_58), .out_59(demultiplexer_10_out_59), .out_60(demultiplexer_10_out_60),
    .out_61(demultiplexer_10_out_61), .out_62(demultiplexer_10_out_62), .out_63(demultiplexer_10_out_63));
  or or_28 (L_DEV5x, demultiplexer_10_out_50, demultiplexer_10_out_51, demultiplexer_10_out_52, demultiplexer_10_out_53, demultiplexer_10_out_54, demultiplexer_10_out_56, demultiplexer_10_out_57, demultiplexer_10_out_58, demultiplexer_10_out_59, demultiplexer_10_out_55);
  or or_29 (L_DEV6x, demultiplexer_10_out_60, demultiplexer_10_out_61, demultiplexer_10_out_63, demultiplexer_10_out_62);
  or or_30 (L_DEV3x, demultiplexer_10_out_30, demultiplexer_10_out_31, demultiplexer_10_out_32, demultiplexer_10_out_33, demultiplexer_10_out_34, demultiplexer_10_out_36, demultiplexer_10_out_37, demultiplexer_10_out_38, demultiplexer_10_out_39, demultiplexer_10_out_35);
  or or_31 (L_DEV4x, demultiplexer_10_out_40, demultiplexer_10_out_41, demultiplexer_10_out_42, demultiplexer_10_out_43, demultiplexer_10_out_44, demultiplexer_10_out_46, demultiplexer_10_out_47, demultiplexer_10_out_48, demultiplexer_10_out_49, demultiplexer_10_out_45);
  or or_32 (L_DEV1x, demultiplexer_10_out_10, demultiplexer_10_out_11, demultiplexer_10_out_12, demultiplexer_10_out_13, demultiplexer_10_out_14, demultiplexer_10_out_16, demultiplexer_10_out_17, demultiplexer_10_out_18, demultiplexer_10_out_19, demultiplexer_10_out_15);
  or or_33 (L_DEV2x, demultiplexer_10_out_20, demultiplexer_10_out_21, demultiplexer_10_out_22, demultiplexer_10_out_23, demultiplexer_10_out_24, demultiplexer_10_out_26, demultiplexer_10_out_27, demultiplexer_10_out_28, demultiplexer_10_out_29, demultiplexer_10_out_25);
  PullDown pulldown_4 (.out(IR2PC));
  PullDown pulldown_5 (.out(IND2PC));
  PullDown pulldown_6 (.out(RAMD2PC));
  PullDown pulldown_7 (.out(ROT2AC));
  PullDown pulldown_8 (.out(RAMD2AC_ADD));
  PullDown pulldown_9 (.out(PC_LD));
  PullDown pulldown_10 (.out(IND2RAMA));
  PullDown pulldown_11 (.out(INC2RAMD));
  PullDown pulldown_12 (.out(PC2RAMD));
  PullDown pulldown_13 (.out(IR2RAMA));
  PullDown pulldown_14 (.out(IND2INC));
  PullDown pulldown_15 (.out(LD2INC));
  PullDown pulldown_16 (.out(RAMA_HOLD));
  PullDown pulldown_17 (.out(DATA_CK));
  PullDown pulldown_18 (.out(IR_CK));
  PullDown pulldown_19 (.out(PC_CK));
  PullDown pulldown_20 (.out(AC_CK));
  PullDown pulldown_21 (.out(IND_CK));
  PullDown pulldown_22 (.out(LINK_CK));
  PullDown pulldown_23 (.out(RAM_WE));
  PullDown pulldown_24 (.out(RAM_OE));
  PullDown pulldown_25 (.out(MQ_CK));
  and and_190 (i_iac, OPR_IAC, 1'b1);
  and and_191 (i_cll, OPR_CLL, 1'b1);
  and and_192 (i_cma, OPR_CMA, 1'b1);
  and and_193 (i_cml, OPR_CML, 1'b1);
  and and_194 (i_osr, OPR_OSR, 1'b1);
  and and_195 (i_hlt, OPR_HLT, 1'b1);
  or or_34 (i_cla, OPR_CLA1, OPR_CLA2);
  and and_196 (i_nop, OPR_NOP, 1'b1);
  and and_197 (i_ral, OPR_LEFT, ~OPR_X2);  // And
  and and_198 (i_rar, OPR_RIGHT, ~OPR_X2);  // And
  and and_199 (i_rtl, OPR_LEFT, OPR_X2);
  and and_200 (i_rtr, OPR_RIGHT, OPR_X2);
  and and_201 (i_snl, OPR_SNLSZL, ~OPR_TSTINV);  // And
  and and_202 (i_sza, OPR_SZASNA, ~OPR_TSTINV);  // And
  and and_203 (i_sma, OPR_SMASPA, ~OPR_TSTINV);  // And
  and and_204 (i_szl, OPR_SNLSZL, OPR_TSTINV);
  and and_205 (i_sna, OPR_SZASNA, OPR_TSTINV);
  and and_206 (i_spa, OPR_SMASPA, OPR_TSTINV);
  and and_207 (i_skp, ~OPR_SNLSZL, ~OPR_SZASNA, ~OPR_SMASPA, OPR_TSTINV);  // And

  // Other names for the same wires on the sheet: RAMADDR[11:0] = {RA3, RA2, RA1, RA0}; PI0[2:0] = PCIN[2:0];
  //   PI1[2:0] = PCIN[5:3]; PI2[2:0] = PCIN[8:6]; PI3[2:0] = PCIN[11:9]; AC0[2:0] = AC[2:0]; AC1[2:0] = AC[5:3];
  //   AC2[2:0] = AC[8:6]; AC3[2:0] = AC[11:9]; IR0[2:0] = BUS_IR[2:0]; IR1[2:0] = BUS_IR[5:3]; IR2[2:0] = BUS_IR[8:6];
  //   IR3[2:0] = BUS_IR[11:9]; PC0[2:0] = BUS_PC[2:0]; PC1[2:0] = BUS_PC[5:3]; PC2[2:0] = BUS_PC[8:6];
  //   PC3[2:0] = BUS_PC[11:9]; DATA[11:0] = {DA3, DA2, DA1, DA0};
  //   STATUS12 (some bits) = {LINK, IRQ_BUS, IRQ_INHIBIT, FLAG_GIE}; INDOUT[11:0] = {IND3, IND2, IND1, IND0};
  //   IRQ_KILL = IOT_IOF; MQ0[2:0] = MQ[2:0]; MQ1[2:0] = MQ[5:3]; MQ2[2:0] = MQ[8:6]; MQ3[2:0] = MQ[11:9];
  //   RD0[2:0] = RAMDATA[2:0]; RD1[2:0] = RAMDATA[5:3]; RD2[2:0] = RAMDATA[8:6]; RD3[2:0] = RAMDATA[11:9]; XTAL = clk

  // Notes on the sheet:
  //   clk: Hz: 2147483647
  //   PCIN
  //   PC
  //   IR
  //   AC
  //   MQ
  //   IND
  //   RAM-A
  //   RAM-D
  //   PC-IN
  //   DATA
  //   SEQ OPR 1 MICROCODES
  //   ------------------------------------
  //   1 CLA CLL
  //   2 CMA CML
  //   3 IAC
  //   4 RAR RAL RTR RTL BSW
  //   ACCUMULATOR
  //   C
  //   LINK
  //   PCOUT
  //   SKON
  //   NOP
  //   AND
  //   TAD
  //   ION
  //   CLA
  //   STATE
  //   INSTRUCTION
  //   RUN
  //   HALT
  //   PC=0200
  //   BREAKPOINT
  //   MAIN DATA-PATHS
  //   RAMADDR
  //   IOF
  //   SRQ
  //   CLL
  //   ISZ
  //   DCA
  //   GTF
  //   CMA
  //   JMS
  //   START/STOP/STEP
  //   CLOCK CYCLE CONTROLLER
  //   contents of eeprom_1 (hex, n*v repeats v):
  //   0,a01,2,3,0,0,f02,e00,0,f02,f02,f02,f02,f02,f02,f02,0,1,2,3,4,6,8,c,10,18,20,30,40,
  //   60,80,c0,100,180,200,29c,300,400,600,6ca,800,fcf,ffe,ffd,ffb,ff7,fef,fdf,e7f,fbf,
  //   f7f,eff,dff,bff,7ff,fff,aaa,555,c00,e00,f00,f80,fe0,ff0,ff8,ffc,7,37,f,1f,3f,7f,ff,
  //   1ff,3ff,fc0,a95,56a,1f8,e07,87,a60,a60,f02,f02,f02,f02,f02,f02,f02,f02,f02,f02,f02,
  //   f02,f02,f02,f02,f02,f02,237,e80,f02,f08,f02,e80,f20,f02,f28,f08,f02,e80,228,f20,f08,
  //   f02,f28,f02,e80,225,f20,f08,f02,f28,f02,e00,e00,f08,a64,e80,222,f20,f08,f02,f28,f02,
  //   e80,220,f20,f08,f02,f28,f02,e80,21e,f20,f08,f02,f28,f02,e80,21c,f20,f08,f02,f28,f02,
  //   e80,21a,f20,f08,f02,f28,f02,e80,218,f20,f08,f02,f28,f02,e80,216,f20,f08,f02,f28,f02,
  //   e80,214,f20,f08,f02,f28,f02,e80,212,f20,f08,f02,f28,f02,e80,211,f20,f08,f02,f28,f02,
  //   e80,236,f48,f02,e80,228,f48,f08,f02,e80,236,f40,f08,f02,e80,228,f40,f02,e80,237,e20,
  //   f20,f02,e80,239,e20,f28,f02,239,e20,f20,f02,e80,238,e20,f28,f02,238,e20,f20,f02,e80,
  //   237,e20,f20,f02,e80,e01,f20,f08,f02,e80,237,e01,f20,f02,e80,241,e01,e01,e01,e01,f20,
  //   f02,e80,e40,e04,f18,f02,e80,e40,e10,228,e04,f18,f08,f02,e80,e40,e04,f10,f08,f02,e80,
  //   e40,e10,228,e04,f10,f02,e80,228,e04,f10,aaa,e40,f18,f02,aae,e10,f10,f02,aa6,e40,f18,
  //   f02,e10,f10,f02,e10,f18,f02,e80,237,f80,f20,f02,e80,f04,e20,f20,f02,e80,e40,e00,f28,
  //   f18,f02,e80,e40,f00,f28,f18,f02,e80,236,228,e20,f20,f02,e80,235,225,e20,f20,f02,e80,
  //   234,222,e20,f20,f02,e80,233,220,e20,f20,f02,e80,232,21e,e20,f20,f02,e80,231,21c,e20,
  //   f20,f02,e80,22f,21a,e20,f20,f02,e80,22e,218,e20,f20,f02,e80,22d,216,e20,f20,f02,e80,
  //   22c,214,e20,f20,f02,e80,22b,212,e20,f20,f02,e80,22a,211,e20,f20,f02,e80,e40,228,228,
  //   f18,f20,f02,e80,e40,23a,225,f18,f20,f02,e80,e40,23b,222,f18,f20,f02,e80,e40,23c,220,
  //   f18,f20,f02,e80,e40,23d,21e,f18,f20,f02,e80,e40,24b,21c,f18,f20,f02,e80,e40,23e,21a,
  //   f18,f20,f02,e80,e40,23f,218,f18,f20,f02,e80,e40,240,216,f18,f20,f02,e80,e40,241,214,
  //   f18,f20,f02,e80,e40,22a,212,f18,f20,f02,e80,e40,237,211,f18,f20,f02,e80,e40,e10,228,
  //   228,f10,f20,f02,e80,e40,236,225,225,e20,f10,f20,f02,e80,e40,235,222,222,e20,f10,f20,
  //   f02,e80,e40,234,220,220,e20,f10,f20,f02,e80,e40,233,21e,21e,e20,f10,f20,f02,e80,e40,
  //   232,21c,21c,e20,f10,f20,f02,e80,e40,231,21a,21a,e20,f10,f20,f02,e80,e40,22f,218,218,
  //   e20,f10,f20,f02,e80,e40,22e,216,216,e20,f10,f20,f02,e80,e40,22d,214,214,e20,f10,f20,
  //   f02,e80,e40,22c,212,212,e20,f10,f20,f02,e80,e40,22b,211,211,e20,f10,f18,f02,e80,e40,
  //   211,213,22c,e20,f10,f20,f02,e80,e40,212,215,22d,e20,f10,f20,f02,e80,e40,214,217,22e,
  //   e20,f10,f20,f02,e80,e40,216,219,22f,e20,f10,f20,f02,e80,e40,218,21b,231,e20,f10,f20,
  //   f02,e80,e40,21a,21d,232,e20,f10,f20,f02,e80,e40,21c,21f,233,e20,f10,f20,f02,e80,e40,
  //   21e,221,234,e20,f10,f20,f02,e80,e40,220,224,235,e20,f10,f20,f02,e80,e40,222,226,236,
  //   e20,f10,f20,f02,e80,e40,225,23a,f18,f20,f02,e80,e40,237,211,f18,f20,f02,e80,e40,213,
  //   213,240,211,e20,f10,f20,f02,e80,e40,215,215,23f,213,e20,f10,f20,f02,e80,e40,217,217,
  //   23e,242,e20,f10,f20,f02,e80,e40,219,219,229,e20,f10,f20,f02,e80,e40,21b,21b,23d,245,
  //   e20,f10,f20,f02,e80,e40,21d,21d,23c,246,e20,f10,f20,f02,e80,e40,21f,21f,230,e20,f10,
  //   f20,f02,e80,e40,221,221,23a,248,e20,f10,f20,f02,e80,e40,224,224,228,249,e20,f10,f20,
  //   f02,e80,e40,226,226,24a,e20,f10,f20,f02,e80,e40,23a,23a,236,e20,f18,f20,f02,e80,e40,
  //   237,237,211,e20,f18,f20,f02,e80,e40,211,e08,f10,f02,e80,e40,210,e08,f20,f02,e80,e40,
  //   210,e08,f18,f02,e80,e40,e10,210,e08,f18,f02,e80,e40,e10,237,e08,e20,f20,f02,e80,e40,
  //   e10,210,e08,236,e20,f28,f18,f02,e80,e40,228,e08,235,e20,f28,f18,f02,e80,e40,225,e08,
  //   234,e20,f28,f18,f02,e80,e40,222,e08,233,e20,f28,f18,f02,e80,e40,220,e08,232,e20,f28,
  //   f18,f02,e80,e40,21e,e08,231,e20,f28,f18,f02,e80,e40,21c,e08,22f,e20,f28,f18,f02,e80,
  //   e40,21a,e08,22e,e20,f28,f18,f02,e80,e40,218,e08,22d,e20,f28,f18,f02,e80,e40,216,e08,
  //   22c,e20,f28,f18,f02,e80,e40,214,e08,22b,e20,f28,f18,f02,e80,e40,212,e08,22a,e20,f28,
  //   f18,f02,e80,e40,211,e08,237,e20,f28,f10,f02,e80,e40,212,e0a,f10,f02,e80,e40,210,e0a,
  //   f20,f02,e80,e40,210,e0a,f18,f02,e80,e40,e10,210,e0a,f18,f02,e80,e40,e10,237,e0a,e20,
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  //   RTF
  //   CML
  //   JMP
  //   RAMDATA
  //   SGT
  //   CAF
  //   IAC
  //   IOT
  //   OPR
  //   RAR
  //   RTR
  //   KCF
  //   RAL
  //   DIR
  //   KSF
  //   KCC
  //   RTL
  //   AUTO
  //   IND
  //   OSR
  //   KRS
  //   SKP
  //   CURR
  //   PAGE
  //   -
  //   0=Instructions1 1=Instructions2
  //   2=JMPJMS 3=JMPJMS-RAND
  //   4=..... 5=.....
  //   6=..... 7=.....
  //   KIE
  //   SZA
  //   SMA
  //   KRB
  //   SPA
  //   SWITCHES
  //   ROTATES
  //   TFL
  //   SNA
  //   INDOUT
  //   TSF
  //   SZL
  //   SNL
  //   TCF
  //   TPC
  //   BANK #
  //   TSK
  //   HLT
  //   LATCHED
  //   DATA
  //   TLS
  //   LATCHED PC
  //   PDP-8/X
  //   Rev 0.2
  //   github.com/SmallRoomLabs/PDP8-X
  //   F
  //   S
  //   L
  //   STEP
  //   PHASE
  //   SEQ OPR 2 MICROCODES
  //   ------------------------------------
  //   1 SMA SPA SZA SZN SNK SZL SKP
  //   2 CLA
  //   3 OSR
  //   4 HLT
  //   SKIP LOGIC
  //   AUTOINDEX
  //   INDIRECT
  //   AC negative
  //   AC=0
  //   LINK<>0
  //   SMA      7500  skip on minus AC
  //   SPA      7510  skip on plus AC
  //   SZA      7440  skip on zero AC
  //   SNA      7450  skip on non-zero AC
  //   SNL      7420  skip on non-zero link
  //   SZL      7430  skip on zero link
  //   IND
  //   STEP1
  //   IND
  //   STEP2
  //   AND i
  //   FETCH OP &
  //   INCREMENT PC
  //   FORCE 4000
  //   INTERRUPT TO IR
  //   AND-i-auto
  //   iAuto 1
  //   iAuto 2
  //   iAuto 3
  //   iAuto 4
  //   603x - KEYBOARD
  //   INSTRUCTIONS
  //   Turn interrupt ON
  //   Keyboard Clear Flags
  //   Keyboard and AC Clear
  //   Keyboard Skip if Flag
  //   Keyboard Read Static
  //   Keyboard Read and Begin next read
  //   Keyboard Interrupt Enable
  //   600x - INTERRUPT
  //   INSTRUCTIONS
  //   Clear All Flags
  //   Turn interrupt OFF
  //   Skip if interrupt ON, and turn OFF
  //   Skip interrupt request
  //   TAD
  //   STEP1
  //   TAD
  //   STEP2
  //   External IRQ
  //   sources
  //   TAD i
  //   Skip on Greater Than flag
  //   Get interrupt flags
  //   Restore interrupt flags
  //   Teleprinter Print Character
  //   Teleprinter Load and Start
  //   Teleprinter Flag set (aka SPF)
  //   Teleprinter Clear Flag
  //   Teleprinter Skip if Flag
  //   Teleprinter Skip (aka SPI)
  //   604x - PRINTER
  //   INSTRUCTIONS
  //   TAD-i-auto
  //   Get address
  //   of M
  //   Save value
  //   from M
  //   indo LATDAT
  //   SKIP IF
  //   AC=ZERO
  //   ISZ i
  //   Save value
  //   from IND
  //   indo LATDAT
  //   ISZ-i-auto
  //   DCA i
  //   DCA-i-auto
  //   Prepare to store
  //   return address
  //   Actually store
  //   return address
  //   Prepare to 
  //   set PC
  //   Actually set
  //   PC
  //   Increment PC
  //   Actually increment
  //   PC
  //   Prepate to store 
  //   return addr
  //   to [ind]
  //   Store return addr
  //   to [ind]
  //   Pause to accept
  //   new PC inc clk
  //   JMS i
  //   JMS i-auto
  //   Prepare to set
  //   new PC
  //   Actually set
  //   new PC
  //   Prepare to set PC
  //   with new vector
  //   JMP i
  //   JMP i-auto
  //   OPR 1
  //   OPR 2
  //   OPR 3
  //   IOT DECODER
  //   604x
  //   TTY PRINTER
  //   SLOW PUNCH
  //   603x
  //   TTY KEYBOARD
  //   SLOW READER
  //   600x
  //   CPU FLAGS & 
  //   INTERRUPT
  //   Keyboard Clear and read Character
  //   OPR_SWP
  //   IR DECODER
  //   OPR DECODER
  //   IOT DECODER
  //   FOR LEDs
endmodule
