// Digital circuit ROTATER.dig as structural Verilog
module ROTATER (
  input  [2:0] OP,
  input  [11:0] AI,
  input  LI,
  input  OE,
  output [11:0] AO,
  output LO
);

  wire not_1_out;

  not not_1 (not_1_out, OE);
  // _74251 _74251_1: pin names not known; wires that end beside it: AI[6], AI[7], AI[8], AI[9], AI[10], AI[11], OP, 1'b0, 1'b0, LI, LI, AI[11], AI[10], AI[0], AI[1], LI, LI, OP[0], OP[1], OP[2], 1'b1, LO
  // _74251 _74251_2: pin names not known; wires that end beside it: 1'b0, not_1_out, AI[0], AI[6], LI, AI[11], AI[1], AI[2], AI[0], AI[0], OP[0], OP[1], OP[2], 1'b1, AO[0]
  // _74251 _74251_3: pin names not known; wires that end beside it: 1'b0, not_1_out, AI[1], AI[7], AI[0], LI, AI[2], AI[3], AI[1], AI[1], OP[0], OP[1], OP[2], 1'b1, AO[1]
  // _74251 _74251_4: pin names not known; wires that end beside it: 1'b0, not_1_out, AI[2], AI[8], AI[1], AI[0], AI[3], AI[4], AI[2], AI[2], OP[0], OP[1], OP[2], 1'b1, AO[2]
  // _74251 _74251_5: pin names not known; wires that end beside it: 1'b0, not_1_out, AI[3], AI[9], AI[2], AI[1], AI[4], AI[5], AI[3], AI[3], OP[0], OP[1], OP[2], 1'b1, AO[3]
  // _74251 _74251_6: pin names not known; wires that end beside it: 1'b0, not_1_out, AI[4], AI[10], AI[3], AI[2], AI[5], AI[6], AI[4], AI[4], OP[0], OP[1], OP[2], 1'b1, AO[4]
  // _74251 _74251_7: pin names not known; wires that end beside it: 1'b0, not_1_out, AI[5], AI[11], AI[4], AI[3], AI[6], AI[7], AI[5], AI[5], OP[0], OP[1], OP[2], 1'b1, AO[5]
  // _74251 _74251_8: pin names not known; wires that end beside it: 1'b0, not_1_out, AI[6], AI[0], AI[5], AI[4], AI[7], AI[8], AI[6], AI[6], OP[0], OP[1], OP[2], 1'b1, AO[6]
  // _74251 _74251_9: pin names not known; wires that end beside it: 1'b0, not_1_out, AI[7], AI[1], AI[6], AI[5], AI[8], AI[9], AI[7], AI[7], OP[0], OP[1], OP[2], 1'b1, AO[7]
  // _74251 _74251_10: pin names not known; wires that end beside it: 1'b0, not_1_out, AI[8], AI[2], AI[7], AI[6], AI[9], AI[10], AI[8], AI[8], OP[0], OP[1], OP[2], 1'b1, AO[8]
  // _74251 _74251_11: pin names not known; wires that end beside it: 1'b0, not_1_out, AI[9], AI[3], AI[8], AI[7], AI[10], AI[11], AI[9], AI[9], OP[0], OP[1], OP[2], 1'b1, AO[9]
  // _74251 _74251_12: pin names not known; wires that end beside it: 1'b0, not_1_out, AI[10], AI[4], AI[9], AI[8], AI[11], LI, AI[10], AI[10], OP[0], OP[1], OP[2], 1'b1, AO[10]
  // _74251 _74251_13: pin names not known; wires that end beside it: 1'b1, 1'b0, not_1_out, AI[11], AI[5], AI[10], AI[9], LI, AI[0], AI[11], AI[11], OP[0], OP[1], OP[2], 1'b1, 1'b0, AO[11]

  // Notes on the sheet:
  //   LINK
  //   LSB
  //   MSB
  //   1 pcs 7404 hex inverter
  //   13 pcs 74251 8-input multiplexe 3-state
endmodule

/* Test case:
LI AI OP LO AO 

 0 0b000000000000 0b000 0 0b000000000000
 0 0b000000000000 0b001 0 0b000000000000
 0 0b000000000000 0b010 0 0b000000000000
 0 0b000000000000 0b011 0 0b000000000000
 0 0b000000000000 0b100 0 0b000000000000
 0 0b000000000000 0b101 0 0b000000000000
 0 0b000000000000 0b110 0 0b000000000000
 0 0b000000000000 0b111 0 0b000000000000
 0 0b000000000001 0b000 0 0b000000000001
 0 0b000000000001 0b001 0 0b000001000000
 0 0b000000000001 0b010 0 0b000000000010
 0 0b000000000001 0b011 0 0b000000000100
 0 0b000000000001 0b100 1 0b000000000000
 0 0b000000000001 0b101 0 0b100000000000
 0 0b000000000001 0b110 0 0b000000000001
 0 0b000000000001 0b111 0 0b000000000001
 0 0b000000000010 0b000 0 0b000000000010
 0 0b000000000010 0b001 0 0b000010000000
 0 0b000000000010 0b010 0 0b000000000100
 0 0b000000000010 0b011 0 0b000000001000
 0 0b000000000010 0b100 0 0b000000000001
 0 0b000000000010 0b101 1 0b000000000000
 0 0b000000000010 0b110 0 0b000000000010
 0 0b000000000010 0b111 0 0b000000000010
 0 0b000000000011 0b000 0 0b000000000011
 0 0b000000000011 0b001 0 0b000011000000
 0 0b000000000011 0b010 0 0b000000000110
 0 0b000000000011 0b011 0 0b000000001100
 0 0b000000000011 0b100 1 0b000000000001
 0 0b000000000011 0b101 1 0b100000000000
 0 0b000000000011 0b110 0 0b000000000011
 0 0b000000000011 0b111 0 0b000000000011
 0 0b000000000100 0b000 0 0b000000000100
 0 0b000000000100 0b001 0 0b000100000000
 0 0b000000000100 0b010 0 0b000000001000
 0 0b000000000100 0b011 0 0b000000010000
 0 0b000000000100 0b100 0 0b000000000010
 0 0b000000000100 0b101 0 0b000000000001
 0 0b000000000100 0b110 0 0b000000000100
 0 0b000000000100 0b111 0 0b000000000100
 0 0b000000000101 0b000 0 0b000000000101
 0 0b000000000101 0b001 0 0b000101000000
 0 0b000000000101 0b010 0 0b000000001010
 0 0b000000000101 0b011 0 0b000000010100
 0 0b000000000101 0b100 1 0b000000000010
 0 0b000000000101 0b101 0 0b100000000001
 0 0b000000000101 0b110 0 0b000000000101
 0 0b000000000101 0b111 0 0b000000000101
 0 0b000000000110 0b000 0 0b000000000110
 0 0b000000000110 0b001 0 0b000110000000
 0 0b000000000110 0b010 0 0b000000001100
 0 0b000000000110 0b011 0 0b000000011000
 0 0b000000000110 0b100 0 0b000000000011
 0 0b000000000110 0b101 1 0b000000000001
 0 0b000000000110 0b110 0 0b000000000110
 0 0b000000000110 0b111 0 0b000000000110
 0 0b000000000111 0b000 0 0b000000000111
 0 0b000000000111 0b001 0 0b000111000000
 0 0b000000000111 0b010 0 0b000000001110
 0 0b000000000111 0b011 0 0b000000011100
 0 0b000000000111 0b100 1 0b000000000011
 0 0b000000000111 0b101 1 0b100000000001
 0 0b000000000111 0b110 0 0b000000000111
 0 0b000000000111 0b111 0 0b000000000111
 0 0b000000001000 0b000 0 0b000000001000
 0 0b000000001000 0b001 0 0b001000000000
 0 0b000000001000 0b010 0 0b000000010000
 0 0b000000001000 0b011 0 0b000000100000
 0 0b000000001000 0b100 0 0b000000000100
 0 0b000000001000 0b101 0 0b000000000010
 0 0b000000001000 0b110 0 0b000000001000
 0 0b000000001000 0b111 0 0b000000001000
 0 0b000000001001 0b000 0 0b000000001001
 0 0b000000001001 0b001 0 0b001001000000
 0 0b000000001001 0b010 0 0b000000010010
 0 0b000000001001 0b011 0 0b000000100100
 0 0b000000001001 0b100 1 0b000000000100
 0 0b000000001001 0b101 0 0b100000000010
 0 0b000000001001 0b110 0 0b000000001001
 0 0b000000001001 0b111 0 0b000000001001
 0 0b000000001010 0b000 0 0b000000001010
 0 0b000000001010 0b001 0 0b001010000000
 0 0b000000001010 0b010 0 0b000000010100
 0 0b000000001010 0b011 0 0b000000101000
 0 0b000000001010 0b100 0 0b000000000101
 0 0b000000001010 0b101 1 0b000000000010
 0 0b000000001010 0b110 0 0b000000001010
 0 0b000000001010 0b111 0 0b000000001010
 0 0b000000001011 0b000 0 0b000000001011
 0 0b000000001011 0b001 0 0b001011000000
 0 0b000000001011 0b010 0 0b000000010110
 0 0b000000001011 0b011 0 0b000000101100
 0 0b000000001011 0b100 1 0b000000000101
 0 0b000000001011 0b101 1 0b100000000010
 0 0b000000001011 0b110 0 0b000000001011
 0 0b000000001011 0b111 0 0b000000001011
 0 0b000000001100 0b000 0 0b000000001100
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*/
