// Digital circuit RaceIssue.dig as structural Verilog
module RaceIssue (
  input  STB,
  input  clk
);

  wire CLK_t, d_ff_1_nq, d_ff_2_nq, d_ff_2_q, nand_1_out, nand_2_out, nand_3_out, switchdt_1_p2;

  D_FF d_ff_1 (.D(STB), .C(CLK_t), .nQ(d_ff_1_nq));  // open: Q
  // SwitchDT switchdt_1: pin names not known; wires that end beside it: CLK_t, switchdt_1_p2, clk
  nand nand_1 (nand_1_out, STB, d_ff_1_nq);
  Counter counter_1 (.en(1'b1), .C(clk), .clr(1'b0), .out(switchdt_1_p2));  // open: ovf
  nand nand_2 (nand_2_out, nand_1_out, nand_3_out);
  nand nand_3 (nand_3_out, nand_2_out, d_ff_2_nq);
  D_FF d_ff_2 (.D(nand_2_out), .C(CLK_t), .Q(d_ff_2_q), .nQ(d_ff_2_nq));

  // Notes on the sheet:
  //   STB: Rising edge latches the parallel data at DIN and starts the serial output stream at TX
  //   clk: Hz: 2147483647
  //   Edge detector
  //   Direct or /2 clock
  //   Clock domains synchronizer
endmodule
