// Digital circuit RisingEdgeDet.dig as structural Verilog
module RisingEdgeDet (
  input  A,
  output Y
);

  wire not_1_out, not_2_out, not_3_out;

  not not_1 (not_1_out, A);
  not not_2 (not_2_out, not_1_out);
  and and_1 (Y, not_3_out, A);
  not not_3 (not_3_out, not_2_out);
endmodule
