// Digital circuit SEQUENCER.dig as structural Verilog
module SEQUENCER (
  input  [4:0] IN,
  output [9:0] STB_bits,
  output [9:0] CK_bits,
  output [3:0] CK_num,
  output PH_FIRST,
  output PH_STB,
  output PH_LAST
);

  wire decoder_1_out_0, decoder_1_out_2, decoder_1_out_3, decoder_1_out_5, decoder_1_out_6, decoder_1_out_8,
       decoder_1_out_9, decoder_1_out_11, decoder_1_out_12, decoder_1_out_14, decoder_1_out_15,
       decoder_1_out_17, decoder_1_out_18, decoder_1_out_20, decoder_1_out_21, decoder_1_out_23,
       decoder_1_out_24, decoder_1_out_26, decoder_1_out_27, decoder_1_out_29;

  Decoder #(.Selector_Bits(5)) decoder_1 (
    .sel(IN), .out_0(decoder_1_out_0), .out_1(STB_bits[0]), .out_2(decoder_1_out_2), .out_3(decoder_1_out_3),
    .out_4(STB_bits[1]), .out_5(decoder_1_out_5), .out_6(decoder_1_out_6), .out_7(STB_bits[2]),
    .out_8(decoder_1_out_8), .out_9(decoder_1_out_9), .out_10(STB_bits[3]), .out_11(decoder_1_out_11),
    .out_12(decoder_1_out_12), .out_13(STB_bits[4]), .out_14(decoder_1_out_14), .out_15(decoder_1_out_15),
    .out_16(STB_bits[5]), .out_17(decoder_1_out_17), .out_18(decoder_1_out_18), .out_19(STB_bits[6]),
    .out_20(decoder_1_out_20), .out_21(decoder_1_out_21), .out_22(STB_bits[7]), .out_23(decoder_1_out_23),
    .out_24(decoder_1_out_24), .out_25(STB_bits[8]), .out_26(decoder_1_out_26), .out_27(decoder_1_out_27),
    .out_28(STB_bits[9]), .out_29(decoder_1_out_29));  // open: out_30, out_31
  or or_1 (CK_bits[0], decoder_1_out_2, STB_bits[0], decoder_1_out_0);
  or or_2 (CK_bits[1], decoder_1_out_5, STB_bits[1], decoder_1_out_3);
  or or_3 (CK_bits[2], decoder_1_out_8, STB_bits[2], decoder_1_out_6);
  or or_4 (CK_bits[3], decoder_1_out_11, STB_bits[3], decoder_1_out_9);
  or or_5 (CK_bits[4], decoder_1_out_14, STB_bits[4], decoder_1_out_12);
  or or_6 (CK_bits[5], decoder_1_out_17, STB_bits[5], decoder_1_out_15);
  or or_7 (CK_bits[6], decoder_1_out_20, STB_bits[6], decoder_1_out_18);
  or or_8 (CK_bits[7], decoder_1_out_23, STB_bits[7], decoder_1_out_21);
  or or_9 (CK_bits[8], decoder_1_out_26, STB_bits[8], decoder_1_out_24);
  or or_10 (CK_bits[9], decoder_1_out_29, STB_bits[9], decoder_1_out_27);
  or or_11 (PH_FIRST, decoder_1_out_0, decoder_1_out_3, decoder_1_out_6, decoder_1_out_9, decoder_1_out_12, decoder_1_out_15, decoder_1_out_18, decoder_1_out_21, decoder_1_out_24, decoder_1_out_27);
  or or_12 (PH_STB, STB_bits[0], STB_bits[1], STB_bits[2], STB_bits[3], STB_bits[4], STB_bits[5], STB_bits[6], STB_bits[7], STB_bits[8], STB_bits[9]);
  or or_13 (PH_LAST, decoder_1_out_2, decoder_1_out_5, decoder_1_out_8, decoder_1_out_11, decoder_1_out_14, decoder_1_out_17, decoder_1_out_20, decoder_1_out_23, decoder_1_out_26, decoder_1_out_29);
  PriorityEncoder #(.Selector_Bits(4)) priorityencoder_1 (
    .in0(CK_bits[0]), .in1(CK_bits[1]), .in2(CK_bits[2]), .in3(CK_bits[3]), .in4(CK_bits[4]),
    .in5(CK_bits[5]), .in6(CK_bits[6]), .in7(CK_bits[7]), .in8(CK_bits[8]), .in9(CK_bits[9]), .in10(1'b0),
    .in11(1'b0), .in12(1'b0), .in13(1'b0), .in14(1'b0), .in15(1'b0), .num(CK_num));  // open: any

  // Other names for the same wires on the sheet: CK0 = CK_bits[0]; CK1 = CK_bits[1]; CK2 = CK_bits[2];
  //   CK3 = CK_bits[3]; CK4 = CK_bits[4]; CK5 = CK_bits[5]; CK6 = CK_bits[6]; CK7 = CK_bits[7]; CK8 = CK_bits[8];
  //   CK9 = CK_bits[9]; STB0 = STB_bits[0]; STB1 = STB_bits[1]; STB2 = STB_bits[2]; STB3 = STB_bits[3];
  //   STB4 = STB_bits[4]; STB5 = STB_bits[5]; STB6 = STB_bits[6]; STB7 = STB_bits[7]; STB8 = STB_bits[8];
  //   STB9 = STB_bits[9]
endmodule
