// Digital circuit SRAM32Kx12.dig as structural Verilog
module SRAM32Kx12 (
  input  [16:0] A,
  input  nCE,
  input  nOE,
  input  nWE,
  output [11:0] D
);

  wire nor_1_out;

  RAMSinglePortSel #(.AddrBits(17), .isProgramMemory("true"), .Bits(12)) TWO_32Kx8 (
    .A(A), .CS(~nCE), .WE(~nWE), .OE(~nOE), .D(D));
  nor nor_1 (nor_1_out, nCE, ~nWE, nOE);  // NOr

  // Notes on the sheet:
  //   nCE: default 1
  //   nOE: default 1
  //   nWE: default 1
endmodule
