// Digital circuit TTY-SIM.dig as structural Verilog
module TTY_SIM (
  input  [7:0] IN,
  input  STB,
  input  ACK,
  input  OE,
  input  CLR,
  input  CLK,
  output [7:0] OUT,
  output RDY,
  output BSY
);

  wire fallingedgedet_1_y, keyboard_1_av, xor_1_out;
  wire [7:0] and_1_out, d_ff_as_1_q, keyboard_1_d, or_1_out;
  wire [15:8] keyboard_1_d_2;

  PullDown pulldown_1 (.out(ACK));
  PullDown pulldown_2 (.out(OE));
  PullDown #(.Bits(8)) pulldown_3 (.out(IN));
  PullDown pulldown_4 (.out(STB));
  PullDown pulldown_5 (.out(CLR));
  PullDown pulldown_6 (.out(CLK));
  FallingEdgeDet fallingedgedet_1 (.A(ACK), .Y(fallingedgedet_1_y));
  Keyboard keyboard_1 (.C(fallingedgedet_1_y), .en(1'b1), .D({keyboard_1_d_2, keyboard_1_d}), .av(keyboard_1_av));
  assign and_1_out = IN & 8'h7f;  // And and_1, 8 bits wide
  // Probe on {keyboard_1_d_2, keyboard_1_d}
  xor xor_1 (xor_1_out, keyboard_1_av, fallingedgedet_1_y);
  Terminal #(.termWidth(80), .termHeight(16)) terminal_1 (.D({{24{1'b0}}, and_1_out}), .C(STB), .en(1'b1));
  D_FF_AS #(.Bits(8)) d_ff_as_1 (.Set(1'b0), .D(keyboard_1_d), .C(xor_1_out), .Clr(CLR), .Q(d_ff_as_1_q));  // open: nQ
  // Probe on d_ff_as_1_q
  assign or_1_out = d_ff_as_1_q | 8'h80;  // Or or_1, 8 bits wide
  assign OUT = OE ? or_1_out : 8'bz;  // Driver driver_1
  RisingEdgeDet risingedgedet_1 (.A(xor_1_out), .Y(RDY));
  FallingEdgeDet fallingedgedet_2 (.A(STB), .Y(BSY));
  PullDown pulldown_7 (.out(STB));

  // Notes on the sheet:
  //   RDY: Has RisingEdge detecor
  //   BSY: Has FallingEdge detector
  //   ACK: Has a FallingEdge detector
endmodule
