// Digital circuit Test-uart1.dig as structural Verilog
module Test_uart1 (
  input  clk
);

  wire button_1_out, button_2_out, port_1_p3, uart_1_busy, uart_1_rdy, uart_1_tx;
  wire [7:0] uart_1_dout;
  wire [15:0] counter_1_out;

  Button button_1 (.out(button_1_out));
  Button button_2 (.out(button_2_out));
  Counter #(.Bits(16)) counter_1 (.en(1'b1), .C(clk), .clr(1'b0), .out(counter_1_out));  // open: ovf
  // Probe RX on port_1_p3
  UART uart_1 (
    .RX(port_1_p3), .ACK(button_1_out), .OE(1'b1), .DIN(8'h55), .STB(button_2_out), .CLK(clk),
    .DOUT(uart_1_dout), .RDY(uart_1_rdy), .TX(uart_1_tx), .BUSY(uart_1_busy));  // open: XTAL, CLEAR
  // Probe TX on uart_1_tx
  // Port port_1: pin names not known; wires that end beside it: uart_1_tx, counter_1_out[0], port_1_p3
  // Probe on uart_1_dout
  // Probe on uart_1_rdy
  // Probe BUSY on uart_1_busy

  // Notes on the sheet:
  //   clk: Hz: 100
endmodule
