// Digital circuit UART-TX.dig as structural Verilog
module UART_TX (
  input  [7:0] DATA,
  input  STB,
  input  CLK,
  output BUSY,
  output TX
);

  wire and_1_out, and_2_out, and_3_out, and_4_out, and_5_out, and_6_out, and_7_out, and_8_out, and_9_out,
       and_10_out, and_11_out, and_12_out, and_13_out, and_14_out, and_15_out, and_16_out, and_17_out,
       and_18_out, and_19_out, and_20_out, and_21_out, and_22_out, and_23_out, and_24_out, and_25_out,
       and_26_out, and_27_out, and_28_out, and_29_out, and_30_out, and_31_out, d_ff_1_q, d_ff_as_1_nq,
       d_ff_as_1_q, d_ff_as_2_nq, d_ff_as_2_q, d_ff_as_3_nq, d_ff_as_3_q, d_ff_as_4_nq, d_ff_as_4_q,
       d_ff_as_5_nq, d_ff_as_5_q, d_ff_as_6_nq, d_ff_as_6_q, d_ff_as_7_nq, d_ff_as_7_q, d_ff_as_8_nq,
       d_ff_as_8_q, d_ff_as_9_nq, d_ff_as_9_q, d_ff_as_10_nq, d_ff_as_10_q, d_ff_as_11_nq, d_ff_as_11_q,
       d_ff_as_12_nq, d_ff_as_12_q, delay_1_out;
  wire [1:0] counter_1_out;

  Counter #(.Bits(2)) counter_1 (.en(1'b1), .C(CLK), .clr(1'b0), .out(counter_1_out));  // open: ovf
  D_FF d_ff_1 (.D(STB), .C(counter_1_out[1]), .Q(d_ff_1_q));  // open: nQ
  Delay delay_1 (.in(d_ff_1_q), .out(delay_1_out));
  and and_1 (and_1_out, d_ff_1_q, ~delay_1_out);  // And
  and and_2 (and_2_out, counter_1_out[1], BUSY);
  and and_3 (and_3_out, and_4_out, and_1_out);
  and and_4 (and_4_out, and_1_out, 1'b1);
  D_FF_AS d_ff_as_1 (.Set(and_4_out), .D(1'b0), .C(and_2_out), .Clr(and_3_out), .Q(d_ff_as_1_q), .nQ(d_ff_as_1_nq));
  LED led_1 (.in(d_ff_as_1_q));
  and and_5 (and_5_out, and_1_out, 1'b1);
  and and_6 (and_6_out, and_5_out, and_1_out);
  LED led_2 (.in(d_ff_as_2_q));
  D_FF_AS d_ff_as_2 (
    .Set(and_5_out), .D(d_ff_as_1_q), .C(and_2_out), .Clr(and_6_out), .Q(d_ff_as_2_q), .nQ(d_ff_as_2_nq));
  and and_7 (and_7_out, and_1_out, DATA[7]);
  D_FF_AS d_ff_as_3 (
    .Set(and_7_out), .D(d_ff_as_2_q), .C(and_2_out), .Clr(and_8_out), .Q(d_ff_as_3_q), .nQ(d_ff_as_3_nq));
  and and_8 (and_8_out, and_7_out, and_1_out);
  LED led_3 (.in(d_ff_as_3_q));
  and and_9 (and_9_out, and_10_out, and_1_out);
  and and_10 (and_10_out, and_1_out, DATA[6]);
  D_FF_AS d_ff_as_4 (
    .Set(and_10_out), .D(d_ff_as_3_q), .C(and_2_out), .Clr(and_9_out), .Q(d_ff_as_4_q), .nQ(d_ff_as_4_nq));
  LED led_4 (.in(d_ff_as_4_q));
  and and_11 (and_11_out, d_ff_as_4_nq, d_ff_as_3_nq, d_ff_as_2_nq, d_ff_as_1_nq);
  and and_12 (and_12_out, and_1_out, DATA[5]);
  and and_13 (and_13_out, and_12_out, and_1_out);
  LED led_5 (.in(d_ff_as_5_q));
  D_FF_AS d_ff_as_5 (
    .Set(and_12_out), .D(d_ff_as_4_q), .C(and_2_out), .Clr(and_13_out), .Q(d_ff_as_5_q), .nQ(d_ff_as_5_nq));
  and and_14 (and_14_out, and_1_out, DATA[4]);
  D_FF_AS d_ff_as_6 (
    .Set(and_14_out), .D(d_ff_as_5_q), .C(and_2_out), .Clr(and_15_out), .Q(d_ff_as_6_q), .nQ(d_ff_as_6_nq));
  and and_15 (and_15_out, and_14_out, and_1_out);
  LED led_6 (.in(d_ff_as_6_q));
  and and_16 (and_16_out, and_17_out, and_1_out);
  and and_17 (and_17_out, and_1_out, DATA[3]);
  D_FF_AS d_ff_as_7 (
    .Set(and_17_out), .D(d_ff_as_6_q), .C(and_2_out), .Clr(and_16_out), .Q(d_ff_as_7_q), .nQ(d_ff_as_7_nq));
  LED led_7 (.in(d_ff_as_7_q));
  and and_18 (and_18_out, and_19_out, and_1_out);
  and and_19 (and_19_out, and_1_out, DATA[2]);
  D_FF_AS d_ff_as_8 (
    .Set(and_19_out), .D(d_ff_as_7_q), .C(and_2_out), .Clr(and_18_out), .Q(d_ff_as_8_q), .nQ(d_ff_as_8_nq));
  LED led_8 (.in(d_ff_as_8_q));
  and and_20 (and_20_out, d_ff_as_8_nq, d_ff_as_7_nq, d_ff_as_6_nq, d_ff_as_5_nq);
  and and_21 (and_21_out, and_22_out, and_1_out);
  and and_22 (and_22_out, and_1_out, DATA[1]);
  D_FF_AS d_ff_as_9 (
    .Set(and_22_out), .D(d_ff_as_8_q), .C(and_2_out), .Clr(and_21_out), .Q(d_ff_as_9_q), .nQ(d_ff_as_9_nq));
  LED led_9 (.in(d_ff_as_9_q));
  and and_23 (and_23_out, and_1_out, DATA[0]);
  and and_24 (and_24_out, and_23_out, and_1_out);
  LED led_10 (.in(d_ff_as_10_q));
  D_FF_AS d_ff_as_10 (
    .Set(and_23_out), .D(d_ff_as_9_q), .C(and_2_out), .Clr(and_24_out), .Q(d_ff_as_10_q), .nQ(d_ff_as_10_nq));
  and and_25 (and_25_out, and_1_out, 1'b0);
  D_FF_AS d_ff_as_11 (
    .Set(and_25_out), .D(d_ff_as_10_q), .C(and_2_out), .Clr(and_26_out), .Q(d_ff_as_11_q), .nQ(d_ff_as_11_nq));
  and and_26 (and_26_out, and_25_out, and_1_out);
  LED led_11 (.in(d_ff_as_11_q));
  and and_27 (and_27_out, and_28_out, and_1_out);
  and and_28 (and_28_out, and_1_out, 1'b0);
  D_FF_AS d_ff_as_12 (
    .Set(and_28_out), .D(d_ff_as_11_q), .C(and_2_out), .Clr(and_27_out), .Q(d_ff_as_12_q), .nQ(d_ff_as_12_nq));
  LED led_12 (.in(d_ff_as_12_q));
  and and_29 (and_29_out, d_ff_as_12_nq, d_ff_as_11_nq, d_ff_as_10_nq, d_ff_as_9_nq);
  // Probe TXCLK on and_2_out
  LED led_13 (.in(and_2_out));
  and and_30 (and_30_out, and_29_out, and_20_out, and_11_out, 1'b1);
  not not_1 (BUSY, and_30_out);
  and and_31 (and_31_out, d_ff_as_12_nq, BUSY);
  LED led_14 (.in(BUSY));
  D_FF d_ff_2 (.D(and_31_out), .C(CLK), .nQ(TX));  // open: Q
  LED led_15 (.in(TX));
endmodule
