// Digital circuit UART-tester.dig as structural Verilog
module UART_tester (
  input  clk
);

  wire button_1_out, button_2_out, button_3_out, comparator_1_eq, counter_2_ovf, port_1_p3, uart_1_busy,
       uart_1_rdy, uart_1_tx;
  wire [5:0] counter_2_out;
  wire [7:0] uart_1_dout;
  wire [31:0] add_1_s, counter_1_out, counter_3_out;

  Button button_1 (.out(button_1_out));
  Counter #(.Bits(32)) counter_1 (.en(1'b1), .C(counter_2_ovf), .clr(button_1_out), .out(counter_1_out));  // open: ovf
  // Probe on counter_1_out
  Add #(.Bits(32)) add_1 (.a(counter_1_out), .b(32'h2710), .c_i(1'b0), .s(add_1_s));  // open: c_o
  Counter #(.Bits(6)) counter_2 (.en(1'b1), .C(comparator_1_eq), .clr(1'b0), .out(counter_2_out), .ovf(counter_2_ovf));
  // Probe on add_1_s
  Counter #(.Bits(32)) counter_3 (.en(1'b1), .C(clk), .clr(comparator_1_eq), .out(counter_3_out));  // open: ovf
  Comparator #(.Bits(32)) comparator_1 (.a(add_1_s), .b(counter_3_out), .eq(comparator_1_eq));  // open: gt, lt
  Button button_2 (.out(button_2_out));
  Button button_3 (.out(button_3_out));
  UART uart_1 (
    .RX(port_1_p3), .ACK(button_2_out), .OE(1'b1), .DIN(8'h55), .STB(comparator_1_eq), .CLK(clk), .XTAL(clk),
    .CLEAR(button_3_out), .DOUT(uart_1_dout), .RDY(uart_1_rdy), .TX(uart_1_tx), .BUSY(uart_1_busy));
  // Port port_1: pin names not known; wires that end beside it: uart_1_tx, clk, port_1_p3
  // Probe on uart_1_dout
  // Probe on uart_1_rdy
  // CntProbe cntprobe_1: pin names not known; wires that end beside it: uart_1_busy

  // Other names for the same wires on the sheet: XTAL = clk

  // Notes on the sheet:
  //   clk: Hz: 2147483647
endmodule
