// Digital circuit UART.dig as structural Verilog
module UART (
  input  RX,
  input  ACK,
  input  OE,
  input  [7:0] DIN,
  input  STB,
  input  CLK,
  input  XTAL,
  input  CLEAR,
  output [7:0] DOUT,
  output RDY,
  output TX,
  output BUSY
);

  wire _74165_1_p18, _74393_1__1qd, _74393_1__2qa, _74393_1__2qd, _74393_2__1qb, _74393_2__1qd,
       _74393_2__2qd, _74595_1_q_a, _74595_1_q_b, _74595_1_q_c, _74595_1_q_d, _74595_1_q_e, _74595_1_q_f,
       _74595_1_q_g, _74595_1_q_h, and_1_out, CLK_t, d_ff_1_nq, d_ff_1_q, fallingedgedet_1_y, nand_1_out,
       nand_2_out, nand_3_out, nand_4_out, nand_5_out, nand_6_out, nand_7_out, nand_8_out, nand_9_out,
       nand_10_out, nand_11_out, nand_12_out, nand_13_out, nand_14_out, nor_1_out, or_1_out, pulldown_3_out,
       pulldown_4_out, pullup_2_out, pullup_3_out;
  wire [7:0] _74373_1_p20;

  PullDown pulldown_1 (.out(STB));
  and and_1 (and_1_out, XTAL, CLEAR);
  PullUp pullup_1 (.out(RX));
  PullDown pulldown_2 (.out(ACK));
  nand nand_1 (nand_1_out, STB, STB);
  xor xor_1 (CLK_t, CLK, and_1_out);
  nand nand_2 (nand_2_out, nand_10_out, _74393_1__1qd);
  // _74373 _74373_1: pin names not known; wires that end beside it: 1'b0, STB, DIN[0], DIN[1], DIN[2], DIN[3], DIN[4], DIN[5], DIN[6], DIN[7], 1'b1, 1'b0, _74373_1_p20[0], _74373_1_p20[1], _74373_1_p20[2], _74373_1_p20[3], _74373_1_p20[4], _74373_1_p20[5], _74373_1_p20[6], _74373_1_p20[7]
  nand nand_3 (nand_3_out, nand_1_out, nand_4_out);
  nand nand_4 (nand_4_out, nand_3_out, d_ff_1_nq);
  nand nand_5 (nand_5_out, nand_2_out, nand_6_out);
  nand nand_6 (nand_6_out, nand_5_out, RX);
  FallingEdgeDet fallingedgedet_1 (.A(nand_2_out), .Y(fallingedgedet_1_y));
  D_FF d_ff_1 (.D(nand_3_out), .C(_74393_2__2qd), .Q(d_ff_1_q), .nQ(d_ff_1_nq));
  _74393 _74393_1 (
    .VCC(1'b1), .GND(1'b0), ._1A(CLK_t), ._1CL(nand_5_out), ._2A(_74393_1__1qd), ._2CL(nand_5_out),
    ._1QD(_74393_1__1qd), ._2QA(_74393_1__2qa), ._2QD(_74393_1__2qd));  // open: _1QA, _1QB, _1QC, _2QB, _2QC
  nand nand_7 (nand_7_out, fallingedgedet_1_y, fallingedgedet_1_y);
  nor nor_1 (nor_1_out, ACK, CLEAR);
  nand nand_8 (nand_8_out, nand_11_out, _74393_2__2qd);
  nand nand_9 (nand_9_out, _74393_1__2qa, _74393_1__2qd);
  RS_FF_AS rs_ff_as_1 (.S(~nand_7_out), .R(~nor_1_out), .Q(RDY));  // open: nQ
  _74393 _74393_2 (
    .VCC(1'b1), .GND(1'b0), ._1A(nand_8_out), ._1CL(d_ff_1_q), ._2A(CLK_t), ._2CL(1'b0),
    ._1QB(_74393_2__1qb), ._1QD(_74393_2__1qd), ._2QD(_74393_2__2qd));  // open: _1QA, _1QC, _2QA, _2QB, _2QC
  PullDown pulldown_3 (.out(pulldown_3_out));
  PullUp pullup_2 (.out(pullup_2_out));
  nand nand_10 (nand_10_out, nand_9_out, nand_9_out);
  nand nand_11 (nand_11_out, _74393_2__1qb, _74393_2__1qd);
  nand nand_12 (nand_12_out, OE, OE);
  // _74165 _74165_1: pin names not known; wires that end beside it: pulldown_3_out, _74373_1_p20[7], pullup_2_out, d_ff_1_nq, pulldown_3_out, 1'b0, _74393_2__2qd, 1'b1, _74373_1_p20[6], _74373_1_p20[5], _74373_1_p20[4], _74373_1_p20[3], _74373_1_p20[2], _74373_1_p20[1], _74373_1_p20[0], 1'b1, 1'b0, _74165_1_p18
  or or_1 (or_1_out, nand_3_out, nand_11_out);
  _74595 _74595_1 (
    .SER(RX), .SCLK(_74393_1__1qd), .RCLK(nand_10_out), .nOE(1'b0), .nCLR(1'b1), .VCC(1'b1), .GND(1'b0),
    .Q_A(_74595_1_q_a), .Q_B(_74595_1_q_b), .Q_C(_74595_1_q_c), .Q_D(_74595_1_q_d), .Q_E(_74595_1_q_e),
    .Q_F(_74595_1_q_f), .Q_G(_74595_1_q_g), .Q_H(_74595_1_q_h));  // open: Q_HH
  nand nand_13 (nand_13_out, d_ff_1_nq, _74165_1_p18);
  nand nand_14 (nand_14_out, or_1_out, nand_13_out);
  PullUp pullup_3 (.out(pullup_3_out));
  PullDown pulldown_4 (.out(pulldown_4_out));
  and and_2 (BUSY, ~CLEAR, or_1_out);  // And
  or or_2 (TX, CLEAR, nand_14_out);
  // _74541 _74541_1: pin names not known; wires that end beside it: pulldown_4_out, _74595_1_q_a, pullup_3_out, nand_12_out, nand_12_out, pullup_3_out, _74595_1_q_b, _74595_1_q_c, _74595_1_q_d, _74595_1_q_e, _74595_1_q_f, _74595_1_q_g, _74595_1_q_h, 1'b1, 1'b0, DOUT[7], DOUT[6], DOUT[5], DOUT[4], DOUT[3], DOUT[2], DOUT[1], DOUT[0]

  // Notes on the sheet:
  //   DOUT: 8 bits of parallel data from the received serial stream. Controlled by the OE input
  //   RDY: Goes high when a full byte of data has been received at the RX. Cleared at the rising edge of the ACK input
  //   RX: Serial data input
  //   ACK: Rising edge acknowledges that the received data has been read. Causes the RDY output to go low.
  //   TX: Serial data output
  //   OE: High level enables the parallel output on DOUT of of the received data
  //   DIN: 8 bit of parallel data to be sent, default 15
  //   BUSY: High while the TX output is transmidding start/data/stopbits.
  //   STB: Rising edge latches the parallel data at DIN and starts the serial output stream at TX
  //   CLK: 16 times the desired baudrate, default 15
  //   XTAL: High level enables the parallel output on DOUT of of the received data
  //   CLEAR: High level enables the parallel output on DOUT of of the received data
  //   SERIAL TRANSMITER
  //   SERIAL RECEIVER
  //   Clock domain synchronizer
  //   2 pcs 7474 Dual D- Flip-Flop
  //   4 pcs 7400 Quad 2-input NAND
  //   2 pcs 74393 Dual 4-bit counter
  //   1 pcs 74165 PISO Shift register
  //   1 pcs 74595 SIPO Shift counter
  //   10-counter, divide-by-16
  //   The Serial Receiver is based on
  //   http://digitarworld.uw.hu/circuits.html
  //   8N1
  //   7S1
  //   7M1
endmodule
