// Digital circuit ind_dir2.dig as structural Verilog
module ind_dir2 (
  input  OP0,
  input  IA,
  input  CP,
  input  IR3,
  input  IR4,
  input  IR5,
  input  IR6,
  input  OP1,
  input  OP2,
  input  A,
  output AUTOIND,
  output IND,
  output DIR,
  output MP
);

  wire ADDR10__17, AND, and_2_out, and_3_out, DCA, IOT, ISZ, JMP, JMS, nor_2_out, nor_3_out, OPR,
       PC_ZEROPAGE, TAD;

  nor nor_1 (PC_ZEROPAGE, A, A, A, A, A);
  Demultiplexer #(.Selector_Bits(3)) demultiplexer_1 (
    .sel({OP2, OP1, OP0}), .in(1'b1), .out_0(AND), .out_1(TAD), .out_2(ISZ), .out_3(DCA), .out_4(JMS),
    .out_5(JMP), .out_6(IOT), .out_7(OPR));
  and and_1 (ADDR10__17, IR3, ~IR4, ~IR5, ~IR6);  // And
  and and_2 (and_2_out, PC_ZEROPAGE, ADDR10__17);
  and and_3 (and_3_out, ~CP, ADDR10__17);  // And
  nor nor_2 (nor_2_out, and_2_out, and_3_out);
  nor nor_3 (nor_3_out, OPR, IOT);
  and and_4 (AUTOIND, nor_3_out, IA, ~nor_2_out);  // And
  and and_5 (IND, nor_3_out, IA, nor_2_out);
  and and_6 (DIR, nor_3_out, ~IA);  // And
  and and_7 (MP, nor_3_out, CP);

  // Notes on the sheet:
  //   CP=0 PAGE ZERO
  //   CP=1 CURRENT PAGE
  //   IA=0 DIRECT
  //   IA=1 INDIRECT
endmodule

/* Test case:
OP0 IA CP IR3 IR4 IR5 IR6 OP1 OP2 A AUTOIND IND DIR MP

0   0  0  0   0   0   0   0   0   0 0       0   1   0
0   0  0  0   0   0   0   0   0   1 0       0   1   0
0   0  0  0   0   0   0   0   1   0 0       0   1   0
0   0  0  0   0   0   0   0   1   1 0       0   1   0
0   0  0  0   0   0   0   1   0   0 0       0   1   0
0   0  0  0   0   0   0   1   0   1 0       0   1   0
0   0  0  0   0   0   0   1   1   0 0       0   0   0
0   0  0  0   0   0   0   1   1   1 0       0   0   0
0   0  0  0   0   0   1   0   0   0 0       0   1   0
0   0  0  0   0   0   1   0   0   1 0       0   1   0
0   0  0  0   0   0   1   0   1   0 0       0   1   0
0   0  0  0   0   0   1   0   1   1 0       0   1   0
0   0  0  0   0   0   1   1   0   0 0       0   1   0
0   0  0  0   0   0   1   1   0   1 0       0   1   0
0   0  0  0   0   0   1   1   1   0 0       0   0   0
0   0  0  0   0   0   1   1   1   1 0       0   0   0
0   0  0  0   0   1   0   0   0   0 0       0   1   0
0   0  0  0   0   1   0   0   0   1 0       0   1   0
0   0  0  0   0   1   0   0   1   0 0       0   1   0
0   0  0  0   0   1   0   0   1   1 0       0   1   0
0   0  0  0   0   1   0   1   0   0 0       0   1   0
0   0  0  0   0   1   0   1   0   1 0       0   1   0
0   0  0  0   0   1   0   1   1   0 0       0   0   0
0   0  0  0   0   1   0   1   1   1 0       0   0   0
0   0  0  0   0   1   1   0   0   0 0       0   1   0
0   0  0  0   0   1   1   0   0   1 0       0   1   0
0   0  0  0   0   1   1   0   1   0 0       0   1   0
0   0  0  0   0   1   1   0   1   1 0       0   1   0
0   0  0  0   0   1   1   1   0   0 0       0   1   0
0   0  0  0   0   1   1   1   0   1 0       0   1   0
0   0  0  0   0   1   1   1   1   0 0       0   0   0
0   0  0  0   0   1   1   1   1   1 0       0   0   0
0   0  0  0   1   0   0   0   0   0 0       0   1   0
0   0  0  0   1   0   0   0   0   1 0       0   1   0
0   0  0  0   1   0   0   0   1   0 0       0   1   0
0   0  0  0   1   0   0   0   1   1 0       0   1   0
0   0  0  0   1   0   0   1   0   0 0       0   1   0
0   0  0  0   1   0   0   1   0   1 0       0   1   0
0   0  0  0   1   0   0   1   1   0 0       0   0   0
0   0  0  0   1   0   0   1   1   1 0       0   0   0
0   0  0  0   1   0   1   0   0   0 0       0   1   0
0   0  0  0   1   0   1   0   0   1 0       0   1   0
0   0  0  0   1   0   1   0   1   0 0       0   1   0
0   0  0  0   1   0   1   0   1   1 0       0   1   0
0   0  0  0   1   0   1   1   0   0 0       0   1   0
0   0  0  0   1   0   1   1   0   1 0       0   1   0
0   0  0  0   1   0   1   1   1   0 0       0   0   0
0   0  0  0   1   0   1   1   1   1 0       0   0   0
0   0  0  0   1   1   0   0   0   0 0       0   1   0
0   0  0  0   1   1   0   0   0   1 0       0   1   0
0   0  0  0   1   1   0   0   1   0 0       0   1   0
0   0  0  0   1   1   0   0   1   1 0       0   1   0
0   0  0  0   1   1   0   1   0   0 0       0   1   0
0   0  0  0   1   1   0   1   0   1 0       0   1   0
0   0  0  0   1   1   0   1   1   0 0       0   0   0
0   0  0  0   1   1   0   1   1   1 0       0   0   0
0   0  0  0   1   1   1   0   0   0 0       0   1   0
0   0  0  0   1   1   1   0   0   1 0       0   1   0
0   0  0  0   1   1   1   0   1   0 0       0   1   0
0   0  0  0   1   1   1   0   1   1 0       0   1   0
0   0  0  0   1   1   1   1   0   0 0       0   1   0
0   0  0  0   1   1   1   1   0   1 0       0   1   0
0   0  0  0   1   1   1   1   1   0 0       0   0   0
0   0  0  0   1   1   1   1   1   1 0       0   0   0
0   0  0  1   0   0   0   0   0   0 0       0   1   0
0   0  0  1   0   0   0   0   0   1 0       0   1   0
0   0  0  1   0   0   0   0   1   0 0       0   1   0
0   0  0  1   0   0   0   0   1   1 0       0   1   0
0   0  0  1   0   0   0   1   0   0 0       0   1   0
0   0  0  1   0   0   0   1   0   1 0       0   1   0
0   0  0  1   0   0   0   1   1   0 0       0   0   0
0   0  0  1   0   0   0   1   1   1 0       0   0   0
0   0  0  1   0   0   1   0   0   0 0       0   1   0
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*/
