// Digital circuit main-flip.dig as structural Verilog
module main_flip (
);

  wire CCC_C, CK_FETCH, DATA_CK, driver_4_out, FORCE4000, INC2RAMD, INCZERO, IND2INC, IND2PC, IND2RAMA,
       IND_CK, IR2PC, IR2RAMA, IR_CK, LD2INC, MP, not_1_out, not_2_out, not_3_out, PC2ADDR, PC2RAMD, PC_CK,
       PC_LD, RAM_OE, RAM_WE, RAMD2PC, SETPC, xor_1_out;
  wire [4:0] BANK;
  wire [11:0] ACBUS2, BUS_IR, LPC, multilatchclr_2_out1, NEWPC, PC, PCIN, RAMADDR, RAMDATA, REG;

  assign ACBUS2 = FORCE4000 ? 12'h800 : 12'bz;  // Driver driver_1
  assign ACBUS2 = PC2RAMD ? PC : 12'bz;  // Driver driver_2
  assign PCIN = SETPC ? NEWPC : 12'bz;  // Driver driver_3
  assign driver_4_out = SETPC ? SETPC : 1'bz;  // Driver driver_4
  assign PC_LD = SETPC ? SETPC : 1'bz;  // Driver driver_5
  assign PCIN = RAMD2PC ? ACBUS2 : 12'bz;  // Driver driver_6
  LED led_1 (.in(IR2PC));
  assign PCIN = SETPC ? NEWPC : 12'bz;  // Driver driver_7
  assign PCIN = IND2PC ? REG : 12'bz;  // Driver driver_8
  // OC12 oc12_1: pin names not known; wires that end beside it: BUS_IR[6:0], LPC[11:7], MP, IR2PC, PCIN[6:0], PCIN[11:7], PCIN
  assign RAMADDR = PC2ADDR ? PC : 12'bz;  // Driver driver_9
  // Probe PCIN on PCIN
  LED led_2 (.in(PC_CK));
  // OC12 oc12_2: pin names not known; wires that end beside it: BUS_IR[6:0], LPC[11:7], MP, IR2PC, PCIN[6:0], PCIN[11:7]
  LED led_3 (.in(IR2PC));
  xor xor_1 (xor_1_out, PC_CK, driver_4_out);
  not not_1 (not_1_out, xor_1_out);
  LED led_4 (.in(PC_LD));
  LED led_5 (.in(RAMD2PC));
  assign PCIN = RAMD2PC ? ACBUS2 : 12'bz;  // Driver driver_10
  LED led_6 (.in(IND2PC));
  assign PCIN = IND2PC ? multilatchclr_2_out1 : 12'bz;  // Driver driver_11
  PC pc_1 (.IN(PCIN), .CLK(not_1_out), .LD(PC_LD), .CLR(1'b0), .LATCH1(CK_FETCH), .LATCH2(SETPC), .PC(PC), .LPC(LPC));
  // OC12 oc12_3: pin names not known; wires that end beside it: BUS_IR[6:0], LPC[11:7], MP, IR2RAMA, RAMADDR[6:0], RAMADDR[11:7]
  LED led_7 (.in(IR2RAMA));
  // Probe LPC on LPC
  // Probe PCOUT on PC
  // OC12 oc12_4: pin names not known; wires that end beside it: BUS_IR[6:0], LPC[11:7], MP, IR2RAMA, RAMADDR[6:0], RAMADDR[11:7]
  LED led_8 (.in(IR2RAMA));
  PC pc_2 (.IN(PCIN), .CLR(1'b0), .LATCH1(CK_FETCH), .LATCH2(SETPC), .PC(PC), .LPC(LPC));  // open: CLK, LD
  LED led_9 (.in(PC2ADDR));
  assign RAMADDR = PC2ADDR ? PC : 12'bz;  // Driver driver_12
  // Probe RAMA on RAMADDR
  LED led_10 (.in(RAM_WE));
  LED led_11 (.in(RAM_OE));
  assign RAMDATA = RAM_WE ? ACBUS2 : 12'bz;  // Driver driver_13
  EEPROM #(.AddrBits(17), .isProgramMemory("true"), .Bits(12)) eeprom_1 (
    .A({BANK, RAMADDR}), .CS(1'b1), .WE(RAM_WE), .OE(RAM_OE), .D(RAMDATA));
  EEPROM #(.AddrBits(17), .isProgramMemory("true"), .Bits(12)) eeprom_2 (
    .A({BANK, RAMADDR}), .CS(1'b1), .WE(RAM_WE), .OE(RAM_OE), .D(RAMDATA));
  assign ACBUS2 = RAM_OE ? RAMDATA : 12'bz;  // Driver driver_14
  // Probe RAMD on RAMDATA
  assign ACBUS2 = RAM_OE ? RAMDATA : 12'bz;  // Driver driver_15
  assign RAMDATA = RAM_WE ? ACBUS2 : 12'bz;  // Driver driver_16
  not not_2 (not_2_out, IR_CK);
  LED led_12 (.in(IR_CK));
  LED led_13 (.in(FORCE4000));
  assign ACBUS2 = FORCE4000 ? 12'h800 : 12'bz;  // Driver driver_17
  LED led_14 (.in(PC2RAMD));
  assign ACBUS2 = PC2RAMD ? PC : 12'bz;  // Driver driver_18
  // TRANSP_LATCH IR: pin names not known; wires that end beside it: ACBUS2, not_2_out, BUS_IR
  // Probe DATA on ACBUS2
  not not_3 (not_3_out, IR_CK);
  LED led_15 (.in(IR_CK));
  // TRANSP_LATCH IR_2: pin names not known; wires that end beside it: ACBUS2, ACBUS2, not_3_out, BUS_IR, BUS_IR
  // Probe IR on BUS_IR
  MultiLatchClr multilatchclr_1 (
    .CLR(CCC_C), .IN(ACBUS2), .LATCH(IND_CK), .OE(1'b1), .OE1(IND2INC), .OE2(IND2RAMA), .OUT1(REG),
    .OUT2(RAMADDR));  // open: mon
  MultiLatchClr multilatchclr_2 (
    .CLR(CCC_C), .IN(ACBUS2), .LATCH(DATA_CK), .OE(1'b1), .OE1(LD2INC), .OE2(1'b0),
    .OUT1(multilatchclr_2_out1));  // open: OUT2, mon
  MultiLatchClr multilatchclr_3 (
    .CLR(CCC_C), .IN(ACBUS2), .LATCH(IND_CK), .OE(1'b1), .OE1(IND2INC), .OE2(IND2RAMA),
    .OUT1(multilatchclr_2_out1), .OUT2(RAMADDR));  // open: mon
  MultiLatchClr multilatchclr_4 (
    .CLR(CCC_C), .IN(ACBUS2), .LATCH(DATA_CK), .OE(1'b1), .OE1(LD2INC), .OE2(1'b0), .OUT1(REG));  // open: OUT2, mon
  INCREMENTER incrementer_1 (.IN(multilatchclr_2_out1), .INC(1'b1), .OE(INC2RAMD), .OUT(ACBUS2), .C(INCZERO));
  INCREMENTER incrementer_2 (.IN(REG), .INC(1'b1), .OE(INC2RAMD), .OUT(ACBUS2), .C(INCZERO));

  // Other names for the same wires on the sheet: DATA[11:0] = ACBUS2

  // Notes on the sheet:
  //   PCIN
  //   RAMADDR
  //   contents of eeprom_1 (hex, n*v repeats v):
  //   0,e00,e00,b00,f02,f02,f02,f02,9b,f02,f02,f02,f02,f02,f02,f02,f02,f02,f02,f02,f02,
  //   f02,f02,f02,f02,f02,f02,f02,f02,f02,f02,f02,f02,f02,f02,f02,f02,f02,f02,f02,f02,f02,
  //   f02,f02,f02,f02,f02,f02,f02,f02,f02,f02,f02,f02,f02,f02,f02,f02,f02,f02,f02,f02,f02,
  //   f02,c07,c1d,e01,a41,e00,e00,c02,e00,e00,c01,e00,e00,c04,e00,e00,c02,e00,e00,c05,e00,
  //   e00,e00,e00,a58,e00,e00,e00,bff,c1a,c19,a5d,c1e,c26,c21,a61,c26,c21,a64,c26,c21,a67,
  //   a5d,e80,c26,c21,a6c,e01,a6b,f02,f02,f02,f02,f02,f02,f02,f02,f02,f02,f02,f02,f02,f02,
  //   f02,82,e00,a82,c20,e80,308,f28,a86,889,a83,0,c21,a8a,c26,b89,ed0,e04,f18,a95,49b,
  //   a92,a8f,e08,f18,a8f,49b,a98,a95,0,d,a,d,a,c1,f6,e1,e9,ec,e1,e2,ec,e5,a0,f3,ef,e6,
  //   f4,f7,e1,f2,e5,f3,ba,d,a,ad,ad,ad,ad,ad,ad,ad,ad,ad,ad,ad,ad,ad,ad,ad,ad,ad,ad,ad,
  //   ad,d,a,30,30,30,3a,20,70,72,69,6e,74,68,65,6c,70,2e,62,69,6e,20,20,20,20,20,20,20,
  //   20,20,20,20,20,20,20,20,20,50,43,3a,30,32,30,30,20,28,54,68,69,73,20,68,65,6c,70,
  //   29,a,d,30,30,31,3a,20,44,30,41,42,2d,49,6e,73,74,54,65,73,74,2d,31,2e,70,74,20,20,
  //   20,20,20,20,20,20,20,20,20,50,43,3a,30,32,30,30,20,53,52,3a,37,37,37,37,20,57,61,
  //   74,63,68,3a,30,31,32,31,20,63,6f,6e,74,40,30,31,34,37,a,d,30,30,32,3a,20,44,30,42,
  //   42,2d,49,6e,73,74,54,65,73,74,2d,32,2e,70,74,20,20,20,20,20,20,20,20,20,20,20,50,
  //   43,3a,30,32,30,30,20,53,52,3a,78,78,78,78,20,57,61,74,63,68,3a,33,37,34,37,a,d,30,
  //   30,33,3a,20,44,30,49,42,2d,4a,4d,50,4a,4d,53,2e,70,74,20,20,20,20,20,20,20,20,20,
  //   20,20,20,20,20,20,50,43,3a,30,32,30,30,20,53,52,3a,78,78,78,78,20,57,61,74,63,68,
  //   3a,33,35,37,31,a,d,30,30,34,3a,20,44,30,4a,42,2d,4a,4d,50,4a,4d,53,2d,52,41,4e,44,
  //   4f,4d,2e,70,74,20,20,20,20,20,20,20,20,50,43,3a,30,32,30,30,20,53,52,3a,30,30,30,
  //   30,20,57,61,74,63,68,3a,30,30,34,34,a,d,30,30,35,3a,20,44,30,44,42,2d,52,61,6e,64,
  //   6f,6d,41,4e,44,2e,70,74,20,20,20,20,20,20,20,20,20,20,20,20,50,43,3a,30,32,30,30,
  //   20,53,52,3a,30,30,30,30,20,57,61,74,63,68,3a,30,32,30,32,a,d,30,30,36,3a,20,44,30,
  //   45,42,2d,52,61,6e,64,6f,6d,2d,54,41,44,2e,70,74,20,20,20,20,20,20,20,20,20,20,20,
  //   50,43,3a,30,32,30,30,20,53,52,3a,30,30,30,30,20,57,61,74,63,68,3a,36,37,37,36,a,d,
  //   30,30,37,3a,20,44,30,46,43,2d,52,61,6e,64,6f,6d,2d,49,53,5a,2e,70,74,20,20,20,20,
  //   20,20,20,20,20,20,20,50,43,3a,30,32,30,30,20,53,52,3a,30,30,30,30,20,57,61,74,63,
  //   68,3a,30,31,37,35,a,d,30,31,30,3a,20,44,30,47,43,2d,52,61,6e,64,6f,6d,2d,44,43,41,
  //   2e,70,74,20,20,20,20,20,20,20,20,20,20,20,50,43,3a,30,32,30,30,20,53,52,3a,30,30,
  //   30,30,20,57,61,74,63,68,20,30,30,30,36,2f,30,30,31,31,a,d,30,31,31,3a,20,44,30,43,
  //   43,2d,41,64,64,54,65,73,74,2e,70,74,20,20,20,20,20,20,20,20,20,20,20,20,20,20,50,
  //   43,3a,30,32,30,30,a,d,30,31,32,3a,20,44,31,41,41,2d,4d,65,6d,6f,72,79,2d,43,68,65,
  //   63,6b,65,72,62,6f,61,72,64,2e,70,74,20,20,50,43,3a,30,32,30,30,a,d,30,31,33,3a,20,
  //   44,31,45,41,2d,4d,65,6d,6f,72,79,2d,41,64,64,72,65,73,73,2e,72,69,6d,20,20,20,20,
  //   20,20,50,43,3a,30,32,30,30,a,d,30,31,34,3a,20,66,6f,63,61,6c,2d,38,2e,62,69,6e,20,
  //   20,20,20,20,20,20,20,20,20,20,20,20,20,20,20,20,20,50,43,3a,30,32,30,30,a,d,30,31,
  //   35,3a,20,49,6e,74,49,4f,2e,62,69,6e,20,20,20,20,20,20,20,20,20,20,20,20,20,20,20,
  //   20,20,20,20,20,50,43,3a,30,31,30,30,a,d,30,31,36,3a,20,49,6e,74,6f,75,74,2e,62,69,
  //   6e,20,20,20,20,20,20,20,20,20,20,20,20,20,20,20,20,20,20,20,50,43,3a,30,31,30,30,
  //   a,d,30,31,37,3a,20,74,73,74,65,73,74,2e,62,69,6e,20,20,20,20,20,20,20,20,20,20,20,
  //   20,20,20,20,20,20,20,20,50,43,3a,30,31,30,30,a,d,bc,e5,ee,e4,be,d,0,f02,f02,f02,f02,
  //   f02,f02,f02,f02,f02,f02,f02,f02,f02,f02,f02,f02,f02,f02,f02,f02,f02,f02,f02,f02,f02,
  //   f02,f02,f02,f02,f02,f02,f02,f02,f02,f02,f02,f02,f02,f02,f02,f02,f02,f02,f02,f02,f02,
  //   f02,f02,f02,f02,f02,f02,f02,f02,f02,f02,f02,f02,f02,f02,f02,f02,f02,f02,f02,f02,f02,
  //   f02,f02,f02,f02,f02,f02,f02,f02,f02,f02,f02,f02,f02,f02,f02,f02,f02,f02,f02,f02,f02,
  //   f02,f02,f02,f02,f02,f02,f02,f02,f02,f02,f02,f02,f02,f02,f02,f02,f02,f02,f02,f02,f02,
  //   f02,f02,f02,f02,f02,f02,f02,f02,f02,f02,f02,f02,f02,f02,f02,f02,f02,f02,f02,f02,f02,
  //   f02,f02,f02,f02,f02,f02,f02,f02,f02,f02,f02,f02,f02,f02,f02,f02,f02,f02,f02,f02,f02,
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  //   contents of eeprom_2 (hex, n*v repeats v):
  //   0,e00,e00,b00,f02,f02,f02,f02,9b,f02,f02,f02,f02,f02,f02,f02,f02,f02,f02,f02,f02,
  //   f02,f02,f02,f02,f02,f02,f02,f02,f02,f02,f02,f02,f02,f02,f02,f02,f02,f02,f02,f02,f02,
  //   f02,f02,f02,f02,f02,f02,f02,f02,f02,f02,f02,f02,f02,f02,f02,f02,f02,f02,f02,f02,f02,
  //   f02,c07,c1d,e01,a41,e00,e00,c02,e00,e00,c01,e00,e00,c04,e00,e00,c02,e00,e00,c05,e00,
  //   e00,e00,e00,a58,e00,e00,e00,bff,c1a,c19,a5d,c1e,c26,c21,a61,c26,c21,a64,c26,c21,a67,
  //   a5d,e80,c26,c21,a6c,e01,a6b,f02,f02,f02,f02,f02,f02,f02,f02,f02,f02,f02,f02,f02,f02,
  //   f02,82,e00,a82,c20,e80,308,f28,a86,889,a83,0,c21,a8a,c26,b89,ed0,e04,f18,a95,49b,
  //   a92,a8f,e08,f18,a8f,49b,a98,a95,0,d,a,d,a,c1,f6,e1,e9,ec,e1,e2,ec,e5,a0,f3,ef,e6,
  //   f4,f7,e1,f2,e5,f3,ba,d,a,ad,ad,ad,ad,ad,ad,ad,ad,ad,ad,ad,ad,ad,ad,ad,ad,ad,ad,ad,
  //   ad,d,a,30,30,30,3a,20,70,72,69,6e,74,68,65,6c,70,2e,62,69,6e,20,20,20,20,20,20,20,
  //   20,20,20,20,20,20,20,20,20,50,43,3a,30,32,30,30,20,28,54,68,69,73,20,68,65,6c,70,
  //   29,a,d,30,30,31,3a,20,44,30,41,42,2d,49,6e,73,74,54,65,73,74,2d,31,2e,70,74,20,20,
  //   20,20,20,20,20,20,20,20,20,50,43,3a,30,32,30,30,20,53,52,3a,37,37,37,37,20,57,61,
  //   74,63,68,3a,30,31,32,31,20,63,6f,6e,74,40,30,31,34,37,a,d,30,30,32,3a,20,44,30,42,
  //   42,2d,49,6e,73,74,54,65,73,74,2d,32,2e,70,74,20,20,20,20,20,20,20,20,20,20,20,50,
  //   43,3a,30,32,30,30,20,53,52,3a,78,78,78,78,20,57,61,74,63,68,3a,33,37,34,37,a,d,30,
  //   30,33,3a,20,44,30,49,42,2d,4a,4d,50,4a,4d,53,2e,70,74,20,20,20,20,20,20,20,20,20,
  //   20,20,20,20,20,20,50,43,3a,30,32,30,30,20,53,52,3a,78,78,78,78,20,57,61,74,63,68,
  //   3a,33,35,37,31,a,d,30,30,34,3a,20,44,30,4a,42,2d,4a,4d,50,4a,4d,53,2d,52,41,4e,44,
  //   4f,4d,2e,70,74,20,20,20,20,20,20,20,20,50,43,3a,30,32,30,30,20,53,52,3a,30,30,30,
  //   30,20,57,61,74,63,68,3a,30,30,34,34,a,d,30,30,35,3a,20,44,30,44,42,2d,52,61,6e,64,
  //   6f,6d,41,4e,44,2e,70,74,20,20,20,20,20,20,20,20,20,20,20,20,50,43,3a,30,32,30,30,
  //   20,53,52,3a,30,30,30,30,20,57,61,74,63,68,3a,30,32,30,32,a,d,30,30,36,3a,20,44,30,
  //   45,42,2d,52,61,6e,64,6f,6d,2d,54,41,44,2e,70,74,20,20,20,20,20,20,20,20,20,20,20,
  //   50,43,3a,30,32,30,30,20,53,52,3a,30,30,30,30,20,57,61,74,63,68,3a,36,37,37,36,a,d,
  //   30,30,37,3a,20,44,30,46,43,2d,52,61,6e,64,6f,6d,2d,49,53,5a,2e,70,74,20,20,20,20,
  //   20,20,20,20,20,20,20,50,43,3a,30,32,30,30,20,53,52,3a,30,30,30,30,20,57,61,74,63,
  //   68,3a,30,31,37,35,a,d,30,31,30,3a,20,44,30,47,43,2d,52,61,6e,64,6f,6d,2d,44,43,41,
  //   2e,70,74,20,20,20,20,20,20,20,20,20,20,20,50,43,3a,30,32,30,30,20,53,52,3a,30,30,
  //   30,30,20,57,61,74,63,68,20,30,30,30,36,2f,30,30,31,31,a,d,30,31,31,3a,20,44,30,43,
  //   43,2d,41,64,64,54,65,73,74,2e,70,74,20,20,20,20,20,20,20,20,20,20,20,20,20,20,50,
  //   43,3a,30,32,30,30,a,d,30,31,32,3a,20,44,31,41,41,2d,4d,65,6d,6f,72,79,2d,43,68,65,
  //   63,6b,65,72,62,6f,61,72,64,2e,70,74,20,20,50,43,3a,30,32,30,30,a,d,30,31,33,3a,20,
  //   44,31,45,41,2d,4d,65,6d,6f,72,79,2d,41,64,64,72,65,73,73,2e,72,69,6d,20,20,20,20,
  //   20,20,50,43,3a,30,32,30,30,a,d,30,31,34,3a,20,66,6f,63,61,6c,2d,38,2e,62,69,6e,20,
  //   20,20,20,20,20,20,20,20,20,20,20,20,20,20,20,20,20,50,43,3a,30,32,30,30,a,d,30,31,
  //   35,3a,20,49,6e,74,49,4f,2e,62,69,6e,20,20,20,20,20,20,20,20,20,20,20,20,20,20,20,
  //   20,20,20,20,20,50,43,3a,30,31,30,30,a,d,30,31,36,3a,20,49,6e,74,6f,75,74,2e,62,69,
  //   6e,20,20,20,20,20,20,20,20,20,20,20,20,20,20,20,20,20,20,20,50,43,3a,30,31,30,30,
  //   a,d,30,31,37,3a,20,74,73,74,65,73,74,2e,62,69,6e,20,20,20,20,20,20,20,20,20,20,20,
  //   20,20,20,20,20,20,20,20,50,43,3a,30,31,30,30,a,d,bc,e5,ee,e4,be,d,0,f02,f02,f02,f02,
  //   f02,f02,f02,f02,f02,f02,f02,f02,f02,f02,f02,f02,f02,f02,f02,f02,f02,f02,f02,f02,f02,
  //   f02,f02,f02,f02,f02,f02,f02,f02,f02,f02,f02,f02,f02,f02,f02,f02,f02,f02,f02,f02,f02,
  //   f02,f02,f02,f02,f02,f02,f02,f02,f02,f02,f02,f02,f02,f02,f02,f02,f02,f02,f02,f02,f02,
  //   f02,f02,f02,f02,f02,f02,f02,f02,f02,f02,f02,f02,f02,f02,f02,f02,f02,f02,f02,f02,f02,
  //   f02,f02,f02,f02,f02,f02,f02,f02,f02,f02,f02,f02,f02,f02,f02,f02,f02,f02,f02,f02,f02,
  //   f02,f02,f02,f02,f02,f02,f02,f02,f02,f02,f02,f02,f02,f02,f02,f02,f02,f02,f02,f02,f02,
  //   f02,f02,f02,f02,f02,f02,f02,f02,f02,f02,f02,f02,f02,f02,f02,f02,f02,f02,f02,f02,f02,
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  //   RAMDATA
  //   IR
  //   IND-REG
  //   DATA-REG
  //   INCREMENTER (14i 13o)
  //   4
  //   3
  //   8
  //   5
endmodule
