// Digital circuit test2.dig as structural Verilog
module test2 (
  input  I1,
  input  I2,
  input  I3,
  input  I4,
  input  OPR,
  output Y1,
  output Y2,
  output Y3
);

  wire and_1_out, and_2_out, and_3_out, and_4_out, nor_1_out, nor_2_out, nor_3_out, nor_4_out, nor_5_out,
       nor_6_out, not_1_out, not_2_out, not_3_out, not_4_out, not_5_out, not_6_out, not_7_out, not_8_out,
       not_9_out, or_1_out, or_2_out, or_3_out;

  or or_1 (or_1_out, I1, I1, I1);
  not not_1 (not_1_out, I2);
  not not_2 (not_2_out, I3);
  or or_2 (or_2_out, I4, I4, I4);
  nor nor_1 (nor_1_out, I1, I1, I1);
  not not_3 (not_3_out, I3);
  not not_4 (not_4_out, I2);
  nor nor_2 (nor_2_out, I4, I4, I4);
  nor nor_3 (nor_3_out, I1, I1, I1);
  nor nor_4 (nor_4_out, I3, 1'b0, I2);
  nor nor_5 (nor_5_out, I4, I4, I4);
  and and_1 (and_1_out, not_1_out, not_2_out);
  not not_5 (not_5_out, nor_1_out);
  and and_2 (and_2_out, not_3_out, not_4_out);
  not not_6 (not_6_out, and_1_out);
  not not_7 (not_7_out, and_2_out);
  not not_8 (not_8_out, nor_2_out);
  or or_3 (or_3_out, or_1_out, not_6_out, or_2_out);
  and and_3 (and_3_out, nor_3_out, nor_4_out);
  and and_4 (and_4_out, nor_4_out, nor_5_out);
  not not_9 (not_9_out, or_3_out);
  nor nor_6 (nor_6_out, not_5_out, not_7_out, not_8_out);
  and and_5 (Y1, OPR, not_9_out);
  and and_6 (Y2, OPR, nor_6_out);
  and and_7 (Y3, OPR, and_3_out, and_4_out);
endmodule
