// Digital circuit 74393.dig as structural Verilog
module _74393 (
  input  VCC,
  input  GND,
  input  _1A,
  input  _1CL,
  input  _2A,
  input  _2CL,
  output _1QA,
  output _1QB,
  output _1QC,
  output _1QD,
  output _2QA,
  output _2QB,
  output _2QC,
  output _2QD
);

  JK_FF_AS jk_ff_as_1 (.Set(1'b0), .J(1'b1), .C(~_1A), .K(1'b1), .Clr(_1CL), .Q(_1QA));  // open: nQ
  JK_FF_AS jk_ff_as_2 (.Set(1'b0), .J(1'b1), .C(~_1QA), .K(1'b1), .Clr(_1CL), .Q(_1QB));  // open: nQ
  JK_FF_AS jk_ff_as_3 (.Set(1'b0), .J(1'b1), .C(~_1QB), .K(1'b1), .Clr(_1CL), .Q(_1QC));  // open: nQ
  JK_FF_AS jk_ff_as_4 (.Set(1'b0), .J(1'b1), .C(~_1QC), .K(1'b1), .Clr(_1CL), .Q(_1QD));  // open: nQ
  PowerSupply powersupply_1 (.VDD(VCC), .GND(GND));
  JK_FF_AS jk_ff_as_5 (.Set(1'b0), .J(1'b1), .C(~_2A), .K(1'b1), .Clr(_2CL), .Q(_2QA));  // open: nQ
  JK_FF_AS jk_ff_as_6 (.Set(1'b0), .J(1'b1), .C(~_2QA), .K(1'b1), .Clr(_2CL), .Q(_2QB));  // open: nQ
  JK_FF_AS jk_ff_as_7 (.Set(1'b0), .J(1'b1), .C(~_2QB), .K(1'b1), .Clr(_2CL), .Q(_2QC));  // open: nQ
  JK_FF_AS jk_ff_as_8 (.Set(1'b0), .J(1'b1), .C(~_2QC), .K(1'b1), .Clr(_2CL), .Q(_2QD));  // open: nQ

  // Notes on the sheet:
  //   VCC: pin 14, default 1
  //   GND: pin 7
  //   _1A: pin 1, default 1
  //   _1CL: pin 2, default 1
  //   _1QA: pin 3
  //   _1QB: pin 4
  //   _1QC: pin 5
  //   _1QD: pin 6
  //   _2A: pin 13, default 1
  //   _2CL: pin 12, default 1
  //   _2QA: pin 11
  //   _2QB: pin 10
  //   _2QC: pin 9
  //   _2QD: pin 8
endmodule
