// Digital circuit ADDAND.dig as structural Verilog
module ADDAND (
  input  [11:0] A,
  input  [11:0] B,
  input  CI,
  input  OE_ADD,
  input  OE_AND,
  output [11:0] S,
  output CO
);

  wire _74157_1_p1, _74157_1_p2, _74157_1_p6, _74157_1_p13, _74157_2_p1, _74157_2_p2, _74157_2_p6,
       _74283_1_p10, _74283_1_p12, _74283_1_p14, _74283_1_p16, _74283_2_p6, _74283_2_p8, _74283_2_p10,
       _74283_2_p12, _74283_3_p8, _74283_3_p10, _74283_3_p12, _74283_3_p14, _74283_4_p6, _74283_4_p8,
       _74283_4_p10, _74283_4_p12, _74541_2_p17, _74541_2_p18, _74541_2_p19, _74541_4_p18, _74541_4_p19,
       _74541_4_p20, not_1_out, not_2_out;
  wire [3:0] _74157_3_p13, _74157_4_p13, _74283_5_p8;
  wire [11:0] and_1_out;

  and and_1 (and_1_out[0], A[0], B[0]);
  and and_2 (and_1_out[1], A[1], B[1]);
  and and_3 (and_1_out[2], A[2], B[2]);
  and and_4 (and_1_out[3], A[3], B[3]);
  and and_5 (and_1_out[4], A[4], B[4]);
  and and_6 (and_1_out[5], A[5], B[5]);
  and and_7 (and_1_out[6], A[6], B[6]);
  and and_8 (and_1_out[7], A[7], B[7]);
  and and_9 (and_1_out[8], A[8], B[8]);
  and and_10 (and_1_out[9], A[9], B[9]);
  and and_11 (and_1_out[10], A[10], B[10]);
  and and_12 (and_1_out[11], A[11], B[11]);
  // _74157 _74157_1: pin names not known; wires that end beside it: _74157_1_p1, _74157_1_p2, 1'b0, 1'b0, 1'b0, _74157_1_p6, 1'b0, 1'b0, 1'b0, 1'b0, 1'b1, 1'b0, _74157_1_p13
  // _74283 _74283_1: pin names not known; wires that end beside it: 1'b0, 1'b1, B[11], B[10], B[9], B[8], A[11], _74157_1_p6, A[10], _74283_1_p10, A[9], _74283_1_p12, A[8], _74283_1_p14, 1'b1, _74283_1_p16, 1'b0, 1'b1, B[11], B[10]
  // _74283 _74283_2: pin names not known; wires that end beside it: B[9], B[8], A[11], _74157_1_p2, A[10], _74283_2_p6, A[9], _74283_2_p8, A[8], _74283_2_p10, 1'b0, _74283_2_p12, 1'b0, 1'b1
  // _74157 _74157_2: pin names not known; wires that end beside it: _74157_2_p1, _74157_2_p2, 1'b0, 1'b0, 1'b0, _74157_2_p6, 1'b0, 1'b0, 1'b0, 1'b0, 1'b1, 1'b0, _74157_1_p1
  // _74157 _74157_3: pin names not known; wires that end beside it: _74157_1_p1, _74283_2_p12, _74283_2_p10, _74283_2_p8, _74283_2_p6, _74283_1_p16, _74283_1_p14, _74283_1_p12, _74283_1_p10, 1'b0, 1'b1, 1'b0, _74157_3_p13[0], _74157_3_p13[1], _74157_3_p13[2], _74157_3_p13[3]
  // _74283 _74283_3: pin names not known; wires that end beside it: B[7], B[6], B[5], B[4], A[7], _74157_2_p6, A[6], _74283_3_p8, A[5], _74283_3_p10, A[4], _74283_3_p12, 1'b1, _74283_3_p14, 1'b0, 1'b1, B[7], B[6]
  // _74283 _74283_4: pin names not known; wires that end beside it: B[5], B[4], A[7], _74157_2_p2, A[6], _74283_4_p6, A[5], _74283_4_p8, A[4], _74283_4_p10, 1'b0, _74283_4_p12, 1'b0, 1'b1
  // _74157 _74157_4: pin names not known; wires that end beside it: _74157_2_p1, _74283_4_p12, _74283_4_p10, _74283_4_p8, _74283_4_p6, _74283_3_p14, _74283_3_p12, _74283_3_p10, _74283_3_p8, 1'b0, 1'b1, 1'b0, _74157_4_p13[0], _74157_4_p13[1], _74157_4_p13[2], _74157_4_p13[3]
  // _74283 _74283_5: pin names not known; wires that end beside it: B[3], B[2], B[1], B[0], A[3], _74157_2_p1, A[2], _74283_5_p8[3], A[1], _74283_5_p8[2], A[0], _74283_5_p8[1], CI, _74283_5_p8[0]
  not not_1 (not_1_out, OE_AND);
  not not_2 (not_2_out, OE_ADD);
  // _74541 _74541_1: pin names not known; wires that end beside it: not_1_out, not_1_out, and_1_out[0], and_1_out[1], and_1_out[2], and_1_out[3], and_1_out[4], and_1_out[5], and_1_out[6], and_1_out[7], 1'b1, 1'b0, S[0], S[1], S[2], S[3], S[4], S[5], S[6], S[7]
  // _74541 _74541_2: pin names not known; wires that end beside it: not_1_out, not_1_out, and_1_out[8], and_1_out[9], and_1_out[10], and_1_out[11], 1'b0, 1'b0, 1'b0, 1'b0, 1'b1, 1'b0, S[8], S[9], S[10], S[11], _74541_2_p17, _74541_2_p18, _74541_2_p19, _74541_2_p17, _74541_2_p18, _74541_2_p19
  // _74541 _74541_3: pin names not known; wires that end beside it: not_2_out, not_2_out, _74283_5_p8[0], _74283_5_p8[1], _74283_5_p8[2], _74283_5_p8[3], _74157_4_p13[0], _74157_4_p13[1], _74157_4_p13[2], _74157_4_p13[3], 1'b1, 1'b0, S[0], S[1], S[2], S[3], S[4], S[5], S[6], S[7]
  // _74541 _74541_4: pin names not known; wires that end beside it: not_2_out, not_2_out, _74157_3_p13[0], _74157_3_p13[1], _74157_3_p13[2], _74157_3_p13[3], _74157_1_p13, 1'b0, 1'b0, 1'b0, 1'b1, 1'b0, S[8], S[9], S[10], S[11], CO, _74541_4_p18, _74541_4_p19, _74541_4_p20, _74541_4_p18, _74541_4_p19, _74541_4_p20

  // Notes on the sheet:
  //   1 pcs 7404 hex inverter
  //   3 pcs 7408 Quad AND 
  //   5 pcs 74283 4-bit adder
  //   4 pcs 74157 Quad 2-to-1 multiplexer
  //   4 pcs 74541 Octal buffer 3-state
endmodule
