// Digital circuit AUTOCAPTURE.dig as structural Verilog
module AUTOCAPTURE (
  input  [11:0] D,
  input  [11:0] A,
  input  WR,
  output [11:0] _10,
  output [11:0] _11,
  output [11:0] _12,
  output [11:0] _13,
  output [11:0] _14,
  output [11:0] _15,
  output [11:0] _16,
  output [11:0] _17
);

  wire and_1_out, and_2_out, and_3_out, and_4_out, and_5_out, and_6_out, and_7_out, and_8_out,
       comparator_1_eq, comparator_2_eq, comparator_3_eq, comparator_4_eq, comparator_5_eq, comparator_6_eq,
       comparator_7_eq, comparator_8_eq;

  Comparator #(.Bits(12)) comparator_1 (.a(A), .b(12'h8), .eq(comparator_1_eq));  // open: gt, lt
  Comparator #(.Bits(12)) comparator_2 (.a(A), .b(12'h9), .eq(comparator_2_eq));  // open: gt, lt
  Comparator #(.Bits(12)) comparator_3 (.a(A), .b(12'ha), .eq(comparator_3_eq));  // open: gt, lt
  Comparator #(.Bits(12)) comparator_4 (.a(A), .b(12'hb), .eq(comparator_4_eq));  // open: gt, lt
  Comparator #(.Bits(12)) comparator_5 (.a(A), .b(12'hc), .eq(comparator_5_eq));  // open: gt, lt
  Comparator #(.Bits(12)) comparator_6 (.a(A), .b(12'hd), .eq(comparator_6_eq));  // open: gt, lt
  Comparator #(.Bits(12)) comparator_7 (.a(A), .b(12'he), .eq(comparator_7_eq));  // open: gt, lt
  Comparator #(.Bits(12)) comparator_8 (.a(A), .b(12'hf), .eq(comparator_8_eq));  // open: gt, lt
  and and_1 (and_1_out, comparator_1_eq, WR);
  and and_2 (and_2_out, comparator_2_eq, WR);
  and and_3 (and_3_out, comparator_3_eq, WR);
  and and_4 (and_4_out, comparator_4_eq, WR);
  and and_5 (and_5_out, comparator_5_eq, WR);
  and and_6 (and_6_out, comparator_6_eq, WR);
  and and_7 (and_7_out, comparator_7_eq, WR);
  and and_8 (and_8_out, comparator_8_eq, WR);
  Register #(.Bits(12)) register_1 (.D(D), .C(and_1_out), .en(1'b1), .Q(_10));
  Register #(.Bits(12)) register_2 (.D(D), .C(and_2_out), .en(1'b1), .Q(_11));
  Register #(.Bits(12)) register_3 (.D(D), .C(and_3_out), .en(1'b1), .Q(_12));
  Register #(.Bits(12)) register_4 (.D(D), .C(and_4_out), .en(1'b1), .Q(_13));
  Register #(.Bits(12)) register_5 (.D(D), .C(and_5_out), .en(1'b1), .Q(_14));
  Register #(.Bits(12)) register_6 (.D(D), .C(and_6_out), .en(1'b1), .Q(_15));
  Register #(.Bits(12)) register_7 (.D(D), .C(and_7_out), .en(1'b1), .Q(_16));
  Register #(.Bits(12)) register_8 (.D(D), .C(and_8_out), .en(1'b1), .Q(_17));
endmodule
