// Digital circuit CLORIN.dig as structural Verilog
module CLORIN (
  input  [11:0] IN,
  input  [7:0] CLR,
  input  [11:0] DOR,
  input  INV,
  output [11:0] OUT
);

  wire and_1_out, and_2_out, and_3_out, and_4_out, and_5_out, and_6_out, and_7_out, and_8_out, and_9_out,
       and_10_out, and_11_out, and_12_out, nand_1_out, nand_2_out, nor_1_out, nor_2_out, nor_3_out,
       nor_4_out, or_1_out, or_2_out, or_3_out, or_4_out, or_5_out, or_6_out, or_7_out, or_8_out, or_9_out,
       or_10_out, or_11_out, or_12_out;

  nor nor_1 (nor_1_out, CLR[0], CLR[1]);
  nor nor_2 (nor_2_out, CLR[2], CLR[3]);
  nor nor_3 (nor_3_out, CLR[4], CLR[5]);
  nor nor_4 (nor_4_out, CLR[6], CLR[7]);
  nand nand_1 (nand_1_out, nor_1_out, nor_2_out, nor_3_out, nor_4_out);
  nand nand_2 (nand_2_out, nand_1_out, nand_1_out, nand_1_out, nand_1_out);
  and and_1 (and_1_out, IN[0], nand_2_out);
  and and_2 (and_2_out, IN[1], nand_2_out);
  and and_3 (and_3_out, IN[2], nand_2_out);
  and and_4 (and_4_out, IN[3], nand_2_out);
  and and_5 (and_5_out, IN[4], nand_2_out);
  and and_6 (and_6_out, IN[5], nand_2_out);
  and and_7 (and_7_out, IN[6], nand_2_out);
  and and_8 (and_8_out, IN[7], nand_2_out);
  and and_9 (and_9_out, IN[8], nand_2_out);
  and and_10 (and_10_out, IN[9], nand_2_out);
  and and_11 (and_11_out, IN[10], nand_2_out);
  and and_12 (and_12_out, IN[11], nand_2_out);
  or or_1 (or_1_out, and_1_out, DOR[0]);
  or or_2 (or_2_out, and_2_out, DOR[1]);
  or or_3 (or_3_out, and_3_out, DOR[2]);
  or or_4 (or_4_out, and_4_out, DOR[3]);
  or or_5 (or_5_out, and_5_out, DOR[4]);
  or or_6 (or_6_out, and_6_out, DOR[5]);
  or or_7 (or_7_out, and_7_out, DOR[6]);
  or or_8 (or_8_out, and_8_out, DOR[7]);
  or or_9 (or_9_out, and_9_out, DOR[8]);
  or or_10 (or_10_out, and_10_out, DOR[9]);
  or or_11 (or_11_out, and_11_out, DOR[10]);
  or or_12 (or_12_out, and_12_out, DOR[11]);
  xor xor_1 (OUT[0], or_1_out, INV);
  xor xor_2 (OUT[1], or_2_out, INV);
  xor xor_3 (OUT[2], or_3_out, INV);
  xor xor_4 (OUT[3], or_4_out, INV);
  xor xor_5 (OUT[4], or_5_out, INV);
  xor xor_6 (OUT[5], or_6_out, INV);
  xor xor_7 (OUT[6], or_7_out, INV);
  xor xor_8 (OUT[7], or_8_out, INV);
  xor xor_9 (OUT[8], or_9_out, INV);
  xor xor_10 (OUT[9], or_10_out, INV);
  xor xor_11 (OUT[10], or_11_out, INV);
  xor xor_12 (OUT[11], or_12_out, INV);

  // Notes on the sheet:
  //   1 pcs 7402 quad 2-inpt NOR
  //   3 pcs 7408 quad 2-input AND
  //   1 pcs 7420 dual 4-input NAND
  //   3 pcs 7432 quad 2-input OR
  //   3 pcs 7486 quad 2-input XOR
endmodule
