// Digital circuit IOT-BASE-DECODER.dig as structural Verilog
module IOT_BASE_DECODER (
  input  [11:0] IR,
  input  IOT,
  input  CK_FETCH,
  input  CK_3,
  output _600x,
  output _601x,
  output _602x,
  output _603x,
  output _604x,
  output _605x,
  output _606x,
  output _607x,
  output _62x0,
  output _62x1,
  output _62x2,
  output _62x3,
  output _62x4,
  output _62x5,
  output _62x6,
  output _62x7,
  output DONE
);

  wire and_1_out, nor_1_out, nor_2_out, nor_3_out, not_1_out, not_2_out, not_3_out, not_4_out, not_5_out,
       not_6_out;

  and and_1 (and_1_out, CK_3, IOT);
  not not_1 (not_1_out, 1'b0);
  not not_2 (not_2_out, 1'b0);
  not not_3 (not_3_out, 1'b0);
  assign DONE = and_1_out ? and_1_out : 1'bz;  // Driver driver_1
  not not_4 (not_4_out, IOT);
  not not_5 (not_5_out, IR[7]);
  nor nor_1 (nor_1_out, CK_FETCH, 1'b0, not_4_out);
  nor nor_2 (nor_2_out, IR[8], IR[7], IR[6]);
  nor nor_3 (nor_3_out, IR[6], not_5_out, IR[8]);
  not not_6 (not_6_out, nor_1_out);
  // _74238 _74238_1: pin names not known; wires that end beside it: 1'b1, 1'b0, nor_2_out, not_6_out, 1'b0, IR[3], IR[4], IR[5], _600x, _601x, _602x, _603x, _604x, _605x, _606x, _607x
  // _74238 _74238_2: pin names not known; wires that end beside it: 1'b1, 1'b0, nor_3_out, not_6_out, 1'b0, IR[0], IR[1], IR[2], _62x0, _62x1, _62x2, _62x3, _62x4, _62x5, _62x6, _62x7

  // Notes on the sheet:
  //   _600x: IOT_DEVCPU
  //   _601x: IOT_DEVHSR
  //   _602x: IOT_DEVHSP
  //   _603x: IOT_DEVBKD
  //   _604x: IOT_DEVPRI
  //   1 pcs 7404 Hex inverter
  //   1 pcs 7427 Triple 3-input NOR
  //   2 pcs 74238 Decoder 3-to-8
  //   op 60Y*
  //   op 62*Y
endmodule
