// Digital circuit IR-DECODER.dig as structural Verilog
module IR_DECODER (
  input  [11:0] LATCHED_PC,
  input  [11:0] BUS_IR,
  output plus__plus_IND,
  output IND,
  output DIR,
  output MP,
  output AND,
  output TAD,
  output ISZ,
  output DCA,
  output JMS,
  output JMP,
  output IOT,
  output OPR
);

  wire and_1_out, and_2_out, and_3_out, nor_3_out, nor_4_out, nor_5_out, nor_6_out, nor_7_out, not_1_out,
       not_2_out, not_3_out, not_4_out, not_5_out, not_6_out;

  // NOr nor_1 has open pins: In_1=1'b0, In_2=1'b0, out=open
  // NOr nor_2 has open pins: In_1=1'b0, In_2=1'b0, out=open
  not not_1 (not_1_out, 1'b0);
  not not_2 (not_2_out, 1'b0);
  not not_3 (not_3_out, 1'b0);
  nor nor_3 (nor_3_out, BUS_IR[4], BUS_IR[5], BUS_IR[6]);
  nor nor_4 (nor_4_out, LATCHED_PC[7], LATCHED_PC[8], LATCHED_PC[9]);
  nor nor_5 (nor_5_out, LATCHED_PC[10], LATCHED_PC[11], 1'b0);
  and and_1 (and_1_out, BUS_IR[3], nor_3_out);
  not not_4 (not_4_out, BUS_IR[7]);
  // _74238 _74238_1: pin names not known; wires that end beside it: 1'b1, 1'b0, 1'b1, 1'b0, 1'b0, BUS_IR[9], BUS_IR[10], BUS_IR[11], AND, TAD, ISZ, DCA, JMS, JMP, IOT, OPR
  and and_2 (and_2_out, nor_4_out, nor_5_out, and_1_out);
  and and_3 (and_3_out, not_4_out, and_1_out);
  nor nor_6 (nor_6_out, and_2_out, and_3_out);
  nor nor_7 (nor_7_out, OPR, IOT);
  not not_5 (not_5_out, nor_6_out);
  not not_6 (not_6_out, BUS_IR[8]);
  and and_4 (plus__plus_IND, nor_7_out, BUS_IR[8], not_5_out);
  and and_5 (IND, nor_7_out, BUS_IR[8], nor_6_out);
  and and_6 (DIR, nor_7_out, not_6_out);
  and and_7 (MP, nor_7_out, BUS_IR[7]);
  // Pins of 1 and 12 bits meet at BUS_IR
  // Pins of 1 and 12 bits meet at LATCHED_PC

  // Notes on the sheet:
  //   IR DECODER
  //   1 pcs 7402 Quad 2-input NOR
  //   1 pcs 7404 Hex inverter
  //   1 pcs 7408 Quad 2-input AND
  //   1 pcs 7411 Triple 3-input AND
  //   1 pcs 7427 Triple 3-input NOR
  //   1 pcs 74238 Decoder 3-to-8
  //   CP=0 PAGE ZERO
  //   CP=1 CURRENT PAGE
  //   IA=0 DIRECT
  //   IA=1 INDIRECT
endmodule
