// Digital circuit LINK.dig as structural Verilog
module LINK (
  input  ANDADD_Carry,
  input  RAMD2AC_ADD,
  input  LINK_CK,
  input  OPR_CLL,
  input  CLL,
  input  RTF_LINK,
  input  OPR_CML,
  input  INC_carry,
  input  OPR_IAC,
  input  ROTATE_OUT,
  input  STB_1,
  input  CLEAR,
  output LINK,
  output ROTATE_IN
);

  wire _7474_1_p6, _7474_1_p11, and_1_out, and_2_out, and_3_out, not_1_out, not_2_out, or_1_out, or_2_out,
       xor_2_out;

  not not_1 (not_1_out, CLEAR);
  and and_1 (and_1_out, ANDADD_Carry, RAMD2AC_ADD);
  or or_1 (or_1_out, CLL, OPR_CLL);
  or or_2 (or_2_out, RTF_LINK, OPR_CML);
  and and_2 (and_2_out, INC_carry, OPR_IAC);
  not not_2 (not_2_out, or_1_out);
  // _7474 _7474_1: pin names not known; wires that end beside it: 1'b1, and_1_out, STB_1, not_1_out, 1'b1, _7474_1_p6, LINK_CK, not_1_out, 1'b1, 1'b0, _7474_1_p11, LINK
  xor xor_1 (_7474_1_p6, ROTATE_OUT, _7474_1_p11);
  and and_3 (and_3_out, LINK, not_2_out);
  xor xor_2 (xor_2_out, and_3_out, or_2_out);
  xor xor_3 (ROTATE_IN, xor_2_out, and_2_out);

  // Notes on the sheet:
  //   TAD
  //   CLL
  //   1 pcs 7474 Dual D-FlipFlop
  //   1 pcs Quad 2-input XOR
  //   1 pcs Quad 2-input AND
  //   1 pcs Quad 2-input OR
  //   1 pcs Hex inverter
  //   CML
  //   ROTATES
endmodule
