// Digital circuit MEMORY.dig as structural Verilog
module MEMORY (
  input  [11:0] ADDR,
  input  [2:0] FLD,
  input  [11:0] BNK,
  input  OE,
  input  WE,
  output [11:0] DATA
);

  wire not_1_out, not_2_out;

  not not_1 (not_1_out, WE);
  not not_2 (not_2_out, OE);
  RAMSinglePortSel #(.AddrBits(20), .isProgramMemory("true"), .Bits(12)) TWO_32Kx8 (
    .A({FLD, BNK[4:0], ADDR}), .CS(~1'b0), .WE(~not_1_out), .OE(~not_2_out), .D(DATA));
  // Pins of 5 and 12 bits meet at BNK

  // Notes on the sheet:
  //   OE: default 1
  //   WE: default 1
endmodule
