// Digital circuit OPR-DECODER.dig as structural Verilog
module OPR_DECODER (
  input  [11:0] BUS_IR,
  input  OPR,
  output OPR1,
  output OPR2,
  output OPR3,
  output IAC,
  output X2,
  output LEFT,
  output RIGHT,
  output CML,
  output CMA,
  output CLL,
  output CLA1,
  output NA1,
  output HLT,
  output OSR,
  output TSTINV,
  output SNLSZL,
  output SZASNA,
  output SMASPA,
  output CLA2,
  output MQL,
  output SWP,
  output MQA,
  output SCA,
  output CLA_3,
  output LSR,
  output ASL,
  output SHL,
  output NMI,
  output DVI,
  output MUY,
  output SCL,
  output NOP0,
  output NOP
);

  wire and_20_out, and_21_out, and_22_out, and_23_out, and_28_out, and_29_out, nor_1_out, nor_2_out,
       nor_3_out, not_1_out, not_2_out;

  not not_1 (not_1_out, BUS_IR[8]);
  not not_2 (not_2_out, BUS_IR[0]);
  and and_1 (OPR1, not_1_out, OPR);
  and and_2 (OPR2, not_2_out, BUS_IR[8], OPR);
  and and_3 (OPR3, BUS_IR[8], BUS_IR[0], OPR);
  and and_4 (IAC, BUS_IR[0], OPR1);
  and and_5 (X2, BUS_IR[1], OPR1);
  and and_6 (LEFT, BUS_IR[2], OPR1);
  and and_7 (RIGHT, BUS_IR[3], OPR1);
  and and_8 (CML, BUS_IR[4], OPR1);
  and and_9 (CMA, BUS_IR[5], OPR1);
  and and_10 (CLL, BUS_IR[6], OPR1);
  and and_11 (CLA1, BUS_IR[7], OPR1);
  and and_12 (NA1, BUS_IR[0], OPR2);
  and and_13 (HLT, BUS_IR[1], OPR2);
  and and_14 (OSR, BUS_IR[2], OPR2);
  and and_15 (TSTINV, BUS_IR[3], OPR2);
  and and_16 (SNLSZL, BUS_IR[4], OPR2);
  and and_17 (SZASNA, BUS_IR[5], OPR2);
  and and_18 (SMASPA, BUS_IR[6], OPR2);
  and and_19 (CLA2, BUS_IR[7], OPR2);
  nor nor_1 (nor_1_out, BUS_IR[0], BUS_IR[1], BUS_IR[2]);
  nor nor_2 (nor_2_out, 1'b0, BUS_IR[3], BUS_IR[4]);
  nor nor_3 (nor_3_out, BUS_IR[5], BUS_IR[6], BUS_IR[7]);
  and and_20 (and_20_out, OPR3, BUS_IR[0]);
  and and_21 (and_21_out, OPR3, BUS_IR[1]);
  and and_22 (and_22_out, OPR3, BUS_IR[2]);
  and and_23 (and_23_out, OPR3, BUS_IR[3]);
  and and_24 (MQL, OPR3, BUS_IR[4]);
  and and_25 (SCA, OPR3, BUS_IR[5]);
  and and_26 (MQA, OPR3, BUS_IR[6]);
  and and_27 (CLA_3, OPR3, BUS_IR[7]);
  and and_28 (and_28_out, nor_1_out, nor_2_out);
  and and_29 (and_29_out, nor_2_out, nor_3_out);
  and and_30 (SWP, MQL, MQA);
  and and_31 (NOP, OPR, and_28_out, and_29_out);
  // _74238 _74238_1: pin names not known; wires that end beside it: and_20_out, 1'b1, 1'b0, 1'b1, 1'b0, 1'b0, and_21_out, and_22_out, and_23_out, NOP0, SCL, MUY, DVI, NMI, SHL, ASL, LSR
  // Not not_3 has open pins: in=1'b0, out=open
  // Not not_4 has open pins: in=1'b0, out=open
  // Not not_5 has open pins: in=1'b0, out=open
  // Not not_6 has open pins: in=1'b0, out=open
  // Pins of 1 and 12 bits meet at BUS_IR

  // Notes on the sheet:
  //   OPR DECODER
  //   OPR1
  //   OPR2
  //   OPR3
  //   1 pcs 7404 Hex inverter
  //   7 pcs 7408 Quad 2-input AND
  //   1 pcs 7411 Triple 3-input AND
  //   1 pcs 7427 Triple 3-input NOR
  //   1 pcs 74238 Decoder 3-to-8
endmodule
