// Digital circuit RAMSPY.dig as structural Verilog
module RAMSPY (
  input  [11:0] A,
  input  [24:0] DAW,
  output [11:0] O
);

  wire and_1_out, comparator_1_eq;

  Comparator #(.Bits(12)) comparator_1 (.a(DAW[23:12]), .b(A), .eq(comparator_1_eq));  // open: gt, lt
  and and_1 (and_1_out, comparator_1_eq, DAW[24]);
  Register #(.Bits(12)) register_1 (.D(DAW[11:0]), .C(and_1_out), .en(1'b1), .Q(O));
  // Pins of 1 and 12 bits meet at O

  // Notes on the sheet:
  //   RAM-DATA(12)
  //   RAM-ADDRESS(12)
  //   RAM_WE
endmodule
