// Digital circuit SERIAL.dig as structural Verilog
module SERIAL (
  input  [11:0] AC,
  input  [2:0] IR_L3,
  input  IOT_DEVKBD,
  input  IOT_DEVPRI,
  input  STB1,
  input  CK1,
  input  IOT_CAF,
  input  CLEAR,
  input  XTAL,
  output PC_CK,
  output AC_CK,
  output OR_KBD,
  output ROT2AC,
  output CLA_KCC,
  output FLAG_KBDIE,
  output FLAG_KBD,
  output FLAG_PRNCOMPLETE,
  output [7:0] KBD8,
  output IRQ
);

  wire _74238_1_p12, _74238_1_p16, _74238_2_p12, _74238_2_p16, and_2_out, and_3_out, and_4_out, and_5_out,
       and_6_out, and_7_out, and_8_out, and_9_out, and_10_out, and_11_out, and_12_out, IOT_KCC, IOT_KCF,
       IOT_KIE, IOT_KRB, IOT_KRS, IOT_KSF, IOT_TCF, IOT_TFL, IOT_TLS, IOT_TPC, IOT_TSF, IOT_TSK, or_1_out,
       or_2_out, or_4_out, or_5_out, or_6_out, or_7_out, risingedgedet_1_y, risingedgedet_2_y, TTY_BSY,
       TTY_RDY, TTY_STB;

  or or_1 (or_1_out, FLAG_PRNCOMPLETE, FLAG_KBD);
  LED led_1 (.in(or_1_out));
  // _74238 _74238_1: pin names not known; wires that end beside it: 1'b1, 1'b0, IOT_DEVKBD, 1'b0, 1'b0, IR_L3[0], IR_L3[1], IR_L3[2], IOT_KCF, IOT_KSF, IOT_KCC, _74238_1_p12, IOT_KRS, IOT_KIE, IOT_KRB, _74238_1_p16, _74238_1_p12, _74238_1_p16
  // _74238 _74238_2: pin names not known; wires that end beside it: 1'b1, 1'b0, IOT_DEVPRI, 1'b0, 1'b0, IR_L3[0], IR_L3[1], IR_L3[2], IOT_TFL, IOT_TSF, IOT_TCF, _74238_2_p12, IOT_TPC, IOT_TSK, IOT_TLS, _74238_2_p16, _74238_2_p12, _74238_2_p16
  and and_1 (IRQ, FLAG_KBDIE, or_1_out);
  or or_2 (or_2_out, IOT_KCF, IOT_KCC, IOT_KRB, CLEAR);
  and and_2 (and_2_out, IOT_KCC, CK1);
  and and_3 (and_3_out, IOT_KCC, STB1);
  and and_4 (and_4_out, IOT_KRB, CK1);
  and and_5 (and_5_out, IOT_KRB, STB1);
  or or_3 (TTY_STB, IOT_TPC, IOT_TLS);
  LED led_2 (.in(TTY_STB));
  // CntProbe cntprobe_1: pin names not known; wires that end beside it: TTY_RDY
  RS_FF_AS KBD (.S(TTY_RDY), .R(or_2_out), .Q(FLAG_KBD));  // open: nQ
  LED led_3 (.in(or_2_out));
  LED led_4 (.in(and_2_out));
  assign ROT2AC = and_2_out ? and_2_out : 1'bz;  // Driver driver_1
  assign CLA_KCC = and_2_out ? and_2_out : 1'bz;  // Driver driver_2
  LED led_5 (.in(and_3_out));
  assign AC_CK = and_3_out ? and_3_out : 1'bz;  // Driver driver_3
  LED led_6 (.in(and_4_out));
  assign ROT2AC = and_4_out ? and_4_out : 1'bz;  // Driver driver_4
  assign OR_KBD = and_4_out ? and_4_out : 1'bz;  // Driver driver_5
  assign CLA_KCC = and_4_out ? and_4_out : 1'bz;  // Driver driver_6
  LED led_7 (.in(and_5_out));
  assign AC_CK = and_5_out ? and_5_out : 1'bz;  // Driver driver_7
  // CntProbe cntprobe_2: pin names not known; wires that end beside it: FLAG_KBD
  LED led_8 (.in(FLAG_KBD));
  or or_4 (or_4_out, FLAG_PRNCOMPLETE, FLAG_KBD);
  or or_5 (or_5_out, TTY_BSY, IOT_TFL);
  or or_6 (or_6_out, IOT_TLS, IOT_TCF, IOT_CAF, CLEAR);
  and and_6 (and_6_out, IOT_TSF, CK1, FLAG_PRNCOMPLETE);
  and and_7 (and_7_out, IOT_TSK, CK1, or_4_out);
  LED led_9 (.in(or_5_out));
  LED led_10 (.in(or_6_out));
  LED led_11 (.in(and_6_out));
  assign PC_CK = and_6_out ? and_6_out : 1'bz;  // Driver driver_8
  LED led_12 (.in(and_7_out));
  assign PC_CK = and_7_out ? and_7_out : 1'bz;  // Driver driver_9
  RisingEdgeDet risingedgedet_1 (.A(or_5_out), .Y(risingedgedet_1_y));
  RisingEdgeDet risingedgedet_2 (.A(or_6_out), .Y(risingedgedet_2_y));
  and and_8 (and_8_out, IOT_KIE, AC[0]);
  LED led_13 (.in(and_8_out));
  and and_9 (and_9_out, IOT_KIE, ~AC[0]);  // And
  LED led_14 (.in(and_9_out));
  and and_10 (and_10_out, IOT_KSF, CK1, FLAG_KBD);
  and and_11 (and_11_out, IOT_KRS, CK1);
  and and_12 (and_12_out, IOT_KRS, STB1);
  or or_7 (or_7_out, and_8_out, CLEAR, IOT_CAF);
  LED led_15 (.in(and_10_out));
  LED led_16 (.in(and_11_out));
  LED led_17 (.in(and_12_out));
  RS_FF_AS PRN (.S(risingedgedet_1_y), .R(risingedgedet_2_y), .Q(FLAG_PRNCOMPLETE));  // open: nQ
  RS_FF_AS #(.Default(1)) KBD_IE (.S(or_7_out), .R(and_9_out), .Q(FLAG_KBDIE));  // open: nQ
  assign PC_CK = and_10_out ? and_10_out : 1'bz;  // Driver driver_10
  assign ROT2AC = and_11_out ? and_11_out : 1'bz;  // Driver driver_11
  assign OR_KBD = and_11_out ? and_11_out : 1'bz;  // Driver driver_12
  assign AC_CK = and_12_out ? and_12_out : 1'bz;  // Driver driver_13
  LED led_18 (.in(FLAG_PRNCOMPLETE));
  LED led_19 (.in(FLAG_KBDIE));
  TTY tty_1 (
    .IN(AC[7:0]), .STB(TTY_STB), .ACK(FLAG_KBD), .OE(OR_KBD), .CLR(CLEAR), .CLK(XTAL), .OUT(KBD8),
    .RDY(TTY_RDY), .BSY(TTY_BSY));

  // Other names for the same wires on the sheet: CCC_C = CLEAR; CK_1 = CK1; STB_1 = STB1; TTY_ACK = FLAG_KBD

  // Notes on the sheet:
  //   603x
  //   TTY KEYBOARD
  //   SLOW READER
  //   603x - IOT Keyboard
  //   KCF: The keyboard flag, signalling input data ready, 
  //   is cleared.
  //   KCC: The keyboard flag is reset, the accumulator is 
  //   cleared, and the process of reading the next 
  //   character of input is initiated
  //   KRS: The 8-bit character in the keyboard buffer 
  //   is ored with the accumulator.
  //   604x - IOT Printer
  //   TPC: The least significant 8-bits of the accumulator 
  //   is copied to the print buffer, initiating output.
  //   Keyboard Clear Flags
  //   Keyboard and AC Clear
  //   Keyboard Read and 
  //   Begin next read
  //   604x
  //   TTY PRINTER
  //   SLOW PUNCH
  //   Teleprinter Print Character
  //   Teleprinter Load and Start
  //   Teleprinter Flag set (aka SPF)
  //   Teleprinter Clear Flag
  //   Clear All Flags
  //   Teleprinter Skip if Flag
  //   Teleprinter Skip (aka SPI)
  //   KRB: The 8 bit character in the keyboard buffer is 
  //   transferred to the accumulator, and the keyboard 
  //   flag is cleared, allowing the reading of the next 
  //   character to begin. In effect, this operation combines 
  //   the KCC and KRS operations;
  //   TFL: The printer flag, signalling output complete, is set.
  //   Keyboard Interrupt Enable
  //   Keyboard Skip if Flag
  //   Keyboard Read Static
  //   KSF: If the keyboard flag is set, indicating that input 
  //   data is ready, the next instruction in sequence is 
  //   skipped.
  //   TSF: If the printer flag is set, indicating output 
  //   is complete, the next instruction in sequence is 
  //   skipped.
  //   KIE: The accumulator is loaded into the device 
  //   control register (the interrupt enable and status 
  //   report control bits).
  //   TSK: If either the print flag or the keyboard flag are 
  //   set, the next instruction in sequence is skipped.
endmodule
