// Digital circuit SKIP.dig as structural Verilog
module SKIP (
  input  [11:0] AC,
  input  LINK,
  input  SZASNA,
  input  SMASPA,
  input  SNLSZL,
  input  TSTINV,
  input  SK1,
  input  SK2,
  input  SK3,
  output SKIP
);

  wire and_1_out, and_2_out, and_3_out, or_1_out, or_2_out, or_3_out, or_4_out, or_5_out, or_6_out,
       xor_1_out, xor_2_out;

  or or_1 (or_1_out, AC[0], AC[1], AC[2], AC[3]);
  or or_2 (or_2_out, AC[4], AC[5], AC[6], AC[7]);
  or or_3 (or_3_out, AC[8], AC[9], AC[10], AC[11]);
  or or_4 (or_4_out, or_1_out, or_2_out, or_3_out);
  xor xor_1 (xor_1_out, 1'b1, or_4_out);
  and and_1 (and_1_out, xor_1_out, SZASNA);
  and and_2 (and_2_out, AC[11], SMASPA);
  and and_3 (and_3_out, LINK, SNLSZL);
  or or_5 (or_5_out, and_1_out, and_2_out, and_3_out);
  or or_6 (or_6_out, 1'b0, 1'b0, 1'b0);
  xor xor_2 (xor_2_out, or_5_out, TSTINV);
  PullDown pulldown_1 (.out(SK1));
  PullDown pulldown_2 (.out(SK2));
  PullDown pulldown_3 (.out(SK3));
  or or_7 (SKIP, xor_2_out, SK1, SK2, SK3);

  // Notes on the sheet:
  //   AC=0
  //   AC negative
  //   LINK<>0
  //   2 pcs 4-input OR
  //   1 pcs 2-input AND
  //   1 pcs 2 input XOR
  //   1 pcs 3 input OR
  //   SMA      7500  skip on minus AC
  //   SPA      7510  skip on plus AC
  //   SZA      7440  skip on zero AC
  //   SNA      7450  skip on non-zero AC
  //   SNL      7420  skip on non-zero link
  //   SZL      7430  skip on zero link
endmodule
