// Digital circuit SRAM32Kx8.dig as structural Verilog
module SRAM32Kx8 (
  input  [14:0] A,
  input  nCE,
  input  nOE,
  input  nWE,
  output [11:0] D
);

  RAMSinglePortSel #(.AddrBits(15), .Bits(12)) ramsingleportsel (.A(A), .CS(~nCE), .WE(~nWE), .OE(~nOE), .D(D));
  // NOr nor_1 has open pins: In_1=nCE, In_2=nWE, In_3=nOE, out=open
  // Pins of 1 and 12 bits meet at D

  // Notes on the sheet:
  //   nCE: default 1
  //   nOE: default 1
  //   nWE: default 1
endmodule
