// Digital circuit TEST-ADDER.dig as structural Verilog
module TEST_ADDER (
  input  in_1,
  input  clk
);

  wire add_1_c_o, adder_1_p6, comparator_1_eq, comparator_2_eq, counter_1_ovf;
  wire [11:0] add_1_s, adder_1_p5;
  wire [24:0] counter_1_out;

  Counter #(.Bits(25)) counter_1 (.en(1'b1), .C(clk), .clr(1'b0), .out(counter_1_out), .ovf(counter_1_ovf));
  // CntProbe cntprobe_1: pin names not known; wires that end beside it: counter_1_ovf
  // ADDER adder_1: pin names not known; wires that end beside it: counter_1_out[11:0], counter_1_out[23:12], counter_1_out[24], in_1, adder_1_p5, adder_1_p6
  Add #(.Bits(12)) add_1 (
    .a(counter_1_out[11:0]), .b(counter_1_out[23:12]), .c_i(counter_1_out[24]), .s(add_1_s), .c_o(add_1_c_o));
  // Probe on counter_1_out[23:12]
  // Probe on counter_1_out[11:0]
  // Probe on adder_1_p5
  // Probe on adder_1_p6
  // Probe on add_1_s
  // Probe on add_1_c_o
  Comparator #(.Bits(12)) comparator_1 (.a(adder_1_p5), .b(add_1_s), .eq(comparator_1_eq));  // open: gt, lt
  Comparator comparator_2 (.a(adder_1_p6), .b(add_1_c_o), .eq(comparator_2_eq));  // open: gt, lt
  // also tied to VCC on the sheet: {comparator_1_eq, comparator_2_eq}

  // Notes on the sheet:
  //   in_1: default 1
  //   clk: Hz: 2147483647
endmodule
