// Digital circuit TRANSP.LATCH.dig as structural Verilog
module TRANSP_LATCH (
  input  [11:0] D,
  input  HLD,
  output [11:0] Q
);

  wire and_1_out, and_2_out, and_3_out, and_4_out, and_5_out, and_6_out, and_7_out, and_8_out, and_9_out,
       and_10_out, and_11_out, and_12_out, and_13_out, and_14_out, and_15_out, and_16_out, and_17_out,
       and_18_out, and_19_out, and_20_out, and_21_out, and_22_out, and_23_out, and_24_out, not_1_out;

  not not_1 (not_1_out, HLD);
  and and_1 (and_1_out, not_1_out, D[0]);
  and and_2 (and_2_out, not_1_out, ~D[0]);  // And
  and and_3 (and_3_out, not_1_out, D[1]);
  and and_4 (and_4_out, not_1_out, ~D[1]);  // And
  and and_5 (and_5_out, not_1_out, D[2]);
  and and_6 (and_6_out, not_1_out, ~D[2]);  // And
  and and_7 (and_7_out, not_1_out, D[3]);
  and and_8 (and_8_out, not_1_out, ~D[3]);  // And
  and and_9 (and_9_out, not_1_out, D[4]);
  and and_10 (and_10_out, not_1_out, ~D[4]);  // And
  and and_11 (and_11_out, not_1_out, D[5]);
  and and_12 (and_12_out, not_1_out, ~D[5]);  // And
  and and_13 (and_13_out, not_1_out, D[6]);
  and and_14 (and_14_out, not_1_out, ~D[6]);  // And
  and and_15 (and_15_out, not_1_out, D[7]);
  and and_16 (and_16_out, not_1_out, ~D[7]);  // And
  and and_17 (and_17_out, not_1_out, D[8]);
  and and_18 (and_18_out, not_1_out, ~D[8]);  // And
  and and_19 (and_19_out, not_1_out, D[9]);
  and and_20 (and_20_out, not_1_out, ~D[9]);  // And
  and and_21 (and_21_out, not_1_out, D[10]);
  and and_22 (and_22_out, not_1_out, ~D[10]);  // And
  and and_23 (and_23_out, not_1_out, D[11]);
  and and_24 (and_24_out, not_1_out, ~D[11]);  // And
  RS_FF_AS rs_ff_as_1 (.S(and_1_out), .R(and_2_out), .Q(Q[0]));  // open: nQ
  RS_FF_AS rs_ff_as_2 (.S(and_3_out), .R(and_4_out), .Q(Q[1]));  // open: nQ
  RS_FF_AS rs_ff_as_3 (.S(and_5_out), .R(and_6_out), .Q(Q[2]));  // open: nQ
  RS_FF_AS rs_ff_as_4 (.S(and_7_out), .R(and_8_out), .Q(Q[3]));  // open: nQ
  RS_FF_AS rs_ff_as_5 (.S(and_9_out), .R(and_10_out), .Q(Q[4]));  // open: nQ
  RS_FF_AS rs_ff_as_6 (.S(and_11_out), .R(and_12_out), .Q(Q[5]));  // open: nQ
  RS_FF_AS rs_ff_as_7 (.S(and_13_out), .R(and_14_out), .Q(Q[6]));  // open: nQ
  RS_FF_AS rs_ff_as_8 (.S(and_15_out), .R(and_16_out), .Q(Q[7]));  // open: nQ
  RS_FF_AS rs_ff_as_9 (.S(and_17_out), .R(and_18_out), .Q(Q[8]));  // open: nQ
  RS_FF_AS rs_ff_as_10 (.S(and_19_out), .R(and_20_out), .Q(Q[9]));  // open: nQ
  RS_FF_AS rs_ff_as_11 (.S(and_21_out), .R(and_22_out), .Q(Q[10]));  // open: nQ
  RS_FF_AS rs_ff_as_12 (.S(and_23_out), .R(and_24_out), .Q(Q[11]));  // open: nQ
  // Pins of 1 and 12 bits meet at D
  // Pins of 1 and 12 bits meet at Q
endmodule
