// Digital circuit TTY.dig as structural Verilog
module TTY (
  input  [7:0] IN,
  input  STB,
  input  ACK,
  input  OE,
  input  CLR,
  input  CLK,
  output [7:0] OUT,
  output RDY,
  output BSY
);

  wire fallingedgedet_1_y, port_1_p3, uart_1_busy, uart_1_rdy, uart_1_tx;
  wire [15:0] counter_1_out;

  FallingEdgeDet fallingedgedet_1 (.A(ACK), .Y(fallingedgedet_1_y));
  Counter #(.Bits(16)) counter_1 (.en(1'b1), .C(CLK), .clr(1'b0), .out(counter_1_out));  // open: ovf
  UART uart_1 (
    .RX(port_1_p3), .ACK(fallingedgedet_1_y), .OE(OE), .DIN(IN), .STB(STB), .CLK(counter_1_out[1]),
    .XTAL(CLK), .CLEAR(CLR), .DOUT(OUT), .RDY(uart_1_rdy), .TX(uart_1_tx), .BUSY(uart_1_busy));
  // Port port_1: pin names not known; wires that end beside it: uart_1_tx, counter_1_out[1], port_1_p3
  RisingEdgeDet risingedgedet_1 (.A(uart_1_rdy), .Y(RDY));
  FallingEdgeDet fallingedgedet_2 (.A(uart_1_busy), .Y(BSY));

  // Notes on the sheet:
  //   RDY: Has RisingEdge detecor
  //   BSY: Has FallingEdge detector
  //   ACK: Has a FallingEdge detector
endmodule
