// Digital circuit UART-RX.dig as structural Verilog
module UART_RX (
  input  CLK,
  input  ACK,
  input  RX,
  output FULL,
  output [7:0] DATA
);

  wire _74161_1_p11, _74161_1_p12, _74161_1_p13, _74161_1_p14, _74161_1_p15, _74161_1_p16, _74161_2_p12,
       _74161_2_p13, _74161_2_p14, _74161_2_p15, and_1_out, delay_1_out, nand_1_out, nand_2_out, nand_3_out,
       not_1_out;

  // _74161 _74161_1: pin names not known; wires that end beside it: 1'b0, 1'b0, 1'b0, 1'b0, 1'b1, CLK, 1'b1, 1'b1, 1'b1, 1'b0, _74161_1_p11, _74161_1_p12, _74161_1_p13, _74161_1_p14, _74161_1_p15, _74161_1_p16, _74161_1_p12, _74161_1_p14, _74161_1_p15, _74161_1_p16
  // _74161 _74161_2: pin names not known; wires that end beside it: 1'b0, 1'b0, 1'b0, 1'b0, 1'b1, _74161_1_p13, 1'b1, 1'b1, 1'b1, 1'b0, _74161_1_p11, _74161_2_p12, _74161_2_p13, _74161_2_p14, _74161_2_p15, _74161_2_p13, _74161_2_p14
  nand nand_1 (nand_1_out, _74161_2_p12, _74161_2_p15);
  not not_1 (not_1_out, nand_1_out);
  nand nand_2 (nand_2_out, _74161_1_p13, not_1_out);
  nand nand_3 (nand_3_out, nand_2_out, _74161_1_p11);
  nand nand_4 (_74161_1_p11, nand_3_out, RX);
  Delay delay_1 (.in(nand_3_out), .out(delay_1_out));
  // _74164 _74164_1: pin names not known; wires that end beside it: 1'b1, 1'b0, RX, RX, _74161_1_p13, 1'b1, DATA[7], DATA[6], DATA[5], DATA[4], DATA[3], DATA[2], DATA[1], DATA[0]
  and and_1 (and_1_out, nand_3_out, ~delay_1_out);  // And
  RS_FF_AS rs_ff_as_1 (.S(and_1_out), .R(ACK), .Q(FULL));  // open: nQ

  // Notes on the sheet:
  //   http://digitarworld.uw.hu/circuits.html
  //   ? pcs 7400 Quad 2-input NAND
  //   ? pcs 7404 Hex inverter
  //   1 pcs 74164 SIPO Shift register
  //   2 pcs 74161 4 bit counter
endmodule
