// Digital circuit UART-TX-Tester.dig as structural Verilog
module UART_TX_Tester (
  input  [7:0] DIN,
  input  STB,
  output TX,
  output BUSY
);

  wire _74165_1_p21, _74393_1__1qa, _74393_1__1qb, _74393_1__1qc, _74393_1__1qd, _74393_1__2qa,
       _74393_1__2qb, _74393_1__2qc, _74393_1__2qd, CLK, d_ff_1_nq, d_ff_1_q, nand_1_out, nand_2_out,
       nand_3_out, nand_4_out, nand_5_out, nand_6_out;

  Button button_1 (.out(CLK));
  nand nand_1 (nand_1_out, STB, STB);
  // Probe CLK on CLK
  nand nand_2 (nand_2_out, nand_1_out, nand_3_out);
  nand nand_3 (nand_3_out, nand_2_out, d_ff_1_nq);
  D_FF d_ff_1 (.D(nand_2_out), .C(_74393_1__2qd), .Q(d_ff_1_q), .nQ(d_ff_1_nq));
  nand nand_4 (nand_4_out, nand_5_out, _74393_1__2qd);
  _74393 _74393_1 (
    .VCC(1'b1), .GND(1'b0), ._1A(nand_4_out), ._1CL(d_ff_1_q), ._2A(CLK), ._2CL(1'b0), ._1QA(_74393_1__1qa),
    ._1QB(_74393_1__1qb), ._1QC(_74393_1__1qc), ._1QD(_74393_1__1qd), ._2QA(_74393_1__2qa),
    ._2QB(_74393_1__2qb), ._2QC(_74393_1__2qc), ._2QD(_74393_1__2qd));
  nand nand_5 (nand_5_out, _74393_1__1qb, _74393_1__1qd);
  // _74165 _74165_1: pin names not known; wires that end beside it: _74393_1__1qa, _74393_1__1qc, _74393_1__2qa, _74393_1__2qb, _74393_1__2qc, _74393_1__2qd, d_ff_1_nq, DIN[7], 1'b0, _74393_1__2qd, 1'b1, DIN[6], DIN[5], DIN[4], DIN[3], DIN[2], DIN[1], DIN[0], 1'b1, 1'b0, _74165_1_p21
  or or_1 (BUSY, nand_2_out, nand_5_out);
  nand nand_6 (nand_6_out, d_ff_1_nq, _74165_1_p21);
  nand nand_7 (TX, BUSY, nand_6_out);

  // Notes on the sheet:
  //   TX: Serial data output
  //   DIN: 8 bit of parallel data to be sent, default 15
  //   BUSY: High while the TX output is transmidding start/data/stopbits.
  //   STB: Rising edge latches the parallel data at DIN and starts the serial output stream at TX
  //   SERIAL TRANSMITER
  //   Clock domain synchronizer
  //   10-counter, divide-by-16
endmodule
