// Digital circuit UART-TX.dig as structural Verilog
module UART_TX (
  input  CLK,
  input  nSTB,
  input  [7:0] D,
  output TX,
  output BUSY
);

  wire _74165_1_p15, _74393_1__1qa, _74393_1__1qd, _74393_1__2qa, _74393_1__2qb, _74393_1__2qc,
       _74393_1__2qd, d_ff_1_nq, d_ff_1_q, nand_1_out, nand_2_out, nand_3_out;

  nand nand_1 (nand_1_out, nSTB, nand_2_out);
  nand nand_2 (nand_2_out, nand_1_out, d_ff_1_nq);
  D_FF d_ff_1 (.D(nand_1_out), .C(_74393_1__2qb), .Q(d_ff_1_q), .nQ(d_ff_1_nq));
  nand nand_3 (nand_3_out, BUSY, _74393_1__2qb);
  _74393 _74393_1 (
    .VCC(1'b1), .GND(1'b0), ._1A(nand_3_out), ._1CL(d_ff_1_q), ._2A(CLK), ._2CL(1'b0), ._1QA(_74393_1__1qa),
    ._1QD(_74393_1__1qd), ._2QA(_74393_1__2qa), ._2QB(_74393_1__2qb), ._2QC(_74393_1__2qc),
    ._2QD(_74393_1__2qd));  // open: _1QB, _1QC
  nand nand_4 (BUSY, _74393_1__1qa, _74393_1__1qd);
  // _74165 _74165_1: pin names not known; wires that end beside it: nSTB, 1'b1, 1'b0, _74393_1__2qb, 1'b1, 1'b1, 1'b1, 1'b1, 1'b1, 1'b1, D[7], D[6], 1'b1, 1'b0, _74165_1_p15
  // _74165 _74165_2: pin names not known; wires that end beside it: nSTB, D[5], 1'b0, _74393_1__2qb, _74165_1_p15, D[4], D[3], D[2], D[1], D[0], 1'b0, 1'b1, 1'b1, 1'b0, TX
  // Pins of 1 and 8 bits meet at D

  // Notes on the sheet:
  //   CLK: Hz: 20
  //   1 pcs 7400   Quad 2-input NAND
  //   1 pcs 7474   D Flip-Flop
  //   1 pcs 74393 Dual 4-bit counters
  //   2 pcs 74165 PISO Shift register
endmodule
