// Digital circuit UART2.dig as structural Verilog
module UART2 (
  input  RX,
  input  ACK,
  input  OE,
  input  [7:0] DIN,
  input  STB,
  input  CLK,
  output [7:0] DOUT,
  output RDY,
  output TX,
  output BUSY
);

  wire _74165_1_p15, _74393_1__1qd, _74393_1__2qa, _74393_1__2qd, _74393_2__1qb, _74393_2__1qd,
       _74393_2__2qd, d_ff_1_nq, d_ff_2_nq, d_ff_3_nq, d_ff_3_q, nand_1_out, nand_2_out, nand_3_out,
       nand_4_out, nand_5_out, nand_6_out, nand_7_out, nand_9_out, nand_10_out, nand_11_out, nand_12_out,
       nand_13_out, nand_15_out;

  D_FF d_ff_1 (.D(STB), .C(CLK), .nQ(d_ff_1_nq));  // open: Q
  nand nand_1 (nand_1_out, nand_12_out, _74393_1__1qd);
  D_FF d_ff_2 (.D(ACK), .C(CLK), .nQ(d_ff_2_nq));  // open: Q
  nand nand_2 (nand_2_out, STB, d_ff_1_nq);
  nand nand_3 (nand_3_out, nand_1_out, nand_4_out);
  nand nand_4 (nand_4_out, nand_3_out, RX);
  nand nand_5 (nand_5_out, ACK, d_ff_2_nq);
  nand nand_6 (nand_6_out, nand_2_out, nand_7_out);
  nand nand_7 (nand_7_out, nand_6_out, d_ff_3_nq);
  _74393 _74393_1 (
    .VCC(1'b1), .GND(1'b0), ._1A(CLK), ._1CL(nand_3_out), ._2A(_74393_1__1qd), ._2CL(nand_3_out),
    ._1QD(_74393_1__1qd), ._2QA(_74393_1__2qa), ._2QD(_74393_1__2qd));  // open: _1QA, _1QB, _1QC, _2QB, _2QC
  D_FF d_ff_3 (.D(nand_6_out), .C(_74393_2__2qd), .Q(d_ff_3_q), .nQ(d_ff_3_nq));
  nand nand_8 (RDY, nand_3_out, nand_9_out);
  nand nand_9 (nand_9_out, RDY, nand_5_out);
  nand nand_10 (nand_10_out, _74393_1__2qa, _74393_1__2qd);
  nand nand_11 (nand_11_out, BUSY, _74393_2__2qd);
  nand nand_12 (nand_12_out, nand_10_out, nand_10_out);
  _74393 _74393_2 (
    .VCC(1'b1), .GND(1'b0), ._1A(nand_11_out), ._1CL(d_ff_3_q), ._2A(CLK), ._2CL(1'b0), ._1QB(_74393_2__1qb),
    ._1QD(_74393_2__1qd), ._2QD(_74393_2__2qd));  // open: _1QA, _1QC, _2QA, _2QB, _2QC
  nand nand_13 (nand_13_out, OE, OE);
  nand nand_14 (BUSY, _74393_2__1qb, _74393_2__1qd);
  // _74165 _74165_1: pin names not known; wires that end beside it: d_ff_3_nq, DIN[7], 1'b0, _74393_2__2qd, 1'b1, DIN[6], DIN[5], DIN[4], DIN[3], DIN[2], DIN[1], DIN[0], 1'b1, 1'b0, _74165_1_p15
  _74595 _74595_1 (
    .SER(RX), .SCLK(_74393_1__1qd), .RCLK(nand_12_out), .nOE(nand_13_out), .nCLR(1'b1), .VCC(1'b1),
    .GND(1'b0), .Q_A(DOUT[7]), .Q_B(DOUT[6]), .Q_C(DOUT[5]), .Q_D(DOUT[4]), .Q_E(DOUT[3]), .Q_F(DOUT[2]),
    .Q_G(DOUT[1]), .Q_H(DOUT[0]));  // open: Q_HH
  nand nand_15 (nand_15_out, d_ff_3_nq, _74165_1_p15);
  nand nand_16 (TX, BUSY, nand_15_out);

  // Notes on the sheet:
  //   DOUT: 8 bits of parallel data from the received serial stream. Controlled by the OE input
  //   RDY: Goes high when a full byte of data has been received at the RX. Cleared at the rising edge of the ACK input
  //   RX: Serial data input
  //   ACK: Rising edge acknowledges that the received data has been read. Causes the RDY output to go low.
  //   TX: Serial data output
  //   OE: High level enables the parallel output on DOUT of of the received data
  //   DIN: 8 bit of parallel data to be sent, default 15
  //   BUSY: High while the TX output is transmidding start/data/stopbits.
  //   STB: Rising edge latches the parallel data at DIN and starts the serial output stream at TX
  //   CLK: 16 times the desired baudrate, default 15
  //   The Serial Receiver is based on
  //   http://digitarworld.uw.hu/circuits.html
  //   2 pcs 7474 Dual D- Flip-Flop
  //   4 pcs 7400 Quad 2-input NAND
  //   2 pcs 74393 Dual 4-bit counter
  //   1 pcs 74165 PISO Shift register
  //   1 pcs 74595 SIPO Shift counter
endmodule
