// Digital circuit ind_dir.dig as structural Verilog
module ind_dir (
  input  OP0,
  input  IA,
  input  CP,
  input  IR3,
  input  IR4,
  input  IR5,
  input  IR6,
  input  OP1,
  input  OP2,
  input  A,
  output AUTOIND,
  output IND,
  output DIR,
  output MP
);

  wire _74138_1_p9, _74138_1_p10, _74138_1_p11, _74138_1_p12, _74138_1_p13, _74138_1_p14, _74138_1_p15,
       _74138_1_p16, AND, and_1_out, and_2_out, and_3_out, DCA, IOT, ISZ, JMP, JMS, nor_1_out, nor_3_out,
       nor_4_out, nor_5_out, nor_6_out, not_10_out, not_11_out, not_12_out, OPR, TAD;

  nor nor_1 (nor_1_out, IR4, IR5, IR6);
  // NOr nor_2 has open pins: In_1=1'b0, In_2=1'b0, In_3=1'b0, out=open
  // Not not_1 has open pins: in=1'b0, out=open
  nor nor_3 (nor_3_out, A, A, A);
  nor nor_4 (nor_4_out, A, A, 1'b0);
  and and_1 (and_1_out, IR3, nor_1_out);
  // _74138 _74138_1: pin names not known; wires that end beside it: 1'b1, 1'b0, 1'b1, 1'b0, 1'b0, OP0, OP1, OP2, _74138_1_p9, _74138_1_p10, _74138_1_p11, _74138_1_p12, _74138_1_p13, _74138_1_p14, _74138_1_p15, _74138_1_p16
  not not_2 (AND, _74138_1_p9);
  not not_3 (TAD, _74138_1_p10);
  not not_4 (ISZ, _74138_1_p11);
  not not_5 (DCA, _74138_1_p12);
  not not_6 (JMS, _74138_1_p13);
  not not_7 (JMP, _74138_1_p14);
  not not_8 (IOT, _74138_1_p15);
  not not_9 (OPR, _74138_1_p16);
  not not_10 (not_10_out, CP);
  and and_2 (and_2_out, nor_3_out, nor_4_out, and_1_out);
  and and_3 (and_3_out, not_10_out, and_1_out);
  nor nor_5 (nor_5_out, and_2_out, 1'b0, and_3_out);
  not not_11 (not_11_out, nor_5_out);
  not not_12 (not_12_out, IA);
  nor nor_6 (nor_6_out, OPR, 1'b0, IOT);
  and and_4 (AUTOIND, nor_6_out, IA, not_11_out);
  and and_5 (IND, nor_6_out, IA, nor_5_out);
  and and_6 (DIR, nor_6_out, not_12_out);
  and and_7 (MP, nor_6_out, CP);
  LED led_1 (.in(AUTOIND));
  LED led_2 (.in(IND));
  LED led_3 (.in(DIR));
  LED led_4 (.in(MP));

  // Notes on the sheet:
  //   IA=0 DIRECT
  //   IA=1 INDIRECT
  //   CP=0 PAGE ZERO
  //   CP=1 CURRENT PAGE
  //   2 pcs 7404 Hex inverter
  //   1 pcs 7408 Quad 2-input AND
  //   1 pcs 7411 Triple 3-input AND
  //   2 pcs 7427 Triple 3-input NOR
  //   1 pcs 74138 Decoder 3-to-8
endmodule

/* Test case:
OP0 IA CP IR3 IR4 IR5 IR6 OP1 OP2 A AUTOIND IND DIR MP

0   0  0  0   0   0   0   0   0   0 0       0   1   0
0   0  0  0   0   0   0   0   0   1 0       0   1   0
0   0  0  0   0   0   0   0   1   0 0       0   1   0
0   0  0  0   0   0   0   0   1   1 0       0   1   0
0   0  0  0   0   0   0   1   0   0 0       0   1   0
0   0  0  0   0   0   0   1   0   1 0       0   1   0
0   0  0  0   0   0   0   1   1   0 0       0   0   0
0   0  0  0   0   0   0   1   1   1 0       0   0   0
0   0  0  0   0   0   1   0   0   0 0       0   1   0
0   0  0  0   0   0   1   0   0   1 0       0   1   0
0   0  0  0   0   0   1   0   1   0 0       0   1   0
0   0  0  0   0   0   1   0   1   1 0       0   1   0
0   0  0  0   0   0   1   1   0   0 0       0   1   0
0   0  0  0   0   0   1   1   0   1 0       0   1   0
0   0  0  0   0   0   1   1   1   0 0       0   0   0
0   0  0  0   0   0   1   1   1   1 0       0   0   0
0   0  0  0   0   1   0   0   0   0 0       0   1   0
0   0  0  0   0   1   0   0   0   1 0       0   1   0
0   0  0  0   0   1   0   0   1   0 0       0   1   0
0   0  0  0   0   1   0   0   1   1 0       0   1   0
0   0  0  0   0   1   0   1   0   0 0       0   1   0
0   0  0  0   0   1   0   1   0   1 0       0   1   0
0   0  0  0   0   1   0   1   1   0 0       0   0   0
0   0  0  0   0   1   0   1   1   1 0       0   0   0
0   0  0  0   0   1   1   0   0   0 0       0   1   0
0   0  0  0   0   1   1   0   0   1 0       0   1   0
0   0  0  0   0   1   1   0   1   0 0       0   1   0
0   0  0  0   0   1   1   0   1   1 0       0   1   0
0   0  0  0   0   1   1   1   0   0 0       0   1   0
0   0  0  0   0   1   1   1   0   1 0       0   1   0
0   0  0  0   0   1   1   1   1   0 0       0   0   0
0   0  0  0   0   1   1   1   1   1 0       0   0   0
0   0  0  0   1   0   0   0   0   0 0       0   1   0
0   0  0  0   1   0   0   0   0   1 0       0   1   0
0   0  0  0   1   0   0   0   1   0 0       0   1   0
0   0  0  0   1   0   0   0   1   1 0       0   1   0
0   0  0  0   1   0   0   1   0   0 0       0   1   0
0   0  0  0   1   0   0   1   0   1 0       0   1   0
0   0  0  0   1   0   0   1   1   0 0       0   0   0
0   0  0  0   1   0   0   1   1   1 0       0   0   0
0   0  0  0   1   0   1   0   0   0 0       0   1   0
0   0  0  0   1   0   1   0   0   1 0       0   1   0
0   0  0  0   1   0   1   0   1   0 0       0   1   0
0   0  0  0   1   0   1   0   1   1 0       0   1   0
0   0  0  0   1   0   1   1   0   0 0       0   1   0
0   0  0  0   1   0   1   1   0   1 0       0   1   0
0   0  0  0   1   0   1   1   1   0 0       0   0   0
0   0  0  0   1   0   1   1   1   1 0       0   0   0
0   0  0  0   1   1   0   0   0   0 0       0   1   0
0   0  0  0   1   1   0   0   0   1 0       0   1   0
0   0  0  0   1   1   0   0   1   0 0       0   1   0
0   0  0  0   1   1   0   0   1   1 0       0   1   0
0   0  0  0   1   1   0   1   0   0 0       0   1   0
0   0  0  0   1   1   0   1   0   1 0       0   1   0
0   0  0  0   1   1   0   1   1   0 0       0   0   0
0   0  0  0   1   1   0   1   1   1 0       0   0   0
0   0  0  0   1   1   1   0   0   0 0       0   1   0
0   0  0  0   1   1   1   0   0   1 0       0   1   0
0   0  0  0   1   1   1   0   1   0 0       0   1   0
0   0  0  0   1   1   1   0   1   1 0       0   1   0
0   0  0  0   1   1   1   1   0   0 0       0   1   0
0   0  0  0   1   1   1   1   0   1 0       0   1   0
0   0  0  0   1   1   1   1   1   0 0       0   0   0
0   0  0  0   1   1   1   1   1   1 0       0   0   0
0   0  0  1   0   0   0   0   0   0 0       0   1   0
0   0  0  1   0   0   0   0   0   1 0       0   1   0
0   0  0  1   0   0   0   0   1   0 0       0   1   0
0   0  0  1   0   0   0   0   1   1 0       0   1   0
0   0  0  1   0   0   0   1   0   0 0       0   1   0
0   0  0  1   0   0   0   1   0   1 0       0   1   0
0   0  0  1   0   0   0   1   1   0 0       0   0   0
0   0  0  1   0   0   0   1   1   1 0       0   0   0
0   0  0  1   0   0   1   0   0   0 0       0   1   0
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*/
