// Digital circuit test1.dig as structural Verilog
module test1 (
  input  IOT,
  input  CK,
  output Y1,
  output Y2,
  output Y3
);

  wire not_1_out, not_2_out, not_3_out, or_1_out;

  not not_1 (not_1_out, CK);
  and and_1 (Y1, not_1_out, IOT);
  not not_2 (not_2_out, IOT);
  not not_3 (not_3_out, IOT);
  or or_1 (or_1_out, CK, not_2_out);
  nor nor_1 (Y3, CK, not_3_out);
  not not_4 (Y2, or_1_out);
endmodule
