// Digital circuit jonsson.dig as structural Verilog
module jonsson (
  input  RESET,
  input  CLK
);

  wire and_1_out, and_2_out, and_3_out, and_4_out, and_5_out, and_6_out, and_7_out, and_8_out, and_9_out,
       and_10_out, and_11_out, and_12_out, and_13_out, and_14_out, and_15_out, and_16_out, and_17_out,
       and_18_out, and_19_out, and_20_out, jk_ff_as_1_nq, jk_ff_as_1_q, jk_ff_as_2_nq, jk_ff_as_2_q,
       jk_ff_as_3_nq, jk_ff_as_3_q, jk_ff_as_4_nq, jk_ff_as_4_q, jk_ff_as_5_nq, jk_ff_as_5_q, jk_ff_as_6_nq,
       jk_ff_as_6_q, jk_ff_as_7_nq, jk_ff_as_7_q, jk_ff_as_8_nq, jk_ff_as_8_q, jk_ff_as_9_nq, jk_ff_as_9_q,
       jk_ff_as_10_nq, jk_ff_as_10_q;

  LED led_1 (.in(and_1_out));
  and and_1 (and_1_out, jk_ff_as_1_nq, jk_ff_as_10_nq);
  LED led_2 (.in(and_2_out));
  and and_2 (and_2_out, jk_ff_as_1_q, jk_ff_as_2_nq);
  LED led_3 (.in(and_3_out));
  and and_3 (and_3_out, jk_ff_as_2_q, jk_ff_as_3_nq);
  JK_FF_AS jk_ff_as_1 (
    .Set(1'b0), .J(jk_ff_as_10_nq), .C(CLK), .K(jk_ff_as_10_q), .Clr(RESET), .Q(jk_ff_as_1_q),
    .nQ(jk_ff_as_1_nq));
  LED led_4 (.in(and_4_out));
  and and_4 (and_4_out, jk_ff_as_3_q, jk_ff_as_4_nq);
  LED led_5 (.in(and_5_out));
  and and_5 (and_5_out, jk_ff_as_4_q, jk_ff_as_5_nq);
  JK_FF_AS jk_ff_as_2 (
    .Set(1'b0), .J(jk_ff_as_1_q), .C(CLK), .K(jk_ff_as_1_nq), .Clr(RESET), .Q(jk_ff_as_2_q),
    .nQ(jk_ff_as_2_nq));
  LED led_6 (.in(and_6_out));
  and and_6 (and_6_out, jk_ff_as_5_q, jk_ff_as_6_nq);
  LED led_7 (.in(and_7_out));
  and and_7 (and_7_out, jk_ff_as_6_q, jk_ff_as_7_nq);
  JK_FF_AS jk_ff_as_3 (
    .Set(1'b0), .J(jk_ff_as_2_q), .C(CLK), .K(jk_ff_as_2_nq), .Clr(RESET), .Q(jk_ff_as_3_q),
    .nQ(jk_ff_as_3_nq));
  LED led_8 (.in(and_8_out));
  and and_8 (and_8_out, jk_ff_as_7_q, jk_ff_as_8_nq);
  LED led_9 (.in(and_9_out));
  and and_9 (and_9_out, jk_ff_as_8_q, jk_ff_as_9_nq);
  JK_FF_AS jk_ff_as_4 (
    .Set(1'b0), .J(jk_ff_as_3_q), .C(CLK), .K(jk_ff_as_3_nq), .Clr(RESET), .Q(jk_ff_as_4_q),
    .nQ(jk_ff_as_4_nq));
  LED led_10 (.in(and_10_out));
  and and_10 (and_10_out, jk_ff_as_9_q, jk_ff_as_10_nq);
  LED led_11 (.in(and_11_out));
  and and_11 (and_11_out, jk_ff_as_1_q, jk_ff_as_10_q);
  JK_FF_AS jk_ff_as_5 (
    .Set(1'b0), .J(jk_ff_as_4_q), .C(CLK), .K(jk_ff_as_4_nq), .Clr(RESET), .Q(jk_ff_as_5_q),
    .nQ(jk_ff_as_5_nq));
  LED led_12 (.in(and_12_out));
  and and_12 (and_12_out, jk_ff_as_1_nq, jk_ff_as_2_q);
  LED led_13 (.in(and_13_out));
  and and_13 (and_13_out, jk_ff_as_2_nq, jk_ff_as_3_q);
  JK_FF_AS jk_ff_as_6 (
    .Set(1'b0), .J(jk_ff_as_5_q), .C(CLK), .K(jk_ff_as_5_nq), .Clr(RESET), .Q(jk_ff_as_6_q),
    .nQ(jk_ff_as_6_nq));
  LED led_14 (.in(and_14_out));
  and and_14 (and_14_out, jk_ff_as_3_nq, jk_ff_as_4_q);
  LED led_15 (.in(and_15_out));
  and and_15 (and_15_out, jk_ff_as_4_nq, jk_ff_as_5_q);
  JK_FF_AS jk_ff_as_7 (
    .Set(1'b0), .J(jk_ff_as_6_q), .C(CLK), .K(jk_ff_as_6_nq), .Clr(RESET), .Q(jk_ff_as_7_q),
    .nQ(jk_ff_as_7_nq));
  LED led_16 (.in(and_16_out));
  and and_16 (and_16_out, jk_ff_as_5_nq, jk_ff_as_6_q);
  LED led_17 (.in(and_17_out));
  and and_17 (and_17_out, jk_ff_as_6_nq, jk_ff_as_7_q);
  JK_FF_AS jk_ff_as_8 (
    .Set(1'b0), .J(jk_ff_as_7_q), .C(CLK), .K(jk_ff_as_7_nq), .Clr(RESET), .Q(jk_ff_as_8_q),
    .nQ(jk_ff_as_8_nq));
  LED led_18 (.in(and_18_out));
  and and_18 (and_18_out, jk_ff_as_7_nq, jk_ff_as_8_q);
  LED led_19 (.in(and_19_out));
  and and_19 (and_19_out, jk_ff_as_8_nq, jk_ff_as_9_q);
  JK_FF_AS jk_ff_as_9 (
    .Set(1'b0), .J(jk_ff_as_8_q), .C(CLK), .K(jk_ff_as_8_nq), .Clr(RESET), .Q(jk_ff_as_9_q),
    .nQ(jk_ff_as_9_nq));
  LED led_20 (.in(and_20_out));
  and and_20 (and_20_out, jk_ff_as_9_nq, jk_ff_as_10_q);
  JK_FF_AS jk_ff_as_10 (
    .Set(1'b0), .J(jk_ff_as_9_q), .C(CLK), .K(jk_ff_as_9_nq), .Clr(RESET), .Q(jk_ff_as_10_q),
    .nQ(jk_ff_as_10_nq));
endmodule
